// Logisim project cpu24 - 单周期+单级中断+多级中断+理想流水线+EX段气泡流水线+EX段重定向流水线+EX段流水线中断.circ as structural Verilog: 34 circuits, main circuit ◇单周期MIPS
module \单周期MIPS  (
  input  IR1,
  input  IR2,
  input  IR3,
  output RegWrite,
  output MemWrite,
  output [31:0] PC,
  output [31:0] IR,
  output [31:0] RDin,
  output [31:0] MDin,
  output [31:0] LedData
);

  wire AluSrcB, and_1_out, and_2_out, and_3_out, and_6_out, and_7_out, Beq, BLEZ, BLEZ_LESS, Bne, CLK,
       clock_1_out, clock_2_out, comparator_1_eq, comparator_2_eq, comparator_3_eq, comparator_4_eq,
       comparator_4_lt, d_ff_2_q, equal, ERET, Exit, Go, IR1_t, IR2_t, IR3_t, IRA, IRB, IRC, JAL, JMP, JR,
       LBU, MemToReg, nand_1_out, or_1_out, or_5_out, Pause, RegDst, SignedExt, Stop, SysCall, W1, W2, W3;
  wire [1:0] pull_resistor_1_node;
  wire [3:0] AluOp;
  wire [4:0] multiplexer_1_out, multiplexer_2_out, multiplexer_3_out;
  wire [7:0] pull_resistor_4_node, pull_resistor_5_node, pull_resistor_6_node;
  wire [12:0] CNT_num;
  wire [15:0] \总周期数 ;
  wire [31:0] adder_1_out, adder_2_out, adder_3_out, bit_extender_1_out, bit_extender_2_out,
       bit_extender_3_out, mips_regifile_1_r1, multiplexer_4_out, multiplexer_5_out, multiplexer_6_out,
       multiplexer_7_out, multiplexer_8_out, multiplexer_9_out, multiplexer_10_out, pull_resistor_2_node;
  wire [31:1] mips_alu_1_result;
  wire [31:8] pull_resistor_3_node_2, pull_resistor_4_node_2, pull_resistor_5_node_2, pull_resistor_6_node_2;
  wire [31:24] pull_resistor_3_node;

  Clock #(.highDuration(1), .lowDuration(1)) clock_1 (.out(clock_1_out));
  Button _1 (.out(IRA));
  Button _2 (.out(IRB));
  Button _3 (.out(IRC));
  Button \u_继续运行  (.out(Go));
  LED #(.active("true")) led_1 (.in(W1));
  LED #(.active("true")) led_2 (.in(W2));
  LED #(.active("true")) led_3 (.in(W3));
  Hex_Digit_Display hex_digit_display_1 (.value(LedData[31:28]));  // open: dp
  or or_1 (or_1_out, Pause, Exit);
  Hex_Digit_Display hex_digit_display_2 (.value(LedData[27:24]));  // open: dp
  Hex_Digit_Display hex_digit_display_3 (.value(LedData[23:20]));  // open: dp
  D_Flip_Flop #(.trigger("rising"), .Pre_Clr_Positions("ABOVE_BELOW"), .NegatePresetClear("false"), .enable("false"), .NewFFLayout("true")) d_ff_1 (
    .clk(or_1_out), .D(1'b1), .Qn(Stop), .reset(and_1_out));  // open: Q, preset
  and and_1 (and_1_out, ~Exit, Go);  // AND_Gate
  // Probe on multiplexer_8_out
  Hex_Digit_Display hex_digit_display_4 (.value(LedData[19:16]));  // open: dp
  Hex_Digit_Display hex_digit_display_5 (.value(LedData[15:12]));  // open: dp
  Hex_Digit_Display hex_digit_display_6 (.value(LedData[11:8]));  // open: dp
  Hex_Digit_Display hex_digit_display_7 (.value(LedData[7:4]));  // open: dp
  // Probe on \总周期数 
  Register #(.width(32), .trigger("rising"), .Select("low")) u_PC (
    .D(multiplexer_8_out), .en(Stop), .Q(PC), .clk(CLK));  // open: clr
  // Probe on PC
  Hex_Digit_Display hex_digit_display_8 (.value(LedData[3:0]));  // open: dp
  Counter #(.width(16), .max('hffff), .ongoal("wrap"), .trigger("rising"), .behavior("new")) counter_1 (
    .count(Stop), .Q(\总周期数 ), .clk(CLK));  // open: load, D, carry, clr, preset, down
  or or_2 (IR1_t, IR1, IRA);
  // Mips_Probe mips_probe_1: pin names not known; wires that end beside it: IR
  ROM #(.addrWidth(10), .dataWidth(32), .Select("high")) rom_1 (.addr(PC[11:2]), .data(IR));
  Adder #(.width(32)) adder_1 (.a(PC), .b(32'h4), .out(adder_1_out), .cin(1'b0));  // open: cout
  or or_3 (IR2_t, IR2, IRB);
  Multiplexer #(.select(2), .width(5), .disabled("Z"), .enable("false")) multiplexer_1 (
    .in0(IR[15:11]), .in1(IR[20:16]), .in2({5{1'b1}}), .in3({5{1'b1}}), .out(multiplexer_1_out),
    .sel({JAL, RegDst}));
  assign bit_extender_1_out = {{16{1'b0}}, IR[15:0]};  // Bit_Extender bit_extender_1
  assign bit_extender_2_out = {{16{IR[15]}}, IR[15:0]};  // Bit_Extender bit_extender_2
  Pull_Resistor #(.pull(0)) pull_resistor_1 (.node({IR[15:0], pull_resistor_1_node}));
  Multiplexer #(.select(1), .width(5), .disabled("Z"), .enable("false")) multiplexer_2 (
    .in0(IR[25:21]), .in1(5'b00010), .out(multiplexer_2_out), .sel(SysCall));
  Multiplexer #(.select(1), .width(5), .disabled("Z"), .enable("false")) multiplexer_3 (
    .in0(IR[20:16]), .in1(5'b00100), .out(multiplexer_3_out), .sel(SysCall));
  assign bit_extender_3_out = {{14{IR[15]}}, {IR[15:0], pull_resistor_1_node}};  // Bit_Extender bit_extender_3
  or or_4 (IR3_t, IR3, IRC);
  MIPS_Regifile mips_regifile_1 (
    .Din(RDin), .Clk(CLK), .R1(mips_regifile_1_r1), .R2(MDin), .WE(RegWrite), .W_num(multiplexer_1_out),
    .R1_num(multiplexer_2_out), .R2_num(multiplexer_3_out));
  Multiplexer #(.select(1), .width(32), .disabled("Z"), .enable("false")) multiplexer_4 (
    .in0(bit_extender_1_out), .in1(bit_extender_2_out), .out(multiplexer_4_out), .sel(SignedExt));
  Adder #(.width(32)) adder_2 (.a(adder_1_out), .b(bit_extender_3_out), .out(adder_2_out));  // open: cin, cout
  Multiplexer #(.select(1), .width(32), .disabled("Z"), .enable("false")) multiplexer_5 (
    .in0(MDin), .in1(multiplexer_4_out), .out(multiplexer_5_out), .sel(AluSrcB));
  Pull_Resistor #(.pull(0)) pull_resistor_2 (.node({pull_resistor_2_node[31:28], IR[25:0], pull_resistor_2_node[1:0]}));
  // Probe on adder_1_out
  // Probe on adder_2_out
  Comparator #(.width(32), .mode("twosComplement")) comparator_1 (
    .a(32'h32), .b(mips_regifile_1_r1), .eq(comparator_1_eq));  // open: gt, lt
  Comparator #(.width(32), .mode("twosComplement")) comparator_2 (
    .a(32'ha), .b(mips_regifile_1_r1), .eq(comparator_2_eq));  // open: gt, lt
  Comparator #(.width(32), .mode("twosComplement")) comparator_3 (
    .a(32'h22), .b(mips_regifile_1_r1), .eq(comparator_3_eq));  // open: gt, lt
  MIPS_ALU mips_alu_1 (
    .X(mips_regifile_1_r1), .Y(multiplexer_5_out), .AluOP(AluOp), .Equal(equal),
    .Result({mips_alu_1_result, BLEZ_LESS}), .shamt(IR[10:6]));  // open: Result_2
  or or_5 (or_5_out, and_2_out, and_3_out, and_7_out);
  and and_2 (and_2_out, Beq, equal);
  and and_3 (and_3_out, BLEZ_LESS, BLEZ);
  and and_4 (Pause, SysCall, comparator_1_eq);
  and and_5 (Exit, SysCall, comparator_2_eq);
  and and_6 (and_6_out, SysCall, comparator_3_eq);
  Multiplexer #(.select(1), .width(32), .disabled("Z"), .enable("false")) multiplexer_6 (
    .in0({pull_resistor_2_node[31:28], IR[25:0], pull_resistor_2_node[1:0]}), .in1(mips_regifile_1_r1),
    .out(multiplexer_6_out), .sel(JR));
  Multiplexer #(.select(1), .width(32), .disabled("Z"), .enable("false")) multiplexer_7 (
    .in0(adder_1_out), .in1(adder_2_out), .out(multiplexer_7_out), .sel(or_5_out));
  and and_7 (and_7_out, ~equal, Bne);  // AND_Gate
  Register #(.width(32), .trigger("rising"), .Select("low")) register_1 (
    .D(multiplexer_5_out), .en(and_6_out), .Q(LedData), .clk(CLK));  // open: clr
  Adder #(.width(32)) adder_3 (.a(PC), .b(32'h4), .out(adder_3_out));  // open: cin, cout
  Multiplexer #(.select(1), .width(32), .disabled("Z"), .enable("false")) multiplexer_8 (
    .in0(multiplexer_7_out), .in1(multiplexer_6_out), .out(multiplexer_8_out), .sel(JMP));
  Pull_Resistor #(.pull(0)) pull_resistor_3 (.node({pull_resistor_3_node_2, pull_resistor_3_node}));
  Pull_Resistor #(.pull(0)) pull_resistor_4 (.node({pull_resistor_4_node_2, pull_resistor_4_node}));
  Pull_Resistor #(.pull(0)) pull_resistor_5 (.node({pull_resistor_5_node_2, pull_resistor_5_node}));
  Pull_Resistor #(.pull(0)) pull_resistor_6 (.node({pull_resistor_6_node_2, pull_resistor_6_node}));
  Multiplexer #(.select(1), .width(32), .disabled("Z"), .enable("false")) multiplexer_9 (
    .in0({pull_resistor_3_node, pull_resistor_5_node, pull_resistor_4_node, pull_resistor_6_node}),
    .in1(multiplexer_10_out), .out(multiplexer_9_out), .sel(LBU));
  RAM #(.addrWidth(10), .dataWidth(32), .bus("separate"), .Select("high")) ram_1 (
    .addr(mips_alu_1_result[11:2]), .din(MDin),
    .data({pull_resistor_3_node, pull_resistor_5_node, pull_resistor_4_node, pull_resistor_6_node}),
    .str(MemWrite), .clk(CLK));  // open: sel, ld, clr
  D_Flip_Flop #(.trigger("high"), .Pre_Clr_Positions("LEGACY"), .NegatePresetClear("false"), .enable("true"), .NewFFLayout("false")) d_ff_2 (.Q(d_ff_2_q));  // open: clk, D, Qn, preset, en, reset
  // Probe on 13'h55
  Multiplexer #(.select(2), .width(32), .disabled("Z"), .enable("false")) multiplexer_10 (
    .in0({pull_resistor_6_node_2, pull_resistor_6_node}),
    .in1({pull_resistor_4_node_2, pull_resistor_4_node}),
    .in2({pull_resistor_5_node_2, pull_resistor_5_node}),
    .in3({pull_resistor_3_node_2, pull_resistor_3_node}), .out(multiplexer_10_out),
    .sel({mips_alu_1_result[1], BLEZ_LESS}));
  Multiplexer #(.select(2), .width(32), .disabled("Z"), .enable("false")) multiplexer_11 (
    .in0({mips_alu_1_result, BLEZ_LESS}), .in1(multiplexer_9_out), .in2(adder_3_out), .in3(adder_3_out),
    .out(RDin), .sel({JAL, MemToReg}));
  Comparator #(.width(13), .mode("twosComplement")) comparator_4 (
    .a(CNT_num), .b(13'h55), .eq(comparator_4_eq), .lt(comparator_4_lt));  // open: gt
  Clock #(.highDuration(1), .lowDuration(1)) clock_2 (.out(clock_2_out));
  nand nand_1 (nand_1_out, d_ff_2_q, comparator_4_eq);
  Counter #(.width(13), .max('h1fff), .ongoal("stay"), .trigger("rising"), .behavior("old")) counter_2 (
    .count(comparator_4_lt), .Q(CNT_num), .clk(clock_2_out));  // open: load, D, carry, clr, preset
  assign CLK = nand_1_out ? clock_2_out : 1'bz;  // Controlled_Buffer controlled_buffer_1
  Pull_Resistor #(.pull(1)) pull_resistor_7 (.node(CLK));
  \单周期硬布线控制器  \u_单周期硬布线控制器_1  (
    .Func(IR[5:0]), .OP(IR[31:26]), .ALU_OP(AluOp), .MemToReg(MemToReg), .MemWrite(MemWrite),
    .ALU_SRC(AluSrcB), .RegWrite(RegWrite), .SysCALL(SysCall), .SignedExt(SignedExt), .RegDst(RegDst),
    .JR(JR), .JMP(JMP), .Beq(Beq), .JAL(JAL), .Bne(Bne), .ERET(ERET), .LBU(LBU), .BLEZ(BLEZ));

  // Other names for the same wires on the sheet: Func[5:0] = IR[5:0]; OP[5:0] = IR[31:26]

  // Notes on the sheet:
  //   中断源
  //   中断等待指示
  //   总复位信号应将除ROM以外所有存储组件全部清零
  //   数码管输出
  //   数码管输出应该用寄存器锁存，否则显示数据只能一闪而过
  //   指令存储器
  //   rs
  //   指令字
  //   contents of rom_1 (hex, n*v repeats v):
  //   20110001 8000c05 20110001 20120002 20130003 8000c09 20110001 20120002 20130003 8000c0d 20110001
  //   20120002 20130003 8000c11 20110001 20120002 20130003 c000cf1 20100001 20110001 118fc0 112020
  //   20020022 c 118882 12200001 8000c15 112020 20020022 c 20110001 118880 112020 20020022 c 12200001
  //   8000c1f 20110001 118fc0 112020 20020022 c 1188c3 112020 20020022 c 118903 112020 20020022 c 118903
  //   112020 20020022 c 118903 112020 20020022 c 118903 112020 20020022 c 118903 112020 20020022 c 118903
  //   112020 20020022 c 118903 112020 20020022 c 20100001 109fc0 139fc3 8021 2012000c 24160003 26100001
  //   3210000f 20080008 20090001 139900 2709825 132020 20020022 c 1094022 1500fff9 22100001 2018000f
  //   2188024 108700 20080008 20090001 139902 2709825 132021 20020022 c 1094022 1500fff9 108702 2c9b022
  //   12c00001 8000c50 4020 1084027 84400 3508ffff 82021 20020022 c 2010ffff 20110000 ae300000 22100001
  //   22310004 ae300000 22100001 22310004 ae300000 22100001 22310004 ae300000 22100001 22310004 ae300000
  //   22100001 22310004 ae300000 22100001 22310004 ae300000 22100001 22310004 ae300000 22100001 22310004
  //   ae300000 22100001 22310004 ae300000 22100001 22310004 ae300000 22100001 22310004 ae300000 22100001
  //   22310004 ae300000 22100001 22310004 ae300000 22100001 22310004 ae300000 22100001 22310004 ae300000
  //   22100001 22310004 22100001 8020 2011003c 8e130000 8e340000 274402a 11000002 ae330000 ae140000
  //   2231fffc 1611fff8 102020 20020022 c 22100004 2011003c 1611fff2 20020032 c 2008ffff 20117777 112020
  //   20020022 c 200b0010 2288826 112020 20020022 c 216bffff 1560fffa 20020032 c 2008ffff 20090000
  //   20111997 112020 20020022 c 2288820 2e291949 1120fffa 20020032 c 20090000 200b0010 34118483 20120404
  //   118c00 129400 36318281 22520404 ad310000 2328820 21290004 216bffff 1560fffb 200b0020 20090000
  //   91310000 112020 20020022 c 21290001 216bffff 1560fff9 20020032 c 2011fff1 112020 20020022 c 22310001
  //   1a20fffb 2002000a c 20100000 22100001 102020 20020022 c 22100002 102020 20020022 c 22100003 102020
  //   20020022 c 22100004 102020 20020022 c 22100005 102020 20020022 c 22100006 102020 20020022 c 22100007
  //   102020 20020022 c 22100008 102020 20020022 20020022 c 3e00008
  //   rd
  //   OP
  //   Func
  //   rt
  //   为方便自动评测，需要输出PC，IR，寄存器堆写如数据RDin
  //   RAM写使能MemWrite、RAM写入数据MDin等信号
  //   控制位
  //   暂停节拍，不能为0
  //   戳工具置1进入计数暂停模式，ctrl+k时钟自动运行到对应节拍暂停
  //   ctrl+k关闭时钟连续运行，将控制位置零，进入单步调试模式调试
  //   用这个时钟源需要去掉电路中的其他时钟源
  //   可计数暂停的时钟源
  //   JMP
  //   JR
  //   OP
  //   Func
  //   Syscall
  //   Beq
  //   Bne
  //   MemToReg
  //   MemWrite
  //   AluOP
  //   AluSrcB
  //   RegWrite
  //   JAL
  //   RegDst
endmodule

// 单周期硬布线控制器
module \单周期硬布线控制器  (
  input  [5:0] OP,
  input  [5:0] Func,
  output [3:0] ALU_OP,
  output MemToReg,
  output MemWrite,
  output ALU_SRC,
  output RegWrite,
  output SysCALL,
  output SignedExt,
  output RegDst,
  output Beq,
  output Bne,
  output JR,
  output JMP,
  output JAL,
  output ERET,
  output LBU,
  output BLEZ
);

  \运算控制器自动生成  \u_运算控制器自动生成_1  (
    .OP0(OP[0]), .OP1(OP[1]), .OP2(OP[2]), .OP3(OP[3]), .OP4(OP[4]), .OP5(OP[5]), .F0(Func[0]), .F1(Func[1]),
    .F2(Func[2]), .F3(Func[3]), .F4(Func[4]), .F5(Func[5]), .S0(ALU_OP[0]), .S1(ALU_OP[1]), .S2(ALU_OP[2]),
    .S3(ALU_OP[3]));
  \控制信号自动生成  \u_控制信号自动生成_1  (
    .OP0(OP[0]), .OP1(OP[1]), .OP2(OP[2]), .OP3(OP[3]), .OP4(OP[4]), .OP5(OP[5]), .F0(Func[0]), .F1(Func[1]),
    .F2(Func[2]), .F3(Func[3]), .F4(Func[4]), .F5(Func[5]), .MemToReg(MemToReg), .MemWrite(MemWrite),
    .ALU_SRC(ALU_SRC), .RegWrite(RegWrite), .SysCALL(SysCALL), .SignedExt(SignedExt), .RegDst(RegDst),
    .BEQ(Beq), .BNE(Bne), .JR(JR), .JUMP(JMP), .JAL(JAL), .ERET(ERET), .LBU(LBU), .BLEZ(BLEZ));

  // Other names for the same wires on the sheet: OP_CODE[5:0] = OP

  // Notes on the sheet:
  //   运算器控制器，根据指令生成运算器功能选择信号
  //   控制信号生成，产生数据通路需要的其他控制信号
endmodule

// 运算器控制器
module \运算控制器自动生成  (
  input  OP0,
  input  OP1,
  input  OP2,
  input  OP3,
  input  OP4,
  input  OP5,
  input  F0,
  input  F1,
  input  F2,
  input  F3,
  input  F4,
  input  F5,
  output S0,
  output S1,
  output S2,
  output S3
);

  wire and_1_out, and_2_out, and_3_out, and_4_out, and_5_out, and_6_out, and_7_out, and_8_out, and_9_out,
       and_10_out, and_11_out, and_12_out, and_13_out, and_14_out, and_15_out, and_16_out, and_17_out,
       and_18_out, and_19_out, and_20_out, and_21_out, and_22_out, and_23_out, and_24_out, and_25_out,
       and_26_out, and_27_out, and_28_out, and_29_out, and_30_out, and_31_out, and_32_out, and_33_out,
       and_34_out, and_35_out, and_36_out, and_37_out, and_38_out, and_39_out, and_40_out, and_41_out,
       and_42_out, and_43_out, not_1_out, not_2_out, not_3_out, not_4_out, not_5_out, not_6_out, not_7_out,
       not_8_out, not_9_out, not_10_out, not_11_out, not_12_out, not_13_out, not_14_out, not_15_out,
       not_16_out, not_17_out, not_18_out, not_19_out, not_20_out, not_21_out, not_22_out, not_23_out,
       not_24_out, not_25_out, not_26_out, not_27_out, not_28_out, not_29_out, not_30_out, not_31_out,
       not_32_out, not_33_out, not_34_out, not_35_out, not_36_out, not_37_out, not_38_out, not_39_out,
       not_40_out, not_41_out, not_42_out, not_43_out, not_44_out, not_45_out, not_46_out, not_47_out,
       not_48_out, not_49_out, not_50_out, not_51_out, not_52_out, not_53_out, not_54_out, not_55_out,
       not_56_out, not_57_out, not_58_out, not_59_out, not_60_out, not_61_out, not_62_out, not_63_out,
       not_64_out, not_65_out, not_66_out, not_67_out, not_68_out, not_69_out, not_70_out, not_71_out,
       not_72_out, not_73_out, not_74_out, not_75_out, not_76_out, not_77_out, not_78_out, not_79_out,
       not_80_out, not_81_out, not_82_out, not_83_out, not_84_out, not_85_out, not_86_out, not_87_out,
       not_88_out, not_89_out, not_90_out, not_91_out, not_92_out, not_93_out, not_94_out, not_95_out,
       not_96_out, not_97_out, not_98_out, not_99_out, not_100_out, not_101_out, not_102_out, not_103_out,
       not_104_out, not_105_out, not_106_out, not_107_out, not_108_out, not_109_out, not_110_out,
       not_111_out, not_112_out, not_113_out, not_114_out, not_115_out, not_116_out, not_117_out,
       not_118_out, not_119_out, not_120_out, not_121_out, not_122_out, not_123_out, not_124_out,
       not_125_out, not_126_out, not_127_out, not_128_out, not_129_out, not_130_out, not_131_out,
       not_132_out, not_133_out, not_134_out, not_135_out, not_136_out, not_137_out, not_138_out,
       not_139_out, not_140_out, not_141_out, not_142_out, not_143_out, not_144_out, not_145_out,
       not_146_out, not_147_out, not_148_out, not_149_out, not_150_out, not_151_out, not_152_out,
       not_153_out, not_154_out, not_155_out, not_156_out, not_157_out, not_158_out, not_159_out,
       not_160_out, not_161_out, not_162_out, not_163_out, not_164_out, not_165_out, not_166_out,
       not_167_out, not_168_out, not_169_out, not_170_out, not_171_out, not_172_out, not_173_out,
       not_174_out, not_175_out, not_176_out, not_177_out, not_178_out, not_179_out, not_180_out,
       not_181_out, not_182_out, not_183_out, not_184_out, not_185_out, not_186_out, not_187_out,
       not_188_out, not_189_out, not_190_out, not_191_out, not_192_out, not_193_out, not_194_out,
       not_195_out, not_196_out, not_197_out, not_198_out, not_199_out, not_200_out, not_201_out,
       not_202_out, not_203_out, not_204_out, not_205_out, not_206_out, not_207_out, not_208_out,
       not_209_out, not_210_out, not_211_out, not_212_out, not_213_out, not_214_out, not_215_out,
       not_216_out, not_217_out, not_218_out, not_219_out, not_220_out, not_221_out, not_222_out,
       not_223_out, not_224_out, not_225_out, not_226_out, not_227_out, not_228_out, not_229_out,
       not_230_out, not_231_out, not_232_out, not_233_out, not_234_out, not_235_out, not_236_out,
       not_237_out, not_238_out, not_239_out, not_240_out, not_241_out, not_242_out, not_243_out,
       not_244_out, not_245_out, not_246_out, not_247_out, not_248_out, not_249_out, not_250_out,
       not_251_out, not_252_out, not_253_out, not_254_out, not_255_out, not_256_out, not_257_out,
       not_258_out, not_259_out, not_260_out, not_261_out, not_262_out, not_263_out, not_264_out,
       not_265_out, not_266_out, not_267_out, not_268_out, not_269_out, not_270_out, not_271_out,
       not_272_out, not_273_out, not_274_out, not_275_out, not_276_out, not_277_out, not_278_out,
       not_279_out, not_280_out;

  not not_1 (not_1_out, OP5);
  not not_2 (not_2_out, OP4);
  not not_3 (not_3_out, OP3);
  not not_4 (not_4_out, OP2);
  not not_5 (not_5_out, OP1);
  not not_6 (not_6_out, OP0);
  not not_7 (not_7_out, F5);
  not not_8 (not_8_out, F4);
  not not_9 (not_9_out, F3);
  not not_10 (not_10_out, F2);
  not not_11 (not_11_out, OP5);
  not not_12 (not_12_out, OP4);
  not not_13 (not_13_out, OP3);
  not not_14 (not_14_out, OP2);
  not not_15 (not_15_out, OP1);
  not not_16 (not_16_out, OP0);
  not not_17 (not_17_out, F4);
  not not_18 (not_18_out, F3);
  not not_19 (not_19_out, F2);
  not not_20 (not_20_out, F1);
  not not_21 (not_21_out, F0);
  not not_22 (not_22_out, OP5);
  not not_23 (not_23_out, OP4);
  not not_24 (not_24_out, OP3);
  not not_25 (not_25_out, OP2);
  not not_26 (not_26_out, OP1);
  not not_27 (not_27_out, OP0);
  not not_28 (not_28_out, F4);
  not not_29 (not_29_out, F3);
  not not_30 (not_30_out, F2);
  not not_31 (not_31_out, F1);
  not not_32 (not_32_out, OP5);
  not not_33 (not_33_out, OP4);
  not not_34 (not_34_out, OP3);
  not not_35 (not_35_out, OP2);
  not not_36 (not_36_out, OP1);
  not not_37 (not_37_out, OP0);
  not not_38 (not_38_out, F4);
  not not_39 (not_39_out, F3);
  not not_40 (not_40_out, F1);
  not not_41 (not_41_out, F0);
  not not_42 (not_42_out, OP5);
  not not_43 (not_43_out, OP4);
  not not_44 (not_44_out, OP3);
  not not_45 (not_45_out, OP2);
  not not_46 (not_46_out, OP1);
  not not_47 (not_47_out, OP0);
  not not_48 (not_48_out, F4);
  not not_49 (not_49_out, F2);
  not not_50 (not_50_out, F0);
  not not_51 (not_51_out, OP5);
  not not_52 (not_52_out, OP4);
  not not_53 (not_53_out, OP2);
  not not_54 (not_54_out, OP1);
  not not_55 (not_55_out, OP0);
  not not_56 (not_56_out, OP5);
  not not_57 (not_57_out, OP4);
  not not_58 (not_58_out, OP1);
  not not_59 (not_59_out, OP0);
  not not_60 (not_60_out, OP5);
  not not_61 (not_61_out, OP4);
  not not_62 (not_62_out, OP2);
  not not_63 (not_63_out, OP1);
  not not_64 (not_64_out, OP5);
  not not_65 (not_65_out, OP4);
  not not_66 (not_66_out, OP2);
  not not_67 (not_67_out, OP0);
  not not_68 (not_68_out, OP4);
  not not_69 (not_69_out, OP3);
  not not_70 (not_70_out, OP2);
  not not_71 (not_71_out, OP4);
  not not_72 (not_72_out, OP2);
  not not_73 (not_73_out, OP5);
  not not_74 (not_74_out, OP4);
  not not_75 (not_75_out, OP3);
  not not_76 (not_76_out, OP2);
  not not_77 (not_77_out, OP1);
  not not_78 (not_78_out, OP0);
  not not_79 (not_79_out, F4);
  not not_80 (not_80_out, F3);
  not not_81 (not_81_out, F0);
  not not_82 (not_82_out, OP4);
  not not_83 (not_83_out, OP3);
  not not_84 (not_84_out, OP1);
  not not_85 (not_85_out, OP0);
  not not_86 (not_86_out, OP5);
  not not_87 (not_87_out, OP4);
  not not_88 (not_88_out, OP3);
  not not_89 (not_89_out, OP0);
  not not_90 (not_90_out, OP5);
  not not_91 (not_91_out, OP4);
  not not_92 (not_92_out, OP3);
  not not_93 (not_93_out, OP2);
  not not_94 (not_94_out, OP1);
  not not_95 (not_95_out, OP0);
  not not_96 (not_96_out, F5);
  not not_97 (not_97_out, F4);
  not not_98 (not_98_out, F3);
  not not_99 (not_99_out, F2);
  not not_100 (not_100_out, F0);
  not not_101 (not_101_out, OP5);
  not not_102 (not_102_out, OP4);
  not not_103 (not_103_out, OP3);
  not not_104 (not_104_out, OP2);
  not not_105 (not_105_out, OP1);
  not not_106 (not_106_out, OP0);
  not not_107 (not_107_out, F4);
  not not_108 (not_108_out, F3);
  not not_109 (not_109_out, F2);
  not not_110 (not_110_out, F0);
  not not_111 (not_111_out, OP5);
  not not_112 (not_112_out, OP4);
  not not_113 (not_113_out, OP3);
  not not_114 (not_114_out, OP2);
  not not_115 (not_115_out, OP1);
  not not_116 (not_116_out, OP0);
  not not_117 (not_117_out, F4);
  not not_118 (not_118_out, F3);
  not not_119 (not_119_out, F1);
  not not_120 (not_120_out, F0);
  not not_121 (not_121_out, OP5);
  not not_122 (not_122_out, OP4);
  not not_123 (not_123_out, OP3);
  not not_124 (not_124_out, OP2);
  not not_125 (not_125_out, OP1);
  not not_126 (not_126_out, OP0);
  not not_127 (not_127_out, F4);
  not not_128 (not_128_out, F3);
  not not_129 (not_129_out, OP5);
  not not_130 (not_130_out, OP4);
  not not_131 (not_131_out, OP3);
  not not_132 (not_132_out, OP2);
  not not_133 (not_133_out, OP1);
  not not_134 (not_134_out, OP0);
  not not_135 (not_135_out, F4);
  not not_136 (not_136_out, F2);
  not not_137 (not_137_out, F0);
  not not_138 (not_138_out, OP5);
  not not_139 (not_139_out, OP4);
  not not_140 (not_140_out, OP1);
  not not_141 (not_141_out, OP0);
  not not_142 (not_142_out, OP5);
  not not_143 (not_143_out, OP4);
  not not_144 (not_144_out, OP2);
  not not_145 (not_145_out, OP0);
  not not_146 (not_146_out, OP5);
  not not_147 (not_147_out, OP4);
  not not_148 (not_148_out, OP3);
  not not_149 (not_149_out, OP0);
  not not_150 (not_150_out, OP5);
  not not_151 (not_151_out, OP4);
  not not_152 (not_152_out, OP3);
  not not_153 (not_153_out, OP2);
  not not_154 (not_154_out, OP1);
  not not_155 (not_155_out, OP0);
  not not_156 (not_156_out, F4);
  not not_157 (not_157_out, F3);
  not not_158 (not_158_out, F2);
  not not_159 (not_159_out, F1);
  not not_160 (not_160_out, F0);
  not not_161 (not_161_out, OP5);
  not not_162 (not_162_out, OP4);
  not not_163 (not_163_out, OP3);
  not not_164 (not_164_out, OP2);
  not not_165 (not_165_out, OP1);
  not not_166 (not_166_out, OP0);
  not not_167 (not_167_out, F4);
  not not_168 (not_168_out, F3);
  not not_169 (not_169_out, F2);
  not not_170 (not_170_out, F1);
  not not_171 (not_171_out, OP5);
  not not_172 (not_172_out, OP4);
  not not_173 (not_173_out, OP3);
  not not_174 (not_174_out, OP2);
  not not_175 (not_175_out, OP1);
  not not_176 (not_176_out, OP0);
  not not_177 (not_177_out, F4);
  not not_178 (not_178_out, F3);
  not not_179 (not_179_out, F2);
  not not_180 (not_180_out, F0);
  not not_181 (not_181_out, OP5);
  not not_182 (not_182_out, OP4);
  not not_183 (not_183_out, OP3);
  not not_184 (not_184_out, OP2);
  not not_185 (not_185_out, OP1);
  not not_186 (not_186_out, OP0);
  not not_187 (not_187_out, F4);
  not not_188 (not_188_out, F3);
  not not_189 (not_189_out, F1);
  not not_190 (not_190_out, F0);
  not not_191 (not_191_out, OP5);
  not not_192 (not_192_out, OP4);
  not not_193 (not_193_out, OP3);
  not not_194 (not_194_out, OP2);
  not not_195 (not_195_out, OP1);
  not not_196 (not_196_out, OP0);
  not not_197 (not_197_out, F4);
  not not_198 (not_198_out, F2);
  not not_199 (not_199_out, OP5);
  not not_200 (not_200_out, OP4);
  not not_201 (not_201_out, OP2);
  not not_202 (not_202_out, OP1);
  not not_203 (not_203_out, OP0);
  not not_204 (not_204_out, OP5);
  not not_205 (not_205_out, OP4);
  not not_206 (not_206_out, OP1);
  not not_207 (not_207_out, OP0);
  not not_208 (not_208_out, OP5);
  not not_209 (not_209_out, OP4);
  not not_210 (not_210_out, OP2);
  not not_211 (not_211_out, OP1);
  not not_212 (not_212_out, OP4);
  not not_213 (not_213_out, OP3);
  not not_214 (not_214_out, OP2);
  not not_215 (not_215_out, OP4);
  not not_216 (not_216_out, OP2);
  not not_217 (not_217_out, OP5);
  not not_218 (not_218_out, OP4);
  not not_219 (not_219_out, OP2);
  not not_220 (not_220_out, OP4);
  not not_221 (not_221_out, OP3);
  not not_222 (not_222_out, OP1);
  not not_223 (not_223_out, OP0);
  not not_224 (not_224_out, OP5);
  not not_225 (not_225_out, OP4);
  not not_226 (not_226_out, OP3);
  not not_227 (not_227_out, OP2);
  not not_228 (not_228_out, OP1);
  not not_229 (not_229_out, OP0);
  not not_230 (not_230_out, F4);
  not not_231 (not_231_out, F3);
  not not_232 (not_232_out, F1);
  not not_233 (not_233_out, OP5);
  not not_234 (not_234_out, OP4);
  not not_235 (not_235_out, OP3);
  not not_236 (not_236_out, OP2);
  not not_237 (not_237_out, OP1);
  not not_238 (not_238_out, OP0);
  not not_239 (not_239_out, F4);
  not not_240 (not_240_out, F3);
  not not_241 (not_241_out, OP5);
  not not_242 (not_242_out, OP4);
  not not_243 (not_243_out, OP3);
  not not_244 (not_244_out, OP2);
  not not_245 (not_245_out, OP1);
  not not_246 (not_246_out, OP0);
  not not_247 (not_247_out, F4);
  not not_248 (not_248_out, F2);
  not not_249 (not_249_out, F0);
  not not_250 (not_250_out, OP5);
  not not_251 (not_251_out, OP4);
  not not_252 (not_252_out, OP3);
  not not_253 (not_253_out, OP2);
  not not_254 (not_254_out, OP1);
  not not_255 (not_255_out, OP0);
  not not_256 (not_256_out, F4);
  not not_257 (not_257_out, F2);
  not not_258 (not_258_out, OP5);
  not not_259 (not_259_out, OP4);
  not not_260 (not_260_out, OP2);
  not not_261 (not_261_out, OP0);
  not not_262 (not_262_out, OP5);
  not not_263 (not_263_out, OP4);
  not not_264 (not_264_out, OP1);
  not not_265 (not_265_out, OP5);
  not not_266 (not_266_out, OP4);
  not not_267 (not_267_out, OP3);
  not not_268 (not_268_out, OP2);
  not not_269 (not_269_out, OP1);
  not not_270 (not_270_out, OP0);
  not not_271 (not_271_out, F4);
  not not_272 (not_272_out, F3);
  not not_273 (not_273_out, F0);
  not not_274 (not_274_out, OP5);
  not not_275 (not_275_out, OP4);
  not not_276 (not_276_out, OP2);
  not not_277 (not_277_out, OP5);
  not not_278 (not_278_out, OP4);
  not not_279 (not_279_out, OP3);
  not not_280 (not_280_out, OP0);
  and and_1 (and_1_out, not_1_out, not_2_out, not_3_out, not_4_out, not_5_out, not_6_out, not_7_out, not_8_out, not_9_out, not_10_out, F1, F0);
  and and_2 (and_2_out, not_11_out, not_12_out, not_13_out, not_14_out, not_15_out, not_16_out, F5, not_17_out, not_18_out, not_19_out, not_20_out, not_21_out);
  and and_3 (and_3_out, not_22_out, not_23_out, not_24_out, not_25_out, not_26_out, not_27_out, F5, not_28_out, not_29_out, not_30_out, not_31_out, F0);
  and and_4 (and_4_out, not_32_out, not_33_out, not_34_out, not_35_out, not_36_out, not_37_out, F5, not_38_out, not_39_out, F2, not_40_out, not_41_out);
  and and_5 (and_5_out, not_42_out, not_43_out, not_44_out, not_45_out, not_46_out, not_47_out, F5, not_48_out, F3, not_49_out, F1, not_50_out);
  and and_6 (and_6_out, not_51_out, not_52_out, OP3, not_53_out, not_54_out, not_55_out);
  and and_7 (and_7_out, not_56_out, not_57_out, OP3, OP2, not_58_out, not_59_out);
  and and_8 (and_8_out, not_60_out, not_61_out, OP3, not_62_out, not_63_out, OP0);
  and and_9 (and_9_out, not_64_out, not_65_out, OP3, not_66_out, OP1, not_67_out);
  and and_10 (and_10_out, OP5, not_68_out, not_69_out, not_70_out, OP1, OP0);
  and and_11 (and_11_out, OP5, not_71_out, OP3, not_72_out, OP1, OP0);
  and and_12 (and_12_out, not_73_out, not_74_out, not_75_out, not_76_out, not_77_out, not_78_out, F5, not_79_out, not_80_out, F2, F1, not_81_out);
  and and_13 (and_13_out, OP5, not_82_out, not_83_out, OP2, not_84_out, not_85_out);
  and and_14 (and_14_out, not_86_out, not_87_out, not_88_out, OP2, OP1, not_89_out);
  and and_15 (and_15_out, not_90_out, not_91_out, not_92_out, not_93_out, not_94_out, not_95_out, not_96_out, not_97_out, not_98_out, not_99_out, F1, not_100_out);
  and and_16 (and_16_out, not_101_out, not_102_out, not_103_out, not_104_out, not_105_out, not_106_out, F5, not_107_out, not_108_out, not_109_out, F1, not_110_out);
  and and_17 (and_17_out, not_111_out, not_112_out, not_113_out, not_114_out, not_115_out, not_116_out, F5, not_117_out, not_118_out, F2, not_119_out, not_120_out);
  and and_18 (and_18_out, not_121_out, not_122_out, not_123_out, not_124_out, not_125_out, not_126_out, F5, not_127_out, not_128_out, F2, F1, F0);
  and and_19 (and_19_out, not_129_out, not_130_out, not_131_out, not_132_out, not_133_out, not_134_out, F5, not_135_out, F3, not_136_out, F1, not_137_out);
  and and_20 (and_20_out, not_138_out, not_139_out, OP3, OP2, not_140_out, not_141_out);
  and and_21 (and_21_out, not_142_out, not_143_out, OP3, not_144_out, OP1, not_145_out);
  and and_22 (and_22_out, not_146_out, not_147_out, not_148_out, OP2, OP1, not_149_out);
  and and_23 (and_23_out, not_150_out, not_151_out, not_152_out, not_153_out, not_154_out, not_155_out, F5, not_156_out, not_157_out, not_158_out, not_159_out, not_160_out);
  and and_24 (and_24_out, not_161_out, not_162_out, not_163_out, not_164_out, not_165_out, not_166_out, F5, not_167_out, not_168_out, not_169_out, not_170_out, F0);
  and and_25 (and_25_out, not_171_out, not_172_out, not_173_out, not_174_out, not_175_out, not_176_out, F5, not_177_out, not_178_out, not_179_out, F1, not_180_out);
  and and_26 (and_26_out, not_181_out, not_182_out, not_183_out, not_184_out, not_185_out, not_186_out, F5, not_187_out, not_188_out, F2, not_189_out, not_190_out);
  and and_27 (and_27_out, not_191_out, not_192_out, not_193_out, not_194_out, not_195_out, not_196_out, F5, not_197_out, F3, not_198_out, F1, F0);
  and and_28 (and_28_out, not_199_out, not_200_out, OP3, not_201_out, not_202_out, not_203_out);
  and and_29 (and_29_out, not_204_out, not_205_out, OP3, OP2, not_206_out, not_207_out);
  and and_30 (and_30_out, not_208_out, not_209_out, OP3, not_210_out, not_211_out, OP0);
  and and_31 (and_31_out, OP5, not_212_out, not_213_out, not_214_out, OP1, OP0);
  and and_32 (and_32_out, OP5, not_215_out, OP3, not_216_out, OP1, OP0);
  and and_33 (and_33_out, not_217_out, not_218_out, OP3, not_219_out, OP1, OP0);
  and and_34 (and_34_out, OP5, not_220_out, not_221_out, OP2, not_222_out, not_223_out);
  and and_35 (and_35_out, not_224_out, not_225_out, not_226_out, not_227_out, not_228_out, not_229_out, F5, not_230_out, not_231_out, F2, not_232_out, F0);
  and and_36 (and_36_out, not_233_out, not_234_out, not_235_out, not_236_out, not_237_out, not_238_out, F5, not_239_out, not_240_out, F2, F1, F0);
  and and_37 (and_37_out, not_241_out, not_242_out, not_243_out, not_244_out, not_245_out, not_246_out, F5, not_247_out, F3, not_248_out, F1, not_249_out);
  and and_38 (and_38_out, not_250_out, not_251_out, not_252_out, not_253_out, not_254_out, not_255_out, F5, not_256_out, F3, not_257_out, F1, F0);
  and and_39 (and_39_out, not_258_out, not_259_out, OP3, not_260_out, OP1, not_261_out);
  and and_40 (and_40_out, not_262_out, not_263_out, OP3, OP2, not_264_out, OP0);
  and and_41 (and_41_out, not_265_out, not_266_out, not_267_out, not_268_out, not_269_out, not_270_out, F5, not_271_out, not_272_out, F2, F1, not_273_out);
  and and_42 (and_42_out, not_274_out, not_275_out, OP3, not_276_out, OP1, OP0);
  and and_43 (and_43_out, not_277_out, not_278_out, not_279_out, OP2, OP1, not_280_out);
  or or_1 (S1, and_15_out, and_16_out, and_17_out, and_18_out, and_19_out, and_20_out, and_21_out, and_22_out);
  or or_2 (S3, and_35_out, and_36_out, and_37_out, and_38_out, and_39_out, and_40_out, and_41_out, and_42_out, and_43_out);
  or or_3 (S0, and_1_out, and_2_out, and_3_out, and_4_out, and_5_out, and_6_out, and_7_out, and_8_out, and_9_out, and_10_out, and_11_out, and_12_out, and_13_out, and_14_out);
  or or_4 (S2, and_23_out, and_24_out, and_25_out, and_26_out, and_27_out, and_28_out, and_29_out, and_30_out, and_31_out, and_32_out, and_33_out, and_34_out);
endmodule

// 控制信号生成
module \控制信号自动生成  (
  input  OP0,
  input  OP1,
  input  OP2,
  input  OP3,
  input  OP4,
  input  OP5,
  input  F0,
  input  F1,
  input  F2,
  input  F3,
  input  F4,
  input  F5,
  output MemToReg,
  output MemWrite,
  output ALU_SRC,
  output RegWrite,
  output SysCALL,
  output SignedExt,
  output RegDst,
  output BEQ,
  output BNE,
  output JR,
  output JUMP,
  output JAL,
  output ERET,
  output LBU,
  output BLEZ
);

  wire and_1_out, and_2_out, and_4_out, and_5_out, and_6_out, and_7_out, and_8_out, and_9_out, and_10_out,
       and_11_out, and_12_out, and_13_out, and_14_out, and_15_out, and_16_out, and_18_out, and_19_out,
       and_20_out, and_21_out, and_22_out, and_23_out, and_24_out, and_25_out, and_26_out, and_27_out,
       and_31_out, and_32_out, not_1_out, not_2_out, not_3_out, not_4_out, not_5_out, not_6_out, not_7_out,
       not_8_out, not_9_out, not_10_out, not_11_out, not_12_out, not_13_out, not_14_out, not_15_out,
       not_16_out, not_17_out, not_18_out, not_19_out, not_20_out, not_21_out, not_22_out, not_23_out,
       not_24_out, not_25_out, not_26_out, not_27_out, not_28_out, not_29_out, not_30_out, not_31_out,
       not_32_out, not_33_out, not_34_out, not_35_out, not_36_out, not_37_out, not_38_out, not_39_out,
       not_40_out, not_41_out, not_42_out, not_43_out, not_44_out, not_45_out, not_46_out, not_47_out,
       not_48_out, not_49_out, not_50_out, not_51_out, not_52_out, not_53_out, not_54_out, not_55_out,
       not_56_out, not_57_out, not_58_out, not_59_out, not_60_out, not_61_out, not_62_out, not_63_out,
       not_64_out, not_65_out, not_66_out, not_67_out, not_68_out, not_69_out, not_70_out, not_71_out,
       not_72_out, not_73_out, not_74_out, not_75_out, not_76_out, not_77_out, not_78_out, not_79_out,
       not_80_out, not_81_out, not_82_out, not_83_out, not_84_out, not_85_out, not_86_out, not_87_out,
       not_88_out, not_89_out, not_90_out, not_91_out, not_92_out, not_93_out, not_94_out, not_95_out,
       not_96_out, not_97_out, not_98_out, not_99_out, not_100_out, not_101_out, not_102_out, not_103_out,
       not_104_out, not_105_out, not_106_out, not_107_out, not_108_out, not_109_out, not_110_out,
       not_111_out, not_112_out, not_113_out, not_114_out, not_115_out, not_116_out, not_117_out,
       not_118_out, not_119_out, not_120_out, not_121_out, not_122_out, not_123_out, not_124_out,
       not_125_out, not_126_out, not_127_out, not_128_out, not_129_out, not_130_out, not_131_out,
       not_132_out, not_133_out, not_134_out, not_135_out, not_136_out, not_137_out, not_138_out,
       not_139_out, not_140_out, not_141_out, not_142_out, not_143_out, not_144_out, not_145_out,
       not_146_out, not_147_out, not_148_out, not_149_out, not_150_out, not_151_out, not_152_out,
       not_153_out, not_154_out, not_155_out, not_156_out, not_157_out, not_158_out, not_159_out,
       not_160_out, not_161_out, not_162_out, not_163_out, not_164_out, not_165_out, not_166_out,
       not_167_out, not_168_out, not_169_out, not_170_out, not_171_out, not_172_out, not_173_out;

  not not_1 (not_1_out, OP0);
  not not_2 (not_2_out, OP1);
  not not_3 (not_3_out, OP3);
  not not_4 (not_4_out, OP4);
  not not_5 (not_5_out, OP2);
  not not_6 (not_6_out, OP3);
  not not_7 (not_7_out, OP4);
  not not_8 (not_8_out, OP2);
  not not_9 (not_9_out, OP4);
  not not_10 (not_10_out, OP1);
  not not_11 (not_11_out, OP4);
  not not_12 (not_12_out, OP5);
  not not_13 (not_13_out, OP2);
  not not_14 (not_14_out, OP4);
  not not_15 (not_15_out, OP5);
  not not_16 (not_16_out, OP0);
  not not_17 (not_17_out, OP1);
  not not_18 (not_18_out, OP3);
  not not_19 (not_19_out, OP4);
  not not_20 (not_20_out, OP2);
  not not_21 (not_21_out, OP4);
  not not_22 (not_22_out, OP0);
  not not_23 (not_23_out, OP1);
  not not_24 (not_24_out, OP2);
  not not_25 (not_25_out, OP4);
  not not_26 (not_26_out, OP5);
  not not_27 (not_27_out, F0);
  not not_28 (not_28_out, F2);
  not not_29 (not_29_out, F3);
  not not_30 (not_30_out, F4);
  not not_31 (not_31_out, OP0);
  not not_32 (not_32_out, OP1);
  not not_33 (not_33_out, OP2);
  not not_34 (not_34_out, OP4);
  not not_35 (not_35_out, OP5);
  not not_36 (not_36_out, F1);
  not not_37 (not_37_out, F3);
  not not_38 (not_38_out, F4);
  not not_39 (not_39_out, OP0);
  not not_40 (not_40_out, OP1);
  not not_41 (not_41_out, OP2);
  not not_42 (not_42_out, OP4);
  not not_43 (not_43_out, OP5);
  not not_44 (not_44_out, F3);
  not not_45 (not_45_out, F4);
  not not_46 (not_46_out, OP0);
  not not_47 (not_47_out, OP1);
  not not_48 (not_48_out, OP2);
  not not_49 (not_49_out, OP4);
  not not_50 (not_50_out, OP5);
  not not_51 (not_51_out, F2);
  not not_52 (not_52_out, F3);
  not not_53 (not_53_out, F4);
  not not_54 (not_54_out, F5);
  not not_55 (not_55_out, OP0);
  not not_56 (not_56_out, OP1);
  not not_57 (not_57_out, OP2);
  not not_58 (not_58_out, OP4);
  not not_59 (not_59_out, OP5);
  not not_60 (not_60_out, F2);
  not not_61 (not_61_out, F4);
  not not_62 (not_62_out, OP1);
  not not_63 (not_63_out, OP4);
  not not_64 (not_64_out, OP5);
  not not_65 (not_65_out, OP2);
  not not_66 (not_66_out, OP4);
  not not_67 (not_67_out, OP5);
  not not_68 (not_68_out, OP0);
  not not_69 (not_69_out, OP1);
  not not_70 (not_70_out, OP3);
  not not_71 (not_71_out, OP4);
  not not_72 (not_72_out, OP2);
  not not_73 (not_73_out, OP3);
  not not_74 (not_74_out, OP4);
  not not_75 (not_75_out, OP0);
  not not_76 (not_76_out, OP1);
  not not_77 (not_77_out, OP2);
  not not_78 (not_78_out, OP3);
  not not_79 (not_79_out, OP4);
  not not_80 (not_80_out, OP5);
  not not_81 (not_81_out, F0);
  not not_82 (not_82_out, F1);
  not not_83 (not_83_out, F4);
  not not_84 (not_84_out, F5);
  not not_85 (not_85_out, OP5);
  not not_86 (not_86_out, OP4);
  not not_87 (not_87_out, OP2);
  not not_88 (not_88_out, OP1);
  not not_89 (not_89_out, OP0);
  not not_90 (not_90_out, OP5);
  not not_91 (not_91_out, OP4);
  not not_92 (not_92_out, OP1);
  not not_93 (not_93_out, OP0);
  not not_94 (not_94_out, OP5);
  not not_95 (not_95_out, OP4);
  not not_96 (not_96_out, OP2);
  not not_97 (not_97_out, OP0);
  not not_98 (not_98_out, OP4);
  not not_99 (not_99_out, OP3);
  not not_100 (not_100_out, OP2);
  not not_101 (not_101_out, OP4);
  not not_102 (not_102_out, OP2);
  not not_103 (not_103_out, OP4);
  not not_104 (not_104_out, OP3);
  not not_105 (not_105_out, OP1);
  not not_106 (not_106_out, OP0);
  not not_107 (not_107_out, OP1);
  not not_108 (not_108_out, OP4);
  not not_109 (not_109_out, OP5);
  not not_110 (not_110_out, OP2);
  not not_111 (not_111_out, OP4);
  not not_112 (not_112_out, OP5);
  not not_113 (not_113_out, OP0);
  not not_114 (not_114_out, OP1);
  not not_115 (not_115_out, OP3);
  not not_116 (not_116_out, OP4);
  not not_117 (not_117_out, OP2);
  not not_118 (not_118_out, OP3);
  not not_119 (not_119_out, OP4);
  not not_120 (not_120_out, OP0);
  not not_121 (not_121_out, OP3);
  not not_122 (not_122_out, OP4);
  not not_123 (not_123_out, OP5);
  not not_124 (not_124_out, OP1);
  not not_125 (not_125_out, OP3);
  not not_126 (not_126_out, OP4);
  not not_127 (not_127_out, OP5);
  not not_128 (not_128_out, OP0);
  not not_129 (not_129_out, OP1);
  not not_130 (not_130_out, OP2);
  not not_131 (not_131_out, OP3);
  not not_132 (not_132_out, OP4);
  not not_133 (not_133_out, OP5);
  not not_134 (not_134_out, F0);
  not not_135 (not_135_out, F1);
  not not_136 (not_136_out, F2);
  not not_137 (not_137_out, F4);
  not not_138 (not_138_out, F5);
  not not_139 (not_139_out, OP0);
  not not_140 (not_140_out, OP2);
  not not_141 (not_141_out, OP3);
  not not_142 (not_142_out, OP4);
  not not_143 (not_143_out, OP5);
  not not_144 (not_144_out, F0);
  not not_145 (not_145_out, F1);
  not not_146 (not_146_out, F2);
  not not_147 (not_147_out, F4);
  not not_148 (not_148_out, F5);
  not not_149 (not_149_out, OP2);
  not not_150 (not_150_out, OP3);
  not not_151 (not_151_out, OP4);
  not not_152 (not_152_out, OP5);
  not not_153 (not_153_out, OP2);
  not not_154 (not_154_out, OP3);
  not not_155 (not_155_out, OP4);
  not not_156 (not_156_out, OP5);
  not not_157 (not_157_out, OP0);
  not not_158 (not_158_out, OP1);
  not not_159 (not_159_out, OP2);
  not not_160 (not_160_out, OP3);
  not not_161 (not_161_out, OP5);
  not not_162 (not_162_out, F0);
  not not_163 (not_163_out, F1);
  not not_164 (not_164_out, F2);
  not not_165 (not_165_out, F5);
  not not_166 (not_166_out, OP0);
  not not_167 (not_167_out, OP1);
  not not_168 (not_168_out, OP3);
  not not_169 (not_169_out, OP4);
  not not_170 (not_170_out, OP0);
  not not_171 (not_171_out, OP3);
  not not_172 (not_172_out, OP4);
  not not_173 (not_173_out, OP5);
  and and_1 (and_1_out, not_1_out, not_2_out, OP2, not_3_out, not_4_out, OP5);
  and and_2 (and_2_out, OP0, OP1, not_5_out, not_6_out, not_7_out, OP5);
  and and_3 (MemWrite, OP0, OP1, not_8_out, OP3, not_9_out, OP5);
  and and_4 (and_4_out, not_10_out, OP3, not_11_out, not_12_out);
  and and_5 (and_5_out, not_13_out, OP3, not_14_out, not_15_out);
  and and_6 (and_6_out, not_16_out, not_17_out, OP2, not_18_out, not_19_out, OP5);
  and and_7 (and_7_out, OP0, OP1, not_20_out, not_21_out, OP5);
  and and_8 (and_8_out, not_22_out, not_23_out, not_24_out, not_25_out, not_26_out, not_27_out, not_28_out, not_29_out, not_30_out);
  and and_9 (and_9_out, not_31_out, not_32_out, not_33_out, not_34_out, not_35_out, not_36_out, not_37_out, not_38_out, F5);
  and and_10 (and_10_out, not_39_out, not_40_out, not_41_out, not_42_out, not_43_out, F2, not_44_out, not_45_out, F5);
  and and_11 (and_11_out, not_46_out, not_47_out, not_48_out, not_49_out, not_50_out, F1, not_51_out, not_52_out, not_53_out, not_54_out);
  and and_12 (and_12_out, not_55_out, not_56_out, not_57_out, not_58_out, not_59_out, F1, not_60_out, F3, not_61_out, F5);
  and and_13 (and_13_out, not_62_out, OP3, not_63_out, not_64_out);
  and and_14 (and_14_out, not_65_out, OP3, not_66_out, not_67_out);
  and and_15 (and_15_out, not_68_out, not_69_out, OP2, not_70_out, not_71_out, OP5);
  and and_16 (and_16_out, OP0, OP1, not_72_out, not_73_out, not_74_out);
  and and_17 (SysCALL, not_75_out, not_76_out, not_77_out, not_78_out, not_79_out, not_80_out, not_81_out, not_82_out, F2, F3, not_83_out, not_84_out);
  and and_18 (and_18_out, not_85_out, not_86_out, OP3, not_87_out, not_88_out, not_89_out);
  and and_19 (and_19_out, not_90_out, not_91_out, OP3, OP2, not_92_out, not_93_out);
  and and_20 (and_20_out, not_94_out, not_95_out, OP3, not_96_out, OP1, not_97_out);
  and and_21 (and_21_out, OP5, not_98_out, not_99_out, not_100_out, OP1, OP0);
  and and_22 (and_22_out, OP5, not_101_out, OP3, not_102_out, OP1, OP0);
  and and_23 (and_23_out, OP5, not_103_out, not_104_out, OP2, not_105_out, not_106_out);
  and and_24 (and_24_out, not_107_out, OP3, not_108_out, not_109_out);
  and and_25 (and_25_out, not_110_out, OP3, not_111_out, not_112_out);
  and and_26 (and_26_out, not_113_out, not_114_out, OP2, not_115_out, not_116_out, OP5);
  and and_27 (and_27_out, OP0, OP1, not_117_out, not_118_out, not_119_out, OP5);
  and and_28 (BEQ, not_120_out, OP2, not_121_out, not_122_out, not_123_out);
  and and_29 (BNE, OP0, not_124_out, OP2, not_125_out, not_126_out, not_127_out);
  and and_30 (JR, not_128_out, not_129_out, not_130_out, not_131_out, not_132_out, not_133_out, not_134_out, not_135_out, not_136_out, F3, not_137_out, not_138_out);
  and and_31 (and_31_out, not_139_out, not_140_out, not_141_out, not_142_out, not_143_out, not_144_out, not_145_out, not_146_out, F3, not_147_out, not_148_out);
  and and_32 (and_32_out, OP1, not_149_out, not_150_out, not_151_out, not_152_out);
  and and_33 (JAL, OP0, OP1, not_153_out, not_154_out, not_155_out, not_156_out);
  and and_34 (ERET, not_157_out, not_158_out, not_159_out, not_160_out, OP4, not_161_out, not_162_out, not_163_out, not_164_out, F3, F4, not_165_out);
  and and_35 (LBU, not_166_out, not_167_out, OP2, not_168_out, not_169_out, OP5);
  and and_36 (BLEZ, not_170_out, OP1, OP2, not_171_out, not_172_out, not_173_out);
  or or_1 (MemToReg, and_1_out, and_2_out);
  or or_2 (ALU_SRC, and_4_out, and_5_out, and_6_out, and_7_out);
  or or_3 (RegWrite, and_8_out, and_9_out, and_10_out, and_11_out, and_12_out, and_13_out, and_14_out, and_15_out, and_16_out);
  or or_4 (SignedExt, and_18_out, and_19_out, and_20_out, and_21_out, and_22_out, and_23_out);
  or or_5 (RegDst, and_24_out, and_25_out, and_26_out, and_27_out);
  or or_6 (JUMP, and_31_out, and_32_out);
endmodule

// ALU
module MIPS_ALU (
  input  [4:0] shamt,
  input  [31:0] X,
  input  [31:0] Y,
  input  [3:0] AluOP,
  output Equal,
  output [31:0] Result,
  output [31:0] Result_2
);

  wire [0:0] comparator_1_lt, comparator_2_lt;
  wire [31:0] adder_1_out, AND_out, divider_1_out, divider_1_rem, multiplier_1_cout, multiplier_1_out,
       NOR_out, OR_out, shifter_1_out, shifter_2_out, shifter_3_out, subtractor_1_out, XOR_out;

  assign AND_out = X & Y;  // AND_Gate AND, 32 bits wide
  assign OR_out = X | Y;  // OR_Gate OR, 32 bits wide
  Shifter #(.width(32), .shift("ll")) shifter_1 (.in(Y), .\dist (shamt), .out(shifter_1_out));
  Shifter #(.width(32), .shift("ar")) shifter_2 (.in(Y), .\dist (shamt), .out(shifter_2_out));
  Shifter #(.width(32), .shift("lr")) shifter_3 (.in(Y), .\dist (shamt), .out(shifter_3_out));
  Multiplier #(.width(32)) multiplier_1 (.a(X), .b(Y), .out(multiplier_1_out), .cout(multiplier_1_cout));  // open: cin
  Divider #(.width(32)) divider_1 (.a(X), .b(Y), .out(divider_1_out), .rem(divider_1_rem));  // open: upper
  Adder #(.width(32)) adder_1 (.a(X), .b(Y), .out(adder_1_out));  // open: cin, cout
  Subtractor #(.width(32)) subtractor_1 (.a(X), .b(Y), .out(subtractor_1_out));  // open: bin, bout
  assign XOR_out = X ^ Y;  // XOR_Gate XOR, 32 bits wide
  assign NOR_out = ~(X | Y);  // NOR_Gate NOR, 32 bits wide
  Comparator #(.width(32), .mode("twosComplement")) comparator_1 (
    .a(X), .b(Y), .eq(Equal), .lt(comparator_1_lt[0]));  // open: gt
  Comparator #(.width(32), .mode("unsigned")) comparator_2 (.a(X), .b(Y), .lt(comparator_2_lt[0]));  // open: gt, eq
  Multiplexer #(.select(4), .width(32), .disabled("Z"), .enable("false")) multiplexer_1 (
    .in0(shifter_1_out), .in1(shifter_2_out), .in2(shifter_3_out), .in3(multiplier_1_out),
    .in4(divider_1_out), .in5(adder_1_out), .in6(subtractor_1_out), .in7(AND_out), .in8(OR_out),
    .in9(XOR_out), .in10(NOR_out), .in11({{31{1'b0}}, comparator_1_lt[0]}),
    .in12({{31{1'b0}}, comparator_2_lt[0]}), .in13({32{1'b0}}), .in14({32{1'b0}}), .in15({32{1'b0}}),
    .out(Result), .sel(AluOP));
  Multiplexer #(.select(4), .width(32), .disabled("Z"), .enable("false")) multiplexer_2 (
    .in0({32{1'b0}}), .in1({32{1'b0}}), .in2({32{1'b0}}), .in3(multiplier_1_cout), .in4(divider_1_rem),
    .in5({32{1'b0}}), .in6({32{1'b0}}), .in7({32{1'b0}}), .in8({32{1'b0}}), .in9({32{1'b0}}),
    .in10({32{1'b0}}), .in11({32{1'b0}}), .in12({32{1'b0}}), .in13({32{1'b0}}), .in14({32{1'b0}}),
    .in15({32{1'b0}}), .out(Result_2), .sel(AluOP));

  // Other names for the same wires on the sheet: Result2[31:0] = Result_2; S[3:0] = AluOP

  // Notes on the sheet:
  //   不要改变此引脚区域内容，也不要改变ALU封装形式
  //   输入引脚
  //   输出引脚
endmodule

module MIPS_Regifile (
  input  [31:0] Din,
  input  Clk,
  input  WE,
  input  [4:0] R1_num,
  input  [4:0] W_num,
  input  [4:0] R2_num,
  output [31:0] R1,
  output [31:0] R2
);

  // RegisterFile registerfile_1: pin names not known; wires that end beside it: Din, Clk, WE, W_num, R1_num, R2_num, R1, R2
endmodule

module \理想流水线  (
  output RegWrite,
  output MemWrite,
  output [31:0] IF_PC,
  output [31:0] ID_PC,
  output [31:0] EX_PC,
  output [31:0] M_PC,
  output [31:0] WB_PC,
  output [31:0] RDin,
  output [31:0] MDin,
  output [31:0] LedData
);

  wire CLK, clock_1_out, clock_2_out, comparator_1_eq, comparator_1_lt, comparator_2_eq, d_ff_1_qn, d_ff_2_q,
       Go, IR1, IR2, IR3, nand_1_out, not_1_out, RST, SignedExt, Stop, undriven, W1, W2, W3,
       \单周期硬布线控制器_1_alu_src , \单周期硬布线控制器_1_memtoreg , \单周期硬布线控制器_1_memwrite , \单周期硬布线控制器_1_regdst ,
       \单周期硬布线控制器_1_regwrite , \单周期硬布线控制器_1_syscall , \理想流水接口_ex_mem_1_regdst_out ,
       \理想流水接口_ex_mem_1_regwrite_out , \理想流水接口_id_ex_1_alusrcb_out , \理想流水接口_id_ex_1_memtoreg_out ,
       \理想流水接口_id_ex_1_memwrite_out , \理想流水接口_id_ex_1_regdst_out , \理想流水接口_id_ex_1_regwrite_out ,
       \理想流水接口_id_ex_1_syscall_out , \理想流水接口_id_ex_1_传输状态out_表明当前传输数据有效 , \理想流水接口_if_id_1_传输状态out_表明当前传输数据有效 ;
  wire [0:0] \理想流水接口_ex_mem_1_memtoreg_out , \理想流水接口_mem_wb_1_regdst_out ;
  wire [3:0] \单周期硬布线控制器_1_alu_op , \理想流水接口_id_ex_1_aluop_out ;
  wire [4:0] multiplexer_2_out, multiplexer_3_out, multiplexer_4_out;
  wire [12:0] CNT_num;
  wire [15:0] \LoadUse次数 , \总周期数 , \插入气泡数 , \无条件分支数 , \条件分支成功数 ;
  wire [31:0] adder_1_out, adder_2_out, bit_extender_1_out, bit_extender_2_out, EX_IR, ID_IR, IF_IR, MEM_IR,
       mips_alu_1_result, mips_regifile_1_r1, mips_regifile_1_r2, multiplexer_1_out, multiplexer_5_out,
       multiplexer_6_out, multiplexer_7_out, ram_1_data, WB_IR, \理想流水接口_ex_mem_1_alurst_out ,
       \理想流水接口_id_ex_1_imm_out , \理想流水接口_id_ex_1_r1_out , \理想流水接口_id_ex_1_r2_out ;

  Button \u_总复位  (.out(RST));
  Button _1 (.out(IR1));
  Button _2 (.out(IR2));
  Button _3 (.out(IR3));
  // Probe on \总周期数 
  // Probe on \总周期数 
  not not_1 (not_1_out, Stop);
  Counter #(.width(16), .max('hffff), .ongoal("wrap"), .trigger("rising"), .behavior("new")) counter_1 (
    .count(not_1_out), .Q(\总周期数 ), .clk(CLK));  // open: load, D, carry, clr, preset, down
  Button \u_继续运行  (.out(Go));
  LED #(.active("true")) led_1 (.in(W1));
  LED #(.active("true")) led_2 (.in(W2));
  LED #(.active("true")) led_3 (.in(W3));
  Hex_Digit_Display hex_digit_display_1 (.value(LedData[31:28]));  // open: dp
  // Probe on IF_PC[19:0]
  // Mips_Probe mips_probe_1: pin names not known; wires that end beside it: IF_IR
  D_Flip_Flop #(.trigger("rising"), .Pre_Clr_Positions("ABOVE_BELOW"), .NegatePresetClear("false"), .enable("false"), .NewFFLayout("true")) d_ff_1 (
    .clk(Stop), .D(d_ff_1_qn), .Qn(d_ff_1_qn));  // open: Q, preset, reset
  // Probe on adder_1_out
  Hex_Digit_Display hex_digit_display_2 (.value(LedData[27:24]));  // open: dp
  Hex_Digit_Display hex_digit_display_3 (.value(LedData[23:20]));  // open: dp
  // Probe on ID_PC[19:0]
  // Mips_Probe mips_probe_2: pin names not known; wires that end beside it: ID_IR
  Register #(.width(32), .trigger("rising"), .Select("low")) PC (
    .D(multiplexer_1_out), .Q(IF_PC), .clk(CLK));  // open: en, clr
  Multiplexer #(.select(1), .width(32), .disabled("Z"), .enable("false")) multiplexer_1 (
    .in0(adder_1_out), .in1(IF_PC), .out(multiplexer_1_out), .sel(undriven));
  Hex_Digit_Display hex_digit_display_4 (.value(LedData[15:12]));  // open: dp
  Hex_Digit_Display hex_digit_display_5 (.value(LedData[19:16]));  // open: dp
  // Probe on IF_PC
  Hex_Digit_Display hex_digit_display_6 (.value(LedData[11:8]));  // open: dp
  Hex_Digit_Display hex_digit_display_7 (.value(LedData[7:4]));  // open: dp
  Clock #(.highDuration(1), .lowDuration(1)) clock_1 (.out(clock_1_out));
  // Probe on EX_PC[19:0]
  // Mips_Probe mips_probe_3: pin names not known; wires that end beside it: clock_1_out, EX_IR, CLK
  Adder #(.width(32)) adder_1 (.a(IF_PC), .b(32'h4), .out(adder_1_out), .cin(1'b0));  // open: cout
  Hex_Digit_Display hex_digit_display_8 (.value(LedData[3:0]));  // open: dp
  ROM #(.addrWidth(10), .dataWidth(32), .Select("high")) rom_1 (.addr(IF_PC[11:2]), .data(IF_IR));
  // Probe on \总周期数 
  // Probe on M_PC[19:0]
  // Mips_Probe mips_probe_4: pin names not known; wires that end beside it: MEM_IR
  \理想流水接口_IF_ID  \u_理想流水接口_if_id_1  (
    .IR_in(IF_PC), .CLK(CLK), .IR_out(ID_PC), .\传输状态Out_表明当前传输数据有效 (\理想流水接口_if_id_1_传输状态out_表明当前传输数据有效 ),
    .PC_in(IF_IR), .PC_out(ID_IR));  // open: 传输状态In_表明当前传输数据有效, 同步清零_气泡_高电平有效, 使能端_低电平有效_stall_高电平有效
  // Probe on \总周期数 
  // Probe on \无条件分支数 
  // Probe on \条件分支成功数 
  // Probe on \插入气泡数 
  // Probe on \LoadUse次数 
  // Probe on IF_PC[11:0]
  // Probe on WB_PC[19:0]
  // Mips_Probe mips_probe_5: pin names not known; wires that end beside it: WB_IR
  \单周期硬布线控制器  \u_单周期硬布线控制器_1  (
    .Func(ID_IR[5:0]), .OP(ID_IR[31:26]), .ALU_OP(\单周期硬布线控制器_1_alu_op ), .MemToReg(\单周期硬布线控制器_1_memtoreg ),
    .MemWrite(\单周期硬布线控制器_1_memwrite ), .ALU_SRC(\单周期硬布线控制器_1_alu_src ), .RegWrite(\单周期硬布线控制器_1_regwrite ),
    .SysCALL(\单周期硬布线控制器_1_syscall ), .SignedExt(SignedExt), .RegDst(\单周期硬布线控制器_1_regdst ));  // open: JR, JMP, Beq, JAL, Bne, ERET, LBU, BLEZ
  Multiplexer #(.select(1), .width(5), .disabled("Z"), .enable("false")) multiplexer_2 (
    .in0(ID_IR[25:21]), .in1(5'b00010), .out(multiplexer_2_out), .sel(\单周期硬布线控制器_1_syscall ));
  Multiplexer #(.select(1), .width(5), .disabled("Z"), .enable("false")) multiplexer_3 (
    .in0(ID_IR[20:16]), .in1(5'b00100), .out(multiplexer_3_out), .sel(\单周期硬布线控制器_1_syscall ));
  Multiplexer #(.select(2), .width(5), .disabled("Z"), .enable("false")) multiplexer_4 (
    .in0(WB_IR[15:11]), .in1(WB_IR[20:16]), .in2({5{1'b1}}), .in3({5{1'b1}}), .out(multiplexer_4_out),
    .sel({1'b0, \理想流水接口_mem_wb_1_regdst_out [0]}));
  // Probe on EX_PC[11:0]
  // Probe on ID_PC[11:0]
  // Probe on M_PC[11:0]
  D_Flip_Flop #(.trigger("high"), .Pre_Clr_Positions("LEGACY"), .NegatePresetClear("false"), .enable("true"), .NewFFLayout("false")) d_ff_2 (.Q(d_ff_2_q));  // open: clk, D, Qn, preset, en, reset
  // Probe on 13'hc
  MIPS_Regifile mips_regifile_1 (
    .Din(RDin), .Clk(CLK), .R1(mips_regifile_1_r1), .R2(mips_regifile_1_r2), .WE(RegWrite),
    .W_num(multiplexer_4_out), .R1_num(multiplexer_2_out), .R2_num(multiplexer_3_out));
  // Probe on WB_PC[11:0]
  Comparator #(.width(13), .mode("twosComplement")) comparator_1 (
    .a(CNT_num), .b(13'hc), .eq(comparator_1_eq), .lt(comparator_1_lt));  // open: gt
  Clock #(.highDuration(1), .lowDuration(1)) clock_2 (.out(clock_2_out));
  nand nand_1 (nand_1_out, d_ff_2_q, comparator_1_eq);
  Counter #(.width(13), .max('h1fff), .ongoal("stay"), .trigger("rising"), .behavior("old")) counter_2 (
    .count(comparator_1_lt), .Q(CNT_num), .clk(clock_2_out));  // open: load, D, carry, clr, preset
  assign bit_extender_1_out = {{16{1'b0}}, ID_IR[15:0]};  // Bit_Extender bit_extender_1
  assign bit_extender_2_out = {{16{ID_IR[15]}}, ID_IR[15:0]};  // Bit_Extender bit_extender_2
  assign CLK = nand_1_out ? clock_2_out : 1'bz;  // Controlled_Buffer controlled_buffer_1
  Multiplexer #(.select(1), .width(32), .disabled("Z"), .enable("false")) multiplexer_5 (
    .in0(bit_extender_1_out), .in1(bit_extender_2_out), .out(multiplexer_5_out), .sel(SignedExt));
  Pull_Resistor #(.pull(1)) pull_resistor_1 (.node(CLK));
  \理想流水接口_ID_EX  \u_理想流水接口_id_ex_1  (
    .IR_in(ID_PC), .\传输状态In_表明当前传输数据有效 (\理想流水接口_if_id_1_传输状态out_表明当前传输数据有效 ), .CLK(CLK), .IR_out(EX_PC),
    .\传输状态Out_表明当前传输数据有效 (\理想流水接口_id_ex_1_传输状态out_表明当前传输数据有效 ), .PC_in(ID_IR), .PC_out(EX_IR),
    .SignedExt_in(SignedExt), .MemToReg_in(\单周期硬布线控制器_1_memtoreg ),
    .MemToReg_out(\理想流水接口_id_ex_1_memtoreg_out ), .MemWrite_in(\单周期硬布线控制器_1_memwrite ),
    .MemWrite_out(\理想流水接口_id_ex_1_memwrite_out ), .AluOp_in(\单周期硬布线控制器_1_alu_op ),
    .AluOp_out(\理想流水接口_id_ex_1_aluop_out ), .AluSrcB_in(\单周期硬布线控制器_1_alu_src ),
    .AluSrcB_out(\理想流水接口_id_ex_1_alusrcb_out ), .RegWrite_in(\单周期硬布线控制器_1_regwrite ),
    .RegWrite_out(\理想流水接口_id_ex_1_regwrite_out ), .RegDst_in(\单周期硬布线控制器_1_regdst ),
    .RegDst_out(\理想流水接口_id_ex_1_regdst_out ), .R1_in(mips_regifile_1_r1), .R1_out(\理想流水接口_id_ex_1_r1_out ),
    .R2_in(mips_regifile_1_r2), .R2_out(\理想流水接口_id_ex_1_r2_out ), .Imm__in(multiplexer_5_out),
    .Imm_out(\理想流水接口_id_ex_1_imm_out ), .Syscall_in(\单周期硬布线控制器_1_syscall ),
    .Syscall_out(\理想流水接口_id_ex_1_syscall_out ));  // open: 同步清零_气泡_高电平有效, 使能端_低电平有效_stall_高电平有效, SignedExt_out
  Comparator #(.width(32), .mode("twosComplement")) comparator_2 (
    .a(32'ha), .b(\理想流水接口_id_ex_1_r1_out ), .eq(comparator_2_eq));  // open: gt, lt
  Multiplexer #(.select(1), .width(32), .disabled("Z"), .enable("false")) multiplexer_6 (
    .in0(\理想流水接口_id_ex_1_r2_out ), .in1(\理想流水接口_id_ex_1_imm_out ), .out(multiplexer_6_out),
    .sel(\理想流水接口_id_ex_1_alusrcb_out ));
  and and_1 (Stop, comparator_2_eq, \理想流水接口_id_ex_1_syscall_out );
  MIPS_ALU mips_alu_1 (
    .X(\理想流水接口_id_ex_1_r1_out ), .Y(multiplexer_6_out), .AluOP(\理想流水接口_id_ex_1_aluop_out ),
    .Result(mips_alu_1_result), .shamt(EX_IR[10:6]));  // open: Equal, Result_2
  \理想流水接口_EX_MEM  \u_理想流水接口_ex_mem_1  (
    .IR_in(EX_PC), .\传输状态In_表明当前传输数据有效 (\理想流水接口_id_ex_1_传输状态out_表明当前传输数据有效 ), .CLK(CLK), .IR_out(M_PC),
    .PC_in(EX_IR), .PC_out(MEM_IR), .MemToReg_in(\理想流水接口_id_ex_1_memtoreg_out ),
    .MemToReg_out(\理想流水接口_ex_mem_1_memtoreg_out [0]), .MemWrite_in(\理想流水接口_id_ex_1_memwrite_out ),
    .MemWrite_out(MemWrite), .RegWrite_in(\理想流水接口_id_ex_1_regwrite_out ),
    .RegWrite_out(\理想流水接口_ex_mem_1_regwrite_out ), .RegDst_in(\理想流水接口_id_ex_1_regdst_out ),
    .RegDst_out(\理想流水接口_ex_mem_1_regdst_out ), .AluRst_in(mips_alu_1_result),
    .AluRst_out(\理想流水接口_ex_mem_1_alurst_out ), .Mem_in(\理想流水接口_id_ex_1_r2_out ), .Mem_out(MDin));  // open: 传输状态Out_表明当前传输数据有效, 同步清零_气泡_高电平有效, 使能端_低电平有效_stall_高电平有效
  RAM #(.addrWidth(10), .dataWidth(32), .bus("separate"), .Select("high")) ram_1 (
    .addr(\理想流水接口_ex_mem_1_alurst_out [11:2]), .din(MDin), .data(ram_1_data), .str(MemWrite), .clk(CLK));  // open: sel, ld, clr
  Adder #(.width(32)) adder_2 (.a(M_PC), .b(32'h4), .out(adder_2_out));  // open: cin, cout
  Multiplexer #(.select(2), .width(32), .disabled("Z"), .enable("false")) multiplexer_7 (
    .in0(\理想流水接口_ex_mem_1_alurst_out ), .in1(ram_1_data), .in2(adder_2_out), .in3(adder_2_out),
    .out(multiplexer_7_out), .sel({1'b0, \理想流水接口_ex_mem_1_memtoreg_out [0]}));
  \理想流水接口_MEM_WB  \u_理想流水接口_mem_wb_1  (
    .IR_in(M_PC), .CLK(CLK), .IR_out(WB_PC), .PC_in(MEM_IR), .PC_out(WB_IR),
    .RegWrite_in(\理想流水接口_ex_mem_1_regwrite_out ), .RegWrite_out(RegWrite),
    .RegDst_in(\理想流水接口_ex_mem_1_regdst_out ), .RegDst_out(\理想流水接口_mem_wb_1_regdst_out [0]),
    .Reg_in(multiplexer_7_out), .Reg_out(RDin));  // open: 传输状态In_表明当前传输数据有效, 传输状态Out_表明当前传输数据有效, 同步清零_气泡_高电平有效, 使能端_低电平有效_stall_高电平有效

  // Other names for the same wires on the sheet: MEM_PC[31:0] = M_PC

  // Notes on the sheet:
  //   中断源
  //   时空图监测，可删除
  //   中断等待指示
  //   数码管输出
  //   指令存储器
  //   contents of rom_1 (hex, n*v repeats v):
  //   20100000 20110000 20120000 20130000 36100000 36310001 36520002 36730003 ae100000 ae110004 ae120008
  //   ae13000c 2002000a 20110000 20120000 20130000 c
  //   OP
  //   Func
  //   rs
  //   rt
  //   rd
  //   控制位
  //   流水调试日志用
  //   暂停节拍，不能为0
  //   戳工具置1进入计数暂停模式，ctrl+k时钟自动运行到对应节拍暂停
  //   ctrl+k关闭时钟连续运行，将控制位置零，进入单步调试模式调试
  //   用这个时钟源需要去掉电路中的其他时钟源
  //   可计数暂停的时钟源
  //   为方便自动评测，需要输出流水线各段保存的PC值，注意是PC不是PC+4，另外ID段寄存器写入信息，Mem段内存写入信息也要输出
endmodule

module \理想流水接口_IF_ID  (
  input  [31:0] IR_in,
  input  [31:0] PC_in,
  input  \传输状态In_表明当前传输数据有效 ,
  input  CLK,
  input  \同步清零_气泡_高电平有效 ,
  input  \使能端_低电平有效_stall_高电平有效 ,
  output [31:0] IR_out,
  output [31:0] PC_out,
  output \传输状态Out_表明当前传输数据有效 
);

  wire multiplexer_3_out, pull_resistor_2_node;
  wire [31:0] multiplexer_1_out, multiplexer_2_out;

  Multiplexer #(.select(1), .width(32), .disabled("Z"), .enable("false")) multiplexer_1 (
    .in0(IR_in), .in1({32{1'b0}}), .out(multiplexer_1_out), .sel(\同步清零_气泡_高电平有效 ));
  Multiplexer #(.select(1), .width(32), .disabled("Z"), .enable("false")) multiplexer_2 (
    .in0(PC_in), .in1({32{1'b0}}), .out(multiplexer_2_out), .sel(\同步清零_气泡_高电平有效 ));
  Multiplexer #(.select(1), .width(1), .disabled("Z"), .enable("false")) multiplexer_3 (
    .in0(\传输状态In_表明当前传输数据有效 ), .in1(1'b0), .out(multiplexer_3_out), .sel(\同步清零_气泡_高电平有效 ));
  Pull_Resistor #(.pull(0)) pull_resistor_1 (.node(\同步清零_气泡_高电平有效 ));
  Register #(.width(32), .trigger("rising"), .Select("low")) register_1 (
    .D(multiplexer_1_out), .en(pull_resistor_2_node), .Q(IR_out), .clk(CLK));  // open: clr
  Register #(.width(32), .trigger("rising"), .Select("low")) register_2 (
    .D(multiplexer_2_out), .en(pull_resistor_2_node), .Q(PC_out), .clk(CLK));  // open: clr
  Register #(.width(1), .trigger("rising"), .Select("low")) register_3 (
    .D(multiplexer_3_out), .en(pull_resistor_2_node), .Q(\传输状态Out_表明当前传输数据有效 ), .clk(CLK));  // open: clr
  Pull_Resistor #(.pull(0)) pull_resistor_2 (.node(pull_resistor_2_node));
  not not_1 (pull_resistor_2_node, \使能端_低电平有效_stall_高电平有效 );
endmodule

module \理想流水接口_ID_EX  (
  input  [31:0] IR_in,
  input  [31:0] PC_in,
  input  SignedExt_in,
  input  MemToReg_in,
  input  MemWrite_in,
  input  [3:0] AluOp_in,
  input  AluSrcB_in,
  input  RegWrite_in,
  input  RegDst_in,
  input  Syscall_in,
  input  [31:0] R1_in,
  input  [31:0] R2_in,
  input  [31:0] Imm__in,
  input  \传输状态In_表明当前传输数据有效 ,
  input  CLK,
  input  \同步清零_气泡_高电平有效 ,
  input  \使能端_低电平有效_stall_高电平有效 ,
  output [31:0] IR_out,
  output [31:0] PC_out,
  output SignedExt_out,
  output MemToReg_out,
  output MemWrite_out,
  output [3:0] AluOp_out,
  output AluSrcB_out,
  output RegWrite_out,
  output RegDst_out,
  output Syscall_out,
  output [31:0] R1_out,
  output [31:0] R2_out,
  output [31:0] Imm_out,
  output \传输状态Out_表明当前传输数据有效 
);

  wire multiplexer_3_out, multiplexer_4_out, multiplexer_5_out, multiplexer_7_out, multiplexer_8_out,
       multiplexer_9_out, multiplexer_10_out, multiplexer_14_out, pull_resistor_2_node;
  wire [3:0] multiplexer_6_out;
  wire [31:0] multiplexer_1_out, multiplexer_2_out, multiplexer_11_out, multiplexer_12_out,
       multiplexer_13_out;

  Multiplexer #(.select(1), .width(32), .disabled("Z"), .enable("false")) multiplexer_1 (
    .in0(IR_in), .in1({32{1'b0}}), .out(multiplexer_1_out), .sel(\同步清零_气泡_高电平有效 ));
  Multiplexer #(.select(1), .width(32), .disabled("Z"), .enable("false")) multiplexer_2 (
    .in0(PC_in), .in1({32{1'b0}}), .out(multiplexer_2_out), .sel(\同步清零_气泡_高电平有效 ));
  Multiplexer #(.select(1), .width(1), .disabled("Z"), .enable("false")) multiplexer_3 (
    .in0(SignedExt_in), .in1(1'b0), .out(multiplexer_3_out), .sel(\同步清零_气泡_高电平有效 ));
  Multiplexer #(.select(1), .width(1), .disabled("Z"), .enable("false")) multiplexer_4 (
    .in0(MemToReg_in), .in1(1'b0), .out(multiplexer_4_out), .sel(\同步清零_气泡_高电平有效 ));
  Multiplexer #(.select(1), .width(1), .disabled("Z"), .enable("false")) multiplexer_5 (
    .in0(MemWrite_in), .in1(1'b0), .out(multiplexer_5_out), .sel(\同步清零_气泡_高电平有效 ));
  Multiplexer #(.select(1), .width(4), .disabled("Z"), .enable("false")) multiplexer_6 (
    .in0(AluOp_in), .in1(4'b0000), .out(multiplexer_6_out), .sel(\同步清零_气泡_高电平有效 ));
  Multiplexer #(.select(1), .width(1), .disabled("Z"), .enable("false")) multiplexer_7 (
    .in0(AluSrcB_in), .in1(1'b0), .out(multiplexer_7_out), .sel(\同步清零_气泡_高电平有效 ));
  Multiplexer #(.select(1), .width(1), .disabled("Z"), .enable("false")) multiplexer_8 (
    .in0(RegWrite_in), .in1(1'b0), .out(multiplexer_8_out), .sel(\同步清零_气泡_高电平有效 ));
  Multiplexer #(.select(1), .width(1), .disabled("Z"), .enable("false")) multiplexer_9 (
    .in0(RegDst_in), .in1(1'b0), .out(multiplexer_9_out), .sel(\同步清零_气泡_高电平有效 ));
  Multiplexer #(.select(1), .width(1), .disabled("Z"), .enable("false")) multiplexer_10 (
    .in0(Syscall_in), .in1(1'b0), .out(multiplexer_10_out), .sel(\同步清零_气泡_高电平有效 ));
  Multiplexer #(.select(1), .width(32), .disabled("Z"), .enable("false")) multiplexer_11 (
    .in0(R1_in), .in1({32{1'b0}}), .out(multiplexer_11_out), .sel(\同步清零_气泡_高电平有效 ));
  Multiplexer #(.select(1), .width(32), .disabled("Z"), .enable("false")) multiplexer_12 (
    .in0(R2_in), .in1({32{1'b0}}), .out(multiplexer_12_out), .sel(\同步清零_气泡_高电平有效 ));
  Multiplexer #(.select(1), .width(32), .disabled("Z"), .enable("false")) multiplexer_13 (
    .in0(Imm__in), .in1({32{1'b0}}), .out(multiplexer_13_out), .sel(\同步清零_气泡_高电平有效 ));
  Multiplexer #(.select(1), .width(1), .disabled("Z"), .enable("false")) multiplexer_14 (
    .in0(\传输状态In_表明当前传输数据有效 ), .in1(1'b0), .out(multiplexer_14_out), .sel(\同步清零_气泡_高电平有效 ));
  Pull_Resistor #(.pull(0)) pull_resistor_1 (.node(\同步清零_气泡_高电平有效 ));
  Register #(.width(32), .trigger("rising"), .Select("low")) register_1 (
    .D(multiplexer_1_out), .en(pull_resistor_2_node), .Q(IR_out), .clk(CLK));  // open: clr
  Register #(.width(32), .trigger("rising"), .Select("low")) register_2 (
    .D(multiplexer_2_out), .en(pull_resistor_2_node), .Q(PC_out), .clk(CLK));  // open: clr
  Register #(.width(1), .trigger("rising"), .Select("low")) register_3 (
    .D(multiplexer_3_out), .en(pull_resistor_2_node), .Q(SignedExt_out), .clk(CLK));  // open: clr
  Register #(.width(1), .trigger("rising"), .Select("low")) register_4 (
    .D(multiplexer_4_out), .en(pull_resistor_2_node), .Q(MemToReg_out), .clk(CLK));  // open: clr
  Register #(.width(1), .trigger("rising"), .Select("low")) register_5 (
    .D(multiplexer_5_out), .en(pull_resistor_2_node), .Q(MemWrite_out), .clk(CLK));  // open: clr
  Register #(.width(4), .trigger("rising"), .Select("low")) register_6 (
    .D(multiplexer_6_out), .en(pull_resistor_2_node), .Q(AluOp_out), .clk(CLK));  // open: clr
  Register #(.width(1), .trigger("rising"), .Select("low")) register_7 (
    .D(multiplexer_7_out), .en(pull_resistor_2_node), .Q(AluSrcB_out), .clk(CLK));  // open: clr
  Register #(.width(1), .trigger("rising"), .Select("low")) register_8 (
    .D(multiplexer_8_out), .en(pull_resistor_2_node), .Q(RegWrite_out), .clk(CLK));  // open: clr
  Register #(.width(1), .trigger("rising"), .Select("low")) register_9 (
    .D(multiplexer_9_out), .en(pull_resistor_2_node), .Q(RegDst_out), .clk(CLK));  // open: clr
  Register #(.width(1), .trigger("rising"), .Select("low")) register_10 (
    .D(multiplexer_10_out), .en(pull_resistor_2_node), .Q(Syscall_out), .clk(CLK));  // open: clr
  Register #(.width(32), .trigger("rising"), .Select("low")) register_11 (
    .D(multiplexer_11_out), .en(pull_resistor_2_node), .Q(R1_out), .clk(CLK));  // open: clr
  Register #(.width(32), .trigger("rising"), .Select("low")) register_12 (
    .D(multiplexer_12_out), .en(pull_resistor_2_node), .Q(R2_out), .clk(CLK));  // open: clr
  Register #(.width(32), .trigger("rising"), .Select("low")) register_13 (
    .D(multiplexer_13_out), .en(pull_resistor_2_node), .Q(Imm_out), .clk(CLK));  // open: clr
  Register #(.width(1), .trigger("rising"), .Select("low")) register_14 (
    .D(multiplexer_14_out), .en(pull_resistor_2_node), .Q(\传输状态Out_表明当前传输数据有效 ), .clk(CLK));  // open: clr
  Pull_Resistor #(.pull(0)) pull_resistor_2 (.node(pull_resistor_2_node));
  not not_1 (pull_resistor_2_node, \使能端_低电平有效_stall_高电平有效 );
endmodule

module \理想流水接口_EX_MEM  (
  input  [31:0] IR_in,
  input  [31:0] PC_in,
  input  MemToReg_in,
  input  MemWrite_in,
  input  RegWrite_in,
  input  RegDst_in,
  input  [31:0] AluRst_in,
  input  [31:0] Mem_in,
  input  \传输状态In_表明当前传输数据有效 ,
  input  CLK,
  input  \同步清零_气泡_高电平有效 ,
  input  \使能端_低电平有效_stall_高电平有效 ,
  output [31:0] IR_out,
  output [31:0] PC_out,
  output MemToReg_out,
  output MemWrite_out,
  output RegWrite_out,
  output RegDst_out,
  output [31:0] AluRst_out,
  output [31:0] Mem_out,
  output \传输状态Out_表明当前传输数据有效 
);

  wire multiplexer_3_out, multiplexer_4_out, multiplexer_5_out, multiplexer_6_out, multiplexer_9_out,
       pull_resistor_2_node;
  wire [31:0] multiplexer_1_out, multiplexer_2_out, multiplexer_7_out, multiplexer_8_out;

  Multiplexer #(.select(1), .width(32), .disabled("Z"), .enable("false")) multiplexer_1 (
    .in0(IR_in), .in1({32{1'b0}}), .out(multiplexer_1_out), .sel(\同步清零_气泡_高电平有效 ));
  Multiplexer #(.select(1), .width(32), .disabled("Z"), .enable("false")) multiplexer_2 (
    .in0(PC_in), .in1({32{1'b0}}), .out(multiplexer_2_out), .sel(\同步清零_气泡_高电平有效 ));
  Multiplexer #(.select(1), .width(1), .disabled("Z"), .enable("false")) multiplexer_3 (
    .in0(MemToReg_in), .in1(1'b0), .out(multiplexer_3_out), .sel(\同步清零_气泡_高电平有效 ));
  Multiplexer #(.select(1), .width(1), .disabled("Z"), .enable("false")) multiplexer_4 (
    .in0(MemWrite_in), .in1(1'b0), .out(multiplexer_4_out), .sel(\同步清零_气泡_高电平有效 ));
  Multiplexer #(.select(1), .width(1), .disabled("Z"), .enable("false")) multiplexer_5 (
    .in0(RegWrite_in), .in1(1'b0), .out(multiplexer_5_out), .sel(\同步清零_气泡_高电平有效 ));
  Multiplexer #(.select(1), .width(1), .disabled("Z"), .enable("false")) multiplexer_6 (
    .in0(RegDst_in), .in1(1'b0), .out(multiplexer_6_out), .sel(\同步清零_气泡_高电平有效 ));
  Multiplexer #(.select(1), .width(32), .disabled("Z"), .enable("false")) multiplexer_7 (
    .in0(AluRst_in), .in1({32{1'b0}}), .out(multiplexer_7_out), .sel(\同步清零_气泡_高电平有效 ));
  Multiplexer #(.select(1), .width(32), .disabled("Z"), .enable("false")) multiplexer_8 (
    .in0(Mem_in), .in1({32{1'b0}}), .out(multiplexer_8_out), .sel(\同步清零_气泡_高电平有效 ));
  Multiplexer #(.select(1), .width(1), .disabled("Z"), .enable("false")) multiplexer_9 (
    .in0(\传输状态In_表明当前传输数据有效 ), .in1(1'b0), .out(multiplexer_9_out), .sel(\同步清零_气泡_高电平有效 ));
  Pull_Resistor #(.pull(0)) pull_resistor_1 (.node(\同步清零_气泡_高电平有效 ));
  Register #(.width(32), .trigger("rising"), .Select("low")) register_1 (
    .D(multiplexer_1_out), .en(pull_resistor_2_node), .Q(IR_out), .clk(CLK));  // open: clr
  Register #(.width(32), .trigger("rising"), .Select("low")) register_2 (
    .D(multiplexer_2_out), .en(pull_resistor_2_node), .Q(PC_out), .clk(CLK));  // open: clr
  Register #(.width(1), .trigger("rising"), .Select("low")) register_3 (
    .D(multiplexer_3_out), .en(pull_resistor_2_node), .Q(MemToReg_out), .clk(CLK));  // open: clr
  Register #(.width(1), .trigger("rising"), .Select("low")) register_4 (
    .D(multiplexer_4_out), .en(pull_resistor_2_node), .Q(MemWrite_out), .clk(CLK));  // open: clr
  Register #(.width(1), .trigger("rising"), .Select("low")) register_5 (
    .D(multiplexer_5_out), .en(pull_resistor_2_node), .Q(RegWrite_out), .clk(CLK));  // open: clr
  Register #(.width(1), .trigger("rising"), .Select("low")) register_6 (
    .D(multiplexer_6_out), .en(pull_resistor_2_node), .Q(RegDst_out), .clk(CLK));  // open: clr
  Register #(.width(32), .trigger("rising"), .Select("low")) register_7 (
    .D(multiplexer_7_out), .en(pull_resistor_2_node), .Q(AluRst_out), .clk(CLK));  // open: clr
  Register #(.width(32), .trigger("rising"), .Select("low")) register_8 (
    .D(multiplexer_8_out), .en(pull_resistor_2_node), .Q(Mem_out), .clk(CLK));  // open: clr
  Register #(.width(1), .trigger("rising"), .Select("low")) register_9 (
    .D(multiplexer_9_out), .en(pull_resistor_2_node), .Q(\传输状态Out_表明当前传输数据有效 ), .clk(CLK));  // open: clr
  Pull_Resistor #(.pull(0)) pull_resistor_2 (.node(pull_resistor_2_node));
  not not_1 (pull_resistor_2_node, \使能端_低电平有效_stall_高电平有效 );
endmodule

module \理想流水接口_MEM_WB  (
  input  [31:0] IR_in,
  input  [31:0] PC_in,
  input  RegWrite_in,
  input  RegDst_in,
  input  [31:0] Reg_in,
  input  \传输状态In_表明当前传输数据有效 ,
  input  CLK,
  input  \同步清零_气泡_高电平有效 ,
  input  \使能端_低电平有效_stall_高电平有效 ,
  output [31:0] IR_out,
  output [31:0] PC_out,
  output RegWrite_out,
  output RegDst_out,
  output [31:0] Reg_out,
  output \传输状态Out_表明当前传输数据有效 
);

  wire multiplexer_3_out, multiplexer_4_out, multiplexer_6_out, pull_resistor_2_node;
  wire [31:0] multiplexer_1_out, multiplexer_2_out, multiplexer_5_out;

  Multiplexer #(.select(1), .width(32), .disabled("Z"), .enable("false")) multiplexer_1 (
    .in0(IR_in), .in1({32{1'b0}}), .out(multiplexer_1_out), .sel(\同步清零_气泡_高电平有效 ));
  Multiplexer #(.select(1), .width(32), .disabled("Z"), .enable("false")) multiplexer_2 (
    .in0(PC_in), .in1({32{1'b0}}), .out(multiplexer_2_out), .sel(\同步清零_气泡_高电平有效 ));
  Multiplexer #(.select(1), .width(1), .disabled("Z"), .enable("false")) multiplexer_3 (
    .in0(RegWrite_in), .in1(1'b0), .out(multiplexer_3_out), .sel(\同步清零_气泡_高电平有效 ));
  Multiplexer #(.select(1), .width(1), .disabled("Z"), .enable("false")) multiplexer_4 (
    .in0(RegDst_in), .in1(1'b0), .out(multiplexer_4_out), .sel(\同步清零_气泡_高电平有效 ));
  Multiplexer #(.select(1), .width(32), .disabled("Z"), .enable("false")) multiplexer_5 (
    .in0(Reg_in), .in1({32{1'b0}}), .out(multiplexer_5_out), .sel(\同步清零_气泡_高电平有效 ));
  Multiplexer #(.select(1), .width(1), .disabled("Z"), .enable("false")) multiplexer_6 (
    .in0(\传输状态In_表明当前传输数据有效 ), .in1(1'b0), .out(multiplexer_6_out), .sel(\同步清零_气泡_高电平有效 ));
  Pull_Resistor #(.pull(0)) pull_resistor_1 (.node(\同步清零_气泡_高电平有效 ));
  Register #(.width(32), .trigger("rising"), .Select("low")) register_1 (
    .D(multiplexer_1_out), .en(pull_resistor_2_node), .Q(IR_out), .clk(CLK));  // open: clr
  Register #(.width(32), .trigger("rising"), .Select("low")) register_2 (
    .D(multiplexer_2_out), .en(pull_resistor_2_node), .Q(PC_out), .clk(CLK));  // open: clr
  Register #(.width(1), .trigger("rising"), .Select("low")) register_3 (
    .D(multiplexer_3_out), .en(pull_resistor_2_node), .Q(RegWrite_out), .clk(CLK));  // open: clr
  Register #(.width(1), .trigger("rising"), .Select("low")) register_4 (
    .D(multiplexer_4_out), .en(pull_resistor_2_node), .Q(RegDst_out), .clk(CLK));  // open: clr
  Register #(.width(32), .trigger("rising"), .Select("low")) register_5 (
    .D(multiplexer_5_out), .en(pull_resistor_2_node), .Q(Reg_out), .clk(CLK));  // open: clr
  Register #(.width(1), .trigger("rising"), .Select("low")) register_6 (
    .D(multiplexer_6_out), .en(pull_resistor_2_node), .Q(\传输状态Out_表明当前传输数据有效 ), .clk(CLK));  // open: clr
  Pull_Resistor #(.pull(0)) pull_resistor_2 (.node(pull_resistor_2_node));
  not not_1 (pull_resistor_2_node, \使能端_低电平有效_stall_高电平有效 );
endmodule

module \气泡流水线  (
  output RegWrite,
  output MemWrite,
  output [31:0] IF_PC,
  output [31:0] ID_PC,
  output [31:0] EX_PC,
  output [31:0] M_PC,
  output [31:0] WB_PC,
  output [31:0] RDin,
  output [31:0] MDin,
  output [31:0] LedData
);

  wire and_1_out, and_3_out, and_4_out, and_5_out, and_8_out, BLEZ_LESS, CLK, CLK_C, clock_1_out,
       clock_2_out, comparator_1_eq, comparator_1_lt, comparator_2_eq, comparator_3_eq, comparator_4_eq,
       d_ff_2_q, equal, EX_RegWrite, Exit, Go, IF_stall, IR1, IR2, IR3, MEM_RegWrite, nand_1_out, not_1_out,
       or_2_out, or_3_out, or_4_out, Pause, RST, Stop, W1, W2, W3, \单周期硬布线控制器_1_alu_src , \单周期硬布线控制器_1_beq ,
       \单周期硬布线控制器_1_blez , \单周期硬布线控制器_1_bne , \单周期硬布线控制器_1_eret , \单周期硬布线控制器_1_jmp , \单周期硬布线控制器_1_jr ,
       \单周期硬布线控制器_1_lbu , \单周期硬布线控制器_1_memtoreg , \单周期硬布线控制器_1_memwrite , \单周期硬布线控制器_1_regwrite ,
       \单周期硬布线控制器_1_signedext , \单周期硬布线控制器_1_syscall , \条件分支成功 , \气泡流水接口_ex_mem_1_eret_out ,
       \气泡流水接口_ex_mem_1_jal_out , \气泡流水接口_ex_mem_1_lbu_out , \气泡流水接口_ex_mem_1_memtoreg_out ,
       \气泡流水接口_ex_mem_1_regdst_out , \气泡流水接口_ex_mem_1_传输状态out_表明当前传输数据有效 , \气泡流水接口_id_ex_1_alusrcb_out ,
       \气泡流水接口_id_ex_1_beq_out , \气泡流水接口_id_ex_1_blez_out , \气泡流水接口_id_ex_1_bne_out ,
       \气泡流水接口_id_ex_1_eret_out , \气泡流水接口_id_ex_1_jal_out , \气泡流水接口_id_ex_1_jmp_out ,
       \气泡流水接口_id_ex_1_lbu_out , \气泡流水接口_id_ex_1_memtoreg_out , \气泡流水接口_id_ex_1_memwrite_out ,
       \气泡流水接口_id_ex_1_regdst_out , \气泡流水接口_id_ex_1_syscall_out , \气泡流水接口_id_ex_1_传输状态out_表明当前传输数据有效 ,
       \气泡流水接口_if_id_1_传输状态out_表明当前传输数据有效 , \气泡流水接口_mem_wb_1_lbu_out , \源寄存器使用情况_1_r1_used ,
       \源寄存器使用情况_1_r2_used ;
  wire [1:0] pull_resistor_2_node, \单周期硬布线控制器_1_regdst , \气泡流水接口_mem_wb_1_memtoreg_out ;
  wire [1:1] \气泡流水接口_id_ex_1_jr_out ;
  wire [3:0] \单周期硬布线控制器_1_alu_op , \气泡流水接口_id_ex_1_aluop_out ;
  wire [4:0] EX_RegWrite_num, ID_R1_num, ID_R2_num, MEM_RegWrite_num, multiplexer_4_out, WB_RegWrite_num;
  wire [7:0] \气泡流水接口_mem_wb_1_mem_out , \气泡流水接口_mem_wb_1_mem_out_2 , \气泡流水接口_mem_wb_1_mem_out_3 ;
  wire [12:0] CNT_num;
  wire [15:0] \LoadUse次数 , \总周期数 , \插入气泡数 , \无条件分支数 , \条件分支成功数 ;
  wire [31:0] adder_1_out, adder_2_out, adder_3_out, adder_4_out, bit_extender_1_out, bit_extender_2_out,
       bit_extender_3_out, EX_IR, ID_IR, IF_IR, JMP_EX, MEM_IR, multiplexer_1_out, multiplexer_5_out,
       multiplexer_6_out, multiplexer_8_out, multiplexer_9_out, pull_resistor_3_node, ram_1_data, WB_IR,
       \气泡流水接口_ex_mem_1_alurst_out , \气泡流水接口_id_ex_1_imm_out , \气泡流水接口_id_ex_1_r1_out ,
       \气泡流水接口_id_ex_1_r2_out , \气泡流水接口_mem_wb_1_alurst_out , \气泡流水线_mips_regifile_1_r1 ,
       \气泡流水线_mips_regifile_1_r2 ;
  wire [31:1] mips_alu_1_result;
  wire [31:8] pull_resistor_4_node, pull_resistor_5_node, pull_resistor_6_node, pull_resistor_7_node;
  wire [31:24] \气泡流水接口_mem_wb_1_mem_out_4 ;

  Button \u_总复位  (.out(RST));
  Button _1 (.out(IR1));
  Button _2 (.out(IR2));
  Button _3 (.out(IR3));
  // Probe on \总周期数 
  // Probe on \总周期数 
  Button \u_继续运行  (.out(Go));
  LED #(.active("true")) led_1 (.in(W1));
  LED #(.active("true")) led_2 (.in(W2));
  LED #(.active("true")) led_3 (.in(W3));
  // Probe on adder_1_out
  Hex_Digit_Display hex_digit_display_1 (.value(LedData[31:28]));  // open: dp
  // Probe on IF_PC[19:0]
  // Mips_Probe mips_probe_1: pin names not known; wires that end beside it: IF_IR
  // OR_Gate or_1 has open pins: in0=Pause, in1=Exit, out=open
  or or_2 (or_2_out, and_1_out, RST);
  and and_1 (and_1_out, ~Exit, Go);  // AND_Gate
  Multiplexer #(.select(1), .width(32), .disabled("Z"), .enable("false")) multiplexer_1 (
    .in0(adder_1_out), .in1(JMP_EX), .out(multiplexer_1_out), .sel(or_3_out));
  // Probe on JMP_EX
  Hex_Digit_Display hex_digit_display_2 (.value(LedData[23:20]));  // open: dp
  Hex_Digit_Display hex_digit_display_3 (.value(LedData[27:24]));  // open: dp
  // Probe on ID_PC[19:0]
  // Mips_Probe mips_probe_2: pin names not known; wires that end beside it: ID_IR
  D_Flip_Flop #(.trigger("rising"), .Pre_Clr_Positions("ABOVE_BELOW"), .NegatePresetClear("false"), .enable("false"), .NewFFLayout("true")) d_ff_1 (
    .D(1'b1), .Qn(Stop), .reset(or_2_out));  // open: clk, Q, preset
  not not_1 (not_1_out, IF_stall);
  Register #(.width(32), .trigger("rising"), .Select("low")) PC (
    .D(multiplexer_1_out), .en(not_1_out), .Q(IF_PC), .clk(CLK), .clr(RST));
  Hex_Digit_Display hex_digit_display_4 (.value(LedData[15:12]));  // open: dp
  Hex_Digit_Display hex_digit_display_5 (.value(LedData[19:16]));  // open: dp
  Counter #(.width(16), .max('hffff), .ongoal("wrap"), .trigger("rising"), .behavior("new")) counter_1 (
    .count(Stop), .Q(\总周期数 ), .clk(CLK), .clr(RST));  // open: load, D, carry, preset, down
  // Probe on IF_PC
  Hex_Digit_Display hex_digit_display_6 (.value(LedData[7:4]));  // open: dp
  Hex_Digit_Display hex_digit_display_7 (.value(LedData[11:8]));  // open: dp
  Clock #(.highDuration(1), .lowDuration(1)) clock_1 (.out(clock_1_out));
  // Probe on EX_PC[19:0]
  // Mips_Probe mips_probe_3: pin names not known; wires that end beside it: EX_IR, clock_1_out, CLK
  and and_2 (CLK, CLK_C, Stop);
  Adder #(.width(32)) adder_1 (.a(IF_PC), .b(32'h4), .out(adder_1_out), .cin(1'b0));  // open: cout
  Hex_Digit_Display hex_digit_display_8 (.value(LedData[3:0]));  // open: dp
  // Mips_Probe mips_probe_4: pin names not known; wires that end beside it: IF_IR
  ROM #(.addrWidth(10), .dataWidth(32), .Select("high")) rom_1 (.addr(IF_PC[11:2]), .data(IF_IR));
  // Probe on \总周期数 
  // Probe on M_PC[19:0]
  // Mips_Probe mips_probe_5: pin names not known; wires that end beside it: MEM_IR
  \气泡流水接口_IF_ID  \u_气泡流水接口_if_id_1  (
    .IR_in(IF_IR), .\传输状态In_表明当前传输数据有效 (1'b1), .CLK(CLK), .IR_out(ID_IR),
    .\传输状态Out_表明当前传输数据有效 (\气泡流水接口_if_id_1_传输状态out_表明当前传输数据有效 ), .\同步清零_气泡_高电平有效 (or_3_out),
    .\使能端_低电平有效_stall_高电平有效 (IF_stall), .PC_in(IF_PC), .PC_out(ID_PC));
  // Probe on \总周期数 
  // Probe on \无条件分支数 
  // Probe on \条件分支成功数 
  // Probe on \插入气泡数 
  // Probe on \LoadUse次数 
  // Probe on IF_PC[11:0]
  // Probe on WB_PC[19:0]
  // Mips_Probe mips_probe_6: pin names not known; wires that end beside it: IF_stall, WB_IR
  \单周期硬布线控制器  \u_单周期硬布线控制器_1  (
    .Func(ID_IR[5:0]), .OP(ID_IR[31:26]), .ALU_OP(\单周期硬布线控制器_1_alu_op ), .MemToReg(\单周期硬布线控制器_1_memtoreg ),
    .MemWrite(\单周期硬布线控制器_1_memwrite ), .ALU_SRC(\单周期硬布线控制器_1_alu_src ), .RegWrite(\单周期硬布线控制器_1_regwrite ),
    .SysCALL(\单周期硬布线控制器_1_syscall ), .SignedExt(\单周期硬布线控制器_1_signedext ), .RegDst(\单周期硬布线控制器_1_regdst [0]),
    .JR(\单周期硬布线控制器_1_jr ), .JMP(\单周期硬布线控制器_1_jmp ), .Beq(\单周期硬布线控制器_1_beq ), .JAL(\单周期硬布线控制器_1_regdst [1]),
    .Bne(\单周期硬布线控制器_1_bne ), .ERET(\单周期硬布线控制器_1_eret ), .LBU(\单周期硬布线控制器_1_lbu ), .BLEZ(\单周期硬布线控制器_1_blez ));
  Multiplexer #(.select(1), .width(5), .disabled("Z"), .enable("false")) multiplexer_2 (
    .in0(ID_IR[25:21]), .in1(5'b00010), .out(ID_R1_num), .sel(\单周期硬布线控制器_1_syscall ));
  Multiplexer #(.select(1), .width(5), .disabled("Z"), .enable("false")) multiplexer_3 (
    .in0(ID_IR[20:16]), .in1(5'b00100), .out(ID_R2_num), .sel(\单周期硬布线控制器_1_syscall ));
  // Probe on ID_PC[11:0]
  // Probe on EX_PC[11:0]
  \源寄存器使用情况  \u_源寄存器使用情况_1  (
    .OP0(ID_IR[26]), .OP1(ID_IR[27]), .OP2(ID_IR[28]), .OP3(ID_IR[29]), .OP4(ID_IR[30]), .OP5(ID_IR[31]),
    .F0(ID_IR[0]), .F1(ID_IR[1]), .F2(ID_IR[2]), .F3(ID_IR[3]), .F4(ID_IR[4]), .F5(ID_IR[5]),
    .R1_Used(\源寄存器使用情况_1_r1_used ), .R2_Used(\源寄存器使用情况_1_r2_used ));
  // Probe on M_PC[11:0]
  D_Flip_Flop #(.trigger("high"), .Pre_Clr_Positions("LEGACY"), .NegatePresetClear("false"), .enable("true"), .NewFFLayout("false")) d_ff_2 (.Q(d_ff_2_q));  // open: clk, D, Qn, preset, en, reset
  // Probe on 13'h1f4
  // Probe on WB_PC[11:0]
  Comparator #(.width(13), .mode("twosComplement")) comparator_1 (
    .a(CNT_num), .b(13'h1f4), .eq(comparator_1_eq), .lt(comparator_1_lt));  // open: gt
  Clock #(.highDuration(1), .lowDuration(1)) clock_2 (.out(clock_2_out));
  \数据相关检测  \u_数据相关检测_1  (
    .R1_Used(\源寄存器使用情况_1_r1_used ), .R2_Used(\源寄存器使用情况_1_r2_used ), .EX_WriteReg_num(EX_RegWrite_num),
    .MEM_WriteReg_num(MEM_RegWrite_num), .WB_WriteReg_num(WB_RegWrite_num), .R1_num(ID_R1_num),
    .R2_num(ID_R2_num), .EX_RegWrite(EX_RegWrite), .MEM_RegWrite(RegWrite), .WB_RegWrite(MEM_RegWrite),
    .\数据相关 (IF_stall));
  \气泡流水线_MIPS_Regifile  \u_气泡流水线_mips_regifile_1  (
    .Din(RDin), .Clk(CLK), .R1(\气泡流水线_mips_regifile_1_r1 ), .R2(\气泡流水线_mips_regifile_1_r2 ), .WE(RegWrite),
    .W_num(WB_RegWrite_num), .R1_num(ID_R1_num), .R2_num(ID_R2_num));
  nand nand_1 (nand_1_out, d_ff_2_q, comparator_1_eq);
  Counter #(.width(13), .max('h1fff), .ongoal("stay"), .trigger("rising"), .behavior("old")) counter_2 (
    .count(comparator_1_lt), .Q(CNT_num), .clk(clock_2_out));  // open: load, D, carry, clr, preset
  Counter #(.width(16), .max('hffff), .ongoal("wrap"), .trigger("rising"), .behavior("new")) counter_3 (
    .count(IF_stall), .Q(\插入气泡数 ), .clk(CLK), .clr(RST));  // open: load, D, carry, preset, down
  assign bit_extender_1_out = {{16{1'b0}}, ID_IR[15:0]};  // Bit_Extender bit_extender_1
  assign bit_extender_2_out = {{16{ID_IR[15]}}, ID_IR[15:0]};  // Bit_Extender bit_extender_2
  Multiplexer #(.select(2), .width(5), .disabled("Z"), .enable("false")) multiplexer_4 (
    .in0(ID_IR[15:11]), .in1(ID_IR[20:16]), .in2({5{1'b1}}), .in3({5{1'b1}}), .out(multiplexer_4_out),
    .sel(\单周期硬布线控制器_1_regdst ));
  assign CLK_C = nand_1_out ? clock_2_out : 1'bz;  // Controlled_Buffer controlled_buffer_1
  or or_3 (or_3_out, \条件分支成功 , \气泡流水接口_id_ex_1_jmp_out );
  Multiplexer #(.select(1), .width(32), .disabled("Z"), .enable("false")) multiplexer_5 (
    .in0(bit_extender_1_out), .in1(bit_extender_2_out), .out(multiplexer_5_out), .sel(\单周期硬布线控制器_1_signedext ));
  Pull_Resistor #(.pull(1)) pull_resistor_1 (.node(CLK_C));
  Counter #(.width(16), .max('hffff), .ongoal("wrap"), .trigger("rising"), .behavior("new")) \u_无条件分支数  (
    .count(\气泡流水接口_id_ex_1_jmp_out ), .Q(\无条件分支数 ), .clk(CLK), .clr(RST));  // open: load, D, carry, preset, down
  or or_4 (or_4_out, \条件分支成功 , IF_stall, \气泡流水接口_id_ex_1_jmp_out );
  \气泡流水接口_ID_EX  \u_气泡流水接口_id_ex_1  (
    .IR_in(ID_IR), .\传输状态In_表明当前传输数据有效 (\气泡流水接口_if_id_1_传输状态out_表明当前传输数据有效 ), .CLK(CLK), .IR_out(EX_IR),
    .\传输状态Out_表明当前传输数据有效 (\气泡流水接口_id_ex_1_传输状态out_表明当前传输数据有效 ), .\同步清零_气泡_高电平有效 (or_4_out),
    .\使能端_低电平有效_stall_高电平有效 (1'b0), .PC_in(ID_PC), .PC_out(EX_PC), .JMP_in(\单周期硬布线控制器_1_jmp ),
    .JMP_out(\气泡流水接口_id_ex_1_jmp_out ), .MemToReg_in(\单周期硬布线控制器_1_memtoreg ),
    .MemToReg_out(\气泡流水接口_id_ex_1_memtoreg_out ), .MemWrite_in(\单周期硬布线控制器_1_memwrite ),
    .MemWrite_out(\气泡流水接口_id_ex_1_memwrite_out ), .AluOp_in(\单周期硬布线控制器_1_alu_op ),
    .AluOp_out(\气泡流水接口_id_ex_1_aluop_out ), .AluSrcB_in(\单周期硬布线控制器_1_alu_src ),
    .AluSrcB_out(\气泡流水接口_id_ex_1_alusrcb_out ), .RegWrite_in(\单周期硬布线控制器_1_regwrite ),
    .RegWrite_out(EX_RegWrite), .RegDst_in(\单周期硬布线控制器_1_regdst [0]),
    .RegDst_out(\气泡流水接口_id_ex_1_regdst_out ), .R1_in(\气泡流水线_mips_regifile_1_r1 ),
    .R1_out(\气泡流水接口_id_ex_1_r1_out ), .R2_in(\气泡流水线_mips_regifile_1_r2 ), .R2_out(\气泡流水接口_id_ex_1_r2_out ),
    .Imm__in(multiplexer_5_out), .Imm_out(\气泡流水接口_id_ex_1_imm_out ), .Syscall_in(\单周期硬布线控制器_1_syscall ),
    .Syscall_out(\气泡流水接口_id_ex_1_syscall_out ), .Beq_in(\单周期硬布线控制器_1_beq ),
    .Beq_out(\气泡流水接口_id_ex_1_beq_out ), .JR_in(\单周期硬布线控制器_1_jr ), .JR_out(\气泡流水接口_id_ex_1_jr_out [1]),
    .Bne_in(\单周期硬布线控制器_1_bne ), .Bne_out(\气泡流水接口_id_ex_1_bne_out ), .SignedExt_in(\单周期硬布线控制器_1_signedext ),
    .ERET_in(\单周期硬布线控制器_1_eret ), .ERET_out(\气泡流水接口_id_ex_1_eret_out ), .LBU_in(\单周期硬布线控制器_1_lbu ),
    .LBU_out(\气泡流水接口_id_ex_1_lbu_out ), .BLEZ_in(\单周期硬布线控制器_1_blez ), .BLEZ_out(\气泡流水接口_id_ex_1_blez_out ),
    .JAL_in(\单周期硬布线控制器_1_regdst [1]), .JAL_out(\气泡流水接口_id_ex_1_jal_out ), .RegWrite__in(multiplexer_4_out),
    .RegWrite__out(EX_RegWrite_num));  // open: SignedExt_out, R1Forward_in, R1Forward_out, R2Forward_in, R2Forward_out, MFC0_in, MFC0_out, MTC0_in, MTC0_out
  and and_3 (and_3_out, \气泡流水接口_id_ex_1_beq_out , equal);
  and and_4 (and_4_out, \气泡流水接口_id_ex_1_bne_out , ~equal);  // AND_Gate
  and and_5 (and_5_out, \气泡流水接口_id_ex_1_blez_out , BLEZ_LESS);
  or or_5 (\条件分支成功 , and_3_out, and_4_out, and_5_out);
  Counter #(.width(16), .max('hffff), .ongoal("wrap"), .trigger("rising"), .behavior("new")) \u_条件成功分支数  (
    .count(\条件分支成功 ), .Q(\条件分支成功数 ), .clk(CLK), .clr(RST));  // open: load, D, carry, preset, down
  Adder #(.width(32)) adder_2 (.a(32'h4), .b(EX_PC), .out(adder_2_out));  // open: cin, cout
  Pull_Resistor #(.pull(0)) pull_resistor_2 (.node({EX_IR[15:0], pull_resistor_2_node}));
  Multiplexer #(.select(1), .width(32), .disabled("Z"), .enable("false")) multiplexer_6 (
    .in0(\气泡流水接口_id_ex_1_r2_out ), .in1(\气泡流水接口_id_ex_1_imm_out ), .out(multiplexer_6_out),
    .sel(\气泡流水接口_id_ex_1_alusrcb_out ));
  Pull_Resistor #(.pull(0)) pull_resistor_3 (.node({pull_resistor_3_node[31:28], EX_IR[25:0], pull_resistor_3_node[1:0]}));
  Adder #(.width(32)) adder_3 (.a(adder_2_out), .b(bit_extender_3_out), .out(adder_3_out));  // open: cin, cout
  assign bit_extender_3_out = {{14{EX_IR[15]}}, {EX_IR[15:0], pull_resistor_2_node}};  // Bit_Extender bit_extender_3
  and and_6 (Pause, \气泡流水接口_id_ex_1_syscall_out , comparator_2_eq);
  Comparator #(.width(32), .mode("twosComplement")) comparator_2 (
    .a(32'h32), .b(\气泡流水接口_id_ex_1_r1_out ), .eq(comparator_2_eq));  // open: gt, lt
  and and_7 (Exit, \气泡流水接口_id_ex_1_syscall_out , comparator_3_eq);
  Comparator #(.width(32), .mode("twosComplement")) comparator_3 (
    .a(32'ha), .b(\气泡流水接口_id_ex_1_r1_out ), .eq(comparator_3_eq));  // open: gt, lt
  and and_8 (and_8_out, \气泡流水接口_id_ex_1_syscall_out , comparator_4_eq);
  Comparator #(.width(32), .mode("twosComplement")) comparator_4 (
    .a(32'h22), .b(\气泡流水接口_id_ex_1_r1_out ), .eq(comparator_4_eq));  // open: gt, lt
  MIPS_ALU mips_alu_1 (
    .X(\气泡流水接口_id_ex_1_r1_out ), .Y(multiplexer_6_out), .AluOP(\气泡流水接口_id_ex_1_aluop_out ), .Equal(equal),
    .Result({mips_alu_1_result, BLEZ_LESS}), .shamt(EX_IR[10:6]));  // open: Result_2
  Register #(.width(32), .trigger("rising"), .Select("low")) register_1 (
    .D(\气泡流水接口_id_ex_1_r2_out ), .en(and_8_out), .Q(LedData), .clk(CLK));  // open: clr
  Multiplexer #(.select(2), .width(32), .disabled("Z"), .enable("false")) multiplexer_7 (
    .in0({pull_resistor_3_node[31:28], EX_IR[25:0], pull_resistor_3_node[1:0]}), .in1(adder_3_out),
    .in2(\气泡流水接口_id_ex_1_r1_out ), .in3(adder_3_out), .out(JMP_EX),
    .sel({\气泡流水接口_id_ex_1_jr_out [1], \条件分支成功 }));
  // Mips_Probe mips_probe_7: pin names not known; wires that end beside it: MEM_IR
  \气泡流水接口_EX_MEM  \u_气泡流水接口_ex_mem_1  (
    .IR_in(EX_IR), .\传输状态In_表明当前传输数据有效 (\气泡流水接口_id_ex_1_传输状态out_表明当前传输数据有效 ), .CLK(CLK), .IR_out(MEM_IR),
    .\传输状态Out_表明当前传输数据有效 (\气泡流水接口_ex_mem_1_传输状态out_表明当前传输数据有效 ), .\使能端_低电平有效_stall_高电平有效 (1'b0),
    .PC_in(EX_PC), .PC_out(M_PC), .MemToReg_in(\气泡流水接口_id_ex_1_memtoreg_out ),
    .MemToReg_out(\气泡流水接口_ex_mem_1_memtoreg_out ), .MemWrite_in(\气泡流水接口_id_ex_1_memwrite_out ),
    .MemWrite_out(MemWrite), .RegWrite_in(EX_RegWrite), .RegWrite_out(MEM_RegWrite),
    .RegDst_in(\气泡流水接口_id_ex_1_regdst_out ), .RegDst_out(\气泡流水接口_ex_mem_1_regdst_out ),
    .AluRst_in({mips_alu_1_result, BLEZ_LESS}), .AluRst_out(\气泡流水接口_ex_mem_1_alurst_out ),
    .Mem_in(\气泡流水接口_id_ex_1_r2_out ), .Mem_out(MDin), .ERET_in(\气泡流水接口_id_ex_1_eret_out ),
    .ERET_out(\气泡流水接口_ex_mem_1_eret_out ), .LBU_in(\气泡流水接口_id_ex_1_lbu_out ),
    .LBU_out(\气泡流水接口_ex_mem_1_lbu_out ), .JAL_in(\气泡流水接口_id_ex_1_jal_out ),
    .JAL_out(\气泡流水接口_ex_mem_1_jal_out ), .RegWrite__in(EX_RegWrite_num), .RegWrite__out(MEM_RegWrite_num));  // open: 同步清零_气泡_高电平有效
  RAM #(.addrWidth(10), .dataWidth(32), .bus("separate"), .Select("high")) ram_1 (
    .addr(\气泡流水接口_ex_mem_1_alurst_out [11:2]), .din(MDin), .data(ram_1_data), .str(MemWrite), .clk(CLK));  // open: sel, ld, clr
  \气泡流水接口_MEM_WB  \u_气泡流水接口_mem_wb_1  (
    .IR_in(MEM_IR), .\传输状态In_表明当前传输数据有效 (\气泡流水接口_ex_mem_1_传输状态out_表明当前传输数据有效 ), .CLK(CLK), .IR_out(WB_IR),
    .\使能端_低电平有效_stall_高电平有效 (1'b0), .PC_in(M_PC), .PC_out(WB_PC), .RegWrite_in(MEM_RegWrite),
    .RegWrite_out(RegWrite), .RegDst_in(\气泡流水接口_ex_mem_1_regdst_out ), .Mem_in(ram_1_data),
    .Mem_out({\气泡流水接口_mem_wb_1_mem_out_4 , \气泡流水接口_mem_wb_1_mem_out_3 , \气泡流水接口_mem_wb_1_mem_out_2 , \气泡流水接口_mem_wb_1_mem_out }),
    .ERET_in(\气泡流水接口_ex_mem_1_eret_out ), .JAL_in(\气泡流水接口_ex_mem_1_jal_out ),
    .JAL_out(\气泡流水接口_mem_wb_1_memtoreg_out [1]), .RegWrite__in(MEM_RegWrite_num),
    .RegWrite__out(WB_RegWrite_num), .MemToReg_in(\气泡流水接口_ex_mem_1_memtoreg_out ),
    .MemToReg_out(\气泡流水接口_mem_wb_1_memtoreg_out [0]), .LBU_in(\气泡流水接口_ex_mem_1_lbu_out ),
    .LBU_out(\气泡流水接口_mem_wb_1_lbu_out ), .AluRst_in(\气泡流水接口_ex_mem_1_alurst_out ),
    .AluRst_out(\气泡流水接口_mem_wb_1_alurst_out ));  // open: 传输状态Out_表明当前传输数据有效, 同步清零_气泡_高电平有效, RegDst_out, ERET_out
  // Mips_Probe mips_probe_8: pin names not known; wires that end beside it: WB_IR
  Pull_Resistor #(.pull(0)) pull_resistor_4 (.node({pull_resistor_4_node, \气泡流水接口_mem_wb_1_mem_out }));
  Pull_Resistor #(.pull(0)) pull_resistor_5 (.node({pull_resistor_5_node, \气泡流水接口_mem_wb_1_mem_out_2 }));
  Pull_Resistor #(.pull(0)) pull_resistor_6 (.node({pull_resistor_6_node, \气泡流水接口_mem_wb_1_mem_out_3 }));
  Pull_Resistor #(.pull(0)) pull_resistor_7 (.node({pull_resistor_7_node, \气泡流水接口_mem_wb_1_mem_out_4 }));
  Multiplexer #(.select(2), .width(32), .disabled("Z"), .enable("false")) multiplexer_8 (
    .in0({pull_resistor_4_node, \气泡流水接口_mem_wb_1_mem_out }),
    .in1({pull_resistor_5_node, \气泡流水接口_mem_wb_1_mem_out_2 }),
    .in2({pull_resistor_6_node, \气泡流水接口_mem_wb_1_mem_out_3 }),
    .in3({pull_resistor_7_node, \气泡流水接口_mem_wb_1_mem_out_4 }), .out(multiplexer_8_out),
    .sel(\气泡流水接口_mem_wb_1_alurst_out [1:0]));
  Multiplexer #(.select(1), .width(32), .disabled("Z"), .enable("false")) multiplexer_9 (
    .in0({\气泡流水接口_mem_wb_1_mem_out_4 , \气泡流水接口_mem_wb_1_mem_out_3 , \气泡流水接口_mem_wb_1_mem_out_2 , \气泡流水接口_mem_wb_1_mem_out }),
    .in1(multiplexer_8_out), .out(multiplexer_9_out), .sel(\气泡流水接口_mem_wb_1_lbu_out ));
  Multiplexer #(.select(2), .width(32), .disabled("Z"), .enable("false")) multiplexer_10 (
    .in0(\气泡流水接口_mem_wb_1_alurst_out ), .in1(multiplexer_9_out), .in2(adder_4_out), .in3(adder_4_out),
    .out(RDin), .sel(\气泡流水接口_mem_wb_1_memtoreg_out ));
  Adder #(.width(32)) adder_4 (.a(WB_PC), .b(32'h4), .out(adder_4_out));  // open: cin, cout

  // Other names for the same wires on the sheet: MEM_PC[31:0] = M_PC; WB_RegWrite = RegWrite

  // Notes on the sheet:
  //   中断源
  //   时空图监测，可删除
  //   中断等待指示
  //   数码管输出
  //   指令存储器
  //   contents of rom_1 (hex, n*v repeats v):
  //   20110001 8000c05 20110001 20120002 20130003 8000c09 20110001 20120002 20130003 8000c0d 20110001
  //   20120002 20130003 8000c11 20110001 20120002 20130003 c000cb8 20100001 20110001 118fc0 112020
  //   20020022 c 118882 12200001 8000c15 112020 20020022 c 20110001 118880 112020 20020022 c 12200001
  //   8000c1f 20110001 118fc0 112020 20020022 c 1188c3 112020 20020022 c 118903 112020 20020022 c 118903
  //   112020 20020022 c 118903 112020 20020022 c 118903 112020 20020022 c 118903 112020 20020022 c 118903
  //   112020 20020022 c 118903 112020 20020022 c 20100001 109fc0 139fc3 8021 2012000c 24160003 26100001
  //   3210000f 20080008 20090001 139900 2709825 132020 20020022 c 1094022 1500fff9 22100001 2018000f
  //   2188024 108700 20080008 20090001 139902 2709825 132021 20020022 c 1094022 1500fff9 108702 2c9b022
  //   12c00001 8000c50 4020 1084027 84400 3508ffff 82021 20020022 c 2010ffff 20110000 ae300000 22100001
  //   22310004 ae300000 22100001 22310004 ae300000 22100001 22310004 ae300000 22100001 22310004 ae300000
  //   22100001 22310004 ae300000 22100001 22310004 ae300000 22100001 22310004 ae300000 22100001 22310004
  //   ae300000 22100001 22310004 ae300000 22100001 22310004 ae300000 22100001 22310004 ae300000 22100001
  //   22310004 ae300000 22100001 22310004 ae300000 22100001 22310004 ae300000 22100001 22310004 ae300000
  //   22100001 22310004 22100001 8020 2011003c 8e130000 8e340000 274402a 11000002 ae330000 ae140000
  //   2231fffc 1611fff8 102020 20020022 c 22100004 2011003c 1611fff2 20020032 c 20100000 22100001 102020
  //   20020022 c 22100002 102020 20020022 c 22100003 102020 20020022 c 22100004 102020 20020022 c 22100005
  //   102020 20020022 c 22100006 102020 20020022 c 22100007 102020 20020022 c 22100008 102020 20020022
  //   20020022 c 3e00008
  //   OP
  //   Func
  //   rs
  //   rt
  //   OP
  //   Func
  //   控制位
  //   流水调试日志用
  //   暂停节拍，不能为0
  //   戳工具置1进入计数暂停模式，ctrl+k时钟自动运行到对应节拍暂停
  //   ctrl+k关闭时钟连续运行，将控制位置零，进入单步调试模式调试
  //   rd
  //   可计数暂停的时钟源
  //   为方便自动评测，需要输出流水线各段保存的PC值，注意是PC不是PC+4，另外ID段寄存器写入信息，Mem段内存写入信息也要输出
endmodule

module \气泡流水线_MIPS_Regifile  (
  input  [31:0] Din,
  input  Clk,
  input  WE,
  input  [4:0] R1_num,
  input  [4:0] W_num,
  input  [4:0] R2_num,
  output [31:0] R1,
  output [31:0] R2
);

  // RegisterFile registerfile_1: pin names not known; wires that end beside it: Din, Clk, WE, W_num, R1_num, R2_num, R1, R2
endmodule
module \源寄存器使用情况  (
  input  OP0,
  input  OP1,
  input  OP2,
  input  OP3,
  input  OP4,
  input  OP5,
  input  F0,
  input  F1,
  input  F2,
  input  F3,
  input  F4,
  input  F5,
  output R1_Used,
  output R2_Used
);

  wire and_1_out, and_2_out, and_3_out, and_4_out, and_5_out, and_6_out, and_7_out, and_8_out, and_9_out,
       and_10_out, and_11_out, and_12_out, and_13_out, and_14_out, and_15_out, and_16_out, and_17_out,
       and_18_out, and_19_out, and_20_out, and_21_out, and_22_out, and_23_out, and_24_out, and_25_out,
       and_26_out, and_27_out, and_28_out, and_29_out, and_30_out, and_31_out, and_32_out, and_33_out,
       and_34_out, and_35_out, and_36_out, and_37_out, and_38_out, and_39_out, and_40_out, not_1_out,
       not_2_out, not_3_out, not_4_out, not_5_out, not_6_out, not_7_out, not_8_out, not_9_out, not_10_out,
       not_11_out, not_12_out, not_13_out, not_14_out, not_15_out, not_16_out, not_17_out, not_18_out,
       not_19_out, not_20_out, not_21_out, not_22_out, not_23_out, not_24_out, not_25_out, not_26_out,
       not_27_out, not_28_out, not_29_out, not_30_out, not_31_out, not_32_out, not_33_out, not_34_out,
       not_35_out, not_36_out, not_37_out, not_38_out, not_39_out, not_40_out, not_41_out, not_42_out,
       not_43_out, not_44_out, not_45_out, not_46_out, not_47_out, not_48_out, not_49_out, not_50_out,
       not_51_out, not_52_out, not_53_out, not_54_out, not_55_out, not_56_out, not_57_out, not_58_out,
       not_59_out, not_60_out, not_61_out, not_62_out, not_63_out, not_64_out, not_65_out, not_66_out,
       not_67_out, not_68_out, not_69_out, not_70_out, not_71_out, not_72_out, not_73_out, not_74_out,
       not_75_out, not_76_out, not_77_out, not_78_out, not_79_out, not_80_out, not_81_out, not_82_out,
       not_83_out, not_84_out, not_85_out, not_86_out, not_87_out, not_88_out, not_89_out, not_90_out,
       not_91_out, not_92_out, not_93_out, not_94_out, not_95_out, not_96_out, not_97_out, not_98_out,
       not_99_out, not_100_out, not_101_out, not_102_out, not_103_out, not_104_out, not_105_out, not_106_out,
       not_107_out, not_108_out, not_109_out, not_110_out, not_111_out, not_112_out, not_113_out,
       not_114_out, not_115_out, not_116_out, not_117_out, not_118_out, not_119_out, not_120_out,
       not_121_out, not_122_out, not_123_out, not_124_out, not_125_out, not_126_out, not_127_out,
       not_128_out, not_129_out, not_130_out, not_131_out, not_132_out, not_133_out, not_134_out,
       not_135_out, not_136_out, not_137_out, not_138_out, not_139_out, not_140_out, not_141_out,
       not_142_out, not_143_out, not_144_out, not_145_out, not_146_out, not_147_out, not_148_out,
       not_149_out, not_150_out, not_151_out, not_152_out, not_153_out, not_154_out, not_155_out,
       not_156_out, not_157_out, not_158_out, not_159_out, not_160_out, not_161_out, not_162_out,
       not_163_out, not_164_out, not_165_out, not_166_out, not_167_out, not_168_out, not_169_out,
       not_170_out, not_171_out, not_172_out, not_173_out, not_174_out, not_175_out, not_176_out,
       not_177_out, not_178_out, not_179_out, not_180_out, not_181_out, not_182_out, not_183_out,
       not_184_out, not_185_out, not_186_out, not_187_out, not_188_out, not_189_out, not_190_out,
       not_191_out, not_192_out, not_193_out, not_194_out, not_195_out, not_196_out, not_197_out,
       not_198_out, not_199_out, not_200_out, not_201_out, not_202_out, not_203_out, not_204_out,
       not_205_out, not_206_out, not_207_out, not_208_out, not_209_out, not_210_out, not_211_out,
       not_212_out, not_213_out, not_214_out, not_215_out, not_216_out, not_217_out, not_218_out,
       not_219_out, not_220_out, not_221_out, not_222_out, not_223_out, not_224_out, not_225_out,
       not_226_out, not_227_out, not_228_out, not_229_out, not_230_out, not_231_out, not_232_out,
       not_233_out, not_234_out, not_235_out, not_236_out, not_237_out, not_238_out, not_239_out,
       not_240_out, not_241_out, not_242_out, not_243_out, not_244_out, not_245_out, not_246_out,
       not_247_out, not_248_out, not_249_out, not_250_out, not_251_out, not_252_out, not_253_out,
       not_254_out, not_255_out, not_256_out, not_257_out, not_258_out, not_259_out, not_260_out,
       not_261_out, not_262_out, not_263_out, not_264_out, not_265_out, not_266_out, not_267_out,
       not_268_out, not_269_out, not_270_out, not_271_out, not_272_out, not_273_out, not_274_out,
       not_275_out, not_276_out, not_277_out, not_278_out, not_279_out, not_280_out, not_281_out,
       not_282_out, not_283_out, not_284_out, not_285_out, not_286_out, not_287_out, not_288_out,
       not_289_out, not_290_out, not_291_out, not_292_out;

  not not_1 (not_1_out, OP5);
  not not_2 (not_2_out, OP4);
  not not_3 (not_3_out, OP3);
  not not_4 (not_4_out, OP2);
  not not_5 (not_5_out, OP1);
  not not_6 (not_6_out, OP0);
  not not_7 (not_7_out, F4);
  not not_8 (not_8_out, F3);
  not not_9 (not_9_out, F2);
  not not_10 (not_10_out, F1);
  not not_11 (not_11_out, F0);
  not not_12 (not_12_out, OP5);
  not not_13 (not_13_out, OP4);
  not not_14 (not_14_out, OP3);
  not not_15 (not_15_out, OP2);
  not not_16 (not_16_out, OP1);
  not not_17 (not_17_out, OP0);
  not not_18 (not_18_out, F4);
  not not_19 (not_19_out, F3);
  not not_20 (not_20_out, F2);
  not not_21 (not_21_out, F1);
  not not_22 (not_22_out, OP5);
  not not_23 (not_23_out, OP4);
  not not_24 (not_24_out, OP3);
  not not_25 (not_25_out, OP2);
  not not_26 (not_26_out, OP1);
  not not_27 (not_27_out, OP0);
  not not_28 (not_28_out, F4);
  not not_29 (not_29_out, F3);
  not not_30 (not_30_out, F2);
  not not_31 (not_31_out, F0);
  not not_32 (not_32_out, OP5);
  not not_33 (not_33_out, OP4);
  not not_34 (not_34_out, OP3);
  not not_35 (not_35_out, OP2);
  not not_36 (not_36_out, OP1);
  not not_37 (not_37_out, OP0);
  not not_38 (not_38_out, F4);
  not not_39 (not_39_out, F3);
  not not_40 (not_40_out, F1);
  not not_41 (not_41_out, F0);
  not not_42 (not_42_out, OP5);
  not not_43 (not_43_out, OP4);
  not not_44 (not_44_out, OP3);
  not not_45 (not_45_out, OP2);
  not not_46 (not_46_out, OP1);
  not not_47 (not_47_out, OP0);
  not not_48 (not_48_out, F4);
  not not_49 (not_49_out, F3);
  not not_50 (not_50_out, F1);
  not not_51 (not_51_out, OP5);
  not not_52 (not_52_out, OP4);
  not not_53 (not_53_out, OP3);
  not not_54 (not_54_out, OP2);
  not not_55 (not_55_out, OP1);
  not not_56 (not_56_out, OP0);
  not not_57 (not_57_out, F4);
  not not_58 (not_58_out, F3);
  not not_59 (not_59_out, OP5);
  not not_60 (not_60_out, OP4);
  not not_61 (not_61_out, OP3);
  not not_62 (not_62_out, OP2);
  not not_63 (not_63_out, OP1);
  not not_64 (not_64_out, OP0);
  not not_65 (not_65_out, F4);
  not not_66 (not_66_out, F2);
  not not_67 (not_67_out, F0);
  not not_68 (not_68_out, OP5);
  not not_69 (not_69_out, OP4);
  not not_70 (not_70_out, OP3);
  not not_71 (not_71_out, OP2);
  not not_72 (not_72_out, OP1);
  not not_73 (not_73_out, OP0);
  not not_74 (not_74_out, F4);
  not not_75 (not_75_out, F2);
  not not_76 (not_76_out, OP5);
  not not_77 (not_77_out, OP4);
  not not_78 (not_78_out, OP3);
  not not_79 (not_79_out, OP2);
  not not_80 (not_80_out, OP1);
  not not_81 (not_81_out, OP0);
  not not_82 (not_82_out, F5);
  not not_83 (not_83_out, F4);
  not not_84 (not_84_out, F2);
  not not_85 (not_85_out, F1);
  not not_86 (not_86_out, F0);
  not not_87 (not_87_out, OP5);
  not not_88 (not_88_out, OP4);
  not not_89 (not_89_out, OP3);
  not not_90 (not_90_out, OP2);
  not not_91 (not_91_out, OP1);
  not not_92 (not_92_out, OP0);
  not not_93 (not_93_out, F5);
  not not_94 (not_94_out, F4);
  not not_95 (not_95_out, F1);
  not not_96 (not_96_out, F0);
  not not_97 (not_97_out, OP5);
  not not_98 (not_98_out, OP4);
  not not_99 (not_99_out, OP3);
  not not_100 (not_100_out, OP1);
  not not_101 (not_101_out, OP0);
  not not_102 (not_102_out, OP5);
  not not_103 (not_103_out, OP4);
  not not_104 (not_104_out, OP3);
  not not_105 (not_105_out, OP1);
  not not_106 (not_106_out, OP5);
  not not_107 (not_107_out, OP4);
  not not_108 (not_108_out, OP2);
  not not_109 (not_109_out, OP1);
  not not_110 (not_110_out, OP0);
  not not_111 (not_111_out, OP5);
  not not_112 (not_112_out, OP4);
  not not_113 (not_113_out, OP1);
  not not_114 (not_114_out, OP0);
  not not_115 (not_115_out, OP5);
  not not_116 (not_116_out, OP4);
  not not_117 (not_117_out, OP2);
  not not_118 (not_118_out, OP1);
  not not_119 (not_119_out, OP5);
  not not_120 (not_120_out, OP4);
  not not_121 (not_121_out, OP2);
  not not_122 (not_122_out, OP0);
  not not_123 (not_123_out, OP5);
  not not_124 (not_124_out, OP4);
  not not_125 (not_125_out, OP1);
  not not_126 (not_126_out, OP4);
  not not_127 (not_127_out, OP3);
  not not_128 (not_128_out, OP2);
  not not_129 (not_129_out, OP4);
  not not_130 (not_130_out, OP2);
  not not_131 (not_131_out, OP5);
  not not_132 (not_132_out, OP4);
  not not_133 (not_133_out, OP3);
  not not_134 (not_134_out, OP2);
  not not_135 (not_135_out, OP1);
  not not_136 (not_136_out, OP0);
  not not_137 (not_137_out, F4);
  not not_138 (not_138_out, F3);
  not not_139 (not_139_out, F0);
  not not_140 (not_140_out, OP5);
  not not_141 (not_141_out, OP4);
  not not_142 (not_142_out, OP2);
  not not_143 (not_143_out, OP4);
  not not_144 (not_144_out, OP3);
  not not_145 (not_145_out, OP1);
  not not_146 (not_146_out, OP0);
  not not_147 (not_147_out, OP5);
  not not_148 (not_148_out, OP4);
  not not_149 (not_149_out, OP3);
  not not_150 (not_150_out, OP0);
  not not_151 (not_151_out, OP5);
  not not_152 (not_152_out, OP4);
  not not_153 (not_153_out, OP3);
  not not_154 (not_154_out, OP2);
  not not_155 (not_155_out, OP1);
  not not_156 (not_156_out, OP0);
  not not_157 (not_157_out, F5);
  not not_158 (not_158_out, F4);
  not not_159 (not_159_out, F3);
  not not_160 (not_160_out, F2);
  not not_161 (not_161_out, F1);
  not not_162 (not_162_out, F0);
  not not_163 (not_163_out, OP5);
  not not_164 (not_164_out, OP4);
  not not_165 (not_165_out, OP3);
  not not_166 (not_166_out, OP2);
  not not_167 (not_167_out, OP1);
  not not_168 (not_168_out, OP0);
  not not_169 (not_169_out, F5);
  not not_170 (not_170_out, F4);
  not not_171 (not_171_out, F3);
  not not_172 (not_172_out, F2);
  not not_173 (not_173_out, OP5);
  not not_174 (not_174_out, OP4);
  not not_175 (not_175_out, OP3);
  not not_176 (not_176_out, OP2);
  not not_177 (not_177_out, OP1);
  not not_178 (not_178_out, OP0);
  not not_179 (not_179_out, F5);
  not not_180 (not_180_out, F4);
  not not_181 (not_181_out, F3);
  not not_182 (not_182_out, F2);
  not not_183 (not_183_out, F0);
  not not_184 (not_184_out, OP5);
  not not_185 (not_185_out, OP4);
  not not_186 (not_186_out, OP3);
  not not_187 (not_187_out, OP2);
  not not_188 (not_188_out, OP1);
  not not_189 (not_189_out, OP0);
  not not_190 (not_190_out, F4);
  not not_191 (not_191_out, F3);
  not not_192 (not_192_out, F2);
  not not_193 (not_193_out, F1);
  not not_194 (not_194_out, F0);
  not not_195 (not_195_out, OP5);
  not not_196 (not_196_out, OP4);
  not not_197 (not_197_out, OP3);
  not not_198 (not_198_out, OP2);
  not not_199 (not_199_out, OP1);
  not not_200 (not_200_out, OP0);
  not not_201 (not_201_out, F4);
  not not_202 (not_202_out, F3);
  not not_203 (not_203_out, F2);
  not not_204 (not_204_out, F1);
  not not_205 (not_205_out, OP5);
  not not_206 (not_206_out, OP4);
  not not_207 (not_207_out, OP3);
  not not_208 (not_208_out, OP2);
  not not_209 (not_209_out, OP1);
  not not_210 (not_210_out, OP0);
  not not_211 (not_211_out, F4);
  not not_212 (not_212_out, F3);
  not not_213 (not_213_out, F2);
  not not_214 (not_214_out, F0);
  not not_215 (not_215_out, OP5);
  not not_216 (not_216_out, OP4);
  not not_217 (not_217_out, OP3);
  not not_218 (not_218_out, OP2);
  not not_219 (not_219_out, OP1);
  not not_220 (not_220_out, OP0);
  not not_221 (not_221_out, F4);
  not not_222 (not_222_out, F3);
  not not_223 (not_223_out, F1);
  not not_224 (not_224_out, F0);
  not not_225 (not_225_out, OP5);
  not not_226 (not_226_out, OP4);
  not not_227 (not_227_out, OP3);
  not not_228 (not_228_out, OP2);
  not not_229 (not_229_out, OP1);
  not not_230 (not_230_out, OP0);
  not not_231 (not_231_out, F4);
  not not_232 (not_232_out, F3);
  not not_233 (not_233_out, F1);
  not not_234 (not_234_out, OP5);
  not not_235 (not_235_out, OP4);
  not not_236 (not_236_out, OP3);
  not not_237 (not_237_out, OP2);
  not not_238 (not_238_out, OP1);
  not not_239 (not_239_out, OP0);
  not not_240 (not_240_out, F4);
  not not_241 (not_241_out, F3);
  not not_242 (not_242_out, OP5);
  not not_243 (not_243_out, OP4);
  not not_244 (not_244_out, OP3);
  not not_245 (not_245_out, OP2);
  not not_246 (not_246_out, OP1);
  not not_247 (not_247_out, OP0);
  not not_248 (not_248_out, F4);
  not not_249 (not_249_out, F2);
  not not_250 (not_250_out, F0);
  not not_251 (not_251_out, OP5);
  not not_252 (not_252_out, OP4);
  not not_253 (not_253_out, OP3);
  not not_254 (not_254_out, OP2);
  not not_255 (not_255_out, OP1);
  not not_256 (not_256_out, OP0);
  not not_257 (not_257_out, F4);
  not not_258 (not_258_out, F2);
  not not_259 (not_259_out, OP5);
  not not_260 (not_260_out, OP4);
  not not_261 (not_261_out, OP3);
  not not_262 (not_262_out, OP2);
  not not_263 (not_263_out, OP1);
  not not_264 (not_264_out, OP0);
  not not_265 (not_265_out, F5);
  not not_266 (not_266_out, F4);
  not not_267 (not_267_out, F1);
  not not_268 (not_268_out, F0);
  not not_269 (not_269_out, OP5);
  not not_270 (not_270_out, OP4);
  not not_271 (not_271_out, OP3);
  not not_272 (not_272_out, OP1);
  not not_273 (not_273_out, OP0);
  not not_274 (not_274_out, OP5);
  not not_275 (not_275_out, OP4);
  not not_276 (not_276_out, OP3);
  not not_277 (not_277_out, OP1);
  not not_278 (not_278_out, OP4);
  not not_279 (not_279_out, OP2);
  not not_280 (not_280_out, OP5);
  not not_281 (not_281_out, OP4);
  not not_282 (not_282_out, OP3);
  not not_283 (not_283_out, OP2);
  not not_284 (not_284_out, OP1);
  not not_285 (not_285_out, OP0);
  not not_286 (not_286_out, F4);
  not not_287 (not_287_out, F3);
  not not_288 (not_288_out, F0);
  not not_289 (not_289_out, OP5);
  not not_290 (not_290_out, OP4);
  not not_291 (not_291_out, OP3);
  not not_292 (not_292_out, OP0);
  and and_1 (and_1_out, not_1_out, not_2_out, not_3_out, not_4_out, not_5_out, not_6_out, F5, not_7_out, not_8_out, not_9_out, not_10_out, not_11_out);
  and and_2 (and_2_out, not_12_out, not_13_out, not_14_out, not_15_out, not_16_out, not_17_out, F5, not_18_out, not_19_out, not_20_out, not_21_out, F0);
  and and_3 (and_3_out, not_22_out, not_23_out, not_24_out, not_25_out, not_26_out, not_27_out, F5, not_28_out, not_29_out, not_30_out, F1, not_31_out);
  and and_4 (and_4_out, not_32_out, not_33_out, not_34_out, not_35_out, not_36_out, not_37_out, F5, not_38_out, not_39_out, F2, not_40_out, not_41_out);
  and and_5 (and_5_out, not_42_out, not_43_out, not_44_out, not_45_out, not_46_out, not_47_out, F5, not_48_out, not_49_out, F2, not_50_out, F0);
  and and_6 (and_6_out, not_51_out, not_52_out, not_53_out, not_54_out, not_55_out, not_56_out, F5, not_57_out, not_58_out, F2, F1, F0);
  and and_7 (and_7_out, not_59_out, not_60_out, not_61_out, not_62_out, not_63_out, not_64_out, F5, not_65_out, F3, not_66_out, F1, not_67_out);
  and and_8 (and_8_out, not_68_out, not_69_out, not_70_out, not_71_out, not_72_out, not_73_out, F5, not_74_out, F3, not_75_out, F1, F0);
  and and_9 (and_9_out, not_76_out, not_77_out, not_78_out, not_79_out, not_80_out, not_81_out, not_82_out, not_83_out, F3, not_84_out, not_85_out, not_86_out);
  and and_10 (and_10_out, not_87_out, not_88_out, not_89_out, not_90_out, not_91_out, not_92_out, not_93_out, not_94_out, F3, F2, not_95_out, not_96_out);
  and and_11 (and_11_out, not_97_out, not_98_out, not_99_out, OP2, not_100_out, not_101_out);
  and and_12 (and_12_out, not_102_out, not_103_out, not_104_out, OP2, not_105_out, OP0);
  and and_13 (and_13_out, not_106_out, not_107_out, OP3, not_108_out, not_109_out, not_110_out);
  and and_14 (and_14_out, not_111_out, not_112_out, OP3, OP2, not_113_out, not_114_out);
  and and_15 (and_15_out, not_115_out, not_116_out, OP3, not_117_out, not_118_out, OP0);
  and and_16 (and_16_out, not_119_out, not_120_out, OP3, not_121_out, OP1, not_122_out);
  and and_17 (and_17_out, not_123_out, not_124_out, OP3, OP2, not_125_out, OP0);
  and and_18 (and_18_out, OP5, not_126_out, not_127_out, not_128_out, OP1, OP0);
  and and_19 (and_19_out, OP5, not_129_out, OP3, not_130_out, OP1, OP0);
  and and_20 (and_20_out, not_131_out, not_132_out, not_133_out, not_134_out, not_135_out, not_136_out, F5, not_137_out, not_138_out, F2, F1, not_139_out);
  and and_21 (and_21_out, not_140_out, not_141_out, OP3, not_142_out, OP1, OP0);
  and and_22 (and_22_out, OP5, not_143_out, not_144_out, OP2, not_145_out, not_146_out);
  and and_23 (and_23_out, not_147_out, not_148_out, not_149_out, OP2, OP1, not_150_out);
  and and_24 (and_24_out, not_151_out, not_152_out, not_153_out, not_154_out, not_155_out, not_156_out, not_157_out, not_158_out, not_159_out, not_160_out, not_161_out, not_162_out);
  and and_25 (and_25_out, not_163_out, not_164_out, not_165_out, not_166_out, not_167_out, not_168_out, not_169_out, not_170_out, not_171_out, not_172_out, F1, F0);
  and and_26 (and_26_out, not_173_out, not_174_out, not_175_out, not_176_out, not_177_out, not_178_out, not_179_out, not_180_out, not_181_out, not_182_out, F1, not_183_out);
  and and_27 (and_27_out, not_184_out, not_185_out, not_186_out, not_187_out, not_188_out, not_189_out, F5, not_190_out, not_191_out, not_192_out, not_193_out, not_194_out);
  and and_28 (and_28_out, not_195_out, not_196_out, not_197_out, not_198_out, not_199_out, not_200_out, F5, not_201_out, not_202_out, not_203_out, not_204_out, F0);
  and and_29 (and_29_out, not_205_out, not_206_out, not_207_out, not_208_out, not_209_out, not_210_out, F5, not_211_out, not_212_out, not_213_out, F1, not_214_out);
  and and_30 (and_30_out, not_215_out, not_216_out, not_217_out, not_218_out, not_219_out, not_220_out, F5, not_221_out, not_222_out, F2, not_223_out, not_224_out);
  and and_31 (and_31_out, not_225_out, not_226_out, not_227_out, not_228_out, not_229_out, not_230_out, F5, not_231_out, not_232_out, F2, not_233_out, F0);
  and and_32 (and_32_out, not_234_out, not_235_out, not_236_out, not_237_out, not_238_out, not_239_out, F5, not_240_out, not_241_out, F2, F1, F0);
  and and_33 (and_33_out, not_242_out, not_243_out, not_244_out, not_245_out, not_246_out, not_247_out, F5, not_248_out, F3, not_249_out, F1, not_250_out);
  and and_34 (and_34_out, not_251_out, not_252_out, not_253_out, not_254_out, not_255_out, not_256_out, F5, not_257_out, F3, not_258_out, F1, F0);
  and and_35 (and_35_out, not_259_out, not_260_out, not_261_out, not_262_out, not_263_out, not_264_out, not_265_out, not_266_out, F3, F2, not_267_out, not_268_out);
  and and_36 (and_36_out, not_269_out, not_270_out, not_271_out, OP2, not_272_out, not_273_out);
  and and_37 (and_37_out, not_274_out, not_275_out, not_276_out, OP2, not_277_out, OP0);
  and and_38 (and_38_out, OP5, not_278_out, OP3, not_279_out, OP1, OP0);
  and and_39 (and_39_out, not_280_out, not_281_out, not_282_out, not_283_out, not_284_out, not_285_out, F5, not_286_out, not_287_out, F2, F1, not_288_out);
  and and_40 (and_40_out, not_289_out, not_290_out, not_291_out, OP2, OP1, not_292_out);
  or or_1 (R1_Used, and_1_out, and_2_out, and_3_out, and_4_out, and_5_out, and_6_out, and_7_out, and_8_out, and_9_out, and_10_out, and_11_out, and_12_out, and_13_out, and_14_out, and_15_out, and_16_out, and_17_out, and_18_out, and_19_out, and_20_out, and_21_out, and_22_out, and_23_out);
  or or_2 (R2_Used, and_24_out, and_25_out, and_26_out, and_27_out, and_28_out, and_29_out, and_30_out, and_31_out, and_32_out, and_33_out, and_34_out, and_35_out, and_36_out, and_37_out, and_38_out, and_39_out, and_40_out);
endmodule

module \数据相关检测  (
  input  [4:0] R1_num,
  input  [4:0] R2_num,
  input  R1_Used,
  input  R2_Used,
  input  [4:0] EX_WriteReg_num,
  input  EX_RegWrite,
  input  [4:0] MEM_WriteReg_num,
  input  [4:0] WB_WriteReg_num,
  input  MEM_RegWrite,
  input  WB_RegWrite,
  output \数据相关 
);

  wire comparator_1_eq, comparator_3_eq, comparator_5_eq, comparator_6_eq, or_1_out, or_3_out,
       pull_resistor_2_node, pull_resistor_4_node;
  wire [4:0] \数据相关条件_1_out_3 , \数据相关条件_2_out_3 , \数据相关条件_3_out_3 , \数据相关条件_4_out_3 , \数据相关条件_5_out_3 ;

  \数据相关条件  \u_数据相关条件_1  (.R(EX_RegWrite), .R_num(EX_WriteReg_num), .out_3(\数据相关条件_1_out_3 ));
  \数据相关条件  \u_数据相关条件_2  (.R(MEM_RegWrite), .R_num(MEM_WriteReg_num), .out_3(\数据相关条件_2_out_3 ));
  \数据相关条件  \u_数据相关条件_3  (.R(R1_Used), .R_num(R1_num), .out_3(\数据相关条件_3_out_3 ));
  Comparator #(.width(5), .mode("twosComplement")) comparator_1 (
    .a(\数据相关条件_3_out_3 ), .b(\数据相关条件_1_out_3 ), .eq(comparator_1_eq));  // open: gt, lt
  Pull_Resistor #(.pull(0)) pull_resistor_1 (.node(comparator_1_eq));
  Pull_Resistor #(.pull(0)) pull_resistor_2 (.node(pull_resistor_2_node));
  Comparator #(.width(5), .mode("twosComplement")) comparator_2 (
    .a(\数据相关条件_3_out_3 ), .b(\数据相关条件_2_out_3 ), .eq(pull_resistor_2_node));  // open: gt, lt
  or or_1 (or_1_out, pull_resistor_2_node, comparator_1_eq);
  \数据相关条件  \u_数据相关条件_4  (.R(R2_Used), .R_num(R2_num), .out_3(\数据相关条件_4_out_3 ));
  or or_2 (\数据相关 , or_1_out, or_3_out);
  Comparator #(.width(5), .mode("twosComplement")) comparator_3 (
    .a(\数据相关条件_4_out_3 ), .b(\数据相关条件_1_out_3 ), .eq(comparator_3_eq));  // open: gt, lt
  Pull_Resistor #(.pull(0)) pull_resistor_3 (.node(comparator_3_eq));
  Pull_Resistor #(.pull(0)) pull_resistor_4 (.node(pull_resistor_4_node));
  Comparator #(.width(5), .mode("twosComplement")) comparator_4 (
    .a(\数据相关条件_4_out_3 ), .b(\数据相关条件_2_out_3 ), .eq(pull_resistor_4_node));  // open: gt, lt
  or or_3 (or_3_out, pull_resistor_4_node, comparator_3_eq);
  \数据相关条件  \u_数据相关条件_5  (.R(WB_RegWrite), .R_num(WB_WriteReg_num), .out_3(\数据相关条件_5_out_3 ));
  Comparator #(.width(5), .mode("twosComplement")) comparator_5 (
    .b(\数据相关条件_5_out_3 ), .eq(comparator_5_eq));  // open: a, gt, lt
  Pull_Resistor #(.pull(0)) pull_resistor_5 (.node(comparator_5_eq));
  Comparator #(.width(5), .mode("twosComplement")) comparator_6 (
    .b(\数据相关条件_5_out_3 ), .eq(comparator_6_eq));  // open: a, gt, lt
  Pull_Resistor #(.pull(0)) pull_resistor_6 (.node(comparator_6_eq));
endmodule

module \数据相关条件  (
  input  [4:0] R_num,
  input  R,
  output [4:0] out_3
);

  wire and_1_out, comparator_1_eq;

  and and_1 (and_1_out, R, ~comparator_1_eq);  // AND_Gate
  assign out_3 = and_1_out ? R_num : 5'bz;  // Controlled_Buffer controlled_buffer_1
  Comparator #(.width(5), .mode("twosComplement")) comparator_1 (
    .a(R_num), .b({5{1'b0}}), .eq(comparator_1_eq));  // open: gt, lt
endmodule

module \气泡流水接口_IF_ID  (
  input  [31:0] IR_in,
  input  [31:0] PC_in,
  input  \传输状态In_表明当前传输数据有效 ,
  input  CLK,
  input  \同步清零_气泡_高电平有效 ,
  input  \使能端_低电平有效_stall_高电平有效 ,
  output [31:0] IR_out,
  output [31:0] PC_out,
  output \传输状态Out_表明当前传输数据有效 
);

  wire multiplexer_3_out, pull_resistor_2_node;
  wire [31:0] multiplexer_1_out, multiplexer_2_out;

  Multiplexer #(.select(1), .width(32), .disabled("Z"), .enable("false")) multiplexer_1 (
    .in0(IR_in), .in1({32{1'b0}}), .out(multiplexer_1_out), .sel(\同步清零_气泡_高电平有效 ));
  Multiplexer #(.select(1), .width(32), .disabled("Z"), .enable("false")) multiplexer_2 (
    .in0(PC_in), .in1({32{1'b0}}), .out(multiplexer_2_out), .sel(\同步清零_气泡_高电平有效 ));
  Multiplexer #(.select(1), .width(1), .disabled("Z"), .enable("false")) multiplexer_3 (
    .in0(\传输状态In_表明当前传输数据有效 ), .in1(1'b0), .out(multiplexer_3_out), .sel(\同步清零_气泡_高电平有效 ));
  Pull_Resistor #(.pull(0)) pull_resistor_1 (.node(\同步清零_气泡_高电平有效 ));
  Register #(.width(32), .trigger("rising"), .Select("low")) register_1 (
    .D(multiplexer_1_out), .en(pull_resistor_2_node), .Q(IR_out), .clk(CLK));  // open: clr
  Register #(.width(32), .trigger("rising"), .Select("low")) register_2 (
    .D(multiplexer_2_out), .en(pull_resistor_2_node), .Q(PC_out), .clk(CLK));  // open: clr
  Register #(.width(1), .trigger("rising"), .Select("low")) register_3 (
    .D(multiplexer_3_out), .en(pull_resistor_2_node), .Q(\传输状态Out_表明当前传输数据有效 ), .clk(CLK));  // open: clr
  Pull_Resistor #(.pull(0)) pull_resistor_2 (.node(pull_resistor_2_node));
  not not_1 (pull_resistor_2_node, \使能端_低电平有效_stall_高电平有效 );
endmodule

module \气泡流水接口_ID_EX  (
  input  [31:0] IR_in,
  input  [31:0] PC_in,
  input  JMP_in,
  input  Beq_in,
  input  JR_in,
  input  Bne_in,
  input  SignedExt_in,
  input  MemToReg_in,
  input  ERET_in,
  input  MemWrite_in,
  input  LBU_in,
  input  [3:0] AluOp_in,
  input  BLEZ_in,
  input  AluSrcB_in,
  input  RegWrite_in,
  input  JAL_in,
  input  RegDst_in,
  input  Syscall_in,
  input  [4:0] RegWrite__in,
  input  [1:0] R1Forward_in,
  input  [1:0] R2Forward_in,
  input  [31:0] R1_in,
  input  [31:0] R2_in,
  input  [31:0] Imm__in,
  input  MFC0_in,
  input  MTC0_in,
  input  \传输状态In_表明当前传输数据有效 ,
  input  CLK,
  input  \同步清零_气泡_高电平有效 ,
  input  \使能端_低电平有效_stall_高电平有效 ,
  output [31:0] IR_out,
  output [31:0] PC_out,
  output JMP_out,
  output Beq_out,
  output JR_out,
  output Bne_out,
  output SignedExt_out,
  output MemToReg_out,
  output ERET_out,
  output MemWrite_out,
  output LBU_out,
  output [3:0] AluOp_out,
  output BLEZ_out,
  output AluSrcB_out,
  output RegWrite_out,
  output JAL_out,
  output RegDst_out,
  output Syscall_out,
  output [4:0] RegWrite__out,
  output [1:0] R1Forward_out,
  output [1:0] R2Forward_out,
  output [31:0] R1_out,
  output [31:0] R2_out,
  output [31:0] Imm_out,
  output MFC0_out,
  output MTC0_out,
  output \传输状态Out_表明当前传输数据有效 
);

  wire multiplexer_3_out, multiplexer_4_out, multiplexer_5_out, multiplexer_6_out, multiplexer_7_out,
       multiplexer_8_out, multiplexer_9_out, multiplexer_10_out, multiplexer_11_out, multiplexer_13_out,
       multiplexer_14_out, multiplexer_15_out, multiplexer_16_out, multiplexer_17_out, multiplexer_18_out,
       multiplexer_25_out, multiplexer_26_out, multiplexer_27_out, pull_resistor_2_node;
  wire [1:0] multiplexer_20_out, multiplexer_21_out;
  wire [3:0] multiplexer_12_out;
  wire [4:0] multiplexer_19_out;
  wire [31:0] multiplexer_1_out, multiplexer_2_out, multiplexer_22_out, multiplexer_23_out,
       multiplexer_24_out;

  Multiplexer #(.select(1), .width(32), .disabled("Z"), .enable("false")) multiplexer_1 (
    .in0(IR_in), .in1({32{1'b0}}), .out(multiplexer_1_out), .sel(\同步清零_气泡_高电平有效 ));
  Multiplexer #(.select(1), .width(32), .disabled("Z"), .enable("false")) multiplexer_2 (
    .in0(PC_in), .in1({32{1'b0}}), .out(multiplexer_2_out), .sel(\同步清零_气泡_高电平有效 ));
  Multiplexer #(.select(1), .width(1), .disabled("Z"), .enable("false")) multiplexer_3 (
    .in0(JMP_in), .in1(1'b0), .out(multiplexer_3_out), .sel(\同步清零_气泡_高电平有效 ));
  Multiplexer #(.select(1), .width(1), .disabled("Z"), .enable("false")) multiplexer_4 (
    .in0(Beq_in), .in1(1'b0), .out(multiplexer_4_out), .sel(\同步清零_气泡_高电平有效 ));
  Multiplexer #(.select(1), .width(1), .disabled("Z"), .enable("false")) multiplexer_5 (
    .in0(JR_in), .in1(1'b0), .out(multiplexer_5_out), .sel(\同步清零_气泡_高电平有效 ));
  Multiplexer #(.select(1), .width(1), .disabled("Z"), .enable("false")) multiplexer_6 (
    .in0(Bne_in), .in1(1'b0), .out(multiplexer_6_out), .sel(\同步清零_气泡_高电平有效 ));
  Multiplexer #(.select(1), .width(1), .disabled("Z"), .enable("false")) multiplexer_7 (
    .in0(SignedExt_in), .in1(1'b0), .out(multiplexer_7_out), .sel(\同步清零_气泡_高电平有效 ));
  Multiplexer #(.select(1), .width(1), .disabled("Z"), .enable("false")) multiplexer_8 (
    .in0(MemToReg_in), .in1(1'b0), .out(multiplexer_8_out), .sel(\同步清零_气泡_高电平有效 ));
  Multiplexer #(.select(1), .width(1), .disabled("Z"), .enable("false")) multiplexer_9 (
    .in0(ERET_in), .in1(1'b0), .out(multiplexer_9_out), .sel(\同步清零_气泡_高电平有效 ));
  Multiplexer #(.select(1), .width(1), .disabled("Z"), .enable("false")) multiplexer_10 (
    .in0(MemWrite_in), .in1(1'b0), .out(multiplexer_10_out), .sel(\同步清零_气泡_高电平有效 ));
  Multiplexer #(.select(1), .width(1), .disabled("Z"), .enable("false")) multiplexer_11 (
    .in0(LBU_in), .in1(1'b0), .out(multiplexer_11_out), .sel(\同步清零_气泡_高电平有效 ));
  Multiplexer #(.select(1), .width(4), .disabled("Z"), .enable("false")) multiplexer_12 (
    .in0(AluOp_in), .in1(4'b0000), .out(multiplexer_12_out), .sel(\同步清零_气泡_高电平有效 ));
  Multiplexer #(.select(1), .width(1), .disabled("Z"), .enable("false")) multiplexer_13 (
    .in0(BLEZ_in), .in1(1'b0), .out(multiplexer_13_out), .sel(\同步清零_气泡_高电平有效 ));
  Multiplexer #(.select(1), .width(1), .disabled("Z"), .enable("false")) multiplexer_14 (
    .in0(AluSrcB_in), .in1(1'b0), .out(multiplexer_14_out), .sel(\同步清零_气泡_高电平有效 ));
  Multiplexer #(.select(1), .width(1), .disabled("Z"), .enable("false")) multiplexer_15 (
    .in0(RegWrite_in), .in1(1'b0), .out(multiplexer_15_out), .sel(\同步清零_气泡_高电平有效 ));
  Multiplexer #(.select(1), .width(1), .disabled("Z"), .enable("false")) multiplexer_16 (
    .in0(JAL_in), .in1(1'b0), .out(multiplexer_16_out), .sel(\同步清零_气泡_高电平有效 ));
  Multiplexer #(.select(1), .width(1), .disabled("Z"), .enable("false")) multiplexer_17 (
    .in0(RegDst_in), .in1(1'b0), .out(multiplexer_17_out), .sel(\同步清零_气泡_高电平有效 ));
  Multiplexer #(.select(1), .width(1), .disabled("Z"), .enable("false")) multiplexer_18 (
    .in0(Syscall_in), .in1(1'b0), .out(multiplexer_18_out), .sel(\同步清零_气泡_高电平有效 ));
  Multiplexer #(.select(1), .width(5), .disabled("Z"), .enable("false")) multiplexer_19 (
    .in0(RegWrite__in), .in1({5{1'b0}}), .out(multiplexer_19_out), .sel(\同步清零_气泡_高电平有效 ));
  Multiplexer #(.select(1), .width(2), .disabled("Z"), .enable("false")) multiplexer_20 (
    .in0(R1Forward_in), .in1(2'b00), .out(multiplexer_20_out), .sel(\同步清零_气泡_高电平有效 ));
  Multiplexer #(.select(1), .width(2), .disabled("Z"), .enable("false")) multiplexer_21 (
    .in0(R2Forward_in), .in1(2'b00), .out(multiplexer_21_out), .sel(\同步清零_气泡_高电平有效 ));
  Multiplexer #(.select(1), .width(32), .disabled("Z"), .enable("false")) multiplexer_22 (
    .in0(R1_in), .in1({32{1'b0}}), .out(multiplexer_22_out), .sel(\同步清零_气泡_高电平有效 ));
  Multiplexer #(.select(1), .width(32), .disabled("Z"), .enable("false")) multiplexer_23 (
    .in0(R2_in), .in1({32{1'b0}}), .out(multiplexer_23_out), .sel(\同步清零_气泡_高电平有效 ));
  Multiplexer #(.select(1), .width(32), .disabled("Z"), .enable("false")) multiplexer_24 (
    .in0(Imm__in), .in1({32{1'b0}}), .out(multiplexer_24_out), .sel(\同步清零_气泡_高电平有效 ));
  Multiplexer #(.select(1), .width(1), .disabled("Z"), .enable("false")) multiplexer_25 (
    .in0(MFC0_in), .in1(1'b0), .out(multiplexer_25_out), .sel(\同步清零_气泡_高电平有效 ));
  Multiplexer #(.select(1), .width(1), .disabled("Z"), .enable("false")) multiplexer_26 (
    .in0(MTC0_in), .in1(1'b0), .out(multiplexer_26_out), .sel(\同步清零_气泡_高电平有效 ));
  Multiplexer #(.select(1), .width(1), .disabled("Z"), .enable("false")) multiplexer_27 (
    .in0(\传输状态In_表明当前传输数据有效 ), .in1(1'b0), .out(multiplexer_27_out), .sel(\同步清零_气泡_高电平有效 ));
  Pull_Resistor #(.pull(0)) pull_resistor_1 (.node(\同步清零_气泡_高电平有效 ));
  Register #(.width(32), .trigger("rising"), .Select("low")) register_1 (
    .D(multiplexer_1_out), .en(pull_resistor_2_node), .Q(IR_out), .clk(CLK));  // open: clr
  Register #(.width(32), .trigger("rising"), .Select("low")) register_2 (
    .D(multiplexer_2_out), .en(pull_resistor_2_node), .Q(PC_out), .clk(CLK));  // open: clr
  Register #(.width(1), .trigger("rising"), .Select("low")) register_3 (
    .D(multiplexer_3_out), .en(pull_resistor_2_node), .Q(JMP_out), .clk(CLK));  // open: clr
  Register #(.width(1), .trigger("rising"), .Select("low")) register_4 (
    .D(multiplexer_4_out), .en(pull_resistor_2_node), .Q(Beq_out), .clk(CLK));  // open: clr
  Register #(.width(1), .trigger("rising"), .Select("low")) register_5 (
    .D(multiplexer_5_out), .en(pull_resistor_2_node), .Q(JR_out), .clk(CLK));  // open: clr
  Register #(.width(1), .trigger("rising"), .Select("low")) register_6 (
    .D(multiplexer_6_out), .en(pull_resistor_2_node), .Q(Bne_out), .clk(CLK));  // open: clr
  Register #(.width(1), .trigger("rising"), .Select("low")) register_7 (
    .D(multiplexer_7_out), .en(pull_resistor_2_node), .Q(SignedExt_out), .clk(CLK));  // open: clr
  Register #(.width(1), .trigger("rising"), .Select("low")) register_8 (
    .D(multiplexer_8_out), .en(pull_resistor_2_node), .Q(MemToReg_out), .clk(CLK));  // open: clr
  Register #(.width(1), .trigger("rising"), .Select("low")) register_9 (
    .D(multiplexer_9_out), .en(pull_resistor_2_node), .Q(ERET_out), .clk(CLK));  // open: clr
  Register #(.width(1), .trigger("rising"), .Select("low")) register_10 (
    .D(multiplexer_10_out), .en(pull_resistor_2_node), .Q(MemWrite_out), .clk(CLK));  // open: clr
  Register #(.width(1), .trigger("rising"), .Select("low")) register_11 (
    .D(multiplexer_11_out), .en(pull_resistor_2_node), .Q(LBU_out), .clk(CLK));  // open: clr
  Register #(.width(4), .trigger("rising"), .Select("low")) register_12 (
    .D(multiplexer_12_out), .en(pull_resistor_2_node), .Q(AluOp_out), .clk(CLK));  // open: clr
  Register #(.width(1), .trigger("rising"), .Select("low")) register_13 (
    .D(multiplexer_13_out), .en(pull_resistor_2_node), .Q(BLEZ_out), .clk(CLK));  // open: clr
  Register #(.width(1), .trigger("rising"), .Select("low")) register_14 (
    .D(multiplexer_14_out), .en(pull_resistor_2_node), .Q(AluSrcB_out), .clk(CLK));  // open: clr
  Register #(.width(1), .trigger("rising"), .Select("low")) register_15 (
    .D(multiplexer_15_out), .en(pull_resistor_2_node), .Q(RegWrite_out), .clk(CLK));  // open: clr
  Register #(.width(1), .trigger("rising"), .Select("low")) register_16 (
    .D(multiplexer_16_out), .en(pull_resistor_2_node), .Q(JAL_out), .clk(CLK));  // open: clr
  Register #(.width(1), .trigger("rising"), .Select("low")) register_17 (
    .D(multiplexer_17_out), .en(pull_resistor_2_node), .Q(RegDst_out), .clk(CLK));  // open: clr
  Register #(.width(1), .trigger("rising"), .Select("low")) register_18 (
    .D(multiplexer_18_out), .en(pull_resistor_2_node), .Q(Syscall_out), .clk(CLK));  // open: clr
  Register #(.width(5), .trigger("rising"), .Select("low")) register_19 (
    .D(multiplexer_19_out), .en(pull_resistor_2_node), .Q(RegWrite__out), .clk(CLK));  // open: clr
  Register #(.width(2), .trigger("rising"), .Select("low")) register_20 (
    .D(multiplexer_20_out), .en(pull_resistor_2_node), .Q(R1Forward_out), .clk(CLK));  // open: clr
  Register #(.width(2), .trigger("rising"), .Select("low")) register_21 (
    .D(multiplexer_21_out), .en(pull_resistor_2_node), .Q(R2Forward_out), .clk(CLK));  // open: clr
  Register #(.width(32), .trigger("rising"), .Select("low")) register_22 (
    .D(multiplexer_22_out), .en(pull_resistor_2_node), .Q(R1_out), .clk(CLK));  // open: clr
  Register #(.width(32), .trigger("rising"), .Select("low")) register_23 (
    .D(multiplexer_23_out), .en(pull_resistor_2_node), .Q(R2_out), .clk(CLK));  // open: clr
  Register #(.width(32), .trigger("rising"), .Select("low")) register_24 (
    .D(multiplexer_24_out), .en(pull_resistor_2_node), .Q(Imm_out), .clk(CLK));  // open: clr
  Register #(.width(1), .trigger("rising"), .Select("low")) register_25 (
    .D(multiplexer_25_out), .en(pull_resistor_2_node), .Q(MFC0_out), .clk(CLK));  // open: clr
  Register #(.width(1), .trigger("rising"), .Select("low")) register_26 (
    .D(multiplexer_26_out), .en(pull_resistor_2_node), .Q(MTC0_out), .clk(CLK));  // open: clr
  Register #(.width(1), .trigger("rising"), .Select("low")) register_27 (
    .D(multiplexer_27_out), .en(pull_resistor_2_node), .Q(\传输状态Out_表明当前传输数据有效 ), .clk(CLK));  // open: clr
  Pull_Resistor #(.pull(0)) pull_resistor_2 (.node(pull_resistor_2_node));
  not not_1 (pull_resistor_2_node, \使能端_低电平有效_stall_高电平有效 );
endmodule

module \气泡流水接口_EX_MEM  (
  input  [31:0] IR_in,
  input  [31:0] PC_in,
  input  MemToReg_in,
  input  ERET_in,
  input  MemWrite_in,
  input  LBU_in,
  input  RegWrite_in,
  input  JAL_in,
  input  RegDst_in,
  input  [4:0] RegWrite__in,
  input  [31:0] AluRst_in,
  input  [31:0] Mem_in,
  input  \传输状态In_表明当前传输数据有效 ,
  input  CLK,
  input  \同步清零_气泡_高电平有效 ,
  input  \使能端_低电平有效_stall_高电平有效 ,
  output [31:0] IR_out,
  output [31:0] PC_out,
  output MemToReg_out,
  output ERET_out,
  output MemWrite_out,
  output LBU_out,
  output RegWrite_out,
  output JAL_out,
  output RegDst_out,
  output [4:0] RegWrite__out,
  output [31:0] AluRst_out,
  output [31:0] Mem_out,
  output \传输状态Out_表明当前传输数据有效 
);

  wire multiplexer_3_out, multiplexer_4_out, multiplexer_5_out, multiplexer_6_out, multiplexer_7_out,
       multiplexer_8_out, multiplexer_9_out, multiplexer_13_out, pull_resistor_2_node;
  wire [4:0] multiplexer_10_out;
  wire [31:0] multiplexer_1_out, multiplexer_2_out, multiplexer_11_out, multiplexer_12_out;

  Multiplexer #(.select(1), .width(32), .disabled("Z"), .enable("false")) multiplexer_1 (
    .in0(IR_in), .in1({32{1'b0}}), .out(multiplexer_1_out), .sel(\同步清零_气泡_高电平有效 ));
  Multiplexer #(.select(1), .width(32), .disabled("Z"), .enable("false")) multiplexer_2 (
    .in0(PC_in), .in1({32{1'b0}}), .out(multiplexer_2_out), .sel(\同步清零_气泡_高电平有效 ));
  Multiplexer #(.select(1), .width(1), .disabled("Z"), .enable("false")) multiplexer_3 (
    .in0(MemToReg_in), .in1(1'b0), .out(multiplexer_3_out), .sel(\同步清零_气泡_高电平有效 ));
  Multiplexer #(.select(1), .width(1), .disabled("Z"), .enable("false")) multiplexer_4 (
    .in0(ERET_in), .in1(1'b0), .out(multiplexer_4_out), .sel(\同步清零_气泡_高电平有效 ));
  Multiplexer #(.select(1), .width(1), .disabled("Z"), .enable("false")) multiplexer_5 (
    .in0(MemWrite_in), .in1(1'b0), .out(multiplexer_5_out), .sel(\同步清零_气泡_高电平有效 ));
  Multiplexer #(.select(1), .width(1), .disabled("Z"), .enable("false")) multiplexer_6 (
    .in0(LBU_in), .in1(1'b0), .out(multiplexer_6_out), .sel(\同步清零_气泡_高电平有效 ));
  Multiplexer #(.select(1), .width(1), .disabled("Z"), .enable("false")) multiplexer_7 (
    .in0(RegWrite_in), .in1(1'b0), .out(multiplexer_7_out), .sel(\同步清零_气泡_高电平有效 ));
  Multiplexer #(.select(1), .width(1), .disabled("Z"), .enable("false")) multiplexer_8 (
    .in0(JAL_in), .in1(1'b0), .out(multiplexer_8_out), .sel(\同步清零_气泡_高电平有效 ));
  Multiplexer #(.select(1), .width(1), .disabled("Z"), .enable("false")) multiplexer_9 (
    .in0(RegDst_in), .in1(1'b0), .out(multiplexer_9_out), .sel(\同步清零_气泡_高电平有效 ));
  Multiplexer #(.select(1), .width(5), .disabled("Z"), .enable("false")) multiplexer_10 (
    .in0(RegWrite__in), .in1({5{1'b0}}), .out(multiplexer_10_out), .sel(\同步清零_气泡_高电平有效 ));
  Multiplexer #(.select(1), .width(32), .disabled("Z"), .enable("false")) multiplexer_11 (
    .in0(AluRst_in), .in1({32{1'b0}}), .out(multiplexer_11_out), .sel(\同步清零_气泡_高电平有效 ));
  Multiplexer #(.select(1), .width(32), .disabled("Z"), .enable("false")) multiplexer_12 (
    .in0(Mem_in), .in1({32{1'b0}}), .out(multiplexer_12_out), .sel(\同步清零_气泡_高电平有效 ));
  Multiplexer #(.select(1), .width(1), .disabled("Z"), .enable("false")) multiplexer_13 (
    .in0(\传输状态In_表明当前传输数据有效 ), .in1(1'b0), .out(multiplexer_13_out), .sel(\同步清零_气泡_高电平有效 ));
  Pull_Resistor #(.pull(0)) pull_resistor_1 (.node(\同步清零_气泡_高电平有效 ));
  Register #(.width(32), .trigger("rising"), .Select("low")) register_1 (
    .D(multiplexer_1_out), .en(pull_resistor_2_node), .Q(IR_out), .clk(CLK));  // open: clr
  Register #(.width(32), .trigger("rising"), .Select("low")) register_2 (
    .D(multiplexer_2_out), .en(pull_resistor_2_node), .Q(PC_out), .clk(CLK));  // open: clr
  Register #(.width(1), .trigger("rising"), .Select("low")) register_3 (
    .D(multiplexer_3_out), .en(pull_resistor_2_node), .Q(MemToReg_out), .clk(CLK));  // open: clr
  Register #(.width(1), .trigger("rising"), .Select("low")) register_4 (
    .D(multiplexer_4_out), .en(pull_resistor_2_node), .Q(ERET_out), .clk(CLK));  // open: clr
  Register #(.width(1), .trigger("rising"), .Select("low")) register_5 (
    .D(multiplexer_5_out), .en(pull_resistor_2_node), .Q(MemWrite_out), .clk(CLK));  // open: clr
  Register #(.width(1), .trigger("rising"), .Select("low")) register_6 (
    .D(multiplexer_6_out), .en(pull_resistor_2_node), .Q(LBU_out), .clk(CLK));  // open: clr
  Register #(.width(1), .trigger("rising"), .Select("low")) register_7 (
    .D(multiplexer_7_out), .en(pull_resistor_2_node), .Q(RegWrite_out), .clk(CLK));  // open: clr
  Register #(.width(1), .trigger("rising"), .Select("low")) register_8 (
    .D(multiplexer_8_out), .en(pull_resistor_2_node), .Q(JAL_out), .clk(CLK));  // open: clr
  Register #(.width(1), .trigger("rising"), .Select("low")) register_9 (
    .D(multiplexer_9_out), .en(pull_resistor_2_node), .Q(RegDst_out), .clk(CLK));  // open: clr
  Register #(.width(5), .trigger("rising"), .Select("low")) register_10 (
    .D(multiplexer_10_out), .en(pull_resistor_2_node), .Q(RegWrite__out), .clk(CLK));  // open: clr
  Register #(.width(32), .trigger("rising"), .Select("low")) register_11 (
    .D(multiplexer_11_out), .en(pull_resistor_2_node), .Q(AluRst_out), .clk(CLK));  // open: clr
  Register #(.width(32), .trigger("rising"), .Select("low")) register_12 (
    .D(multiplexer_12_out), .en(pull_resistor_2_node), .Q(Mem_out), .clk(CLK));  // open: clr
  Register #(.width(1), .trigger("rising"), .Select("low")) register_13 (
    .D(multiplexer_13_out), .en(pull_resistor_2_node), .Q(\传输状态Out_表明当前传输数据有效 ), .clk(CLK));  // open: clr
  Pull_Resistor #(.pull(0)) pull_resistor_2 (.node(pull_resistor_2_node));
  not not_1 (pull_resistor_2_node, \使能端_低电平有效_stall_高电平有效 );
endmodule

module \气泡流水接口_MEM_WB  (
  input  [31:0] IR_in,
  input  [31:0] PC_in,
  input  MemToReg_in,
  input  ERET_in,
  input  LBU_in,
  input  RegWrite_in,
  input  JAL_in,
  input  RegDst_in,
  input  [4:0] RegWrite__in,
  input  [31:0] Mem_in,
  input  [31:0] AluRst_in,
  input  \传输状态In_表明当前传输数据有效 ,
  input  CLK,
  input  \同步清零_气泡_高电平有效 ,
  input  \使能端_低电平有效_stall_高电平有效 ,
  output [31:0] IR_out,
  output [31:0] PC_out,
  output MemToReg_out,
  output ERET_out,
  output LBU_out,
  output RegWrite_out,
  output JAL_out,
  output RegDst_out,
  output [4:0] RegWrite__out,
  output [31:0] Mem_out,
  output [31:0] AluRst_out,
  output \传输状态Out_表明当前传输数据有效 
);

  wire multiplexer_3_out, multiplexer_4_out, multiplexer_5_out, multiplexer_6_out, multiplexer_7_out,
       multiplexer_8_out, multiplexer_12_out, pull_resistor_2_node;
  wire [4:0] multiplexer_9_out;
  wire [31:0] multiplexer_1_out, multiplexer_2_out, multiplexer_10_out, multiplexer_11_out;

  Multiplexer #(.select(1), .width(32), .disabled("Z"), .enable("false")) multiplexer_1 (
    .in0(IR_in), .in1({32{1'b0}}), .out(multiplexer_1_out), .sel(\同步清零_气泡_高电平有效 ));
  Multiplexer #(.select(1), .width(32), .disabled("Z"), .enable("false")) multiplexer_2 (
    .in0(PC_in), .in1({32{1'b0}}), .out(multiplexer_2_out), .sel(\同步清零_气泡_高电平有效 ));
  Multiplexer #(.select(1), .width(1), .disabled("Z"), .enable("false")) multiplexer_3 (
    .in0(MemToReg_in), .in1(1'b0), .out(multiplexer_3_out), .sel(\同步清零_气泡_高电平有效 ));
  Multiplexer #(.select(1), .width(1), .disabled("Z"), .enable("false")) multiplexer_4 (
    .in0(ERET_in), .in1(1'b0), .out(multiplexer_4_out), .sel(\同步清零_气泡_高电平有效 ));
  Multiplexer #(.select(1), .width(1), .disabled("Z"), .enable("false")) multiplexer_5 (
    .in0(LBU_in), .in1(1'b0), .out(multiplexer_5_out), .sel(\同步清零_气泡_高电平有效 ));
  Multiplexer #(.select(1), .width(1), .disabled("Z"), .enable("false")) multiplexer_6 (
    .in0(RegWrite_in), .in1(1'b0), .out(multiplexer_6_out), .sel(\同步清零_气泡_高电平有效 ));
  Multiplexer #(.select(1), .width(1), .disabled("Z"), .enable("false")) multiplexer_7 (
    .in0(JAL_in), .in1(1'b0), .out(multiplexer_7_out), .sel(\同步清零_气泡_高电平有效 ));
  Multiplexer #(.select(1), .width(1), .disabled("Z"), .enable("false")) multiplexer_8 (
    .in0(RegDst_in), .in1(1'b0), .out(multiplexer_8_out), .sel(\同步清零_气泡_高电平有效 ));
  Multiplexer #(.select(1), .width(5), .disabled("Z"), .enable("false")) multiplexer_9 (
    .in0(RegWrite__in), .in1({5{1'b0}}), .out(multiplexer_9_out), .sel(\同步清零_气泡_高电平有效 ));
  Multiplexer #(.select(1), .width(32), .disabled("Z"), .enable("false")) multiplexer_10 (
    .in0(Mem_in), .in1({32{1'b0}}), .out(multiplexer_10_out), .sel(\同步清零_气泡_高电平有效 ));
  Multiplexer #(.select(1), .width(32), .disabled("Z"), .enable("false")) multiplexer_11 (
    .in0(AluRst_in), .in1({32{1'b0}}), .out(multiplexer_11_out), .sel(\同步清零_气泡_高电平有效 ));
  Multiplexer #(.select(1), .width(1), .disabled("Z"), .enable("false")) multiplexer_12 (
    .in0(\传输状态In_表明当前传输数据有效 ), .in1(1'b0), .out(multiplexer_12_out), .sel(\同步清零_气泡_高电平有效 ));
  Pull_Resistor #(.pull(0)) pull_resistor_1 (.node(\同步清零_气泡_高电平有效 ));
  Register #(.width(32), .trigger("rising"), .Select("low")) register_1 (
    .D(multiplexer_1_out), .en(pull_resistor_2_node), .Q(IR_out), .clk(CLK));  // open: clr
  Register #(.width(32), .trigger("rising"), .Select("low")) register_2 (
    .D(multiplexer_2_out), .en(pull_resistor_2_node), .Q(PC_out), .clk(CLK));  // open: clr
  Register #(.width(1), .trigger("rising"), .Select("low")) register_3 (
    .D(multiplexer_3_out), .en(pull_resistor_2_node), .Q(MemToReg_out), .clk(CLK));  // open: clr
  Register #(.width(1), .trigger("rising"), .Select("low")) register_4 (
    .D(multiplexer_4_out), .en(pull_resistor_2_node), .Q(ERET_out), .clk(CLK));  // open: clr
  Register #(.width(1), .trigger("rising"), .Select("low")) register_5 (
    .D(multiplexer_5_out), .en(pull_resistor_2_node), .Q(LBU_out), .clk(CLK));  // open: clr
  Register #(.width(1), .trigger("rising"), .Select("low")) register_6 (
    .D(multiplexer_6_out), .en(pull_resistor_2_node), .Q(RegWrite_out), .clk(CLK));  // open: clr
  Register #(.width(1), .trigger("rising"), .Select("low")) register_7 (
    .D(multiplexer_7_out), .en(pull_resistor_2_node), .Q(JAL_out), .clk(CLK));  // open: clr
  Register #(.width(1), .trigger("rising"), .Select("low")) register_8 (
    .D(multiplexer_8_out), .en(pull_resistor_2_node), .Q(RegDst_out), .clk(CLK));  // open: clr
  Register #(.width(5), .trigger("rising"), .Select("low")) register_9 (
    .D(multiplexer_9_out), .en(pull_resistor_2_node), .Q(RegWrite__out), .clk(CLK));  // open: clr
  Register #(.width(32), .trigger("rising"), .Select("low")) register_10 (
    .D(multiplexer_10_out), .en(pull_resistor_2_node), .Q(Mem_out), .clk(CLK));  // open: clr
  Register #(.width(32), .trigger("rising"), .Select("low")) register_11 (
    .D(multiplexer_11_out), .en(pull_resistor_2_node), .Q(AluRst_out), .clk(CLK));  // open: clr
  Register #(.width(1), .trigger("rising"), .Select("low")) register_12 (
    .D(multiplexer_12_out), .en(pull_resistor_2_node), .Q(\传输状态Out_表明当前传输数据有效 ), .clk(CLK));  // open: clr
  Pull_Resistor #(.pull(0)) pull_resistor_2 (.node(pull_resistor_2_node));
  not not_1 (pull_resistor_2_node, \使能端_低电平有效_stall_高电平有效 );
endmodule

module \重定向流水线  (
  output RegWrite,
  output MemWrite,
  output [31:0] IF_PC,
  output [31:0] ID_PC,
  output [31:0] EX_PC,
  output [31:0] M_PC,
  output [31:0] WB_PC,
  output [31:0] RDin,
  output [31:0] MDin,
  output [31:0] LedData
);

  wire and_1_out, and_3_out, and_4_out, and_5_out, and_8_out, BLEZ_LESS, CLK, CLK_C, clock_1_out,
       clock_2_out, comparator_1_eq, comparator_1_lt, comparator_2_eq, comparator_3_eq, comparator_4_eq,
       d_ff_2_q, equal, EX_MemToReg, EX_RegWrite, Exit, Go, IF_stall, IR1, IR2, IR3, MEM_MemToReg,
       MEM_RegWrite, nand_1_out, not_1_out, or_1_out, or_2_out, or_3_out, or_4_out, Pause, RST, Stop, W1, W2,
       W3, \单周期硬布线控制器_1_alu_src , \单周期硬布线控制器_1_beq , \单周期硬布线控制器_1_blez , \单周期硬布线控制器_1_bne ,
       \单周期硬布线控制器_1_eret , \单周期硬布线控制器_1_jmp , \单周期硬布线控制器_1_jr , \单周期硬布线控制器_1_lbu , \单周期硬布线控制器_1_memtoreg ,
       \单周期硬布线控制器_1_memwrite , \单周期硬布线控制器_1_regwrite , \单周期硬布线控制器_1_signedext , \单周期硬布线控制器_1_syscall ,
       \条件分支成功 , \气泡流水接口_ex_mem_1_eret_out , \气泡流水接口_ex_mem_1_jal_out , \气泡流水接口_ex_mem_1_lbu_out ,
       \气泡流水接口_ex_mem_1_regdst_out , \气泡流水接口_ex_mem_1_传输状态out_表明当前传输数据有效 , \气泡流水接口_id_ex_1_alusrcb_out ,
       \气泡流水接口_id_ex_1_beq_out , \气泡流水接口_id_ex_1_blez_out , \气泡流水接口_id_ex_1_bne_out ,
       \气泡流水接口_id_ex_1_eret_out , \气泡流水接口_id_ex_1_jal_out , \气泡流水接口_id_ex_1_jmp_out ,
       \气泡流水接口_id_ex_1_lbu_out , \气泡流水接口_id_ex_1_memwrite_out , \气泡流水接口_id_ex_1_regdst_out ,
       \气泡流水接口_id_ex_1_syscall_out , \气泡流水接口_id_ex_1_传输状态out_表明当前传输数据有效 ,
       \气泡流水接口_if_id_1_传输状态out_表明当前传输数据有效 , \气泡流水接口_mem_wb_1_lbu_out , \源寄存器使用情况_1_r1_used ,
       \源寄存器使用情况_1_r2_used ;
  wire [1:0] pull_resistor_2_node, \单周期硬布线控制器_1_regdst , \气泡流水接口_id_ex_1_r1forward_out ,
       \气泡流水接口_id_ex_1_r2forward_out , \气泡流水接口_mem_wb_1_memtoreg_out , \重定向流水线_forword_1_forword1 ,
       \重定向流水线_forword_1_forword2 ;
  wire [1:1] \气泡流水接口_id_ex_1_jr_out ;
  wire [3:0] \单周期硬布线控制器_1_alu_op , \气泡流水接口_id_ex_1_aluop_out ;
  wire [4:0] EX_RegWrite_num, ID_R1_num, ID_R2_num, MEM_RegWrite_num, multiplexer_4_out, WB_RegWrite_num;
  wire [12:0] CNT_num;
  wire [15:0] \LoadUse次数 , \总周期数 , \插入气泡数 , \无条件分支数 , \条件分支成功数 ;
  wire [31:0] adder_1_out, adder_2_out, adder_3_out, adder_4_out, bit_extender_1_out, bit_extender_2_out,
       bit_extender_3_out, EX_IR, ID_IR, IF_IR, JMP_EX, MEM_AluRst, MEM_IR, multiplexer_1_out,
       multiplexer_5_out, multiplexer_6_out, multiplexer_7_out, multiplexer_8_out, multiplexer_10_out,
       multiplexer_11_out, pull_resistor_3_node, ram_1_data, WB_IR, \气泡流水接口_id_ex_1_imm_out ,
       \气泡流水接口_id_ex_1_r1_out , \气泡流水接口_id_ex_1_r2_out , \气泡流水接口_mem_wb_1_alurst_out ,
       \气泡流水接口_mem_wb_1_mem_out , \气泡流水线_mips_regifile_1_r1 , \气泡流水线_mips_regifile_1_r2 ;
  wire [31:1] mips_alu_1_result;
  wire [31:8] pull_resistor_4_node, pull_resistor_5_node, pull_resistor_6_node, pull_resistor_7_node;

  Button \u_总复位  (.out(RST));
  Button _1 (.out(IR1));
  Button _2 (.out(IR2));
  Button _3 (.out(IR3));
  // Probe on \总周期数 
  // Probe on \总周期数 
  Button \u_继续运行  (.out(Go));
  LED #(.active("true")) led_1 (.in(W1));
  LED #(.active("true")) led_2 (.in(W2));
  LED #(.active("true")) led_3 (.in(W3));
  // Probe on adder_1_out
  Hex_Digit_Display hex_digit_display_1 (.value(LedData[31:28]));  // open: dp
  // Probe on IF_PC[19:0]
  // Mips_Probe mips_probe_1: pin names not known; wires that end beside it: IF_IR
  or or_1 (or_1_out, Pause, Exit);
  or or_2 (or_2_out, and_1_out, RST);
  and and_1 (and_1_out, ~Exit, Go);  // AND_Gate
  Multiplexer #(.select(1), .width(32), .disabled("Z"), .enable("false")) multiplexer_1 (
    .in0(adder_1_out), .in1(JMP_EX), .out(multiplexer_1_out), .sel(or_3_out));
  // Probe on JMP_EX
  Hex_Digit_Display hex_digit_display_2 (.value(LedData[23:20]));  // open: dp
  Hex_Digit_Display hex_digit_display_3 (.value(LedData[27:24]));  // open: dp
  // Probe on ID_PC[19:0]
  // Mips_Probe mips_probe_2: pin names not known; wires that end beside it: ID_IR
  D_Flip_Flop #(.trigger("rising"), .Pre_Clr_Positions("ABOVE_BELOW"), .NegatePresetClear("false"), .enable("false"), .NewFFLayout("true")) d_ff_1 (
    .clk(or_1_out), .D(1'b1), .Qn(Stop), .reset(or_2_out));  // open: Q, preset
  not not_1 (not_1_out, IF_stall);
  Register #(.width(32), .trigger("rising"), .Select("low")) PC (
    .D(multiplexer_1_out), .en(not_1_out), .Q(IF_PC), .clk(CLK), .clr(RST));
  Hex_Digit_Display hex_digit_display_4 (.value(LedData[15:12]));  // open: dp
  Hex_Digit_Display hex_digit_display_5 (.value(LedData[19:16]));  // open: dp
  Counter #(.width(16), .max('hffff), .ongoal("wrap"), .trigger("rising"), .behavior("new")) counter_1 (
    .count(Stop), .Q(\总周期数 ), .clk(CLK), .clr(RST));  // open: load, D, carry, preset, down
  // Probe on IF_PC
  Hex_Digit_Display hex_digit_display_6 (.value(LedData[7:4]));  // open: dp
  Hex_Digit_Display hex_digit_display_7 (.value(LedData[11:8]));  // open: dp
  Clock #(.highDuration(1), .lowDuration(1)) clock_1 (.out(clock_1_out));
  // Probe on EX_PC[19:0]
  // Mips_Probe mips_probe_3: pin names not known; wires that end beside it: clock_1_out, CLK_C, EX_IR
  and and_2 (CLK, CLK_C, Stop);
  Adder #(.width(32)) adder_1 (.a(IF_PC), .b(32'h4), .out(adder_1_out), .cin(1'b0));  // open: cout
  Hex_Digit_Display hex_digit_display_8 (.value(LedData[3:0]));  // open: dp
  ROM #(.addrWidth(10), .dataWidth(32), .Select("high")) rom_1 (.addr(IF_PC[11:2]), .data(IF_IR));
  // Probe on \总周期数 
  // Probe on M_PC[19:0]
  // Mips_Probe mips_probe_4: pin names not known; wires that end beside it: MEM_IR
  \气泡流水接口_IF_ID  \u_气泡流水接口_if_id_1  (
    .IR_in(IF_IR), .\传输状态In_表明当前传输数据有效 (1'b1), .CLK(CLK), .IR_out(ID_IR),
    .\传输状态Out_表明当前传输数据有效 (\气泡流水接口_if_id_1_传输状态out_表明当前传输数据有效 ), .\同步清零_气泡_高电平有效 (or_3_out),
    .\使能端_低电平有效_stall_高电平有效 (IF_stall), .PC_in(IF_PC), .PC_out(ID_PC));
  // Probe on \总周期数 
  // Probe on \无条件分支数 
  // Probe on \条件分支成功数 
  // Probe on \插入气泡数 
  // Probe on \LoadUse次数 
  // Probe on IF_PC[11:0]
  // Probe on WB_PC[19:0]
  // Mips_Probe mips_probe_5: pin names not known; wires that end beside it: IF_stall, WB_IR
  \单周期硬布线控制器  \u_单周期硬布线控制器_1  (
    .Func(ID_IR[5:0]), .OP(ID_IR[31:26]), .ALU_OP(\单周期硬布线控制器_1_alu_op ), .MemToReg(\单周期硬布线控制器_1_memtoreg ),
    .MemWrite(\单周期硬布线控制器_1_memwrite ), .ALU_SRC(\单周期硬布线控制器_1_alu_src ), .RegWrite(\单周期硬布线控制器_1_regwrite ),
    .SysCALL(\单周期硬布线控制器_1_syscall ), .SignedExt(\单周期硬布线控制器_1_signedext ), .RegDst(\单周期硬布线控制器_1_regdst [0]),
    .JR(\单周期硬布线控制器_1_jr ), .JMP(\单周期硬布线控制器_1_jmp ), .Beq(\单周期硬布线控制器_1_beq ), .JAL(\单周期硬布线控制器_1_regdst [1]),
    .Bne(\单周期硬布线控制器_1_bne ), .ERET(\单周期硬布线控制器_1_eret ), .LBU(\单周期硬布线控制器_1_lbu ), .BLEZ(\单周期硬布线控制器_1_blez ));
  Multiplexer #(.select(1), .width(5), .disabled("Z"), .enable("false")) multiplexer_2 (
    .in0(ID_IR[25:21]), .in1(5'b00010), .out(ID_R1_num), .sel(\单周期硬布线控制器_1_syscall ));
  Multiplexer #(.select(1), .width(5), .disabled("Z"), .enable("false")) multiplexer_3 (
    .in0(ID_IR[20:16]), .in1(5'b00100), .out(ID_R2_num), .sel(\单周期硬布线控制器_1_syscall ));
  // Probe on ID_PC[11:0]
  // Probe on EX_PC[11:0]
  \源寄存器使用情况  \u_源寄存器使用情况_1  (
    .OP0(ID_IR[26]), .OP1(ID_IR[27]), .OP2(ID_IR[28]), .OP3(ID_IR[29]), .OP4(ID_IR[30]), .OP5(ID_IR[31]),
    .F0(ID_IR[0]), .F1(ID_IR[1]), .F2(ID_IR[2]), .F3(ID_IR[3]), .F4(ID_IR[4]), .F5(ID_IR[5]),
    .R1_Used(\源寄存器使用情况_1_r1_used ), .R2_Used(\源寄存器使用情况_1_r2_used ));
  // Probe on M_PC[11:0]
  D_Flip_Flop #(.trigger("high"), .Pre_Clr_Positions("LEGACY"), .NegatePresetClear("false"), .enable("true"), .NewFFLayout("false")) d_ff_2 (.Q(d_ff_2_q));  // open: clk, D, Qn, preset, en, reset
  // Probe on 13'h343
  \Load_Use相关  \load_use相关_1  (
    .R1_Used(\源寄存器使用情况_1_r1_used ), .R2_Used(\源寄存器使用情况_1_r2_used ), .EX_RegWrite_num(EX_RegWrite_num),
    .R1_num(ID_R1_num), .R2_num(ID_R2_num), .EX_MemToReg(EX_MemToReg), .\Load_Use相关 (IF_stall));
  \重定向流水线_Forword  \u_重定向流水线_forword_1  (
    .Reg1_Used(\源寄存器使用情况_1_r1_used ), .Reg2_Used(\源寄存器使用情况_1_r2_used ), .EX_RegWrite_num(EX_RegWrite_num),
    .MEM_RegWrite_num(MEM_RegWrite_num), .Reg1_num(ID_R1_num), .Reg2_num(ID_R2_num),
    .EX_RegWrite(EX_RegWrite), .MEM_RegWrite(MEM_RegWrite), .Forword1(\重定向流水线_forword_1_forword1 ),
    .Forword2(\重定向流水线_forword_1_forword2 ));
  // Probe on WB_PC[11:0]
  Comparator #(.width(13), .mode("twosComplement")) comparator_1 (
    .a(CNT_num), .b(13'h343), .eq(comparator_1_eq), .lt(comparator_1_lt));  // open: gt
  Clock #(.highDuration(1), .lowDuration(1)) clock_2 (.out(clock_2_out));
  Counter #(.width(16), .max('hffff), .ongoal("wrap"), .trigger("rising"), .behavior("new")) counter_2 (
    .count(IF_stall), .Q(\LoadUse次数 ), .clk(CLK), .clr(RST));  // open: load, D, carry, preset, down
  \气泡流水线_MIPS_Regifile  \u_气泡流水线_mips_regifile_1  (
    .Din(RDin), .Clk(CLK), .R1(\气泡流水线_mips_regifile_1_r1 ), .R2(\气泡流水线_mips_regifile_1_r2 ), .WE(RegWrite),
    .W_num(WB_RegWrite_num), .R1_num(ID_R1_num), .R2_num(ID_R2_num));
  nand nand_1 (nand_1_out, d_ff_2_q, comparator_1_eq);
  Counter #(.width(13), .max('h1fff), .ongoal("stay"), .trigger("rising"), .behavior("old")) counter_3 (
    .count(comparator_1_lt), .Q(CNT_num), .clk(clock_2_out));  // open: load, D, carry, clr, preset
  assign bit_extender_1_out = {{16{1'b0}}, ID_IR[15:0]};  // Bit_Extender bit_extender_1
  assign bit_extender_2_out = {{16{ID_IR[15]}}, ID_IR[15:0]};  // Bit_Extender bit_extender_2
  Multiplexer #(.select(2), .width(5), .disabled("Z"), .enable("false")) multiplexer_4 (
    .in0(ID_IR[15:11]), .in1(ID_IR[20:16]), .in2({5{1'b1}}), .in3({5{1'b1}}), .out(multiplexer_4_out),
    .sel(\单周期硬布线控制器_1_regdst ));
  assign CLK_C = nand_1_out ? clock_2_out : 1'bz;  // Controlled_Buffer controlled_buffer_1
  or or_3 (or_3_out, \条件分支成功 , \气泡流水接口_id_ex_1_jmp_out );
  Multiplexer #(.select(1), .width(32), .disabled("Z"), .enable("false")) multiplexer_5 (
    .in0(bit_extender_1_out), .in1(bit_extender_2_out), .out(multiplexer_5_out), .sel(\单周期硬布线控制器_1_signedext ));
  Pull_Resistor #(.pull(1)) pull_resistor_1 (.node(CLK_C));
  Counter #(.width(16), .max('hffff), .ongoal("wrap"), .trigger("rising"), .behavior("new")) \u_无条件分支数  (
    .count(\气泡流水接口_id_ex_1_jmp_out ), .Q(\无条件分支数 ), .clk(CLK), .clr(RST));  // open: load, D, carry, preset, down
  or or_4 (or_4_out, \条件分支成功 , IF_stall, \气泡流水接口_id_ex_1_jmp_out );
  \气泡流水接口_ID_EX  \u_气泡流水接口_id_ex_1  (
    .IR_in(ID_IR), .\传输状态In_表明当前传输数据有效 (\气泡流水接口_if_id_1_传输状态out_表明当前传输数据有效 ), .CLK(CLK), .IR_out(EX_IR),
    .\传输状态Out_表明当前传输数据有效 (\气泡流水接口_id_ex_1_传输状态out_表明当前传输数据有效 ), .\同步清零_气泡_高电平有效 (or_4_out),
    .\使能端_低电平有效_stall_高电平有效 (1'b0), .PC_in(ID_PC), .PC_out(EX_PC), .JMP_in(\单周期硬布线控制器_1_jmp ),
    .JMP_out(\气泡流水接口_id_ex_1_jmp_out ), .MemToReg_in(\单周期硬布线控制器_1_memtoreg ), .MemToReg_out(EX_MemToReg),
    .MemWrite_in(\单周期硬布线控制器_1_memwrite ), .MemWrite_out(\气泡流水接口_id_ex_1_memwrite_out ),
    .AluOp_in(\单周期硬布线控制器_1_alu_op ), .AluOp_out(\气泡流水接口_id_ex_1_aluop_out ),
    .AluSrcB_in(\单周期硬布线控制器_1_alu_src ), .AluSrcB_out(\气泡流水接口_id_ex_1_alusrcb_out ),
    .RegWrite_in(\单周期硬布线控制器_1_regwrite ), .RegWrite_out(EX_RegWrite), .RegDst_in(\单周期硬布线控制器_1_regdst [0]),
    .RegDst_out(\气泡流水接口_id_ex_1_regdst_out ), .R1_in(\气泡流水线_mips_regifile_1_r1 ),
    .R1_out(\气泡流水接口_id_ex_1_r1_out ), .R2_in(\气泡流水线_mips_regifile_1_r2 ), .R2_out(\气泡流水接口_id_ex_1_r2_out ),
    .Imm__in(multiplexer_5_out), .Imm_out(\气泡流水接口_id_ex_1_imm_out ), .Syscall_in(\单周期硬布线控制器_1_syscall ),
    .Syscall_out(\气泡流水接口_id_ex_1_syscall_out ), .Beq_in(\单周期硬布线控制器_1_beq ),
    .Beq_out(\气泡流水接口_id_ex_1_beq_out ), .JR_in(\单周期硬布线控制器_1_jr ), .JR_out(\气泡流水接口_id_ex_1_jr_out [1]),
    .Bne_in(\单周期硬布线控制器_1_bne ), .Bne_out(\气泡流水接口_id_ex_1_bne_out ), .SignedExt_in(\单周期硬布线控制器_1_signedext ),
    .ERET_in(\单周期硬布线控制器_1_eret ), .ERET_out(\气泡流水接口_id_ex_1_eret_out ), .LBU_in(\单周期硬布线控制器_1_lbu ),
    .LBU_out(\气泡流水接口_id_ex_1_lbu_out ), .BLEZ_in(\单周期硬布线控制器_1_blez ), .BLEZ_out(\气泡流水接口_id_ex_1_blez_out ),
    .JAL_in(\单周期硬布线控制器_1_regdst [1]), .JAL_out(\气泡流水接口_id_ex_1_jal_out ), .RegWrite__in(multiplexer_4_out),
    .RegWrite__out(EX_RegWrite_num), .R1Forward_in(\重定向流水线_forword_1_forword1 ),
    .R1Forward_out(\气泡流水接口_id_ex_1_r1forward_out ), .R2Forward_in(\重定向流水线_forword_1_forword2 ),
    .R2Forward_out(\气泡流水接口_id_ex_1_r2forward_out ));  // open: SignedExt_out, MFC0_in, MFC0_out, MTC0_in, MTC0_out
  and and_3 (and_3_out, \气泡流水接口_id_ex_1_beq_out , equal);
  and and_4 (and_4_out, \气泡流水接口_id_ex_1_bne_out , ~equal);  // AND_Gate
  and and_5 (and_5_out, \气泡流水接口_id_ex_1_blez_out , BLEZ_LESS);
  Multiplexer #(.select(2), .width(32), .disabled("Z"), .enable("false")) multiplexer_6 (
    .in0(\气泡流水接口_id_ex_1_r1_out ), .in1(RDin), .in2(MEM_AluRst), .out(multiplexer_6_out),
    .sel(\气泡流水接口_id_ex_1_r1forward_out ));  // open: in3
  Multiplexer #(.select(2), .width(32), .disabled("Z"), .enable("false")) multiplexer_7 (
    .in0(\气泡流水接口_id_ex_1_r2_out ), .in1(RDin), .in2(MEM_AluRst), .out(multiplexer_7_out),
    .sel(\气泡流水接口_id_ex_1_r2forward_out ));  // open: in3
  or or_5 (\条件分支成功 , and_3_out, and_4_out, and_5_out);
  Counter #(.width(16), .max('hffff), .ongoal("wrap"), .trigger("rising"), .behavior("new")) \u_条件成功分支数  (
    .count(\条件分支成功 ), .Q(\条件分支成功数 ), .clk(CLK), .clr(RST));  // open: load, D, carry, preset, down
  Adder #(.width(32)) adder_2 (.a(32'h4), .b(EX_PC), .out(adder_2_out));  // open: cin, cout
  Pull_Resistor #(.pull(0)) pull_resistor_2 (.node({EX_IR[15:0], pull_resistor_2_node}));
  Multiplexer #(.select(1), .width(32), .disabled("Z"), .enable("false")) multiplexer_8 (
    .in0(multiplexer_7_out), .in1(\气泡流水接口_id_ex_1_imm_out ), .out(multiplexer_8_out),
    .sel(\气泡流水接口_id_ex_1_alusrcb_out ));
  Pull_Resistor #(.pull(0)) pull_resistor_3 (.node({pull_resistor_3_node[31:28], EX_IR[25:0], pull_resistor_3_node[1:0]}));
  Adder #(.width(32)) adder_3 (.a(adder_2_out), .b(bit_extender_3_out), .out(adder_3_out));  // open: cin, cout
  assign bit_extender_3_out = {{14{EX_IR[15]}}, {EX_IR[15:0], pull_resistor_2_node}};  // Bit_Extender bit_extender_3
  and and_6 (Pause, \气泡流水接口_id_ex_1_syscall_out , comparator_2_eq);
  Comparator #(.width(32), .mode("twosComplement")) comparator_2 (
    .a(32'h32), .b(multiplexer_6_out), .eq(comparator_2_eq));  // open: gt, lt
  and and_7 (Exit, \气泡流水接口_id_ex_1_syscall_out , comparator_3_eq);
  Comparator #(.width(32), .mode("twosComplement")) comparator_3 (
    .a(32'ha), .b(multiplexer_6_out), .eq(comparator_3_eq));  // open: gt, lt
  and and_8 (and_8_out, \气泡流水接口_id_ex_1_syscall_out , comparator_4_eq);
  Comparator #(.width(32), .mode("twosComplement")) comparator_4 (
    .a(32'h22), .b(multiplexer_6_out), .eq(comparator_4_eq));  // open: gt, lt
  MIPS_ALU mips_alu_1 (
    .X(multiplexer_6_out), .Y(multiplexer_8_out), .AluOP(\气泡流水接口_id_ex_1_aluop_out ), .Equal(equal),
    .Result({mips_alu_1_result, BLEZ_LESS}), .shamt(EX_IR[10:6]));  // open: Result_2
  Register #(.width(32), .trigger("rising"), .Select("low")) register_1 (
    .D(multiplexer_7_out), .en(and_8_out), .Q(LedData), .clk(CLK));  // open: clr
  Multiplexer #(.select(2), .width(32), .disabled("Z"), .enable("false")) multiplexer_9 (
    .in0({pull_resistor_3_node[31:28], EX_IR[25:0], pull_resistor_3_node[1:0]}), .in1(adder_3_out),
    .in2(multiplexer_6_out), .in3(adder_3_out), .out(JMP_EX), .sel({\气泡流水接口_id_ex_1_jr_out [1], \条件分支成功 }));
  \气泡流水接口_EX_MEM  \u_气泡流水接口_ex_mem_1  (
    .IR_in(EX_IR), .\传输状态In_表明当前传输数据有效 (\气泡流水接口_id_ex_1_传输状态out_表明当前传输数据有效 ), .CLK(CLK), .IR_out(MEM_IR),
    .\传输状态Out_表明当前传输数据有效 (\气泡流水接口_ex_mem_1_传输状态out_表明当前传输数据有效 ), .\使能端_低电平有效_stall_高电平有效 (1'b0),
    .PC_in(EX_PC), .PC_out(M_PC), .MemToReg_in(EX_MemToReg), .MemToReg_out(MEM_MemToReg),
    .MemWrite_in(\气泡流水接口_id_ex_1_memwrite_out ), .MemWrite_out(MemWrite), .RegWrite_in(EX_RegWrite),
    .RegWrite_out(MEM_RegWrite), .RegDst_in(\气泡流水接口_id_ex_1_regdst_out ),
    .RegDst_out(\气泡流水接口_ex_mem_1_regdst_out ), .AluRst_in({mips_alu_1_result, BLEZ_LESS}),
    .AluRst_out(MEM_AluRst), .Mem_in(multiplexer_7_out), .Mem_out(MDin), .ERET_in(\气泡流水接口_id_ex_1_eret_out ),
    .ERET_out(\气泡流水接口_ex_mem_1_eret_out ), .LBU_in(\气泡流水接口_id_ex_1_lbu_out ),
    .LBU_out(\气泡流水接口_ex_mem_1_lbu_out ), .JAL_in(\气泡流水接口_id_ex_1_jal_out ),
    .JAL_out(\气泡流水接口_ex_mem_1_jal_out ), .RegWrite__in(EX_RegWrite_num), .RegWrite__out(MEM_RegWrite_num));  // open: 同步清零_气泡_高电平有效
  RAM #(.addrWidth(10), .dataWidth(32), .bus("separate"), .Select("high")) ram_1 (
    .addr(MEM_AluRst[11:2]), .din(MDin), .data(ram_1_data), .str(MemWrite), .clk(CLK));  // open: sel, ld, clr
  \气泡流水接口_MEM_WB  \u_气泡流水接口_mem_wb_1  (
    .IR_in(MEM_IR), .\传输状态In_表明当前传输数据有效 (\气泡流水接口_ex_mem_1_传输状态out_表明当前传输数据有效 ), .CLK(CLK), .IR_out(WB_IR),
    .\使能端_低电平有效_stall_高电平有效 (1'b0), .PC_in(M_PC), .PC_out(WB_PC), .RegWrite_in(MEM_RegWrite),
    .RegWrite_out(RegWrite), .RegDst_in(\气泡流水接口_ex_mem_1_regdst_out ), .Mem_in(ram_1_data),
    .Mem_out(\气泡流水接口_mem_wb_1_mem_out ), .ERET_in(\气泡流水接口_ex_mem_1_eret_out ),
    .JAL_in(\气泡流水接口_ex_mem_1_jal_out ), .JAL_out(\气泡流水接口_mem_wb_1_memtoreg_out [1]),
    .RegWrite__in(MEM_RegWrite_num), .RegWrite__out(WB_RegWrite_num), .MemToReg_in(MEM_MemToReg),
    .MemToReg_out(\气泡流水接口_mem_wb_1_memtoreg_out [0]), .LBU_in(\气泡流水接口_ex_mem_1_lbu_out ),
    .LBU_out(\气泡流水接口_mem_wb_1_lbu_out ), .AluRst_in(MEM_AluRst), .AluRst_out(\气泡流水接口_mem_wb_1_alurst_out ));  // open: 传输状态Out_表明当前传输数据有效, 同步清零_气泡_高电平有效, RegDst_out, ERET_out
  Pull_Resistor #(.pull(0)) pull_resistor_4 (.node({pull_resistor_4_node, \气泡流水接口_mem_wb_1_mem_out [7:0]}));
  Pull_Resistor #(.pull(0)) pull_resistor_5 (.node({pull_resistor_5_node, \气泡流水接口_mem_wb_1_mem_out [15:8]}));
  Pull_Resistor #(.pull(0)) pull_resistor_6 (.node({pull_resistor_6_node, \气泡流水接口_mem_wb_1_mem_out [23:16]}));
  Pull_Resistor #(.pull(0)) pull_resistor_7 (.node({pull_resistor_7_node, \气泡流水接口_mem_wb_1_mem_out [31:24]}));
  Multiplexer #(.select(2), .width(32), .disabled("Z"), .enable("false")) multiplexer_10 (
    .in0({pull_resistor_4_node, \气泡流水接口_mem_wb_1_mem_out [7:0]}),
    .in1({pull_resistor_5_node, \气泡流水接口_mem_wb_1_mem_out [15:8]}),
    .in2({pull_resistor_6_node, \气泡流水接口_mem_wb_1_mem_out [23:16]}),
    .in3({pull_resistor_7_node, \气泡流水接口_mem_wb_1_mem_out [31:24]}), .out(multiplexer_10_out),
    .sel(\气泡流水接口_mem_wb_1_alurst_out [1:0]));
  Multiplexer #(.select(1), .width(32), .disabled("Z"), .enable("false")) multiplexer_11 (
    .in0(\气泡流水接口_mem_wb_1_mem_out ), .in1(multiplexer_10_out), .out(multiplexer_11_out),
    .sel(\气泡流水接口_mem_wb_1_lbu_out ));
  Multiplexer #(.select(2), .width(32), .disabled("Z"), .enable("false")) multiplexer_12 (
    .in0(\气泡流水接口_mem_wb_1_alurst_out ), .in1(multiplexer_11_out), .in2(adder_4_out), .in3(adder_4_out),
    .out(RDin), .sel(\气泡流水接口_mem_wb_1_memtoreg_out ));
  Adder #(.width(32)) adder_4 (.a(WB_PC), .b(32'h4), .out(adder_4_out));  // open: cin, cout

  // Other names for the same wires on the sheet: MEM_PC[31:0] = M_PC; WB_RDin[31:0] = RDin; WB_RegWrite = RegWrite

  // Notes on the sheet:
  //   中断源
  //   时空图监测，可删除
  //   中断等待指示
  //   数码管输出
  //   指令存储器
  //   contents of rom_1 (hex, n*v repeats v):
  //   20110001 8000c05 20110001 20120002 20130003 8000c09 20110001 20120002 20130003 8000c0d 20110001
  //   20120002 20130003 8000c11 20110001 20120002 20130003 c000cb8 20100001 20110001 118fc0 112020
  //   20020022 c 118882 12200001 8000c15 112020 20020022 c 20110001 118880 112020 20020022 c 12200001
  //   8000c1f 20110001 118fc0 112020 20020022 c 1188c3 112020 20020022 c 118903 112020 20020022 c 118903
  //   112020 20020022 c 118903 112020 20020022 c 118903 112020 20020022 c 118903 112020 20020022 c 118903
  //   112020 20020022 c 118903 112020 20020022 c 20100001 109fc0 139fc3 8021 2012000c 24160003 26100001
  //   3210000f 20080008 20090001 139900 2709825 132020 20020022 c 1094022 1500fff9 22100001 2018000f
  //   2188024 108700 20080008 20090001 139902 2709825 132021 20020022 c 1094022 1500fff9 108702 2c9b022
  //   12c00001 8000c50 4020 1084027 84400 3508ffff 82021 20020022 c 2010ffff 20110000 ae300000 22100001
  //   22310004 ae300000 22100001 22310004 ae300000 22100001 22310004 ae300000 22100001 22310004 ae300000
  //   22100001 22310004 ae300000 22100001 22310004 ae300000 22100001 22310004 ae300000 22100001 22310004
  //   ae300000 22100001 22310004 ae300000 22100001 22310004 ae300000 22100001 22310004 ae300000 22100001
  //   22310004 ae300000 22100001 22310004 ae300000 22100001 22310004 ae300000 22100001 22310004 ae300000
  //   22100001 22310004 22100001 8020 2011003c 8e130000 8e340000 274402a 11000002 ae330000 ae140000
  //   2231fffc 1611fff8 102020 20020022 c 22100004 2011003c 1611fff2 20020032 c 20100000 22100001 102020
  //   20020022 c 22100002 102020 20020022 c 22100003 102020 20020022 c 22100004 102020 20020022 c 22100005
  //   102020 20020022 c 22100006 102020 20020022 c 22100007 102020 20020022 c 22100008 102020 20020022
  //   20020022 c 3e00008
  //   OP
  //   Func
  //   rs
  //   rt
  //   OP
  //   Func
  //   控制位
  //   流水调试日志用
  //   暂停节拍，不能为0
  //   戳工具置1进入计数暂停模式，ctrl+k时钟自动运行到对应节拍暂停
  //   ctrl+k关闭时钟连续运行，将控制位置零，进入单步调试模式调试
  //   rd
  //   可计数暂停的时钟源
  //   为方便自动评测，需要输出流水线各段保存的PC值，注意是PC不是PC+4，另外ID段寄存器写入信息，Mem段内存写入信息也要输出
endmodule

module \Load_Use相关  (
  input  [4:0] R1_num,
  input  [4:0] R2_num,
  input  R1_Used,
  input  R2_Used,
  input  [4:0] EX_RegWrite_num,
  input  EX_MemToReg,
  output \Load_Use相关 
);

  wire comparator_1_eq, pull_resistor_2_node;
  wire [4:0] \数据相关条件_1_out_3 , \数据相关条件_2_out_3 , \数据相关条件_3_out_3 ;

  \数据相关条件  \u_数据相关条件_1  (.R(EX_MemToReg), .R_num(EX_RegWrite_num), .out_3(\数据相关条件_1_out_3 ));
  \数据相关条件  \u_数据相关条件_2  (.R(R1_Used), .R_num(R1_num), .out_3(\数据相关条件_2_out_3 ));
  Comparator #(.width(5), .mode("twosComplement")) comparator_1 (
    .a(\数据相关条件_2_out_3 ), .b(\数据相关条件_1_out_3 ), .eq(comparator_1_eq));  // open: gt, lt
  Pull_Resistor #(.pull(0)) pull_resistor_1 (.node(comparator_1_eq));
  \数据相关条件  \u_数据相关条件_3  (.R(R2_Used), .R_num(R2_num), .out_3(\数据相关条件_3_out_3 ));
  or or_1 (\Load_Use相关 , comparator_1_eq, pull_resistor_2_node);
  Pull_Resistor #(.pull(0)) pull_resistor_2 (.node(pull_resistor_2_node));
  Comparator #(.width(5), .mode("twosComplement")) comparator_2 (
    .a(\数据相关条件_3_out_3 ), .b(\数据相关条件_1_out_3 ), .eq(pull_resistor_2_node));  // open: gt, lt
endmodule

module \重定向流水线_Forword  (
  input  [4:0] Reg1_num,
  input  [4:0] Reg2_num,
  input  Reg1_Used,
  input  Reg2_Used,
  input  [4:0] EX_RegWrite_num,
  input  EX_RegWrite,
  input  [4:0] MEM_RegWrite_num,
  input  MEM_RegWrite,
  output [1:0] Forword1,
  output [1:0] Forword2
);

  wire comparator_1_eq, comparator_3_eq, comparator_4_eq, pull_resistor_2_node;
  wire [4:0] \数据相关条件_1_out_3 , \数据相关条件_2_out_3 , \数据相关条件_3_out_3 , \数据相关条件_4_out_3 ;

  \数据相关条件  \u_数据相关条件_1  (.R(EX_RegWrite), .R_num(EX_RegWrite_num), .out_3(\数据相关条件_1_out_3 ));
  \数据相关条件  \u_数据相关条件_2  (.R(MEM_RegWrite), .R_num(MEM_RegWrite_num), .out_3(\数据相关条件_2_out_3 ));
  \数据相关条件  \u_数据相关条件_3  (.R(Reg1_Used), .R_num(Reg1_num), .out_3(\数据相关条件_3_out_3 ));
  Comparator #(.width(5), .mode("twosComplement")) comparator_1 (
    .a(\数据相关条件_3_out_3 ), .b(\数据相关条件_1_out_3 ), .eq(comparator_1_eq));  // open: gt, lt
  Pull_Resistor #(.pull(0)) pull_resistor_1 (.node(comparator_1_eq));
  Pull_Resistor #(.pull(0)) pull_resistor_2 (.node(pull_resistor_2_node));
  Comparator #(.width(5), .mode("twosComplement")) comparator_2 (
    .a(\数据相关条件_3_out_3 ), .b(\数据相关条件_2_out_3 ), .eq(pull_resistor_2_node));  // open: gt, lt
  Priority_Encoder #(.select(2), .disabled("Z")) priority_encoder_1 (
    .in0(1'b1), .in1(pull_resistor_2_node), .in2(comparator_1_eq), .out(Forword1));  // open: in3, gs, en_out, en_in
  \数据相关条件  \u_数据相关条件_4  (.R(Reg2_Used), .R_num(Reg2_num), .out_3(\数据相关条件_4_out_3 ));
  Comparator #(.width(5), .mode("twosComplement")) comparator_3 (
    .a(\数据相关条件_4_out_3 ), .b(\数据相关条件_1_out_3 ), .eq(comparator_3_eq));  // open: gt, lt
  Pull_Resistor #(.pull(0)) pull_resistor_3 (.node(comparator_3_eq));
  Comparator #(.width(5), .mode("twosComplement")) comparator_4 (
    .a(\数据相关条件_4_out_3 ), .b(\数据相关条件_2_out_3 ), .eq(comparator_4_eq));  // open: gt, lt
  Pull_Resistor #(.pull(0)) pull_resistor_4 (.node(comparator_4_eq));
  Priority_Encoder #(.select(2), .disabled("Z")) priority_encoder_2 (
    .in0(1'b1), .in1(comparator_4_eq), .in2(comparator_3_eq), .out(Forword2));  // open: in3, gs, en_out, en_in
endmodule

module \中断按键参考电路  (
  input  \同步清零信号 ,
  output \与中断屏蔽位与 
);

  wire \_1号中断_out , and_1_out, clock_1_out, d_ff_1_q, or_1_out, or_2_out;

  Clock #(.highDuration(1), .lowDuration(1)) clock_1 (.out(clock_1_out));
  Button \_1号中断  (.out(\_1号中断_out ));
  or or_1 (or_1_out, \与中断屏蔽位与 , d_ff_1_q);
  LED #(.active("true")) \_1号中断等待指示灯  (.in(or_1_out));
  D_Flip_Flop #(.trigger("rising"), .Pre_Clr_Positions("LEGACY"), .NegatePresetClear("false"), .enable("true"), .NewFFLayout("false")) d_ff_1 (
    .clk(\_1号中断_out ), .D(1'b1), .Q(d_ff_1_q), .reset(\与中断屏蔽位与 ));  // open: Qn, preset, en
  or or_2 (or_2_out, d_ff_1_q, \与中断屏蔽位与 );
  and and_1 (and_1_out, or_2_out, ~\同步清零信号 );  // AND_Gate
  D_Flip_Flop #(.trigger("rising"), .Pre_Clr_Positions("LEGACY"), .NegatePresetClear("false"), .enable("true"), .NewFFLayout("false")) IR1 (
    .clk(clock_1_out), .D(and_1_out), .Q(\与中断屏蔽位与 ));  // open: Qn, preset, en, reset
  \单周期硬布线控制器  \u_单周期硬布线控制器_1  ();  // open: Func, OP, ALU_OP, MemToReg, MemWrite, ALU_SRC, RegWrite, SysCALL, SignedExt, RegDst, JR, JMP, Beq, JAL, Bne, ERET, LBU, BLEZ

  // Notes on the sheet:
  //   中断信号采样参考电路
  //   Reset 
endmodule

module \单周期MIPS_单级中断  (
  input  IR1,
  input  IR2,
  input  IR3,
  output RegWrite,
  output MemWrite,
  output [31:0] PC,
  output [31:0] IR,
  output [31:0] RDin,
  output [31:0] MDin,
  output [31:0] LedData
);

  wire AluSrcB, and_1_out, and_2_out, and_3_out, and_6_out, and_7_out, and_8_out, Beq, BLEZ, BLEZ_LESS, Bne,
       CLK, clock_2_out, comparator_1_eq, comparator_2_eq, comparator_3_eq, comparator_4_eq, comparator_5_eq,
       comparator_6_eq, comparator_7_eq, comparator_8_eq, comparator_8_lt, d_ff_2_q, d_ff_3_qn, equal, ERET,
       Exit, Go, IR1_t, IR2_t, IR3_t, IRA, IRB, IRC, JAL, JMP, JR, LBU, MemToReg, nand_1_out, or_1_out,
       or_2_out, or_6_out, Pause, RegDst, SignedExt, Stop, SysCall, W1, W2, W3, \中断请求 ,
       \单周期_单级中断中断控制器_1_intr ;
  wire [1:0] INT_No_q, pull_resistor_4_node, \单周期_单级中断中断控制器_1_intno ;
  wire [3:0] AluOp;
  wire [4:0] multiplexer_3_out, multiplexer_4_out, multiplexer_5_out;
  wire [7:0] pull_resistor_6_node, pull_resistor_8_node;
  wire [12:0] CNT_num;
  wire [15:0] \总周期数 ;
  wire [31:0] adder_1_out, adder_2_out, adder_3_out, bit_extender_1_out, bit_extender_2_out,
       bit_extender_3_out, EPCin, EPCout, IRQ_PC, mips_regifile_1_r1, multiplexer_1_out, multiplexer_6_out,
       multiplexer_7_out, multiplexer_8_out, multiplexer_9_out, multiplexer_10_out, multiplexer_11_out,
       multiplexer_12_out, pull_resistor_5_node;
  wire [31:1] mips_alu_1_result;
  wire [31:8] pull_resistor_6_node_2, pull_resistor_7_node, pull_resistor_8_node_2, pull_resistor_9_node_2;
  wire [31:16] pull_resistor_9_node;

  Clock #(.highDuration(1), .lowDuration(1)) clock_1 ();  // open: out
  Button _1 ();  // open: out
  Button _2 ();  // open: out
  Button _3 ();  // open: out
  Button \u_继续运行  (.out(Go));
  LED #(.active("true")) led_1 (.in(W1));
  LED #(.active("true")) led_2 (.in(W2));
  LED #(.active("true")) led_3 (.in(W3));
  Hex_Digit_Display hex_digit_display_1 (.value(LedData[31:28]));  // open: dp
  Comparator #(.width(16), .mode("twosComplement")) comparator_1 (
    .a(16'h23b), .b(\总周期数 ), .eq(comparator_1_eq));  // open: gt, lt
  Comparator #(.width(16), .mode("twosComplement")) comparator_2 (
    .a(\总周期数 ), .b(16'h1), .eq(comparator_2_eq));  // open: gt, lt
  Comparator #(.width(16), .mode("twosComplement")) comparator_3 (
    .a(\总周期数 ), .b(16'h4), .eq(comparator_3_eq));  // open: gt, lt
  Comparator #(.width(16), .mode("twosComplement")) comparator_4 (
    .a(\总周期数 ), .b(16'h7), .eq(comparator_4_eq));  // open: gt, lt
  Hex_Digit_Display hex_digit_display_2 (.value(LedData[23:20]));  // open: dp
  Hex_Digit_Display hex_digit_display_3 (.value(LedData[27:24]));  // open: dp
  or or_1 (or_1_out, comparator_1_eq, comparator_2_eq);
  assign IRA = or_1_out ? ~CLK : 1'bz;  // Controlled_Inverter controlled_inverter_1
  assign IRB = comparator_3_eq ? ~CLK : 1'bz;  // Controlled_Inverter controlled_inverter_2
  assign IRC = comparator_4_eq ? ~CLK : 1'bz;  // Controlled_Inverter controlled_inverter_3
  Hex_Digit_Display hex_digit_display_4 (.value(LedData[15:12]));  // open: dp
  Hex_Digit_Display hex_digit_display_5 (.value(LedData[19:16]));  // open: dp
  Pull_Resistor #(.pull(0)) pull_resistor_1 (.node(IRA));
  Pull_Resistor #(.pull(0)) pull_resistor_2 (.node(IRB));
  Pull_Resistor #(.pull(0)) pull_resistor_3 (.node(IRC));
  Multiplexer #(.select(1), .width(32), .disabled("Z"), .enable("false")) multiplexer_1 (
    .in0(EPCin), .in1(IRQ_PC), .out(multiplexer_1_out), .sel(\中断请求 ));
  Hex_Digit_Display hex_digit_display_6 (.value(LedData[11:8]));  // open: dp
  Hex_Digit_Display hex_digit_display_7 (.value(LedData[7:4]));  // open: dp
  // Probe on \总周期数 
  Register #(.width(32), .trigger("rising"), .Select("low")) u_PC (
    .D(multiplexer_1_out), .en(Stop), .Q(PC), .clk(CLK));  // open: clr
  // Probe on PC
  Multiplexer #(.select(1), .width(32), .disabled("Z"), .enable("false")) multiplexer_2 (
    .in0(multiplexer_10_out), .in1(EPCout), .out(EPCin), .sel(ERET));
  Hex_Digit_Display hex_digit_display_8 (.value(LedData[3:0]));  // open: dp
  or or_2 (or_2_out, Pause, Exit);
  D_Flip_Flop #(.trigger("rising"), .Pre_Clr_Positions("ABOVE_BELOW"), .NegatePresetClear("false"), .enable("false"), .NewFFLayout("true")) d_ff_1 (
    .clk(or_2_out), .D(1'b1), .Qn(Stop), .reset(and_1_out));  // open: Q, preset
  and and_1 (and_1_out, ~Exit, Go);  // AND_Gate
  or or_3 (IR1_t, IR1, IRA);
  // Mips_Probe mips_probe_1: pin names not known; wires that end beside it: IR
  ROM #(.addrWidth(10), .dataWidth(32), .Select("high")) rom_1 (.addr(PC[11:2]), .data(IR));
  Adder #(.width(32)) adder_1 (.a(PC), .b(32'h4), .out(adder_1_out), .cin(1'b0));  // open: cout
  or or_4 (IR2_t, IR2, IRB);
  Counter #(.width(16), .max('hffff), .ongoal("wrap"), .trigger("rising"), .behavior("new")) counter_1 (
    .count(Stop), .Q(\总周期数 ), .clk(CLK));  // open: load, D, carry, clr, preset, down
  Multiplexer #(.select(2), .width(5), .disabled("Z"), .enable("false")) multiplexer_3 (
    .in0(IR[15:11]), .in1(IR[20:16]), .in2({5{1'b1}}), .in3({5{1'b1}}), .out(multiplexer_3_out),
    .sel({JAL, RegDst}));
  assign bit_extender_1_out = {{16{1'b0}}, IR[15:0]};  // Bit_Extender bit_extender_1
  assign bit_extender_2_out = {{16{IR[15]}}, IR[15:0]};  // Bit_Extender bit_extender_2
  Pull_Resistor #(.pull(0)) pull_resistor_4 (.node({IR[15:0], pull_resistor_4_node}));
  Multiplexer #(.select(1), .width(5), .disabled("Z"), .enable("false")) multiplexer_4 (
    .in0(IR[25:21]), .in1(5'b00010), .out(multiplexer_4_out), .sel(SysCall));
  Multiplexer #(.select(1), .width(5), .disabled("Z"), .enable("false")) multiplexer_5 (
    .in0(IR[20:16]), .in1(5'b00100), .out(multiplexer_5_out), .sel(SysCall));
  assign bit_extender_3_out = {{14{IR[15]}}, {IR[15:0], pull_resistor_4_node}};  // Bit_Extender bit_extender_3
  or or_5 (IR3_t, IR3, IRC);
  MIPS_Regifile mips_regifile_1 (
    .Din(RDin), .Clk(CLK), .R1(mips_regifile_1_r1), .R2(MDin), .WE(RegWrite), .W_num(multiplexer_3_out),
    .R1_num(multiplexer_4_out), .R2_num(multiplexer_5_out));
  Multiplexer #(.select(1), .width(32), .disabled("Z"), .enable("false")) multiplexer_6 (
    .in0(bit_extender_1_out), .in1(bit_extender_2_out), .out(multiplexer_6_out), .sel(SignedExt));
  Adder #(.width(32)) adder_2 (.a(adder_1_out), .b(bit_extender_3_out), .out(adder_2_out));  // open: cin, cout
  Multiplexer #(.select(1), .width(32), .disabled("Z"), .enable("false")) multiplexer_7 (
    .in0(MDin), .in1(multiplexer_6_out), .out(multiplexer_7_out), .sel(AluSrcB));
  Pull_Resistor #(.pull(0)) pull_resistor_5 (.node({pull_resistor_5_node[31:28], IR[25:0], pull_resistor_5_node[1:0]}));
  // Probe on adder_1_out
  // Probe on adder_2_out
  Comparator #(.width(32), .mode("twosComplement")) comparator_5 (
    .a(32'h32), .b(mips_regifile_1_r1), .eq(comparator_5_eq));  // open: gt, lt
  Comparator #(.width(32), .mode("twosComplement")) comparator_6 (
    .a(32'ha), .b(mips_regifile_1_r1), .eq(comparator_6_eq));  // open: gt, lt
  Comparator #(.width(32), .mode("twosComplement")) comparator_7 (
    .a(32'h22), .b(mips_regifile_1_r1), .eq(comparator_7_eq));  // open: gt, lt
  MIPS_ALU mips_alu_1 (
    .X(mips_regifile_1_r1), .Y(multiplexer_7_out), .AluOP(AluOp), .Equal(equal),
    .Result({mips_alu_1_result, BLEZ_LESS}), .shamt(IR[10:6]));  // open: Result_2
  or or_6 (or_6_out, and_3_out, and_2_out, and_7_out);
  and and_2 (and_2_out, BLEZ_LESS, BLEZ);
  and and_3 (and_3_out, Beq, equal);
  and and_4 (Pause, SysCall, comparator_5_eq);
  and and_5 (Exit, SysCall, comparator_6_eq);
  and and_6 (and_6_out, SysCall, comparator_7_eq);
  Multiplexer #(.select(1), .width(32), .disabled("Z"), .enable("false")) multiplexer_8 (
    .in0({pull_resistor_5_node[31:28], IR[25:0], pull_resistor_5_node[1:0]}), .in1(mips_regifile_1_r1),
    .out(multiplexer_8_out), .sel(JR));
  Multiplexer #(.select(1), .width(32), .disabled("Z"), .enable("false")) multiplexer_9 (
    .in0(adder_1_out), .in1(adder_2_out), .out(multiplexer_9_out), .sel(or_6_out));
  and and_7 (and_7_out, ~equal, Bne);  // AND_Gate
  Register #(.width(32), .trigger("rising"), .Select("low")) register_1 (
    .D(multiplexer_7_out), .en(and_6_out), .Q(LedData), .clk(CLK));  // open: clr
  Adder #(.width(32)) adder_3 (.a(PC), .b(32'h4), .out(adder_3_out));  // open: cin, cout
  Multiplexer #(.select(1), .width(32), .disabled("Z"), .enable("false")) multiplexer_10 (
    .in0(multiplexer_9_out), .in1(multiplexer_8_out), .out(multiplexer_10_out), .sel(JMP));
  Pull_Resistor #(.pull(0)) pull_resistor_6 (.node({pull_resistor_6_node_2, pull_resistor_6_node}));
  Pull_Resistor #(.pull(0)) pull_resistor_7 (.node({pull_resistor_7_node, pull_resistor_9_node[31:24]}));
  Pull_Resistor #(.pull(0)) pull_resistor_8 (.node({pull_resistor_8_node_2, pull_resistor_8_node}));
  Pull_Resistor #(.pull(0)) pull_resistor_9 (.node({pull_resistor_9_node_2, pull_resistor_9_node[23:16]}));
  Multiplexer #(.select(1), .width(32), .disabled("Z"), .enable("false")) multiplexer_11 (
    .in0({pull_resistor_9_node, pull_resistor_8_node, pull_resistor_6_node}), .in1(multiplexer_12_out),
    .out(multiplexer_11_out), .sel(LBU));
  RAM #(.addrWidth(10), .dataWidth(32), .bus("separate"), .Select("high")) ram_1 (
    .addr(mips_alu_1_result[11:2]), .din(MDin),
    .data({pull_resistor_9_node, pull_resistor_8_node, pull_resistor_6_node}), .str(MemWrite), .clk(CLK));  // open: sel, ld, clr
  D_Flip_Flop #(.trigger("high"), .Pre_Clr_Positions("LEGACY"), .NegatePresetClear("false"), .enable("true"), .NewFFLayout("false")) d_ff_2 (.Q(d_ff_2_q));  // open: clk, D, Qn, preset, en, reset
  // Probe on 13'hba
  Multiplexer #(.select(2), .width(32), .disabled("Z"), .enable("false")) multiplexer_12 (
    .in0({pull_resistor_6_node_2, pull_resistor_6_node}),
    .in1({pull_resistor_8_node_2, pull_resistor_8_node}),
    .in2({pull_resistor_9_node_2, pull_resistor_9_node[23:16]}),
    .in3({pull_resistor_7_node, pull_resistor_9_node[31:24]}), .out(multiplexer_12_out),
    .sel({mips_alu_1_result[1], BLEZ_LESS}));
  Multiplexer #(.select(2), .width(32), .disabled("Z"), .enable("false")) multiplexer_13 (
    .in0({mips_alu_1_result, BLEZ_LESS}), .in1(multiplexer_11_out), .in2(adder_3_out), .in3(adder_3_out),
    .out(RDin), .sel({JAL, MemToReg}));
  Comparator #(.width(13), .mode("twosComplement")) comparator_8 (
    .a(CNT_num), .b(13'hba), .eq(comparator_8_eq), .lt(comparator_8_lt));  // open: gt
  Clock #(.highDuration(1), .lowDuration(1)) clock_2 (.out(clock_2_out));
  nand nand_1 (nand_1_out, d_ff_2_q, comparator_8_eq);
  Counter #(.width(13), .max('h1fff), .ongoal("stay"), .trigger("rising"), .behavior("old")) counter_2 (
    .count(comparator_8_lt), .Q(CNT_num), .clk(clock_2_out));  // open: load, D, carry, clr, preset
  assign CLK = nand_1_out ? clock_2_out : 1'bz;  // Controlled_Buffer controlled_buffer_1
  Pull_Resistor #(.pull(1)) pull_resistor_10 (.node(CLK));
  D_Flip_Flop #(.trigger("rising"), .Pre_Clr_Positions("LEGACY"), .NegatePresetClear("false"), .enable("true"), .NewFFLayout("false")) d_ff_3 (
    .clk(CLK), .D(and_8_out), .Qn(d_ff_3_qn));  // open: Q, preset, en, reset
  and and_8 (and_8_out, ~ERET, \单周期_单级中断中断控制器_1_intr );  // AND_Gate
  \单周期硬布线控制器  \u_单周期硬布线控制器_1  (
    .Func(IR[5:0]), .OP(IR[31:26]), .ALU_OP(AluOp), .MemToReg(MemToReg), .MemWrite(MemWrite),
    .ALU_SRC(AluSrcB), .RegWrite(RegWrite), .SysCALL(SysCall), .SignedExt(SignedExt), .RegDst(RegDst),
    .JR(JR), .JMP(JMP), .Beq(Beq), .JAL(JAL), .Bne(Bne), .ERET(ERET), .LBU(LBU), .BLEZ(BLEZ));
  Register #(.width(32), .trigger("rising"), .Select("low")) EPC (
    .D(EPCin), .en(\中断请求 ), .Q(EPCout), .clk(CLK));  // open: clr
  \单周期_单级中断中断控制器  \u_单周期_单级中断中断控制器_1  (
    .CLK(CLK), .Key1(IR1_t), .Key2(IR2_t), .Key3(IR3_t), .Clr(ERET), .EDU_TEST(INT_No_q), .IR1W(W1),
    .IR2W(W2), .IR3W(W3), .IntNo(\单周期_单级中断中断控制器_1_intno ), .IntR(\单周期_单级中断中断控制器_1_intr ));
  and and_9 (\中断请求 , d_ff_3_qn, \单周期_单级中断中断控制器_1_intr );
  Multiplexer #(.select(2), .width(32), .disabled("Z"), .enable("false")) multiplexer_14 (
    .in1(32'h30ac), .in2(32'h3150), .in3(32'h31f4), .out(IRQ_PC), .sel(\单周期_单级中断中断控制器_1_intno ));  // open: in0
  Register #(.width(2), .trigger("rising"), .Select("low")) INT_No (
    .D(\单周期_单级中断中断控制器_1_intno ), .en(\中断请求 ), .Q(INT_No_q), .clk(CLK));  // open: clr

  // Other names for the same wires on the sheet: Func[5:0] = IR[5:0]; OP[5:0] = IR[31:26]

  // Notes on the sheet:
  //   中断源
  //   中断等待指示
  //   总复位信号应将除ROM以外所有存储组件全部清零
  //   单级中断测试信号模拟器
  //   数码管输出
  //   数码管输出应该用寄存器锁存，否则显示数据只能一闪而过
  //   指令存储器
  //   rs
  //   指令字
  //   contents of rom_1 (hex, n*v repeats v):
  //   201d07d0 20100001 109fc0 139fc3 8021 2012000c 24160008 26100001 3210000f 20080008 20090001 139900
  //   2709825 132020 20020022 c 1094022 1500fff9 22100001 2018000f 2188024 108700 20080008 20090001 139902
  //   2709825 132021 20020022 c 1094022 1500fff9 108702 2c9b022 12c00001 8000c07 4020 1084027 84400
  //   3508ffff 82021 20020022 c 8000c01 afa20000 23bd0004 afa40000 23bd0004 afb00000 23bd0004 afb30000
  //   23bd0004 afb40000 23bd0004 afb50000 23bd0004 afb60000 23bd0004 20160001 20140003 20150001 168020
  //   108100 2149825 132020 20020022 c 1600fffa 295a022 1680fff7 23bdfffc 8fb60000 23bdfffc 8fb50000
  //   23bdfffc 8fb40000 23bdfffc 8fb30000 23bdfffc 8fb00000 23bdfffc 8fa40000 23bdfffc 8fa20000 42000018
  //   afa20000 23bd0004 afa40000 23bd0004 afb00000 23bd0004 afb30000 23bd0004 afb40000 23bd0004 afb50000
  //   23bd0004 afb60000 23bd0004 20160002 20140003 20150001 168020 108100 2149825 132020 20020022 c
  //   1600fffa 295a022 1680fff7 23bdfffc 8fb60000 23bdfffc 8fb50000 23bdfffc 8fb40000 23bdfffc 8fb30000
  //   23bdfffc 8fb00000 23bdfffc 8fa40000 23bdfffc 8fa20000 42000018 afa20000 23bd0004 afa40000 23bd0004
  //   afb00000 23bd0004 afb30000 23bd0004 afb40000 23bd0004 afb50000 23bd0004 afb60000 23bd0004 20160003
  //   20140003 20150001 168020 108100 2149825 132020 20020022 c 1600fffa 295a022 1680fff7 23bdfffc
  //   8fb60000 23bdfffc 8fb50000 23bdfffc 8fb40000 23bdfffc 8fb30000 23bdfffc 8fb00000 23bdfffc 8fa40000
  //   23bdfffc 8fa20000 42000018
  //   rd
  //   OP
  //   Func
  //   rt
  //   为方便自动评测，需要输出PC，IR，寄存器堆写如数据RDin
  //   RAM写使能MemWrite、RAM写入数据MDin等信号
  //   控制位
  //   暂停节拍，不能为0
  //   戳工具置1进入计数暂停模式，ctrl+k时钟自动运行到对应节拍暂停
  //   ctrl+k关闭时钟连续运行，将控制位置零，进入单步调试模式调试
  //   用这个时钟源需要去掉电路中的其他时钟源
  //   可计数暂停的时钟源
  //   JMP
  //   JR
  //   ERET
  //   OP
  //   Func
  //   Beq
  //   Bne
  //   MemToReg
  //   MemWrite
  //   AluOP
  //   AluSrcB
  //   RegWrite
  //   JAL
  //   RegDst
  //   Syscall
endmodule

// 中断控制器
module \单周期_单级中断中断控制器  (
  input  CLK,
  input  Key1,
  input  Key2,
  input  Key3,
  input  Clr,
  input  [1:0] EDU_TEST,
  output IR1W,
  output IR2W,
  output IR3W,
  output [1:0] IntNo,
  output IntR
);

  wire and_1_out, and_2_out, and_3_out, Clr0, Clr1, Clr2, Clr3, d_ff_1_q, d_ff_2_q, d_ff_3_q, EDU_INT1,
       EDU_INT2, IR1_q, IR2_q, IR3_q, or_1_out, or_3_out, or_6_out, or_7_out, or_8_out;

  or or_1 (or_1_out, Key1, EDU_INT1);
  or or_2 (IR1W, IR1_q, d_ff_2_q);
  or or_3 (or_3_out, Key2, EDU_INT2);
  or or_4 (IR2W, IR2_q, d_ff_3_q);
  D_Flip_Flop #(.trigger("rising"), .Pre_Clr_Positions("LEGACY"), .NegatePresetClear("false"), .enable("true"), .NewFFLayout("false")) d_ff_1 (
    .clk(Key3), .D(1'b1), .Q(d_ff_1_q), .reset(IR3_q));  // open: Qn, preset, en
  or or_5 (IR3W, IR3_q, d_ff_1_q);
  D_Flip_Flop #(.trigger("rising"), .Pre_Clr_Positions("LEGACY"), .NegatePresetClear("false"), .enable("true"), .NewFFLayout("false")) d_ff_2 (
    .clk(or_1_out), .D(1'b1), .Q(d_ff_2_q), .reset(IR1_q));  // open: Qn, preset, en
  D_Flip_Flop #(.trigger("rising"), .Pre_Clr_Positions("LEGACY"), .NegatePresetClear("false"), .enable("true"), .NewFFLayout("false")) d_ff_3 (
    .clk(or_3_out), .D(1'b1), .Q(d_ff_3_q), .reset(IR2_q));  // open: Qn, preset, en
  or or_6 (or_6_out, d_ff_2_q, IR1_q);
  and and_1 (and_1_out, or_6_out, ~Clr1);  // AND_Gate
  or or_7 (or_7_out, d_ff_3_q, IR2_q);
  and and_2 (and_2_out, or_7_out, ~Clr2);  // AND_Gate
  or or_8 (or_8_out, d_ff_1_q, IR3_q);
  and and_3 (and_3_out, or_8_out, ~Clr3);  // AND_Gate
  D_Flip_Flop #(.trigger("rising"), .Pre_Clr_Positions("LEGACY"), .NegatePresetClear("false"), .enable("true"), .NewFFLayout("false")) IR1 (
    .clk(CLK), .D(and_1_out), .Q(IR1_q));  // open: Qn, preset, en, reset
  D_Flip_Flop #(.trigger("rising"), .Pre_Clr_Positions("LEGACY"), .NegatePresetClear("false"), .enable("true"), .NewFFLayout("false")) IR2 (
    .clk(CLK), .D(and_2_out), .Q(IR2_q));  // open: Qn, preset, en, reset
  D_Flip_Flop #(.trigger("rising"), .Pre_Clr_Positions("LEGACY"), .NegatePresetClear("false"), .enable("true"), .NewFFLayout("false")) IR3 (
    .clk(CLK), .D(and_3_out), .Q(IR3_q));  // open: Qn, preset, en, reset
  Priority_Encoder #(.select(2), .disabled(0)) priority_encoder_1 (
    .in1(IR1_q), .in2(IR2_q), .in3(IR3_q), .out(IntNo), .gs(IntR));  // open: in0, en_out, en_in
  Decoder #(.select(2), .tristate("false"), .disabled(0), .enable("true")) decoder_1 (
    .out0(Clr0), .out1(Clr1), .out2(Clr2), .out3(Clr3), .sel(EDU_TEST), .en(Clr));
  Pull_Resistor #(.pull(0)) pull_resistor_1 (.node({EDU_INT2, EDU_INT1}));

  // Other names for the same wires on the sheet: ClrIntNo[1:0] = EDU_TEST

  // Notes on the sheet:
  //   中断等待
  //   中断等待
  //   中断等待
  //   中断信号采样参考电路
  //   Reset 
  //   Reset 
  //   Reset 
  //   中断优先编码器
endmodule
module \单周期MIPS_多级中断  (
  input  IR1,
  input  IR2,
  input  IR3,
  output RegWrite,
  output MemWrite,
  output [31:0] PC,
  output [31:0] IR,
  output [31:0] RDin,
  output [31:0] MDin,
  output [31:0] LedData
);

  wire AluSrcB, and_1_out, and_2_out, and_3_out, and_6_out, and_7_out, and_8_out, Beq, BLEZ, BLEZ_LESS, Bne,
       CLK, clock_2_out, comparator_1_eq, comparator_2_eq, comparator_3_eq, comparator_4_eq, comparator_5_eq,
       comparator_8_eq, comparator_9_eq, comparator_10_eq, comparator_11_eq, comparator_11_lt, d_ff_2_q,
       equal, ERET, Exit, Go, int_change, IR1_t, IR2_t, IR3_t, IRA, IRB, IRC, JAL, JMP, JR, LBU, MemToReg,
       MFC0, MTC0, nand_1_out, or_1_out, or_2_out, or_3_out, or_7_out, or_8_out, or_9_out, or_10_out,
       or_11_out, or_12_out, or_13_out, or_14_out, Pause, pull_resistor_1_node, pull_resistor_2_node,
       pull_resistor_3_node, RegDst, register_2_q, SignedExt, Stop, SysCall, W1, W2, W3, \中断请求 ,
       \单周期_单级中断中断控制器_1_intr ;
  wire [1:0] pull_resistor_4_node, \单周期_单级中断中断控制器_1_intno , \硬件堆栈_no_1_输出 ;
  wire [3:0] AluOp;
  wire [4:0] multiplexer_3_out, multiplexer_4_out, multiplexer_5_out;
  wire [7:0] pull_resistor_8_node, pull_resistor_9_node;
  wire [12:0] CNT_num;
  wire [15:0] \总周期数 ;
  wire [31:0] adder_1_out, adder_2_out, adder_3_out, bit_extender_1_out, bit_extender_2_out,
       bit_extender_3_out, EPCin, EPCout, IRQ_PC, mips_regifile_1_r1, multiplexer_1_out, multiplexer_6_out,
       multiplexer_7_out, multiplexer_8_out, multiplexer_9_out, multiplexer_10_out, multiplexer_11_out,
       multiplexer_12_out, pull_resistor_5_node;
  wire [31:1] mips_alu_1_result;
  wire [31:8] pull_resistor_6_node_2, pull_resistor_7_node, pull_resistor_8_node_2, pull_resistor_9_node_2;
  wire [31:16] pull_resistor_6_node;

  Clock #(.highDuration(1), .lowDuration(1)) clock_1 ();  // open: out
  Button _1 (.out(IRA));
  Button _2 (.out(IRB));
  Button _3 (.out(IRC));
  Button \u_继续运行  (.out(Go));
  LED #(.active("true")) led_1 (.in(W1));
  LED #(.active("true")) led_2 (.in(W2));
  LED #(.active("true")) led_3 (.in(W3));
  Hex_Digit_Display hex_digit_display_1 (.value(LedData[31:28]));  // open: dp
  Comparator #(.width(16), .mode("twosComplement")) comparator_1 (
    .a(\总周期数 ), .b(16'h7), .eq(comparator_1_eq));  // open: gt, lt
  Comparator #(.width(16), .mode("twosComplement")) comparator_2 (
    .a(\总周期数 ), .b(16'h241), .eq(comparator_2_eq));  // open: gt, lt
  Hex_Digit_Display hex_digit_display_2 (.value(LedData[27:24]));  // open: dp
  Hex_Digit_Display hex_digit_display_3 (.value(LedData[23:20]));  // open: dp
  Comparator #(.width(16), .mode("twosComplement")) comparator_3 (
    .a(16'h258), .b(\总周期数 ), .eq(comparator_3_eq));  // open: gt, lt
  or or_1 (or_1_out, comparator_3_eq, comparator_4_eq);
  Comparator #(.width(16), .mode("twosComplement")) comparator_4 (
    .a(\总周期数 ), .b(16'h1), .eq(comparator_4_eq));  // open: gt, lt
  Comparator #(.width(16), .mode("twosComplement")) comparator_5 (
    .a(\总周期数 ), .b(16'h4), .eq(comparator_5_eq));  // open: gt, lt
  or or_2 (or_2_out, comparator_1_eq, comparator_2_eq);
  // Probe on multiplexer_1_out
  Hex_Digit_Display hex_digit_display_4 (.value(LedData[19:16]));  // open: dp
  Hex_Digit_Display hex_digit_display_5 (.value(LedData[15:12]));  // open: dp
  Pull_Resistor #(.pull(0)) pull_resistor_1 (.node(pull_resistor_1_node));
  assign pull_resistor_1_node = or_1_out ? ~CLK : 1'bz;  // Controlled_Inverter controlled_inverter_1
  Pull_Resistor #(.pull(0)) pull_resistor_2 (.node(pull_resistor_2_node));
  assign pull_resistor_2_node = comparator_5_eq ? ~CLK : 1'bz;  // Controlled_Inverter controlled_inverter_2
  Pull_Resistor #(.pull(0)) pull_resistor_3 (.node(pull_resistor_3_node));
  assign pull_resistor_3_node = or_2_out ? ~CLK : 1'bz;  // Controlled_Inverter controlled_inverter_3
  Multiplexer #(.select(1), .width(32), .disabled("Z"), .enable("false")) multiplexer_1 (
    .in0(EPCin), .in1(IRQ_PC), .out(multiplexer_1_out), .sel(\中断请求 ));
  // Probe on EPCin
  Hex_Digit_Display hex_digit_display_6 (.value(LedData[11:8]));  // open: dp
  Hex_Digit_Display hex_digit_display_7 (.value(LedData[7:4]));  // open: dp
  // Probe on \总周期数 
  Register #(.width(32), .trigger("rising"), .Select("low")) u_PC (
    .D(multiplexer_1_out), .en(Stop), .Q(PC), .clk(CLK));  // open: clr
  // Probe on PC
  Multiplexer #(.select(1), .width(32), .disabled("Z"), .enable("false")) multiplexer_2 (
    .in0(multiplexer_10_out), .in1(EPCout), .out(EPCin), .sel(ERET));
  Hex_Digit_Display hex_digit_display_8 (.value(LedData[3:0]));  // open: dp
  or or_3 (or_3_out, Pause, Exit);
  and and_1 (and_1_out, ~Exit, Go);  // AND_Gate
  D_Flip_Flop #(.trigger("rising"), .Pre_Clr_Positions("ABOVE_BELOW"), .NegatePresetClear("false"), .enable("false"), .NewFFLayout("true")) d_ff_1 (
    .clk(or_3_out), .D(1'b1), .Qn(Stop), .reset(and_1_out));  // open: Q, preset
  or or_4 (IR1_t, IR1, IRA);
  Counter #(.width(16), .max('hffff), .ongoal("wrap"), .trigger("rising"), .behavior("new")) counter_1 (
    .count(Stop), .Q(\总周期数 ), .clk(CLK));  // open: load, D, carry, clr, preset, down
  // Mips_Probe mips_probe_1: pin names not known; wires that end beside it: IR
  ROM #(.addrWidth(10), .dataWidth(32), .Select("high")) rom_1 (.addr(PC[11:2]), .data(IR));
  Adder #(.width(32)) adder_1 (.a(PC), .b(32'h4), .out(adder_1_out), .cin(1'b0));  // open: cout
  or or_5 (IR2_t, IR2, IRB);
  Multiplexer #(.select(2), .width(5), .disabled("Z"), .enable("false")) multiplexer_3 (
    .in0(IR[15:11]), .in1(IR[20:16]), .in2({5{1'b1}}), .in3({5{1'b1}}), .out(multiplexer_3_out),
    .sel({JAL, RegDst}));
  assign bit_extender_1_out = {{16{1'b0}}, IR[15:0]};  // Bit_Extender bit_extender_1
  assign bit_extender_2_out = {{16{IR[15]}}, IR[15:0]};  // Bit_Extender bit_extender_2
  Pull_Resistor #(.pull(0)) pull_resistor_4 (.node({IR[15:0], pull_resistor_4_node}));
  Comparator #(.width(32), .mode("unsigned")) comparator_6 (.a(IR), .b(32'h40800000), .eq(MTC0));  // open: gt, lt
  Comparator #(.width(32), .mode("unsigned")) comparator_7 (.a(IR), .b(32'h40000000), .eq(MFC0));  // open: gt, lt
  Multiplexer #(.select(1), .width(5), .disabled("Z"), .enable("false")) multiplexer_4 (
    .in0(IR[25:21]), .in1(5'b00010), .out(multiplexer_4_out), .sel(SysCall));
  Multiplexer #(.select(1), .width(5), .disabled("Z"), .enable("false")) multiplexer_5 (
    .in0(IR[20:16]), .in1(5'b00100), .out(multiplexer_5_out), .sel(SysCall));
  assign bit_extender_3_out = {{14{IR[15]}}, {IR[15:0], pull_resistor_4_node}};  // Bit_Extender bit_extender_3
  or or_6 (IR3_t, IR3, IRC);
  MIPS_Regifile mips_regifile_1 (
    .Din(RDin), .Clk(CLK), .R1(mips_regifile_1_r1), .R2(MDin), .WE(RegWrite), .W_num(multiplexer_3_out),
    .R1_num(multiplexer_4_out), .R2_num(multiplexer_5_out));
  Multiplexer #(.select(1), .width(32), .disabled("Z"), .enable("false")) multiplexer_6 (
    .in0(bit_extender_1_out), .in1(bit_extender_2_out), .out(multiplexer_6_out), .sel(SignedExt));
  Adder #(.width(32)) adder_2 (.a(adder_1_out), .b(bit_extender_3_out), .out(adder_2_out));  // open: cin, cout
  Multiplexer #(.select(1), .width(32), .disabled("Z"), .enable("false")) multiplexer_7 (
    .in0(MDin), .in1(multiplexer_6_out), .out(multiplexer_7_out), .sel(AluSrcB));
  Pull_Resistor #(.pull(0)) pull_resistor_5 (.node({pull_resistor_5_node[31:28], IR[25:0], pull_resistor_5_node[1:0]}));
  // Probe on adder_1_out
  // Probe on adder_2_out
  Comparator #(.width(32), .mode("twosComplement")) comparator_8 (
    .a(32'h32), .b(mips_regifile_1_r1), .eq(comparator_8_eq));  // open: gt, lt
  Comparator #(.width(32), .mode("twosComplement")) comparator_9 (
    .a(32'ha), .b(mips_regifile_1_r1), .eq(comparator_9_eq));  // open: gt, lt
  Comparator #(.width(32), .mode("twosComplement")) comparator_10 (
    .a(32'h22), .b(mips_regifile_1_r1), .eq(comparator_10_eq));  // open: gt, lt
  MIPS_ALU mips_alu_1 (
    .X(mips_regifile_1_r1), .Y(multiplexer_7_out), .AluOP(AluOp), .Equal(equal),
    .Result({mips_alu_1_result, BLEZ_LESS}), .shamt(IR[10:6]));  // open: Result_2
  or or_7 (or_7_out, and_3_out, and_2_out, and_7_out);
  and and_2 (and_2_out, BLEZ_LESS, BLEZ);
  and and_3 (and_3_out, Beq, equal);
  and and_4 (Pause, SysCall, comparator_8_eq);
  and and_5 (Exit, SysCall, comparator_9_eq);
  and and_6 (and_6_out, SysCall, comparator_10_eq);
  Multiplexer #(.select(1), .width(32), .disabled("Z"), .enable("false")) multiplexer_8 (
    .in0({pull_resistor_5_node[31:28], IR[25:0], pull_resistor_5_node[1:0]}), .in1(mips_regifile_1_r1),
    .out(multiplexer_8_out), .sel(JR));
  Multiplexer #(.select(1), .width(32), .disabled("Z"), .enable("false")) multiplexer_9 (
    .in0(adder_1_out), .in1(adder_2_out), .out(multiplexer_9_out), .sel(or_7_out));
  and and_7 (and_7_out, ~equal, Bne);  // AND_Gate
  Register #(.width(32), .trigger("rising"), .Select("low")) register_1 (
    .D(multiplexer_7_out), .en(and_6_out), .Q(LedData), .clk(CLK));  // open: clr
  Adder #(.width(32)) adder_3 (.a(PC), .b(32'h4), .out(adder_3_out));  // open: cin, cout
  Multiplexer #(.select(1), .width(32), .disabled("Z"), .enable("false")) multiplexer_10 (
    .in0(multiplexer_9_out), .in1(multiplexer_8_out), .out(multiplexer_10_out), .sel(JMP));
  Pull_Resistor #(.pull(0)) pull_resistor_6 (.node({pull_resistor_6_node_2, pull_resistor_6_node[23:16]}));
  Pull_Resistor #(.pull(0)) pull_resistor_7 (.node({pull_resistor_7_node, pull_resistor_6_node[31:24]}));
  Pull_Resistor #(.pull(0)) pull_resistor_8 (.node({pull_resistor_8_node_2, pull_resistor_8_node}));
  Pull_Resistor #(.pull(0)) pull_resistor_9 (.node({pull_resistor_9_node_2, pull_resistor_9_node}));
  Multiplexer #(.select(1), .width(32), .disabled("Z"), .enable("false")) multiplexer_11 (
    .in0({pull_resistor_6_node, pull_resistor_9_node, pull_resistor_8_node}), .in1(multiplexer_12_out),
    .out(multiplexer_11_out), .sel(LBU));
  RAM #(.addrWidth(10), .dataWidth(32), .bus("separate"), .Select("high")) ram_1 (
    .addr(mips_alu_1_result[11:2]), .din(MDin),
    .data({pull_resistor_6_node, pull_resistor_9_node, pull_resistor_8_node}), .str(MemWrite), .clk(CLK));  // open: sel, ld, clr
  D_Flip_Flop #(.trigger("high"), .Pre_Clr_Positions("LEGACY"), .NegatePresetClear("false"), .enable("true"), .NewFFLayout("false")) d_ff_2 (.Q(d_ff_2_q));  // open: clk, D, Qn, preset, en, reset
  // Probe on 13'h6
  Multiplexer #(.select(2), .width(32), .disabled("Z"), .enable("false")) multiplexer_12 (
    .in0({pull_resistor_8_node_2, pull_resistor_8_node}),
    .in1({pull_resistor_9_node_2, pull_resistor_9_node}),
    .in2({pull_resistor_6_node_2, pull_resistor_6_node[23:16]}),
    .in3({pull_resistor_7_node, pull_resistor_6_node[31:24]}), .out(multiplexer_12_out),
    .sel({mips_alu_1_result[1], BLEZ_LESS}));
  Multiplexer #(.select(2), .width(32), .disabled("Z"), .enable("false")) multiplexer_13 (
    .in0({mips_alu_1_result, BLEZ_LESS}), .in1(multiplexer_11_out), .in2(adder_3_out), .in3(adder_3_out),
    .out(RDin), .sel({JAL, MemToReg}));
  Comparator #(.width(13), .mode("twosComplement")) comparator_11 (
    .a(CNT_num), .b(13'h6), .eq(comparator_11_eq), .lt(comparator_11_lt));  // open: gt
  Clock #(.highDuration(1), .lowDuration(1)) clock_2 (.out(clock_2_out));
  Counter #(.width(13), .max('h1fff), .ongoal("stay"), .trigger("rising"), .behavior("old")) counter_2 (
    .count(comparator_11_lt), .Q(CNT_num), .clk(clock_2_out));  // open: load, D, carry, clr, preset
  nand nand_1 (nand_1_out, d_ff_2_q, comparator_11_eq);
  or or_8 (or_8_out, MFC0, ERET);
  or or_9 (or_9_out, MTC0, \中断请求 );
  or or_10 (or_10_out, MFC0, ERET);
  or or_11 (or_11_out, MTC0, \中断请求 );
  assign CLK = nand_1_out ? clock_2_out : 1'bz;  // Controlled_Buffer controlled_buffer_1
  Pull_Resistor #(.pull(1)) pull_resistor_10 (.node(CLK));
  \单周期硬布线控制器  \u_单周期硬布线控制器_1  (
    .Func(IR[5:0]), .OP(IR[31:26]), .ALU_OP(AluOp), .MemToReg(MemToReg), .MemWrite(MemWrite),
    .ALU_SRC(AluSrcB), .RegWrite(RegWrite), .SysCALL(SysCall), .SignedExt(SignedExt), .RegDst(RegDst),
    .JR(JR), .JMP(JMP), .Beq(Beq), .JAL(JAL), .Bne(Bne), .ERET(ERET), .LBU(LBU), .BLEZ(BLEZ));
  or or_12 (or_12_out, or_8_out, or_9_out);
  Register #(.width(1), .trigger("rising"), .Select("low")) register_2 (
    .D(and_8_out), .en(or_12_out), .Q(register_2_q), .clk(CLK));  // open: clr
  and and_8 (and_8_out, ~or_10_out, or_11_out);  // AND_Gate
  \单周期_单级中断中断控制器  \u_单周期_单级中断中断控制器_1  (
    .CLK(CLK), .Key1(IR1_t), .Key2(IR2_t), .Key3(IR3_t), .Clr(ERET), .EDU_TEST(\硬件堆栈_no_1_输出 ), .IR1W(W1),
    .IR2W(W2), .IR3W(W3), .IntNo(\单周期_单级中断中断控制器_1_intno ), .IntR(\单周期_单级中断中断控制器_1_intr ));
  \硬件堆栈  \u_硬件堆栈_1  (.CLK(CLK), .\输入 (EPCin), .\读取数据 (ERET), .\输出 (EPCout), .\数据变化 (or_13_out));
  or or_13 (or_13_out, ERET, \中断请求 );
  and and_9 (\中断请求 , ~register_2_q, int_change, \单周期_单级中断中断控制器_1_intr );  // AND_Gate
  Comparator #(.width(2), .mode("unsigned")) comparator_12 (
    .a(\单周期_单级中断中断控制器_1_intno ), .b(\硬件堆栈_no_1_输出 ), .gt(int_change));  // open: eq, lt
  Multiplexer #(.select(2), .width(32), .disabled("Z"), .enable("false")) multiplexer_14 (
    .in1(32'h30ac), .in2(32'h3158), .in3(32'h3204), .out(IRQ_PC), .sel(\单周期_单级中断中断控制器_1_intno ));  // open: in0
  or or_14 (or_14_out, \中断请求 , ERET);
  \硬件堆栈_No  \u_硬件堆栈_no_1  (
    .CLK(CLK), .\读取数据 (ERET), .\数据变化 (or_14_out), .\输入 (\单周期_单级中断中断控制器_1_intno ), .\输出 (\硬件堆栈_no_1_输出 ));

  // Other names for the same wires on the sheet: Func[5:0] = IR[5:0]; OP[5:0] = IR[31:26]

  // Notes on the sheet:
  //   中断源
  //   中断等待指示
  //   总复位信号应将除ROM以外所有存储组件全部清零
  //   多级中断测试信号模拟器
  //   数码管输出
  //   数码管输出应该用寄存器锁存，否则显示数据只能一闪而过
  //   指令存储器
  //   rs
  //   指令字
  //   contents of rom_1 (hex, n*v repeats v):
  //   201d07d0 20100001 109fc0 139fc3 8021 2012000c 24160008 26100001 3210000f 20080008 20090001 139900
  //   2709825 132020 20020022 c 1094022 1500fff9 22100001 2018000f 2188024 108700 20080008 20090001 139902
  //   2709825 132021 20020022 c 1094022 1500fff9 108702 2c9b022 12c00001 8000c07 4020 1084027 84400
  //   3508ffff 82021 20020022 c 8000c01 afa20000 23bd0004 afa40000 23bd0004 afb00000 23bd0004 afb30000
  //   23bd0004 afb40000 23bd0004 afb50000 23bd0004 afb60000 23bd0004 40000000 20160001 20140003 20150001
  //   168020 108100 2149825 132020 20020022 c 1600fffa 295a022 1680fff7 40800000 23bdfffc 8fb60000
  //   23bdfffc 8fb50000 23bdfffc 8fb40000 23bdfffc 8fb30000 23bdfffc 8fb00000 23bdfffc 8fa40000 23bdfffc
  //   8fa20000 42000018 afa20000 23bd0004 afa40000 23bd0004 afb00000 23bd0004 afb30000 23bd0004 afb40000
  //   23bd0004 afb50000 23bd0004 afb60000 23bd0004 40000000 20160002 20140003 20150001 168020 108100
  //   2149825 132020 20020022 c 1600fffa 295a022 1680fff7 40800000 23bdfffc 8fb60000 23bdfffc 8fb50000
  //   23bdfffc 8fb40000 23bdfffc 8fb30000 23bdfffc 8fb00000 23bdfffc 8fa40000 23bdfffc 8fa20000 42000018
  //   afa20000 23bd0004 afa40000 23bd0004 afb00000 23bd0004 afb30000 23bd0004 afb40000 23bd0004 afb50000
  //   23bd0004 afb60000 23bd0004 40000000 20160003 20140003 20150001 168020 108100 2149825 132020 20020022
  //   c 1600fffa 295a022 1680fff7 40800000 23bdfffc 8fb60000 23bdfffc 8fb50000 23bdfffc 8fb40000 23bdfffc
  //   8fb30000 23bdfffc 8fb00000 23bdfffc 8fa40000 23bdfffc 8fa20000 42000018
  //   rd
  //   OP
  //   Func
  //   rt
  //   为方便自动评测，需要输出PC，IR，寄存器堆写如数据RDin
  //   RAM写使能MemWrite、RAM写入数据MDin等信号
  //   控制位
  //   暂停节拍，不能为0
  //   戳工具置1进入计数暂停模式，ctrl+k时钟自动运行到对应节拍暂停
  //   ctrl+k关闭时钟连续运行，将控制位置零，进入单步调试模式调试
  //   用这个时钟源需要去掉电路中的其他时钟源
  //   JMP
  //   JR
  //   ERET
  //   OP
  //   Func
  //   可计数暂停的时钟源
  //   Beq
  //   Bne
  //   MemToReg
  //   MemWrite
  //   AluOP
  //   AluSrcB
  //   RegWrite
  //   JAL
  //   RegDst
  //   Syscall
endmodule

// 硬件堆栈
module \硬件堆栈  (
  input  CLK,
  input  \读取数据 ,
  input  \数据变化 ,
  input  [31:0] \输入 ,
  output [31:0] \输出 
);

  wire and_1_out, demultiplexer_1_out0, demultiplexer_1_out1, demultiplexer_1_out2, demultiplexer_1_out3;
  wire [1:0] SP;
  wire [31:0] multiplexer_1_out, register_1_q, register_2_q, register_3_q, register_4_q;

  and and_1 (and_1_out, \数据变化 , ~\读取数据 );  // AND_Gate
  Demultiplexer #(.select(2), .width(1), .tristate("false"), .disabled("Z"), .enable("false")) demultiplexer_1 (
    .out0(demultiplexer_1_out0), .out1(demultiplexer_1_out1), .out2(demultiplexer_1_out2),
    .out3(demultiplexer_1_out3), .in(and_1_out), .sel(SP));
  Register #(.width(32), .trigger("rising"), .Select("low")) register_1 (
    .D(\输入 ), .en(demultiplexer_1_out0), .Q(register_1_q), .clk(CLK));  // open: clr
  Counter #(.width(2), .max('h3), .ongoal("wrap"), .trigger("falling"), .behavior("new")) counter_1 (
    .count(\数据变化 ), .Q(SP), .clk(CLK), .down(\读取数据 ));  // open: load, D, carry, clr, preset
  Register #(.width(32), .trigger("rising"), .Select("low")) register_2 (
    .D(\输入 ), .en(demultiplexer_1_out2), .Q(register_2_q), .clk(CLK));  // open: clr
  Register #(.width(32), .trigger("rising"), .Select("low")) register_3 (
    .D(\输入 ), .en(demultiplexer_1_out1), .Q(register_3_q), .clk(CLK));  // open: clr
  Register #(.width(32), .trigger("rising"), .Select("low")) register_4 (
    .D(\输入 ), .en(demultiplexer_1_out3), .Q(register_4_q), .clk(CLK));  // open: clr
  Multiplexer #(.select(2), .width(32), .disabled("Z"), .enable("false")) multiplexer_1 (
    .in0(register_1_q), .in1(register_3_q), .in2(register_2_q), .in3(register_4_q), .out(multiplexer_1_out),
    .sel(SP));
  Register #(.width(32), .trigger("rising"), .Select("low")) register_5 (
    .D(multiplexer_1_out), .Q(\输出 ), .clk(CLK));  // open: en, clr

  // Other names for the same wires on the sheet: change = \数据变化 ; input[31:0] = \输入 ; output[31:0] = \输出 ;
  //   read = \读取数据 
endmodule

// 硬件堆栈
module \硬件堆栈_No  (
  input  CLK,
  input  \读取数据 ,
  input  \数据变化 ,
  input  [1:0] \输入 ,
  output [1:0] \输出 
);

  wire and_1_out, demultiplexer_1_out0, demultiplexer_1_out1, demultiplexer_1_out2, demultiplexer_1_out3;
  wire [1:0] multiplexer_1_out, register_1_q, register_2_q, register_3_q, register_4_q, SP;

  and and_1 (and_1_out, \数据变化 , ~\读取数据 );  // AND_Gate
  Demultiplexer #(.select(2), .width(1), .tristate("false"), .disabled("Z"), .enable("false")) demultiplexer_1 (
    .out0(demultiplexer_1_out0), .out1(demultiplexer_1_out1), .out2(demultiplexer_1_out2),
    .out3(demultiplexer_1_out3), .in(and_1_out), .sel(SP));
  Register #(.width(2), .trigger("rising"), .Select("low")) register_1 (
    .D(\输入 ), .en(demultiplexer_1_out0), .Q(register_1_q), .clk(CLK));  // open: clr
  Counter #(.width(2), .max('h3), .ongoal("wrap"), .trigger("falling"), .behavior("new")) counter_1 (
    .count(\数据变化 ), .Q(SP), .clk(CLK), .down(\读取数据 ));  // open: load, D, carry, clr, preset
  Register #(.width(2), .trigger("rising"), .Select("low")) register_2 (
    .D(\输入 ), .en(demultiplexer_1_out2), .Q(register_2_q), .clk(CLK));  // open: clr
  Register #(.width(2), .trigger("rising"), .Select("low")) register_3 (
    .D(\输入 ), .en(demultiplexer_1_out1), .Q(register_3_q), .clk(CLK));  // open: clr
  Register #(.width(2), .trigger("rising"), .Select("low")) register_4 (
    .D(\输入 ), .en(demultiplexer_1_out3), .Q(register_4_q), .clk(CLK));  // open: clr
  Register #(.width(2), .trigger("rising"), .Select("low")) register_5 (
    .D(multiplexer_1_out), .Q(\输出 ), .clk(CLK));  // open: en, clr
  Multiplexer #(.select(2), .width(2), .disabled("Z"), .enable("false")) multiplexer_1 (
    .in0(register_1_q), .in1(register_3_q), .in2(register_2_q), .in3(register_4_q), .out(multiplexer_1_out),
    .sel(SP));

  // Other names for the same wires on the sheet: change = \数据变化 ; input[1:0] = \输入 ; output[1:0] = \输出 ;
  //   read = \读取数据 
endmodule

// buffers
module buffers (
  input  in_1,
  output out_2
);

  wire buffer_1_out, buffer_2_out, buffer_3_out, buffer_4_out, buffer_5_out, buffer_6_out, buffer_7_out,
       buffer_8_out, buffer_9_out, buffer_10_out, buffer_11_out, buffer_12_out, buffer_13_out, buffer_14_out,
       buffer_15_out, buffer_16_out, buffer_17_out, buffer_18_out, buffer_19_out, buffer_20_out,
       buffer_21_out, buffer_22_out, buffer_23_out, buffer_24_out, buffer_25_out, buffer_26_out,
       buffer_28_out, buffer_29_out, buffer_30_out;

  buf buffer_1 (buffer_1_out, in_1);
  buf buffer_2 (buffer_2_out, buffer_1_out);
  buf buffer_3 (buffer_3_out, buffer_4_out);
  buf buffer_4 (buffer_4_out, buffer_2_out);
  buf buffer_5 (buffer_5_out, buffer_3_out);
  buf buffer_6 (buffer_6_out, buffer_5_out);
  buf buffer_7 (buffer_7_out, buffer_8_out);
  buf buffer_8 (buffer_8_out, buffer_10_out);
  buf buffer_9 (buffer_9_out, buffer_6_out);
  buf buffer_10 (buffer_10_out, buffer_9_out);
  buf buffer_11 (buffer_11_out, buffer_12_out);
  buf buffer_12 (buffer_12_out, buffer_7_out);
  buf buffer_13 (buffer_13_out, buffer_11_out);
  buf buffer_14 (buffer_14_out, buffer_13_out);
  buf buffer_15 (buffer_15_out, buffer_17_out);
  buf buffer_16 (buffer_16_out, buffer_15_out);
  buf buffer_17 (buffer_17_out, buffer_18_out);
  buf buffer_18 (buffer_18_out, buffer_14_out);
  buf buffer_19 (buffer_19_out, buffer_21_out);
  buf buffer_20 (buffer_20_out, buffer_19_out);
  buf buffer_21 (buffer_21_out, buffer_16_out);
  buf buffer_22 (buffer_22_out, buffer_20_out);
  buf buffer_23 (buffer_23_out, buffer_25_out);
  buf buffer_24 (buffer_24_out, buffer_26_out);
  buf buffer_25 (buffer_25_out, buffer_22_out);
  buf buffer_26 (buffer_26_out, buffer_23_out);
  buf buffer_27 (out_2, buffer_30_out);
  buf buffer_28 (buffer_28_out, buffer_29_out);
  buf buffer_29 (buffer_29_out, buffer_24_out);
  buf buffer_30 (buffer_30_out, buffer_28_out);
endmodule

module \单周期MIPS_多级中断_软件保护  (
  input  IR1,
  input  IR2,
  input  IR3,
  output RegWrite,
  output MemWrite,
  output [31:0] PC,
  output [31:0] IR,
  output [31:0] RDin,
  output [31:0] MDin,
  output [31:0] LedData
);

  wire AluSrcB, and_1_out, and_2_out, and_3_out, and_6_out, and_7_out, and_8_out, Beq, BLEZ, BLEZ_LESS, Bne,
       CLK, clock_2_out, comparator_1_eq, comparator_2_eq, comparator_3_eq, comparator_4_eq, comparator_5_eq,
       comparator_8_eq, comparator_9_eq, comparator_10_eq, comparator_11_eq, comparator_11_lt, d_ff_2_q,
       equal, ERET, Exit, Go, int_change, int_status, intr, IR1_t, IR2_t, IR3_t, IRA, IRB, IRC, JAL, JMP, JR,
       LBU, MemToReg, MFC0, MTC0, nand_1_out, not_1_out, or_1_out, or_2_out, or_3_out, or_7_out, or_10_out,
       Pause, pull_resistor_1_node, pull_resistor_2_node, pull_resistor_3_node, RegDst, SignedExt, Stop,
       SysCall, W1, W2, W3, \中断请求 , \单周期硬布线控制器_1_regdst , \单周期硬布线控制器_1_regwrite ;
  wire [1:0] pull_resistor_4_node, \单周期_单级中断中断控制器_1_intno , \硬件堆栈_no_1_输出 ;
  wire [3:0] AluOp;
  wire [4:0] multiplexer_3_out, multiplexer_4_out, multiplexer_5_out;
  wire [7:0] pull_resistor_6_node, pull_resistor_8_node;
  wire [12:0] CNT_num;
  wire [15:0] \总周期数 ;
  wire [31:0] adder_1_out, adder_2_out, adder_3_out, bit_extender_1_out, bit_extender_2_out,
       bit_extender_3_out, Coprocessor_0, EPCin, EPCout, IRQ_PC, mips_regifile_1_r1, multiplexer_1_out,
       multiplexer_6_out, multiplexer_7_out, multiplexer_8_out, multiplexer_9_out, multiplexer_10_out,
       multiplexer_11_out, multiplexer_12_out, multiplexer_13_out, multiplexer_14_out, pull_resistor_5_node;
  wire [31:1] mips_alu_1_result, mips_coprocessor_regifile_1_int_status_2;
  wire [31:8] pull_resistor_6_node_2, pull_resistor_7_node, pull_resistor_8_node_2, pull_resistor_9_node_2;
  wire [31:16] pull_resistor_9_node;

  Clock #(.highDuration(1), .lowDuration(1)) clock_1 ();  // open: out
  Button _1 (.out(IRA));
  Button _2 (.out(IRB));
  Button _3 (.out(IRC));
  Button \u_继续运行  (.out(Go));
  LED #(.active("true")) led_1 (.in(W1));
  LED #(.active("true")) led_2 (.in(W2));
  LED #(.active("true")) led_3 (.in(W3));
  Hex_Digit_Display hex_digit_display_1 (.value(LedData[31:28]));  // open: dp
  Comparator #(.width(16), .mode("twosComplement")) comparator_1 (
    .a(\总周期数 ), .b(16'h7), .eq(comparator_1_eq));  // open: gt, lt
  Comparator #(.width(16), .mode("twosComplement")) comparator_2 (
    .a(\总周期数 ), .b(16'h241), .eq(comparator_2_eq));  // open: gt, lt
  Hex_Digit_Display hex_digit_display_2 (.value(LedData[23:20]));  // open: dp
  Hex_Digit_Display hex_digit_display_3 (.value(LedData[27:24]));  // open: dp
  Comparator #(.width(16), .mode("twosComplement")) comparator_3 (
    .a(16'h258), .b(\总周期数 ), .eq(comparator_3_eq));  // open: gt, lt
  or or_1 (or_1_out, comparator_3_eq, comparator_4_eq);
  Comparator #(.width(16), .mode("twosComplement")) comparator_4 (
    .a(\总周期数 ), .b(16'h1), .eq(comparator_4_eq));  // open: gt, lt
  Comparator #(.width(16), .mode("twosComplement")) comparator_5 (
    .a(\总周期数 ), .b(16'h4), .eq(comparator_5_eq));  // open: gt, lt
  or or_2 (or_2_out, comparator_1_eq, comparator_2_eq);
  // Probe on multiplexer_1_out
  Hex_Digit_Display hex_digit_display_4 (.value(LedData[15:12]));  // open: dp
  Hex_Digit_Display hex_digit_display_5 (.value(LedData[19:16]));  // open: dp
  Pull_Resistor #(.pull(0)) pull_resistor_1 (.node(pull_resistor_1_node));
  assign pull_resistor_1_node = or_1_out ? ~CLK : 1'bz;  // Controlled_Inverter controlled_inverter_1
  Pull_Resistor #(.pull(0)) pull_resistor_2 (.node(pull_resistor_2_node));
  assign pull_resistor_2_node = comparator_5_eq ? ~CLK : 1'bz;  // Controlled_Inverter controlled_inverter_2
  Pull_Resistor #(.pull(0)) pull_resistor_3 (.node(pull_resistor_3_node));
  assign pull_resistor_3_node = or_2_out ? ~CLK : 1'bz;  // Controlled_Inverter controlled_inverter_3
  Multiplexer #(.select(1), .width(32), .disabled("Z"), .enable("false")) multiplexer_1 (
    .in0(EPCin), .in1(IRQ_PC), .out(multiplexer_1_out), .sel(\中断请求 ));
  // Probe on EPCin
  Hex_Digit_Display hex_digit_display_6 (.value(LedData[7:4]));  // open: dp
  Hex_Digit_Display hex_digit_display_7 (.value(LedData[11:8]));  // open: dp
  // Probe on \总周期数 
  Register #(.width(32), .trigger("rising"), .Select("low")) u_PC (
    .D(multiplexer_1_out), .en(Stop), .Q(PC), .clk(CLK));  // open: clr
  // Probe on PC
  Multiplexer #(.select(1), .width(32), .disabled("Z"), .enable("false")) multiplexer_2 (
    .in0(multiplexer_11_out), .in1(EPCout), .out(EPCin), .sel(ERET));
  Hex_Digit_Display hex_digit_display_8 (.value(LedData[3:0]));  // open: dp
  or or_3 (or_3_out, Pause, Exit);
  and and_1 (and_1_out, ~Exit, Go);  // AND_Gate
  D_Flip_Flop #(.trigger("rising"), .Pre_Clr_Positions("ABOVE_BELOW"), .NegatePresetClear("false"), .enable("false"), .NewFFLayout("true")) d_ff_1 (
    .clk(or_3_out), .D(1'b1), .Qn(Stop), .reset(and_1_out));  // open: Q, preset
  or or_4 (IR1_t, IR1, IRA);
  // Mips_Probe mips_probe_1: pin names not known; wires that end beside it: IR
  ROM #(.addrWidth(10), .dataWidth(32), .Select("high")) rom_1 (.addr(PC[11:2]), .data(IR));
  Adder #(.width(32)) adder_1 (.a(PC), .b(32'h4), .out(adder_1_out), .cin(1'b0));  // open: cout
  or or_5 (IR2_t, IR2, IRB);
  Counter #(.width(16), .max('hffff), .ongoal("wrap"), .trigger("rising"), .behavior("new")) counter_1 (
    .count(Stop), .Q(\总周期数 ), .clk(CLK));  // open: load, D, carry, clr, preset, down
  Multiplexer #(.select(2), .width(5), .disabled("Z"), .enable("false")) multiplexer_3 (
    .in0(IR[15:11]), .in1(IR[20:16]), .in2({5{1'b1}}), .in3({5{1'b1}}), .out(multiplexer_3_out),
    .sel({JAL, RegDst}));
  assign bit_extender_1_out = {{16{1'b0}}, IR[15:0]};  // Bit_Extender bit_extender_1
  assign bit_extender_2_out = {{16{IR[15]}}, IR[15:0]};  // Bit_Extender bit_extender_2
  Pull_Resistor #(.pull(0)) pull_resistor_4 (.node({IR[15:0], pull_resistor_4_node}));
  Multiplexer #(.select(1), .width(5), .disabled("Z"), .enable("false")) multiplexer_4 (
    .in0(IR[25:21]), .in1(5'b00010), .out(multiplexer_4_out), .sel(SysCall));
  Multiplexer #(.select(1), .width(5), .disabled("Z"), .enable("false")) multiplexer_5 (
    .in0(IR[20:16]), .in1(5'b00100), .out(multiplexer_5_out), .sel(SysCall));
  assign bit_extender_3_out = {{14{IR[15]}}, {IR[15:0], pull_resistor_4_node}};  // Bit_Extender bit_extender_3
  Comparator #(.width(11), .mode("unsigned")) comparator_6 (.a(IR[31:21]), .b(11'h204), .eq(MTC0));  // open: gt, lt
  Comparator #(.width(11), .mode("unsigned")) comparator_7 (.a(IR[31:21]), .b(11'h200), .eq(MFC0));  // open: gt, lt
  \单周期硬布线控制器  \u_单周期硬布线控制器_1  (
    .Func(IR[5:0]), .OP(IR[31:26]), .ALU_OP(AluOp), .MemToReg(MemToReg), .MemWrite(MemWrite),
    .ALU_SRC(AluSrcB), .RegWrite(\单周期硬布线控制器_1_regwrite ), .SysCALL(SysCall), .SignedExt(SignedExt),
    .RegDst(\单周期硬布线控制器_1_regdst ), .JR(JR), .JMP(JMP), .Beq(Beq), .JAL(JAL), .Bne(Bne), .ERET(ERET),
    .LBU(LBU), .BLEZ(BLEZ));
  or or_6 (IR3_t, IR3, IRC);
  MIPS_Regifile mips_regifile_1 (
    .Din(RDin), .Clk(CLK), .R1(mips_regifile_1_r1), .R2(MDin), .WE(RegWrite), .W_num(multiplexer_3_out),
    .R1_num(multiplexer_4_out), .R2_num(multiplexer_5_out));
  Multiplexer #(.select(1), .width(32), .disabled("Z"), .enable("false")) multiplexer_6 (
    .in0(bit_extender_1_out), .in1(bit_extender_2_out), .out(multiplexer_6_out), .sel(SignedExt));
  Adder #(.width(32)) adder_2 (.a(adder_1_out), .b(bit_extender_3_out), .out(adder_2_out));  // open: cin, cout
  Multiplexer #(.select(1), .width(32), .disabled("Z"), .enable("false")) multiplexer_7 (
    .in0(MDin), .in1(multiplexer_6_out), .out(multiplexer_7_out), .sel(AluSrcB));
  Pull_Resistor #(.pull(0)) pull_resistor_5 (.node({pull_resistor_5_node[31:28], IR[25:0], pull_resistor_5_node[1:0]}));
  // Probe on adder_1_out
  // Probe on adder_2_out
  Comparator #(.width(32), .mode("twosComplement")) comparator_8 (
    .a(32'h32), .b(mips_regifile_1_r1), .eq(comparator_8_eq));  // open: gt, lt
  Comparator #(.width(32), .mode("twosComplement")) comparator_9 (
    .a(32'ha), .b(mips_regifile_1_r1), .eq(comparator_9_eq));  // open: gt, lt
  Comparator #(.width(32), .mode("twosComplement")) comparator_10 (
    .a(32'h22), .b(mips_regifile_1_r1), .eq(comparator_10_eq));  // open: gt, lt
  MIPS_ALU mips_alu_1 (
    .X(mips_regifile_1_r1), .Y(multiplexer_7_out), .AluOP(AluOp), .Equal(equal),
    .Result({mips_alu_1_result, BLEZ_LESS}), .shamt(IR[10:6]));  // open: Result_2
  or or_7 (or_7_out, and_2_out, and_3_out, and_7_out);
  and and_2 (and_2_out, Beq, equal);
  and and_3 (and_3_out, BLEZ_LESS, BLEZ);
  or or_8 (RegWrite, MFC0, \单周期硬布线控制器_1_regwrite );
  or or_9 (RegDst, MFC0, \单周期硬布线控制器_1_regdst );
  and and_4 (Pause, SysCall, comparator_8_eq);
  and and_5 (Exit, SysCall, comparator_9_eq);
  and and_6 (and_6_out, SysCall, comparator_10_eq);
  Multiplexer #(.select(1), .width(32), .disabled("Z"), .enable("false")) multiplexer_8 (
    .in0({pull_resistor_5_node[31:28], IR[25:0], pull_resistor_5_node[1:0]}), .in1(mips_regifile_1_r1),
    .out(multiplexer_8_out), .sel(JR));
  Multiplexer #(.select(1), .width(32), .disabled("Z"), .enable("false")) multiplexer_9 (
    .in0(adder_1_out), .in1(adder_2_out), .out(multiplexer_9_out), .sel(or_7_out));
  and and_7 (and_7_out, ~equal, Bne);  // AND_Gate
  and and_8 (and_8_out, ~ERET, intr);  // AND_Gate
  Multiplexer #(.select(1), .width(32), .disabled("Z"), .enable("false")) multiplexer_10 (
    .in0({32{1'b0}}), .in1(32'h1), .out(multiplexer_10_out), .sel(and_8_out));
  MIPS_Coprocessor__Regifile mips_coprocessor_regifile_1 (
    .Din(MDin), .Clk(CLK), .R1(Coprocessor_0), .WE(MTC0), .W_num(IR[15:11]), .R1_num(IR[15:11]),
    .INT_STATUS_2({mips_coprocessor_regifile_1_int_status_2, int_status}), .EPC_2(EPCout), .in_6(\中断请求 ),
    .EPC(EPCin), .INT_STATUS(multiplexer_10_out), .ERET(ERET));  // open: out_11, out_12, out_13, out_14, out_15, out_16, out_17, out_18, out_19, out_20, out_21, out_23, out_25, out_26, out_27, out_28, out_29, out_30, out_31, out_32, out_33, out_34, out_35, out_36, out_37, out_38, out_39, out_40, out_41, out_10
  Register #(.width(32), .trigger("rising"), .Select("low")) register_1 (
    .D(multiplexer_7_out), .en(and_6_out), .Q(LedData), .clk(CLK));  // open: clr
  Adder #(.width(32)) adder_3 (.a(PC), .b(32'h4), .out(adder_3_out));  // open: cin, cout
  Multiplexer #(.select(1), .width(32), .disabled("Z"), .enable("false")) multiplexer_11 (
    .in0(multiplexer_9_out), .in1(multiplexer_8_out), .out(multiplexer_11_out), .sel(JMP));
  Pull_Resistor #(.pull(0)) pull_resistor_6 (.node({pull_resistor_6_node_2, pull_resistor_6_node}));
  Pull_Resistor #(.pull(0)) pull_resistor_7 (.node({pull_resistor_7_node, pull_resistor_9_node[31:24]}));
  Pull_Resistor #(.pull(0)) pull_resistor_8 (.node({pull_resistor_8_node_2, pull_resistor_8_node}));
  Pull_Resistor #(.pull(0)) pull_resistor_9 (.node({pull_resistor_9_node_2, pull_resistor_9_node[23:16]}));
  Multiplexer #(.select(1), .width(32), .disabled("Z"), .enable("false")) multiplexer_12 (
    .in0({pull_resistor_9_node, pull_resistor_6_node, pull_resistor_8_node}), .in1(multiplexer_13_out),
    .out(multiplexer_12_out), .sel(LBU));
  RAM #(.addrWidth(10), .dataWidth(32), .bus("separate"), .Select("high")) ram_1 (
    .addr(mips_alu_1_result[11:2]), .din(MDin),
    .data({pull_resistor_9_node, pull_resistor_6_node, pull_resistor_8_node}), .str(MemWrite), .clk(CLK));  // open: sel, ld, clr
  D_Flip_Flop #(.trigger("high"), .Pre_Clr_Positions("LEGACY"), .NegatePresetClear("false"), .enable("true"), .NewFFLayout("false")) d_ff_2 (.Q(d_ff_2_q));  // open: clk, D, Qn, preset, en, reset
  // Probe on 13'hd6
  Multiplexer #(.select(2), .width(32), .disabled("Z"), .enable("false")) multiplexer_13 (
    .in0({pull_resistor_8_node_2, pull_resistor_8_node}),
    .in1({pull_resistor_6_node_2, pull_resistor_6_node}),
    .in2({pull_resistor_9_node_2, pull_resistor_9_node[23:16]}),
    .in3({pull_resistor_7_node, pull_resistor_9_node[31:24]}), .out(multiplexer_13_out),
    .sel({mips_alu_1_result[1], BLEZ_LESS}));
  Multiplexer #(.select(2), .width(32), .disabled("Z"), .enable("false")) multiplexer_14 (
    .in0({mips_alu_1_result, BLEZ_LESS}), .in1(multiplexer_12_out), .in2(adder_3_out), .in3(adder_3_out),
    .out(multiplexer_14_out), .sel({JAL, MemToReg}));
  not not_1 (not_1_out, int_status);
  Comparator #(.width(13), .mode("twosComplement")) comparator_11 (
    .a(CNT_num), .b(13'hd6), .eq(comparator_11_eq), .lt(comparator_11_lt));  // open: gt
  Clock #(.highDuration(1), .lowDuration(1)) clock_2 (.out(clock_2_out));
  and and_9 (\中断请求 , not_1_out, int_change, intr);
  \单周期_单级中断中断控制器  \u_单周期_单级中断中断控制器_1  (
    .CLK(CLK), .Key1(IR1_t), .Key2(IR2_t), .Key3(IR3_t), .Clr(ERET), .EDU_TEST(\硬件堆栈_no_1_输出 ), .IR1W(W1),
    .IR2W(W2), .IR3W(W3), .IntNo(\单周期_单级中断中断控制器_1_intno ), .IntR(intr));
  Counter #(.width(13), .max('h1fff), .ongoal("stay"), .trigger("rising"), .behavior("old")) counter_2 (
    .count(comparator_11_lt), .Q(CNT_num), .clk(clock_2_out));  // open: load, D, carry, clr, preset
  Multiplexer #(.select(1), .width(32), .disabled("Z"), .enable("false")) multiplexer_15 (
    .in0(multiplexer_14_out), .in1(Coprocessor_0), .out(RDin), .sel(MFC0));
  Comparator #(.width(2), .mode("unsigned")) comparator_12 (
    .a(\单周期_单级中断中断控制器_1_intno ), .b(\硬件堆栈_no_1_输出 ), .gt(int_change));  // open: eq, lt
  nand nand_1 (nand_1_out, d_ff_2_q, comparator_11_eq);
  Multiplexer #(.select(2), .width(32), .disabled("Z"), .enable("false")) multiplexer_16 (
    .in1(32'h30ac), .in2(32'h3174), .in3(32'h323c), .out(IRQ_PC), .sel(\单周期_单级中断中断控制器_1_intno ));  // open: in0
  assign CLK = nand_1_out ? clock_2_out : 1'bz;  // Controlled_Buffer controlled_buffer_1
  Pull_Resistor #(.pull(1)) pull_resistor_10 (.node(CLK));
  \硬件堆栈_No  \u_硬件堆栈_no_1  (
    .CLK(CLK), .\读取数据 (ERET), .\数据变化 (or_10_out), .\输入 (\单周期_单级中断中断控制器_1_intno ), .\输出 (\硬件堆栈_no_1_输出 ));
  or or_10 (or_10_out, \中断请求 , ERET);

  // Other names for the same wires on the sheet: Func[5:0] = IR[5:0]; OP[5:0] = IR[31:26]

  // Notes on the sheet:
  //   中断源
  //   中断等待指示
  //   总复位信号应将除ROM以外所有存储组件全部清零
  //   多级中断测试信号模拟器
  //   数码管输出
  //   数码管输出应该用寄存器锁存，否则显示数据只能一闪而过
  //   指令存储器
  //   rs
  //   指令字
  //   contents of rom_1 (hex, n*v repeats v):
  //   201d07d0 20100001 109fc0 139fc3 8021 2012000c 24160008 26100001 3210000f 20080008 20090001 139900
  //   2709825 132020 20020022 c 1094022 1500fff9 22100001 2018000f 2188024 108700 20080008 20090001 139902
  //   2709825 132021 20020022 c 1094022 1500fff9 108702 2c9b022 12c00001 8000c07 4020 1084027 84400
  //   3508ffff 82021 20020022 c 8000c01 afa20000 23bd0004 afa40000 23bd0004 afb00000 23bd0004 afb30000
  //   23bd0004 afb40000 23bd0004 afb50000 23bd0004 afb60000 23bd0004 40167000 afb60000 23bd0004 40806000
  //   20160001 20140003 20150001 168020 108100 2149825 132020 20020022 c 1600fffa 295a022 1680fff7
  //   20160001 40966000 23bdfffc 8fb60000 40967000 23bdfffc 8fb60000 23bdfffc 8fb50000 23bdfffc 8fb40000
  //   23bdfffc 8fb30000 23bdfffc 8fb00000 23bdfffc 8fa40000 23bdfffc 8fa20000 42000018 afa20000 23bd0004
  //   afa40000 23bd0004 afb00000 23bd0004 afb30000 23bd0004 afb40000 23bd0004 afb50000 23bd0004 afb60000
  //   23bd0004 40167000 afb60000 23bd0004 40806000 20160002 20140003 20150001 168020 108100 2149825 132020
  //   20020022 c 1600fffa 295a022 1680fff7 20160001 40966000 23bdfffc 8fb60000 40967000 23bdfffc 8fb60000
  //   23bdfffc 8fb50000 23bdfffc 8fb40000 23bdfffc 8fb30000 23bdfffc 8fb00000 23bdfffc 8fa40000 23bdfffc
  //   8fa20000 42000018 afa20000 23bd0004 afa40000 23bd0004 afb00000 23bd0004 afb30000 23bd0004 afb40000
  //   23bd0004 afb50000 23bd0004 afb60000 23bd0004 40167000 afb60000 23bd0004 40806000 20160003 20140003
  //   20150001 168020 108100 2149825 132020 20020022 c 1600fffa 295a022 1680fff7 20160001 40966000
  //   23bdfffc 8fb60000 40967000 23bdfffc 8fb60000 23bdfffc 8fb50000 23bdfffc 8fb40000 23bdfffc 8fb30000
  //   23bdfffc 8fb00000 23bdfffc 8fa40000 23bdfffc 8fa20000 42000018
  //   rd
  //   OP
  //   Func
  //   rt
  //   rd
  //   JMP
  //   Beq
  //   JR
  //   Bne
  //   ERET
  //   OP
  //   JAL
  //   Func
  //   Syscall
  //   MemToReg
  //   MemWrite
  //   AluOP
  //   AluSrcB
  //   RegWrite
  //   RegDst
  //   为方便自动评测，需要输出PC，IR，寄存器堆写如数据RDin
  //   RAM写使能MemWrite、RAM写入数据MDin等信号
  //   控制位
  //   暂停节拍，不能为0
  //   戳工具置1进入计数暂停模式，ctrl+k时钟自动运行到对应节拍暂停
  //   ctrl+k关闭时钟连续运行，将控制位置零，进入单步调试模式调试
  //   用这个时钟源需要去掉电路中的其他时钟源
  //   可计数暂停的时钟源
endmodule

module MIPS_Coprocessor__Regifile (
  input  [31:0] Din,
  input  [4:0] R1_num,
  input  Clk,
  input  ERET,
  input  WE,
  input  in_6,
  input  [31:0] EPC,
  input  [4:0] W_num,
  input  [31:0] INT_STATUS,
  output [31:0] out_10,
  output [31:0] out_11,
  output [31:0] out_12,
  output [31:0] out_13,
  output [31:0] out_14,
  output [31:0] out_15,
  output [31:0] out_16,
  output [31:0] out_17,
  output [31:0] out_18,
  output [31:0] out_19,
  output [31:0] out_20,
  output [31:0] out_21,
  output [31:0] INT_STATUS_2,
  output [31:0] out_23,
  output [31:0] EPC_2,
  output [31:0] out_25,
  output [31:0] out_26,
  output [31:0] out_27,
  output [31:0] out_28,
  output [31:0] out_29,
  output [31:0] out_30,
  output [31:0] out_31,
  output [31:0] out_32,
  output [31:0] out_33,
  output [31:0] out_34,
  output [31:0] out_35,
  output [31:0] out_36,
  output [31:0] out_37,
  output [31:0] out_38,
  output [31:0] out_39,
  output [31:0] out_40,
  output [31:0] out_41,
  output [31:0] R1
);

  wire demultiplexer_1_out0, demultiplexer_1_out1, demultiplexer_1_out2, demultiplexer_1_out3,
       demultiplexer_1_out4, demultiplexer_1_out5, demultiplexer_1_out6, demultiplexer_1_out7,
       demultiplexer_1_out8, demultiplexer_1_out9, demultiplexer_1_out10, demultiplexer_1_out11,
       demultiplexer_1_out12, demultiplexer_1_out13, demultiplexer_1_out14, demultiplexer_1_out15,
       demultiplexer_1_out16, demultiplexer_1_out17, demultiplexer_1_out18, demultiplexer_1_out19,
       demultiplexer_1_out20, demultiplexer_1_out21, demultiplexer_1_out22, demultiplexer_1_out23,
       demultiplexer_1_out24, demultiplexer_1_out25, demultiplexer_1_out26, demultiplexer_1_out27,
       demultiplexer_1_out28, demultiplexer_1_out29, demultiplexer_1_out30, demultiplexer_1_out31, or_1_out,
       or_2_out, or_3_out, or_4_out;
  wire [31:0] multiplexer_1_out, multiplexer_2_out;

  Register #(.width(32), .trigger("rising"), .Select("low")) register_1 (
    .D(Din), .en(demultiplexer_1_out0), .Q(out_10), .clk(Clk));  // open: clr
  Register #(.width(32), .trigger("rising"), .Select("low")) register_2 (
    .D(Din), .en(demultiplexer_1_out1), .Q(out_11), .clk(Clk));  // open: clr
  Register #(.width(32), .trigger("rising"), .Select("low")) register_3 (
    .D(Din), .en(demultiplexer_1_out2), .Q(out_12), .clk(Clk));  // open: clr
  Register #(.width(32), .trigger("rising"), .Select("low")) register_4 (
    .D(Din), .en(demultiplexer_1_out3), .Q(out_13), .clk(Clk));  // open: clr
  Register #(.width(32), .trigger("rising"), .Select("low")) register_5 (
    .D(Din), .en(demultiplexer_1_out4), .Q(out_14), .clk(Clk));  // open: clr
  Register #(.width(32), .trigger("rising"), .Select("low")) register_6 (
    .D(Din), .en(demultiplexer_1_out5), .Q(out_15), .clk(Clk));  // open: clr
  Register #(.width(32), .trigger("rising"), .Select("low")) register_7 (
    .D(Din), .en(demultiplexer_1_out6), .Q(out_16), .clk(Clk));  // open: clr
  Register #(.width(32), .trigger("rising"), .Select("low")) register_8 (
    .D(Din), .en(demultiplexer_1_out7), .Q(out_17), .clk(Clk));  // open: clr
  Register #(.width(32), .trigger("rising"), .Select("low")) register_9 (
    .D(Din), .en(demultiplexer_1_out8), .Q(out_18), .clk(Clk));  // open: clr
  Register #(.width(32), .trigger("rising"), .Select("low")) register_10 (
    .D(Din), .en(demultiplexer_1_out9), .Q(out_19), .clk(Clk));  // open: clr
  Register #(.width(32), .trigger("rising"), .Select("low")) register_11 (
    .D(Din), .en(demultiplexer_1_out10), .Q(out_20), .clk(Clk));  // open: clr
  or or_1 (or_1_out, in_6, ERET);
  Register #(.width(32), .trigger("rising"), .Select("low")) register_12 (
    .D(Din), .en(demultiplexer_1_out11), .Q(out_21), .clk(Clk));  // open: clr
  Multiplexer #(.select(1), .width(32), .disabled("Z"), .enable("false")) multiplexer_1 (
    .in0(Din), .in1(INT_STATUS), .out(multiplexer_1_out), .sel(or_1_out));
  Register #(.width(32), .trigger("rising"), .Select("low")) register_13 (
    .D(multiplexer_1_out), .en(or_2_out), .Q(INT_STATUS_2), .clk(Clk));  // open: clr
  or or_2 (or_2_out, or_3_out, demultiplexer_1_out12);
  or or_3 (or_3_out, ERET, in_6);
  Register #(.width(32), .trigger("rising"), .Select("low")) register_14 (
    .D(Din), .en(demultiplexer_1_out13), .Q(out_23), .clk(Clk));  // open: clr
  Multiplexer #(.select(1), .width(32), .disabled("Z"), .enable("false")) multiplexer_2 (
    .in0(Din), .in1(EPC), .out(multiplexer_2_out), .sel(in_6));
  Register #(.width(32), .trigger("rising"), .Select("low")) register_15 (
    .D(multiplexer_2_out), .en(or_4_out), .Q(EPC_2), .clk(Clk));  // open: clr
  or or_4 (or_4_out, in_6, demultiplexer_1_out14);
  Register #(.width(32), .trigger("rising"), .Select("low")) register_16 (
    .D(Din), .en(demultiplexer_1_out15), .Q(out_25), .clk(Clk));  // open: clr
  Register #(.width(32), .trigger("rising"), .Select("low")) register_17 (
    .D(Din), .en(demultiplexer_1_out16), .Q(out_26), .clk(Clk));  // open: clr
  Register #(.width(32), .trigger("rising"), .Select("low")) register_18 (
    .D(Din), .en(demultiplexer_1_out17), .Q(out_27), .clk(Clk));  // open: clr
  Register #(.width(32), .trigger("rising"), .Select("low")) register_19 (
    .D(Din), .en(demultiplexer_1_out18), .Q(out_28), .clk(Clk));  // open: clr
  Register #(.width(32), .trigger("rising"), .Select("low")) register_20 (
    .D(Din), .en(demultiplexer_1_out19), .Q(out_29), .clk(Clk));  // open: clr
  Register #(.width(32), .trigger("rising"), .Select("low")) register_21 (
    .D(Din), .en(demultiplexer_1_out20), .Q(out_30), .clk(Clk));  // open: clr
  Register #(.width(32), .trigger("rising"), .Select("low")) register_22 (
    .D(Din), .en(demultiplexer_1_out21), .Q(out_31), .clk(Clk));  // open: clr
  Register #(.width(32), .trigger("rising"), .Select("low")) register_23 (
    .D(Din), .en(demultiplexer_1_out22), .Q(out_32), .clk(Clk));  // open: clr
  Register #(.width(32), .trigger("rising"), .Select("low")) register_24 (
    .D(Din), .en(demultiplexer_1_out23), .Q(out_33), .clk(Clk));  // open: clr
  Register #(.width(32), .trigger("rising"), .Select("low")) register_25 (
    .D(Din), .en(demultiplexer_1_out24), .Q(out_34), .clk(Clk));  // open: clr
  Register #(.width(32), .trigger("rising"), .Select("low")) register_26 (
    .D(Din), .en(demultiplexer_1_out25), .Q(out_35), .clk(Clk));  // open: clr
  Register #(.width(32), .trigger("rising"), .Select("low")) register_27 (
    .D(Din), .en(demultiplexer_1_out26), .Q(out_36), .clk(Clk));  // open: clr
  Register #(.width(32), .trigger("rising"), .Select("low")) register_28 (
    .D(Din), .en(demultiplexer_1_out27), .Q(out_37), .clk(Clk));  // open: clr
  Register #(.width(32), .trigger("rising"), .Select("low")) register_29 (
    .D(Din), .en(demultiplexer_1_out28), .Q(out_38), .clk(Clk));  // open: clr
  Register #(.width(32), .trigger("rising"), .Select("low")) register_30 (
    .D(Din), .en(demultiplexer_1_out29), .Q(out_39), .clk(Clk));  // open: clr
  Register #(.width(32), .trigger("rising"), .Select("low")) register_31 (
    .D(Din), .en(demultiplexer_1_out30), .Q(out_40), .clk(Clk));  // open: clr
  Register #(.width(32), .trigger("rising"), .Select("low")) register_32 (
    .D(Din), .en(demultiplexer_1_out31), .Q(out_41), .clk(Clk));  // open: clr
  Demultiplexer #(.select(5), .width(1), .tristate("false"), .disabled("Z"), .enable("false")) demultiplexer_1 (
    .out0(demultiplexer_1_out0), .out1(demultiplexer_1_out1), .out2(demultiplexer_1_out2),
    .out3(demultiplexer_1_out3), .out4(demultiplexer_1_out4), .out5(demultiplexer_1_out5),
    .out6(demultiplexer_1_out6), .out7(demultiplexer_1_out7), .out8(demultiplexer_1_out8),
    .out9(demultiplexer_1_out9), .out10(demultiplexer_1_out10), .out11(demultiplexer_1_out11),
    .out12(demultiplexer_1_out12), .out13(demultiplexer_1_out13), .out14(demultiplexer_1_out14),
    .out15(demultiplexer_1_out15), .out16(demultiplexer_1_out16), .out17(demultiplexer_1_out17),
    .out18(demultiplexer_1_out18), .out19(demultiplexer_1_out19), .out20(demultiplexer_1_out20),
    .out21(demultiplexer_1_out21), .out22(demultiplexer_1_out22), .out23(demultiplexer_1_out23),
    .out24(demultiplexer_1_out24), .out25(demultiplexer_1_out25), .out26(demultiplexer_1_out26),
    .out27(demultiplexer_1_out27), .out28(demultiplexer_1_out28), .out29(demultiplexer_1_out29),
    .out30(demultiplexer_1_out30), .out31(demultiplexer_1_out31), .in(WE), .sel(W_num));
  Multiplexer #(.select(5), .width(32), .disabled("Z"), .enable("false")) multiplexer_3 (
    .in0(out_10), .in1(out_11), .in2(out_12), .in3(out_13), .in4(out_14), .in5(out_15), .in6(out_16),
    .in7(out_17), .in8(out_18), .in9(out_19), .in10(out_20), .in11(out_21), .in12(INT_STATUS_2),
    .in13(out_23), .in14(EPC_2), .in15(out_25), .in16(out_26), .in17(out_27), .in18(out_28), .in19(out_29),
    .in20(out_30), .in21(out_31), .in22(out_32), .in23(out_33), .in24(out_34), .in25(out_35), .in26(out_36),
    .in27(out_37), .in28(out_38), .in29(out_39), .in30(out_40), .in31(out_41), .out(R1), .sel(R1_num));

  // Other names for the same wires on the sheet: 中断请求 = in_6
endmodule

module \重定向流水线_中断  (
  output RegWrite,
  output MemWrite,
  output [31:0] IF_PC,
  output [31:0] ID_PC,
  output [31:0] EX_PC,
  output [31:0] M_PC,
  output [31:0] WB_PC,
  output [31:0] RDin,
  output [31:0] MDin,
  output [31:0] LedData
);

  wire and_1_out, and_3_out, and_4_out, and_5_out, and_6_out, and_9_out, BLEZ_LESS, CLK, CLK_C, clock_1_out,
       clock_2_out, comparator_1_eq, comparator_2_eq, comparator_3_eq, comparator_3_lt, comparator_4_eq,
       comparator_5_eq, comparator_6_eq, comparator_8_eq, comparator_9_eq, comparator_10_eq,
       comparator_11_eq, comparator_12_eq, controlled_inverter_1_out, controlled_inverter_2_out,
       controlled_inverter_3_out, d_ff_2_q, equal, EX_ERET, EX_MemToReg, EX_MFC0, EX_MTC0, EX_RegWrite,
       EX_valid, Exit, Go, IF_stall, int_change, IR1, IR2, IR3, MEM_MemToReg, MEM_RegWrite, nand_1_out,
       not_1_out, or_1_out, or_2_out, or_3_out, or_4_out, or_5_out, or_7_out, or_8_out, or_9_out, or_10_out,
       or_11_out, or_12_out, or_13_out, or_14_out, or_15_out, Pause, register_1_q, RST, Stop, W1, W2, W3,
       \中断请求 , \单周期_单级中断中断控制器_1_intr , \单周期硬布线控制器_1_alu_src , \单周期硬布线控制器_1_beq , \单周期硬布线控制器_1_blez ,
       \单周期硬布线控制器_1_bne , \单周期硬布线控制器_1_eret , \单周期硬布线控制器_1_jmp , \单周期硬布线控制器_1_jr , \单周期硬布线控制器_1_lbu ,
       \单周期硬布线控制器_1_memtoreg , \单周期硬布线控制器_1_memwrite , \单周期硬布线控制器_1_regwrite , \单周期硬布线控制器_1_signedext ,
       \单周期硬布线控制器_1_syscall , \条件分支成功 , \气泡流水接口_ex_mem_1_eret_out , \气泡流水接口_ex_mem_1_jal_out ,
       \气泡流水接口_ex_mem_1_lbu_out , \气泡流水接口_ex_mem_1_regdst_out , \气泡流水接口_ex_mem_1_传输状态out_表明当前传输数据有效 ,
       \气泡流水接口_id_ex_1_alusrcb_out , \气泡流水接口_id_ex_1_beq_out , \气泡流水接口_id_ex_1_blez_out ,
       \气泡流水接口_id_ex_1_bne_out , \气泡流水接口_id_ex_1_jal_out , \气泡流水接口_id_ex_1_jmp_out ,
       \气泡流水接口_id_ex_1_lbu_out , \气泡流水接口_id_ex_1_memwrite_out , \气泡流水接口_id_ex_1_regdst_out ,
       \气泡流水接口_id_ex_1_syscall_out , \气泡流水接口_if_id_1_传输状态out_表明当前传输数据有效 , \气泡流水接口_mem_wb_1_lbu_out ,
       \源寄存器使用情况_1_r1_used , \源寄存器使用情况_1_r2_used ;
  wire [1:0] pull_resistor_2_node, \单周期_单级中断中断控制器_1_intno , \单周期硬布线控制器_1_regdst ,
       \气泡流水接口_id_ex_1_r1forward_out , \气泡流水接口_id_ex_1_r2forward_out , \气泡流水接口_mem_wb_1_memtoreg_out ,
       \硬件堆栈_no_1_输出 , \重定向流水线_forword_1_forword1 , \重定向流水线_forword_1_forword2 ;
  wire [1:1] \气泡流水接口_id_ex_1_jr_out ;
  wire [3:0] \单周期硬布线控制器_1_alu_op , \气泡流水接口_id_ex_1_aluop_out ;
  wire [4:0] EX_RegWrite_num, ID_R1_num, ID_R2_num, MEM_RegWrite_num, multiplexer_5_out, WB_RegWrite_num;
  wire [12:0] CNT_num;
  wire [15:0] \LoadUse次数 , \总周期数 , \插入气泡数 , \无条件分支数 , \条件分支成功数 ;
  wire [31:0] adder_1_out, adder_2_out, adder_3_out, adder_4_out, bit_extender_1_out, bit_extender_2_out,
       bit_extender_3_out, EX_IR, EX_PC_intr, ID_IR, IF_IR, IRQ_PC, JMP_EX, MEM_AluRst, MEM_IR,
       multiplexer_1_out, multiplexer_2_out, multiplexer_6_out, multiplexer_7_out, multiplexer_8_out,
       multiplexer_9_out, multiplexer_12_out, multiplexer_13_out, pull_resistor_3_node, ram_1_data, WB_IR,
       \气泡流水接口_id_ex_1_imm_out , \气泡流水接口_id_ex_1_r1_out , \气泡流水接口_id_ex_1_r2_out ,
       \气泡流水接口_mem_wb_1_alurst_out , \气泡流水接口_mem_wb_1_mem_out , \气泡流水线_mips_regifile_1_r1 ,
       \气泡流水线_mips_regifile_1_r2 ;
  wire [31:1] mips_alu_1_result;
  wire [31:8] pull_resistor_4_node, pull_resistor_5_node, pull_resistor_6_node, pull_resistor_7_node;

  Button \u_总复位  (.out(RST));
  Button _1 (.out(IR1));
  Button _2 (.out(IR2));
  Button _3 (.out(IR3));
  // Probe on \总周期数 
  // Probe on \总周期数 
  Button \u_继续运行  (.out(Go));
  LED #(.active("true")) led_1 (.in(W1));
  LED #(.active("true")) led_2 (.in(W2));
  LED #(.active("true")) led_3 (.in(W3));
  // Probe on adder_1_out
  Hex_Digit_Display hex_digit_display_1 (.value(LedData[31:28]));  // open: dp
  // Probe on IF_PC[19:0]
  // Mips_Probe mips_probe_1: pin names not known; wires that end beside it: IF_IR
  or or_1 (or_1_out, Pause, Exit);
  or or_2 (or_2_out, and_1_out, RST);
  and and_1 (and_1_out, ~Exit, Go);  // AND_Gate
  Multiplexer #(.select(1), .width(32), .disabled("Z"), .enable("false")) multiplexer_1 (
    .in0(adder_1_out), .in1(multiplexer_2_out), .out(multiplexer_1_out), .sel(or_4_out));
  // Probe on multiplexer_2_out
  Multiplexer #(.select(2), .width(32), .disabled("Z"), .enable("false")) multiplexer_2 (
    .in0(JMP_EX), .in1(IRQ_PC), .in2(EX_PC_intr), .in3(EX_PC_intr), .out(multiplexer_2_out),
    .sel({EX_ERET, \中断请求 }));
  Hex_Digit_Display hex_digit_display_2 (.value(LedData[23:20]));  // open: dp
  Hex_Digit_Display hex_digit_display_3 (.value(LedData[27:24]));  // open: dp
  // Probe on ID_PC[19:0]
  // Mips_Probe mips_probe_2: pin names not known; wires that end beside it: ID_IR
  D_Flip_Flop #(.trigger("rising"), .Pre_Clr_Positions("ABOVE_BELOW"), .NegatePresetClear("false"), .enable("false"), .NewFFLayout("true")) d_ff_1 (
    .clk(or_1_out), .D(1'b1), .Qn(Stop), .reset(or_2_out));  // open: Q, preset
  not not_1 (not_1_out, IF_stall);
  Register #(.width(32), .trigger("rising"), .Select("low")) PC (
    .D(multiplexer_1_out), .en(not_1_out), .Q(IF_PC), .clk(CLK), .clr(RST));
  Hex_Digit_Display hex_digit_display_4 (.value(LedData[15:12]));  // open: dp
  Hex_Digit_Display hex_digit_display_5 (.value(LedData[19:16]));  // open: dp
  Counter #(.width(16), .max('hffff), .ongoal("wrap"), .trigger("rising"), .behavior("new")) counter_1 (
    .count(Stop), .Q(\总周期数 ), .clk(CLK), .clr(RST));  // open: load, D, carry, preset, down
  // Probe on IF_PC
  Hex_Digit_Display hex_digit_display_6 (.value(LedData[7:4]));  // open: dp
  Hex_Digit_Display hex_digit_display_7 (.value(LedData[11:8]));  // open: dp
  Clock #(.highDuration(1), .lowDuration(1)) clock_1 (.out(clock_1_out));
  // Probe on EX_PC[19:0]
  // Mips_Probe mips_probe_3: pin names not known; wires that end beside it: clock_1_out, CLK_C, EX_IR
  and and_2 (CLK, CLK_C, Stop);
  Adder #(.width(32)) adder_1 (.a(IF_PC), .b(32'h4), .out(adder_1_out), .cin(1'b0));  // open: cout
  Hex_Digit_Display hex_digit_display_8 (.value(LedData[3:0]));  // open: dp
  ROM #(.addrWidth(10), .dataWidth(32), .Select("high")) rom_1 (.addr(IF_PC[11:2]), .data(IF_IR));
  // Probe on \总周期数 
  // Probe on M_PC[19:0]
  // Mips_Probe mips_probe_4: pin names not known; wires that end beside it: MEM_IR
  \气泡流水接口_IF_ID  \u_气泡流水接口_if_id_1  (
    .IR_in(IF_IR), .\传输状态In_表明当前传输数据有效 (1'b1), .CLK(CLK), .IR_out(ID_IR),
    .\传输状态Out_表明当前传输数据有效 (\气泡流水接口_if_id_1_传输状态out_表明当前传输数据有效 ), .\同步清零_气泡_高电平有效 (or_4_out),
    .\使能端_低电平有效_stall_高电平有效 (IF_stall), .PC_in(IF_PC), .PC_out(ID_PC));
  // Probe on \总周期数 
  // Probe on \无条件分支数 
  // Probe on \条件分支成功数 
  // Probe on \插入气泡数 
  // Probe on \LoadUse次数 
  // Probe on IF_PC[11:0]
  // Probe on WB_PC[19:0]
  // Mips_Probe mips_probe_5: pin names not known; wires that end beside it: WB_IR
  \单周期硬布线控制器  \u_单周期硬布线控制器_1  (
    .Func(ID_IR[5:0]), .OP(ID_IR[31:26]), .ALU_OP(\单周期硬布线控制器_1_alu_op ), .MemToReg(\单周期硬布线控制器_1_memtoreg ),
    .MemWrite(\单周期硬布线控制器_1_memwrite ), .ALU_SRC(\单周期硬布线控制器_1_alu_src ), .RegWrite(\单周期硬布线控制器_1_regwrite ),
    .SysCALL(\单周期硬布线控制器_1_syscall ), .SignedExt(\单周期硬布线控制器_1_signedext ), .RegDst(\单周期硬布线控制器_1_regdst [0]),
    .JR(\单周期硬布线控制器_1_jr ), .JMP(\单周期硬布线控制器_1_jmp ), .Beq(\单周期硬布线控制器_1_beq ), .JAL(\单周期硬布线控制器_1_regdst [1]),
    .Bne(\单周期硬布线控制器_1_bne ), .ERET(\单周期硬布线控制器_1_eret ), .LBU(\单周期硬布线控制器_1_lbu ), .BLEZ(\单周期硬布线控制器_1_blez ));
  Multiplexer #(.select(1), .width(5), .disabled("Z"), .enable("false")) multiplexer_3 (
    .in0(ID_IR[25:21]), .in1(5'b00010), .out(ID_R1_num), .sel(\单周期硬布线控制器_1_syscall ));
  Multiplexer #(.select(1), .width(5), .disabled("Z"), .enable("false")) multiplexer_4 (
    .in0(ID_IR[20:16]), .in1(5'b00100), .out(ID_R2_num), .sel(\单周期硬布线控制器_1_syscall ));
  Comparator #(.width(32), .mode("unsigned")) comparator_1 (
    .a(ID_IR), .b(32'h40800000), .eq(comparator_1_eq));  // open: gt, lt
  Comparator #(.width(32), .mode("unsigned")) comparator_2 (
    .a(ID_IR), .b(32'h40000000), .eq(comparator_2_eq));  // open: gt, lt
  // Probe on EX_PC[11:0]
  // Probe on ID_PC[11:0]
  \源寄存器使用情况  \u_源寄存器使用情况_1  (
    .OP0(ID_IR[26]), .OP1(ID_IR[27]), .OP2(ID_IR[28]), .OP3(ID_IR[29]), .OP4(ID_IR[30]), .OP5(ID_IR[31]),
    .F0(ID_IR[0]), .F1(ID_IR[1]), .F2(ID_IR[2]), .F3(ID_IR[3]), .F4(ID_IR[4]), .F5(ID_IR[5]),
    .R1_Used(\源寄存器使用情况_1_r1_used ), .R2_Used(\源寄存器使用情况_1_r2_used ));
  // Probe on M_PC[11:0]
  D_Flip_Flop #(.trigger("high"), .Pre_Clr_Positions("LEGACY"), .NegatePresetClear("false"), .enable("true"), .NewFFLayout("false")) d_ff_2 (.Q(d_ff_2_q));  // open: clk, D, Qn, preset, en, reset
  // Probe on 13'h12
  \Load_Use相关  \load_use相关_1  (
    .R1_Used(\源寄存器使用情况_1_r1_used ), .R2_Used(\源寄存器使用情况_1_r2_used ), .EX_RegWrite_num(EX_RegWrite_num),
    .R1_num(ID_R1_num), .R2_num(ID_R2_num), .EX_MemToReg(EX_MemToReg), .\Load_Use相关 (IF_stall));
  \重定向流水线_Forword  \u_重定向流水线_forword_1  (
    .Reg1_Used(\源寄存器使用情况_1_r1_used ), .Reg2_Used(\源寄存器使用情况_1_r2_used ), .EX_RegWrite_num(EX_RegWrite_num),
    .MEM_RegWrite_num(MEM_RegWrite_num), .Reg1_num(ID_R1_num), .Reg2_num(ID_R2_num),
    .EX_RegWrite(EX_RegWrite), .MEM_RegWrite(MEM_RegWrite), .Forword1(\重定向流水线_forword_1_forword1 ),
    .Forword2(\重定向流水线_forword_1_forword2 ));
  // Probe on WB_PC[11:0]
  Comparator #(.width(13), .mode("twosComplement")) comparator_3 (
    .a(CNT_num), .b(13'h12), .eq(comparator_3_eq), .lt(comparator_3_lt));  // open: gt
  Clock #(.highDuration(1), .lowDuration(1)) clock_2 (.out(clock_2_out));
  Counter #(.width(16), .max('hffff), .ongoal("wrap"), .trigger("rising"), .behavior("new")) counter_2 (
    .count(IF_stall), .Q(\LoadUse次数 ), .clk(CLK), .clr(RST));  // open: load, D, carry, preset, down
  \气泡流水线_MIPS_Regifile  \u_气泡流水线_mips_regifile_1  (
    .Din(RDin), .Clk(CLK), .R1(\气泡流水线_mips_regifile_1_r1 ), .R2(\气泡流水线_mips_regifile_1_r2 ), .WE(RegWrite),
    .W_num(WB_RegWrite_num), .R1_num(ID_R1_num), .R2_num(ID_R2_num));
  nand nand_1 (nand_1_out, d_ff_2_q, comparator_3_eq);
  Counter #(.width(13), .max('h1fff), .ongoal("stay"), .trigger("rising"), .behavior("old")) counter_3 (
    .count(comparator_3_lt), .Q(CNT_num), .clk(clock_2_out));  // open: load, D, carry, clr, preset
  assign bit_extender_1_out = {{16{1'b0}}, ID_IR[15:0]};  // Bit_Extender bit_extender_1
  assign bit_extender_2_out = {{16{ID_IR[15]}}, ID_IR[15:0]};  // Bit_Extender bit_extender_2
  Multiplexer #(.select(2), .width(5), .disabled("Z"), .enable("false")) multiplexer_5 (
    .in0(ID_IR[15:11]), .in1(ID_IR[20:16]), .in2({5{1'b1}}), .in3({5{1'b1}}), .out(multiplexer_5_out),
    .sel(\单周期硬布线控制器_1_regdst ));
  assign CLK_C = nand_1_out ? clock_2_out : 1'bz;  // Controlled_Buffer controlled_buffer_1
  or or_3 (or_3_out, \中断请求 , EX_ERET, \条件分支成功 );
  or or_4 (or_4_out, or_3_out, \气泡流水接口_id_ex_1_jmp_out );
  Multiplexer #(.select(1), .width(32), .disabled("Z"), .enable("false")) multiplexer_6 (
    .in0(bit_extender_1_out), .in1(bit_extender_2_out), .out(multiplexer_6_out), .sel(\单周期硬布线控制器_1_signedext ));
  Pull_Resistor #(.pull(1)) pull_resistor_1 (.node(CLK_C));
  Counter #(.width(16), .max('hffff), .ongoal("wrap"), .trigger("rising"), .behavior("new")) \u_无条件分支数  (
    .count(\气泡流水接口_id_ex_1_jmp_out ), .Q(\无条件分支数 ), .clk(CLK), .clr(RST));  // open: load, D, carry, preset, down
  or or_5 (or_5_out, or_3_out, IF_stall, \气泡流水接口_id_ex_1_jmp_out );
  \气泡流水接口_ID_EX  \u_气泡流水接口_id_ex_1  (
    .IR_in(ID_IR), .\传输状态In_表明当前传输数据有效 (\气泡流水接口_if_id_1_传输状态out_表明当前传输数据有效 ), .CLK(CLK), .IR_out(EX_IR),
    .\传输状态Out_表明当前传输数据有效 (EX_valid), .\同步清零_气泡_高电平有效 (or_5_out), .\使能端_低电平有效_stall_高电平有效 (1'b0),
    .PC_in(ID_PC), .PC_out(EX_PC), .JMP_in(\单周期硬布线控制器_1_jmp ), .JMP_out(\气泡流水接口_id_ex_1_jmp_out ),
    .MemToReg_in(\单周期硬布线控制器_1_memtoreg ), .MemToReg_out(EX_MemToReg), .MemWrite_in(\单周期硬布线控制器_1_memwrite ),
    .MemWrite_out(\气泡流水接口_id_ex_1_memwrite_out ), .AluOp_in(\单周期硬布线控制器_1_alu_op ),
    .AluOp_out(\气泡流水接口_id_ex_1_aluop_out ), .AluSrcB_in(\单周期硬布线控制器_1_alu_src ),
    .AluSrcB_out(\气泡流水接口_id_ex_1_alusrcb_out ), .RegWrite_in(\单周期硬布线控制器_1_regwrite ),
    .RegWrite_out(EX_RegWrite), .RegDst_in(\单周期硬布线控制器_1_regdst [0]),
    .RegDst_out(\气泡流水接口_id_ex_1_regdst_out ), .R1_in(\气泡流水线_mips_regifile_1_r1 ),
    .R1_out(\气泡流水接口_id_ex_1_r1_out ), .R2_in(\气泡流水线_mips_regifile_1_r2 ), .R2_out(\气泡流水接口_id_ex_1_r2_out ),
    .Imm__in(multiplexer_6_out), .Imm_out(\气泡流水接口_id_ex_1_imm_out ), .Syscall_in(\单周期硬布线控制器_1_syscall ),
    .Syscall_out(\气泡流水接口_id_ex_1_syscall_out ), .Beq_in(\单周期硬布线控制器_1_beq ),
    .Beq_out(\气泡流水接口_id_ex_1_beq_out ), .JR_in(\单周期硬布线控制器_1_jr ), .JR_out(\气泡流水接口_id_ex_1_jr_out [1]),
    .Bne_in(\单周期硬布线控制器_1_bne ), .Bne_out(\气泡流水接口_id_ex_1_bne_out ), .SignedExt_in(\单周期硬布线控制器_1_signedext ),
    .ERET_in(\单周期硬布线控制器_1_eret ), .ERET_out(EX_ERET), .LBU_in(\单周期硬布线控制器_1_lbu ),
    .LBU_out(\气泡流水接口_id_ex_1_lbu_out ), .BLEZ_in(\单周期硬布线控制器_1_blez ), .BLEZ_out(\气泡流水接口_id_ex_1_blez_out ),
    .JAL_in(\单周期硬布线控制器_1_regdst [1]), .JAL_out(\气泡流水接口_id_ex_1_jal_out ), .RegWrite__in(multiplexer_5_out),
    .RegWrite__out(EX_RegWrite_num), .R1Forward_in(\重定向流水线_forword_1_forword1 ),
    .R1Forward_out(\气泡流水接口_id_ex_1_r1forward_out ), .R2Forward_in(\重定向流水线_forword_1_forword2 ),
    .R2Forward_out(\气泡流水接口_id_ex_1_r2forward_out ), .MFC0_in(comparator_1_eq), .MFC0_out(EX_MTC0),
    .MTC0_in(comparator_2_eq), .MTC0_out(EX_MFC0));  // open: SignedExt_out
  and and_3 (and_3_out, \气泡流水接口_id_ex_1_beq_out , equal);
  and and_4 (and_4_out, \气泡流水接口_id_ex_1_bne_out , ~equal);  // AND_Gate
  and and_5 (and_5_out, \气泡流水接口_id_ex_1_blez_out , BLEZ_LESS);
  Multiplexer #(.select(2), .width(32), .disabled("Z"), .enable("false")) multiplexer_7 (
    .in0(\气泡流水接口_id_ex_1_r1_out ), .in1(RDin), .in2(MEM_AluRst), .out(multiplexer_7_out),
    .sel(\气泡流水接口_id_ex_1_r1forward_out ));  // open: in3
  Multiplexer #(.select(2), .width(32), .disabled("Z"), .enable("false")) multiplexer_8 (
    .in0(\气泡流水接口_id_ex_1_r2_out ), .in1(RDin), .in2(MEM_AluRst), .out(multiplexer_8_out),
    .sel(\气泡流水接口_id_ex_1_r2forward_out ));  // open: in3
  or or_6 (\条件分支成功 , and_3_out, and_4_out, and_5_out);
  or or_7 (or_7_out, EX_MFC0, EX_ERET);
  or or_8 (or_8_out, EX_MTC0, \中断请求 );
  or or_9 (or_9_out, EX_MFC0, EX_ERET);
  or or_10 (or_10_out, EX_MTC0, \中断请求 );
  Counter #(.width(16), .max('hffff), .ongoal("wrap"), .trigger("rising"), .behavior("new")) \u_条件成功分支数  (
    .count(\条件分支成功 ), .Q(\条件分支成功数 ), .clk(CLK), .clr(RST));  // open: load, D, carry, preset, down
  Adder #(.width(32)) adder_2 (.a(32'h4), .b(EX_PC), .out(adder_2_out));  // open: cin, cout
  Pull_Resistor #(.pull(0)) pull_resistor_2 (.node({EX_IR[15:0], pull_resistor_2_node}));
  Multiplexer #(.select(1), .width(32), .disabled("Z"), .enable("false")) multiplexer_9 (
    .in0(multiplexer_8_out), .in1(\气泡流水接口_id_ex_1_imm_out ), .out(multiplexer_9_out),
    .sel(\气泡流水接口_id_ex_1_alusrcb_out ));
  or or_11 (or_11_out, or_7_out, or_8_out);
  and and_6 (and_6_out, ~or_9_out, or_10_out);  // AND_Gate
  Pull_Resistor #(.pull(0)) pull_resistor_3 (.node({pull_resistor_3_node[31:28], EX_IR[25:0], pull_resistor_3_node[1:0]}));
  Adder #(.width(32)) adder_3 (.a(adder_2_out), .b(bit_extender_3_out), .out(adder_3_out));  // open: cin, cout
  assign bit_extender_3_out = {{14{EX_IR[15]}}, {EX_IR[15:0], pull_resistor_2_node}};  // Bit_Extender bit_extender_3
  and and_7 (Pause, \气泡流水接口_id_ex_1_syscall_out , comparator_4_eq);
  Comparator #(.width(32), .mode("twosComplement")) comparator_4 (
    .a(32'h32), .b(multiplexer_7_out), .eq(comparator_4_eq));  // open: gt, lt
  and and_8 (Exit, \气泡流水接口_id_ex_1_syscall_out , comparator_5_eq);
  Comparator #(.width(32), .mode("twosComplement")) comparator_5 (
    .a(32'ha), .b(multiplexer_7_out), .eq(comparator_5_eq));  // open: gt, lt
  and and_9 (and_9_out, \气泡流水接口_id_ex_1_syscall_out , comparator_6_eq);
  Comparator #(.width(32), .mode("twosComplement")) comparator_6 (
    .a(32'h22), .b(multiplexer_7_out), .eq(comparator_6_eq));  // open: gt, lt
  Register #(.width(1), .trigger("rising"), .Select("low")) register_1 (
    .D(and_6_out), .en(or_11_out), .Q(register_1_q), .clk(CLK));  // open: clr
  MIPS_ALU mips_alu_1 (
    .X(multiplexer_7_out), .Y(multiplexer_9_out), .AluOP(\气泡流水接口_id_ex_1_aluop_out ), .Equal(equal),
    .Result({mips_alu_1_result, BLEZ_LESS}), .shamt(EX_IR[10:6]));  // open: Result_2
  Register #(.width(32), .trigger("rising"), .Select("low")) register_2 (
    .D(multiplexer_8_out), .en(and_9_out), .Q(LedData), .clk(CLK));  // open: clr
  \硬件堆栈  \u_硬件堆栈_1  (.CLK(CLK), .\输入 (EX_PC), .\读取数据 (EX_ERET), .\输出 (EX_PC_intr), .\数据变化 (or_12_out));
  or or_12 (or_12_out, EX_ERET, \中断请求 );
  and and_10 (\中断请求 , ~register_1_q, EX_valid, int_change, \单周期_单级中断中断控制器_1_intr );  // AND_Gate
  \单周期_单级中断中断控制器  \u_单周期_单级中断中断控制器_1  (
    .CLK(CLK), .Key1(IR1), .Key2(IR2), .Key3(IR3), .Clr(EX_ERET), .EDU_TEST(\硬件堆栈_no_1_输出 ), .IR1W(W1),
    .IR2W(W2), .IR3W(W3), .IntNo(\单周期_单级中断中断控制器_1_intno ), .IntR(\单周期_单级中断中断控制器_1_intr ));
  Multiplexer #(.select(2), .width(32), .disabled("Z"), .enable("false")) multiplexer_10 (
    .in0({pull_resistor_3_node[31:28], EX_IR[25:0], pull_resistor_3_node[1:0]}), .in1(adder_3_out),
    .in2(multiplexer_7_out), .in3(adder_3_out), .out(JMP_EX), .sel({\气泡流水接口_id_ex_1_jr_out [1], \条件分支成功 }));
  Comparator #(.width(2), .mode("unsigned")) comparator_7 (
    .a(\单周期_单级中断中断控制器_1_intno ), .b(\硬件堆栈_no_1_输出 ), .gt(int_change));  // open: eq, lt
  Multiplexer #(.select(2), .width(32), .disabled("Z"), .enable("false")) multiplexer_11 (
    .in1(32'h30ac), .in2(32'h3158), .in3(32'h3204), .out(IRQ_PC), .sel(\单周期_单级中断中断控制器_1_intno ));  // open: in0
  \气泡流水接口_EX_MEM  \u_气泡流水接口_ex_mem_1  (
    .IR_in(EX_IR), .\传输状态In_表明当前传输数据有效 (EX_valid), .CLK(CLK), .IR_out(MEM_IR),
    .\传输状态Out_表明当前传输数据有效 (\气泡流水接口_ex_mem_1_传输状态out_表明当前传输数据有效 ), .\使能端_低电平有效_stall_高电平有效 (1'b0),
    .PC_in(EX_PC), .PC_out(M_PC), .MemToReg_in(EX_MemToReg), .MemToReg_out(MEM_MemToReg),
    .MemWrite_in(\气泡流水接口_id_ex_1_memwrite_out ), .MemWrite_out(MemWrite), .RegWrite_in(EX_RegWrite),
    .RegWrite_out(MEM_RegWrite), .RegDst_in(\气泡流水接口_id_ex_1_regdst_out ),
    .RegDst_out(\气泡流水接口_ex_mem_1_regdst_out ), .AluRst_in({mips_alu_1_result, BLEZ_LESS}),
    .AluRst_out(MEM_AluRst), .Mem_in(multiplexer_8_out), .Mem_out(MDin), .ERET_in(EX_ERET),
    .ERET_out(\气泡流水接口_ex_mem_1_eret_out ), .LBU_in(\气泡流水接口_id_ex_1_lbu_out ),
    .LBU_out(\气泡流水接口_ex_mem_1_lbu_out ), .JAL_in(\气泡流水接口_id_ex_1_jal_out ),
    .JAL_out(\气泡流水接口_ex_mem_1_jal_out ), .RegWrite__in(EX_RegWrite_num), .RegWrite__out(MEM_RegWrite_num));  // open: 同步清零_气泡_高电平有效
  \硬件堆栈_No  \u_硬件堆栈_no_1  (
    .CLK(CLK), .\读取数据 (EX_ERET), .\数据变化 (or_13_out), .\输入 (\单周期_单级中断中断控制器_1_intno ), .\输出 (\硬件堆栈_no_1_输出 ));
  or or_13 (or_13_out, EX_ERET, \中断请求 );
  RAM #(.addrWidth(10), .dataWidth(32), .bus("separate"), .Select("high")) ram_1 (
    .addr(MEM_AluRst[11:2]), .din(MDin), .data(ram_1_data), .str(MemWrite), .clk(CLK));  // open: sel, ld, clr
  \气泡流水接口_MEM_WB  \u_气泡流水接口_mem_wb_1  (
    .IR_in(MEM_IR), .\传输状态In_表明当前传输数据有效 (\气泡流水接口_ex_mem_1_传输状态out_表明当前传输数据有效 ), .CLK(CLK), .IR_out(WB_IR),
    .\使能端_低电平有效_stall_高电平有效 (1'b0), .PC_in(M_PC), .PC_out(WB_PC), .RegWrite_in(MEM_RegWrite),
    .RegWrite_out(RegWrite), .RegDst_in(\气泡流水接口_ex_mem_1_regdst_out ), .Mem_in(ram_1_data),
    .Mem_out(\气泡流水接口_mem_wb_1_mem_out ), .ERET_in(\气泡流水接口_ex_mem_1_eret_out ),
    .JAL_in(\气泡流水接口_ex_mem_1_jal_out ), .JAL_out(\气泡流水接口_mem_wb_1_memtoreg_out [1]),
    .RegWrite__in(MEM_RegWrite_num), .RegWrite__out(WB_RegWrite_num), .MemToReg_in(MEM_MemToReg),
    .MemToReg_out(\气泡流水接口_mem_wb_1_memtoreg_out [0]), .LBU_in(\气泡流水接口_ex_mem_1_lbu_out ),
    .LBU_out(\气泡流水接口_mem_wb_1_lbu_out ), .AluRst_in(MEM_AluRst), .AluRst_out(\气泡流水接口_mem_wb_1_alurst_out ));  // open: 传输状态Out_表明当前传输数据有效, 同步清零_气泡_高电平有效, RegDst_out, ERET_out
  Pull_Resistor #(.pull(0)) pull_resistor_4 (.node({pull_resistor_4_node, \气泡流水接口_mem_wb_1_mem_out [7:0]}));
  Pull_Resistor #(.pull(0)) pull_resistor_5 (.node({pull_resistor_5_node, \气泡流水接口_mem_wb_1_mem_out [15:8]}));
  Pull_Resistor #(.pull(0)) pull_resistor_6 (.node({pull_resistor_6_node, \气泡流水接口_mem_wb_1_mem_out [23:16]}));
  Pull_Resistor #(.pull(0)) pull_resistor_7 (.node({pull_resistor_7_node, \气泡流水接口_mem_wb_1_mem_out [31:24]}));
  Multiplexer #(.select(2), .width(32), .disabled("Z"), .enable("false")) multiplexer_12 (
    .in0({pull_resistor_4_node, \气泡流水接口_mem_wb_1_mem_out [7:0]}),
    .in1({pull_resistor_5_node, \气泡流水接口_mem_wb_1_mem_out [15:8]}),
    .in2({pull_resistor_6_node, \气泡流水接口_mem_wb_1_mem_out [23:16]}),
    .in3({pull_resistor_7_node, \气泡流水接口_mem_wb_1_mem_out [31:24]}), .out(multiplexer_12_out),
    .sel(\气泡流水接口_mem_wb_1_alurst_out [1:0]));
  Multiplexer #(.select(1), .width(32), .disabled("Z"), .enable("false")) multiplexer_13 (
    .in0(\气泡流水接口_mem_wb_1_mem_out ), .in1(multiplexer_12_out), .out(multiplexer_13_out),
    .sel(\气泡流水接口_mem_wb_1_lbu_out ));
  Multiplexer #(.select(2), .width(32), .disabled("Z"), .enable("false")) multiplexer_14 (
    .in0(\气泡流水接口_mem_wb_1_alurst_out ), .in1(multiplexer_13_out), .in2(adder_4_out), .in3(adder_4_out),
    .out(RDin), .sel(\气泡流水接口_mem_wb_1_memtoreg_out ));
  Adder #(.width(32)) adder_4 (.a(WB_PC), .b(32'h4), .out(adder_4_out));  // open: cin, cout
  Comparator #(.width(16), .mode("twosComplement")) comparator_8 (
    .a(16'h258), .b(\总周期数 ), .eq(comparator_8_eq));  // open: gt, lt
  Comparator #(.width(16), .mode("twosComplement")) comparator_9 (
    .a(\总周期数 ), .b(16'h1), .eq(comparator_9_eq));  // open: gt, lt
  Comparator #(.width(16), .mode("twosComplement")) comparator_10 (
    .a(\总周期数 ), .b(16'h4), .eq(comparator_10_eq));  // open: gt, lt
  Comparator #(.width(16), .mode("twosComplement")) comparator_11 (
    .a(\总周期数 ), .b(16'h7), .eq(comparator_11_eq));  // open: gt, lt
  Comparator #(.width(16), .mode("twosComplement")) comparator_12 (
    .a(\总周期数 ), .b(16'h241), .eq(comparator_12_eq));  // open: gt, lt
  or or_14 (or_14_out, comparator_8_eq, comparator_9_eq);
  assign controlled_inverter_1_out = or_14_out ? ~CLK : 1'bz;  // Controlled_Inverter controlled_inverter_1
  assign controlled_inverter_2_out = comparator_10_eq ? ~CLK : 1'bz;  // Controlled_Inverter controlled_inverter_2
  or or_15 (or_15_out, comparator_11_eq, comparator_12_eq);
  assign controlled_inverter_3_out = or_15_out ? ~CLK : 1'bz;  // Controlled_Inverter controlled_inverter_3
  Pull_Resistor #(.pull(0)) pull_resistor_8 (.node(controlled_inverter_1_out));
  Pull_Resistor #(.pull(0)) pull_resistor_9 (.node(controlled_inverter_2_out));
  Pull_Resistor #(.pull(0)) pull_resistor_10 (.node(controlled_inverter_3_out));

  // Other names for the same wires on the sheet: MEM_PC[31:0] = M_PC; WB_RDin[31:0] = RDin; WB_RegWrite = RegWrite

  // Notes on the sheet:
  //   中断源
  //   时空图监测，可删除
  //   中断等待指示
  //   数码管输出
  //   指令存储器
  //   contents of rom_1 (hex, n*v repeats v):
  //   201d07d0 20100001 109fc0 139fc3 8021 2012000c 24160008 26100001 3210000f 20080008 20090001 139900
  //   2709825 132020 20020022 c 1094022 1500fff9 22100001 2018000f 2188024 108700 20080008 20090001 139902
  //   2709825 132021 20020022 c 1094022 1500fff9 108702 2c9b022 12c00001 8000c07 4020 1084027 84400
  //   3508ffff 82021 20020022 c 8000c01 afa20000 23bd0004 afa40000 23bd0004 afb00000 23bd0004 afb30000
  //   23bd0004 afb40000 23bd0004 afb50000 23bd0004 afb60000 23bd0004 40000000 20160001 20140003 20150001
  //   168020 108100 2149825 132020 20020022 c 1600fffa 295a022 1680fff7 40800000 23bdfffc 8fb60000
  //   23bdfffc 8fb50000 23bdfffc 8fb40000 23bdfffc 8fb30000 23bdfffc 8fb00000 23bdfffc 8fa40000 23bdfffc
  //   8fa20000 42000018 afa20000 23bd0004 afa40000 23bd0004 afb00000 23bd0004 afb30000 23bd0004 afb40000
  //   23bd0004 afb50000 23bd0004 afb60000 23bd0004 40000000 20160002 20140003 20150001 168020 108100
  //   2149825 132020 20020022 c 1600fffa 295a022 1680fff7 40800000 23bdfffc 8fb60000 23bdfffc 8fb50000
  //   23bdfffc 8fb40000 23bdfffc 8fb30000 23bdfffc 8fb00000 23bdfffc 8fa40000 23bdfffc 8fa20000 42000018
  //   afa20000 23bd0004 afa40000 23bd0004 afb00000 23bd0004 afb30000 23bd0004 afb40000 23bd0004 afb50000
  //   23bd0004 afb60000 23bd0004 40000000 20160003 20140003 20150001 168020 108100 2149825 132020 20020022
  //   c 1600fffa 295a022 1680fff7 40800000 23bdfffc 8fb60000 23bdfffc 8fb50000 23bdfffc 8fb40000 23bdfffc
  //   8fb30000 23bdfffc 8fb00000 23bdfffc 8fa40000 23bdfffc 8fa20000 42000018
  //   OP
  //   Func
  //   rs
  //   rt
  //   OP
  //   Func
  //   控制位
  //   流水调试日志用
  //   暂停节拍，不能为0
  //   戳工具置1进入计数暂停模式，ctrl+k时钟自动运行到对应节拍暂停
  //   ctrl+k关闭时钟连续运行，将控制位置零，进入单步调试模式调试
  //   rd
  //   可计数暂停的时钟源
  //   为方便自动评测，需要输出流水线各段保存的PC值，注意是PC不是PC+4，另外ID段寄存器写入信息，Mem段内存写入信息也要输出
  //   多级中断测试信号模拟器
endmodule

module \封装正确性测试  (
);

  wire IR1, IR2, IR3, MemW, RegW;
  wire [31:0] EX_PC, ID_PC, IF_PC, IR, LED, MDin, MDinr, MEM_PC, PC, RDin, RDinr, WB_PC;

  \单周期MIPS  \u_单周期mips_1  (
    .RegWrite(RegW), .MemWrite(MemW), .PC(PC), .IR(IR), .RDin(RDin), .MDin(MDin), .LedData(LED));  // open: IR1, IR2, IR3
  \气泡流水线  \u_气泡流水线_1  (
    .RegWrite(RegW), .MemWrite(MemW), .IF_PC(IF_PC), .ID_PC(ID_PC), .EX_PC(EX_PC), .M_PC(MEM_PC),
    .WB_PC(WB_PC), .RDin(RDinr), .MDin(MDinr), .LedData(LED));
  \单周期MIPS_单级中断  \u_单周期mips_单级中断_1  (
    .IR1(IR1), .IR2(IR2), .IR3(IR3), .RegWrite(RegW), .MemWrite(MemW), .PC(PC), .IR(IR), .RDin(RDin),
    .MDin(MDin), .LedData(LED));
  \理想流水线  \u_理想流水线_1  (
    .RegWrite(RegW), .MemWrite(MemW), .IF_PC(IF_PC), .ID_PC(ID_PC), .EX_PC(EX_PC), .M_PC(MEM_PC),
    .WB_PC(WB_PC), .RDin(RDinr), .MDin(MDinr), .LedData(LED));
  \重定向流水线  \u_重定向流水线_1  (
    .RegWrite(RegW), .MemWrite(MemW), .IF_PC(IF_PC), .ID_PC(ID_PC), .EX_PC(EX_PC), .M_PC(MEM_PC),
    .WB_PC(WB_PC), .RDin(RDinr), .MDin(MDinr), .LedData(LED));
  \单周期MIPS_多级中断  \u_单周期mips_多级中断_1  (
    .IR1(IR1), .IR2(IR2), .IR3(IR3), .RegWrite(RegW), .MemWrite(MemW), .PC(PC), .IR(IR), .RDin(RDin),
    .MDin(MDin), .LedData(LED));

  // Notes on the sheet:
  //   单周期封装测试
  //   气泡流水封装测试
  //   单周期+单级中断封装测试
  //   请检查上面封装有无位宽不匹配，引脚标签是否和连接的标签相对应，否则无法在educoder平台上正确测试
  //   理想流水封装测试
  //   重定向流水封装测试
  //   单周期+多级中断封装测试
endmodule
