// Logisim project cpu24.circ as structural Verilog: 34 circuits, main circuit ◇单周期MIPS
module \单周期MIPS  (
  input  IR1,
  input  IR2,
  input  IR3,
  output RegWrite,
  output MemWrite,
  output [31:0] PC,
  output [31:0] IR,
  output [31:0] RDin,
  output [31:0] MDin,
  output [31:0] LedData
);

  wire AluSrcB, and_1_out, and_2_out, and_3_out, Beq, Beq_Bne, BGEZ, Bne, CLK, clock_2_out, comparator_1_eq,
       comparator_2_eq, comparator_3_eq, comparator_3_lt, controlled_buffer_1_out, d_ff_1_q, Equal, ERET, Go,
       Halt, IR1_t, IR2_t, IR3_t, IRA, IRB, IRC, JAL, JMP, JR, LBU, LED_EN, MemToReg, nand_1_out, not_1_out,
       not_2_out, not_3_out, not_4_out, or_1_out, RegDst, SigendExt, SV, Syscall, W1, W2, W3;
  wire [1:0] xor_1_out;
  wire [3:0] AluOP;
  wire [4:0] multiplexer_2_out, multiplexer_3_out, multiplexer_4_out, multiplexer_5_out, multiplexer_9_out;
  wire [7:0] bit_extender_3_out;
  wire [12:0] CNT_num;
  wire [15:0] \总周期数 ;
  wire [31:0] BGEZ_RES, bit_extender_1_out, bit_extender_2_out, multiplexer_1_out, multiplexer_7_out,
       multiplexer_8_out, multiplexer_10_out, multiplexer_12_out, PC_4, PC_imm, PC_JR, ram_1_data,
       shifter_1_out, undriven;

  Clock #(.highDuration(1), .lowDuration(1)) clock_1 (.out(CLK));
  Button _1 (.out(IRA));
  Button _2 (.out(IRB));
  Button _3 (.out(IRC));
  Button \u_继续运行  (.out(Go));
  LED #(.active("true")) led_1 (.in(W1));
  LED #(.active("true")) led_2 (.in(W2));
  LED #(.active("true")) led_3 (.in(W3));
  Hex_Digit_Display hex_digit_display_1 (.value(LedData[31:28]));  // open: dp
  Hex_Digit_Display hex_digit_display_2 (.value(LedData[27:24]));  // open: dp
  Hex_Digit_Display hex_digit_display_3 (.value(LedData[23:20]));  // open: dp
  Multiplexer #(.select(3), .width(32), .disabled("Z"), .enable("false")) multiplexer_1 (
    .in0(PC_4), .in1(PC_imm), .in2({PC_4[31:28], IR[25:0], 2'b00}), .in6(PC_JR), .out(multiplexer_1_out),
    .sel({JR, JMP, Beq_Bne}));  // open: in3, in4, in5, in7
  Hex_Digit_Display hex_digit_display_4 (.value(LedData[15:12]));  // open: dp
  Hex_Digit_Display hex_digit_display_5 (.value(LedData[19:16]));  // open: dp
  \单周期硬布线控制器  \u_单周期硬布线控制器_1  (
    .Func(IR[5:0]), .OP(IR[31:26]), .ALU_OP(AluOP), .MemToReg(MemToReg), .MemWrite(MemWrite),
    .ALU_SRC(AluSrcB), .RegWrite(RegWrite), .SysCALL(Syscall), .SignedExt(SigendExt), .RegDst(RegDst),
    .JR(JR), .JMP(JMP), .Beq(Beq), .JAL(JAL), .Bne(Bne), .ERET(ERET), .SV(SV), .LBU(LBU), .BGEZ(BGEZ));
  Register #(.width(32), .trigger("rising"), .Select("low")) u_PC (
    .D(multiplexer_1_out), .en(or_1_out), .Q(PC), .clk(CLK));  // open: clr
  or or_1 (or_1_out, not_1_out, Go);
  not not_1 (not_1_out, Halt);
  Hex_Digit_Display hex_digit_display_6 (.value(LedData[7:4]));  // open: dp
  Hex_Digit_Display hex_digit_display_7 (.value(LedData[11:8]));  // open: dp
  // Probe on \总周期数 
  // Probe on PC
  Hex_Digit_Display hex_digit_display_8 (.value(LedData[3:0]));  // open: dp
  // Probe on IR
  // Mips_Probe mips_probe_1: pin names not known; wires that end beside it: IR
  ROM #(.addrWidth(10), .dataWidth(32), .Select("high")) rom_1 (.addr(PC[11:2]), .data(IR));
  or or_2 (IR1_t, IR1, IRA);
  Comparator #(.width(32), .mode("twosComplement")) comparator_1 (
    .a(BGEZ_RES), .b({32{1'b0}}), .eq(comparator_1_eq));  // open: gt, lt
  not not_2 (not_2_out, Equal);
  or or_3 (IR2_t, IR2, IRB);
  and and_1 (and_1_out, BGEZ, comparator_1_eq);
  and and_2 (and_2_out, Beq, Equal);
  and and_3 (and_3_out, Bne, not_2_out);
  or or_4 (Beq_Bne, and_1_out, and_2_out, and_3_out);
  Multiplexer #(.select(1), .width(5), .disabled("Z"), .enable("false")) multiplexer_2 (
    .in0(IR[20:16]), .in1(IR[15:11]), .out(multiplexer_2_out), .sel(RegDst));
  or or_5 (IR3_t, IR3, IRC);
  Register #(.width(32), .trigger("rising"), .Select("low")) register_1 (
    .D(MDin), .en(LED_EN), .Q(LedData), .clk(CLK));  // open: clr
  Multiplexer #(.select(1), .width(5), .disabled("Z"), .enable("false")) multiplexer_3 (
    .in0(IR[25:21]), .in1(5'b00010), .out(multiplexer_3_out), .sel(Syscall));
  Multiplexer #(.select(1), .width(5), .disabled("Z"), .enable("false")) multiplexer_4 (
    .in0(IR[20:16]), .in1(5'b00100), .out(multiplexer_4_out), .sel(Syscall));
  Multiplexer #(.select(1), .width(5), .disabled("Z"), .enable("false")) multiplexer_5 (
    .in0(multiplexer_2_out), .in1({5{1'b1}}), .out(multiplexer_5_out), .sel(JAL));
  // Probe on multiplexer_3_out
  // Probe on multiplexer_4_out
  // Probe on multiplexer_5_out
  Multiplexer #(.select(1), .width(32), .disabled("Z"), .enable("false")) multiplexer_6 (
    .in0(multiplexer_10_out), .in1(PC_4), .out(RDin), .sel(JAL));
  Comparator #(.width(32), .mode("twosComplement")) comparator_2 (
    .a(PC_JR), .b(32'h22), .eq(comparator_2_eq));  // open: gt, lt
  MIPS_Regifile mips_regifile_1 (
    .Din(RDin), .Clk(CLK), .R1(PC_JR), .R2(MDin), .WE(RegWrite), .W_num(multiplexer_5_out),
    .R1_num(multiplexer_3_out), .R2_num(multiplexer_4_out));
  not not_3 (not_3_out, Halt);
  Counter #(.width(16), .max('hffff), .ongoal("wrap"), .trigger("rising"), .behavior("new")) counter_1 (
    .count(not_3_out), .Q(\总周期数 ), .clk(CLK));  // open: load, D, carry, clr, preset, down
  not not_4 (not_4_out, comparator_2_eq);
  assign bit_extender_1_out = {{16{1'b0}}, IR[15:0]};  // Bit_Extender bit_extender_1
  assign bit_extender_2_out = {{16{IR[15]}}, IR[15:0]};  // Bit_Extender bit_extender_2
  and and_4 (LED_EN, Syscall, comparator_2_eq);
  and and_5 (Halt, Syscall, not_4_out);
  Multiplexer #(.select(2), .width(32), .disabled("Z"), .enable("false")) multiplexer_7 (
    .in0(MDin), .in1(MDin), .in2(bit_extender_1_out), .in3(bit_extender_2_out), .out(multiplexer_7_out),
    .sel({AluSrcB, SigendExt}));
  Shifter #(.width(32), .shift("ll")) shifter_1 (.in(bit_extender_2_out), .\dist (5'b00010), .out(shifter_1_out));
  Multiplexer #(.select(1), .width(32), .disabled("Z"), .enable("false")) multiplexer_8 (
    .in0(multiplexer_7_out), .in1({32{1'b0}}), .out(multiplexer_8_out), .sel(BGEZ));
  Adder #(.width(32)) adder_1 (.a(shifter_1_out), .b(PC_4), .out(PC_imm));  // open: cin, cout
  D_Flip_Flop #(.trigger("high"), .Pre_Clr_Positions("LEGACY"), .NegatePresetClear("false"), .enable("true"), .NewFFLayout("false")) d_ff_1 (.Q(d_ff_1_q));  // open: clk, D, Qn, preset, en, reset
  // Probe on 13'h608
  MIPS_ALU mips_alu_1 (
    .X(PC_JR), .Y(multiplexer_8_out), .AluOP(AluOP), .Equal(Equal), .Result(BGEZ_RES),
    .shamt(multiplexer_9_out));  // open: Result_2
  Multiplexer #(.select(1), .width(5), .disabled("Z"), .enable("false")) multiplexer_9 (
    .in0(IR[10:6]), .in1(PC_JR[4:0]), .out(multiplexer_9_out), .sel(SV));
  Multiplexer #(.select(1), .width(32), .disabled("Z"), .enable("false")) multiplexer_10 (
    .in0(multiplexer_12_out), .in1(undriven), .out(multiplexer_10_out), .sel(LBU));
  Clock #(.highDuration(1), .lowDuration(1)) clock_2 (.out(clock_2_out));
  Adder #(.width(32)) adder_2 (.a(PC), .b(32'h4), .out(PC_4));  // open: cin, cout
  // Probe on PC_imm
  Bit_Extender #(.in_width(32), .out_width(8), .\type ("zero")) bit_extender_3 (
    .in(undriven), .out(bit_extender_3_out));
  Comparator #(.width(13), .mode("twosComplement")) comparator_3 (
    .a(CNT_num), .b(13'h608), .eq(comparator_3_eq), .lt(comparator_3_lt));  // open: gt
  Multiplexer #(.select(2), .width(8), .disabled("Z"), .enable("false")) multiplexer_11 (
    .in0(multiplexer_12_out[7:0]), .in1(multiplexer_12_out[15:8]), .in2(multiplexer_12_out[23:16]),
    .in3(multiplexer_12_out[31:24]), .out(bit_extender_3_out), .sel(xor_1_out));
  nand nand_1 (nand_1_out, d_ff_1_q, comparator_3_eq);
  Counter #(.width(13), .max('h1fff), .ongoal("stay"), .trigger("rising"), .behavior("old")) counter_2 (
    .count(comparator_3_lt), .Q(CNT_num), .clk(clock_2_out));  // open: load, D, carry, clr, preset
  RAM #(.addrWidth(10), .dataWidth(32), .bus("separate"), .Select("high")) ram_1 (
    .addr(BGEZ_RES[11:2]), .din(MDin), .data(ram_1_data), .str(MemWrite), .clk(CLK));  // open: sel, ld, clr
  assign xor_1_out = BGEZ_RES[1:0] ^ 2'b11;  // XOR_Gate xor_1, 2 bits wide
  assign controlled_buffer_1_out = nand_1_out ? clock_2_out : 1'bz;  // Controlled_Buffer controlled_buffer_1
  Pull_Resistor #(.pull(1)) pull_resistor_1 (.node(controlled_buffer_1_out));
  // Probe on PC_JR
  Multiplexer #(.select(1), .width(32), .disabled("Z"), .enable("false")) multiplexer_12 (
    .in0(BGEZ_RES), .in1(ram_1_data), .out(multiplexer_12_out), .sel(MemToReg));

  // Other names for the same wires on the sheet: a0[31:0] = MDin; OP[5:0] = IR[31:26]; addr[25:0] = IR[25:0];
  //   Func[5:0] = IR[5:0]; imm[15:0] = IR[15:0]; PC_J_JAL[31:2] = {PC_4[31:28], IR[25:0]}; shamt[4:0] = IR[10:6];
  //   rd[4:0] = IR[15:11]; rt[4:0] = IR[20:16]; rs[4:0] = IR[25:21]; R1[31:0] = PC_JR; v0[31:0] = PC_JR;
  //   Vaddr[31:0] = BGEZ_RES

  // Notes on the sheet:
  //   中断源
  //   中断等待指示
  //   总复位信号应将除ROM以外所有存储组件全部清零
  //   JMP
  //   JR
  //   SigendExt
  //   ERET
  //   SV
  //   LBU
  //   BGEZ
  //   OP
  //   Func
  //   数码管输出
  //   Beq
  //   Bne
  //   MemToReg
  //   MemWrite
  //   AluOP
  //   AluSrcB
  //   RegWrite
  //   JAL
  //   RegDst
  //   Syscall
  //   数码管输出应该用寄存器锁存，否则显示数据只能一闪而过
  //   指令存储器
  //   指令字
  //   contents of rom_1 (hex, n*v repeats v):
  //   20110001 8000c05 20110001 20120002 20130003 8000c09 20110001 20120002 20130003 8000c0d 20110001
  //   20120002 20130003 8000c11 20110001 20120002 20130003 c000cbb 20100001 20110001 118fc0 112020
  //   20020022 c 118882 12200001 8000c15 112020 20020022 c 20110001 118880 112020 20020022 c 12200001
  //   8000c1f 20110001 118fc0 112020 20020022 c 1188c3 112020 20020022 c 118903 112020 20020022 c 118903
  //   112020 20020022 c 118903 112020 20020022 c 118903 112020 20020022 c 118903 112020 20020022 c 118903
  //   112020 20020022 c 118903 112020 20020022 c 20100001 109fc0 139fc3 8021 2012000c 24160003 26100001
  //   3210000f 20080008 20090001 139900 2709825 132020 20020022 c 1094022 1500fff9 22100001 2018000f
  //   2188024 108700 20080008 20090001 139902 2709825 132021 20020022 c 1094022 1500fff9 108702 2c9b022
  //   12c00001 8000c50 4020 1084027 84400 3508ffff 82021 20020022 c 2010ffff 20110000 ae300000 22100001
  //   22310004 ae300000 22100001 22310004 ae300000 22100001 22310004 ae300000 22100001 22310004 ae300000
  //   22100001 22310004 ae300000 22100001 22310004 ae300000 22100001 22310004 ae300000 22100001 22310004
  //   ae300000 22100001 22310004 ae300000 22100001 22310004 ae300000 22100001 22310004 ae300000 22100001
  //   22310004 ae300000 22100001 22310004 ae300000 22100001 22310004 ae300000 22100001 22310004 ae300000
  //   22100001 22310004 22100001 8020 2011003c 8e130000 8e340000 274402a 11000002 ae330000 ae140000
  //   2231fffc 1611fff8 102020 20020022 c 22100004 2011003c 1611fff2 20020032 c 8000c00 2002000a c
  //   20100000 22100001 102020 20020022 c 22100002 102020 20020022 c 22100003 102020 20020022 c 22100004
  //   102020 20020022 c 22100005 102020 20020022 c 22100006 102020 20020022 c 22100007 102020 20020022 c
  //   22100008 102020 20020022 20020022 c 3e00008
  //   OP
  //   Func
  //   rs
  //   rt
  //   rd
  //   为方便自动评测，需要输出PC，IR，寄存器堆写如数据RDin
  //   RAM写使能MemWrite、RAM写入数据MDin等信号
  //   控制位
  //   暂停节拍，不能为0
  //   戳工具置1进入计数暂停模式，ctrl+k时钟自动运行到对应节拍暂停
  //   ctrl+k关闭时钟连续运行，将控制位置零，进入单步调试模式调试
  //   用这个时钟源需要去掉电路中的其他时钟源
  //   无跳转时PC的值
  //   Beq或Bne时PC的值
  //   可计数暂停的时钟源
  //   J或JAL指令时PC的值
  //   jr指令时PC的值
endmodule

// 单周期硬布线控制器
module \单周期硬布线控制器  (
  input  [5:0] OP,
  input  [5:0] Func,
  output [3:0] ALU_OP,
  output MemToReg,
  output MemWrite,
  output ALU_SRC,
  output RegWrite,
  output SysCALL,
  output SignedExt,
  output RegDst,
  output Beq,
  output Bne,
  output JR,
  output JMP,
  output JAL,
  output ERET,
  output SV,
  output LBU,
  output BGEZ
);

  \运算控制器自动生成  \u_运算控制器自动生成_1  (
    .OP0(OP[0]), .OP1(OP[1]), .OP2(OP[2]), .OP3(OP[3]), .OP4(OP[4]), .OP5(OP[5]), .F0(Func[0]), .F1(Func[1]),
    .F2(Func[2]), .F3(Func[3]), .F4(Func[4]), .F5(Func[5]), .S0(ALU_OP[0]), .S1(ALU_OP[1]), .S2(ALU_OP[2]),
    .S3(ALU_OP[3]));
  \控制信号自动生成  \u_控制信号自动生成_1  (
    .OP0(OP[0]), .OP1(OP[1]), .OP2(OP[2]), .MemToReg(MemToReg), .OP3(OP[3]), .OP4(OP[4]), .OP5(OP[5]),
    .MemWrite(MemWrite), .F0(Func[0]), .F1(Func[1]), .F2(Func[2]), .F3(Func[3]), .ALU_SRC(ALU_SRC),
    .F4(Func[4]), .F5(Func[5]), .RegWrite(RegWrite), .SysCALL(SysCALL), .SignedExt(SignedExt),
    .RegDst(RegDst), .BEQ(Beq), .BNE(Bne), .JR(JR), .JUMP(JMP), .JAL(JAL), .ERET(ERET), .SV(SV), .LBU(LBU),
    .BGEZ(BGEZ));

  // Other names for the same wires on the sheet: OP_CODE[5:0] = OP

  // Notes on the sheet:
  //   控制信号生成，产生数据通路需要的其他控制信号
  //   运算器控制器，根据指令生成运算器功能选择信号
endmodule

// 运算器控制器
module \运算控制器自动生成  (
  input  OP0,
  input  OP1,
  input  OP2,
  input  OP3,
  input  OP4,
  input  OP5,
  input  F0,
  input  F1,
  input  F2,
  input  F3,
  input  F4,
  input  F5,
  output S0,
  output S1,
  output S2,
  output S3
);

  wire and_1_out, and_2_out, and_3_out, and_4_out, and_5_out, and_6_out, and_7_out, and_8_out, and_9_out,
       and_10_out, and_11_out, and_12_out, and_13_out, and_14_out, and_15_out, and_16_out, and_17_out,
       and_18_out, and_19_out, and_20_out, and_21_out, and_22_out, and_23_out, and_24_out, and_25_out,
       and_26_out, and_27_out, and_28_out, and_29_out, and_30_out, and_31_out, and_32_out, and_33_out,
       and_34_out, and_35_out, and_36_out, and_37_out, and_38_out, and_39_out, and_40_out, not_1_out,
       not_2_out, not_3_out, not_4_out, not_5_out, not_6_out, not_7_out, not_8_out, not_9_out, not_10_out,
       not_11_out, not_12_out, not_13_out, not_14_out, not_15_out, not_16_out, not_17_out, not_18_out,
       not_19_out, not_20_out, not_21_out, not_22_out, not_23_out, not_24_out, not_25_out, not_26_out,
       not_27_out, not_28_out, not_29_out, not_30_out, not_31_out, not_32_out, not_33_out, not_34_out,
       not_35_out, not_36_out, not_37_out, not_38_out, not_39_out, not_40_out, not_41_out, not_42_out,
       not_43_out, not_44_out, not_45_out, not_46_out, not_47_out, not_48_out, not_49_out, not_50_out,
       not_51_out, not_52_out, not_53_out, not_54_out, not_55_out, not_56_out, not_57_out, not_58_out,
       not_59_out, not_60_out, not_61_out, not_62_out, not_63_out, not_64_out, not_65_out, not_66_out,
       not_67_out, not_68_out, not_69_out, not_70_out, not_71_out, not_72_out, not_73_out, not_74_out,
       not_75_out, not_76_out, not_77_out, not_78_out, not_79_out, not_80_out, not_81_out, not_82_out,
       not_83_out, not_84_out, not_85_out, not_86_out, not_87_out, not_88_out, not_89_out, not_90_out,
       not_91_out, not_92_out, not_93_out, not_94_out, not_95_out, not_96_out, not_97_out, not_98_out,
       not_99_out, not_100_out, not_101_out, not_102_out, not_103_out, not_104_out, not_105_out, not_106_out,
       not_107_out, not_108_out, not_109_out, not_110_out, not_111_out, not_112_out, not_113_out,
       not_114_out, not_115_out, not_116_out, not_117_out, not_118_out, not_119_out, not_120_out,
       not_121_out, not_122_out, not_123_out, not_124_out, not_125_out, not_126_out, not_127_out,
       not_128_out, not_129_out, not_130_out, not_131_out, not_132_out, not_133_out, not_134_out,
       not_135_out, not_136_out, not_137_out, not_138_out, not_139_out, not_140_out, not_141_out,
       not_142_out, not_143_out, not_144_out, not_145_out, not_146_out, not_147_out, not_148_out,
       not_149_out, not_150_out, not_151_out, not_152_out, not_153_out, not_154_out, not_155_out,
       not_156_out, not_157_out, not_158_out, not_159_out, not_160_out, not_161_out, not_162_out,
       not_163_out, not_164_out, not_165_out, not_166_out, not_167_out, not_168_out, not_169_out,
       not_170_out, not_171_out, not_172_out, not_173_out, not_174_out, not_175_out, not_176_out,
       not_177_out, not_178_out, not_179_out, not_180_out, not_181_out, not_182_out, not_183_out,
       not_184_out, not_185_out, not_186_out, not_187_out, not_188_out, not_189_out, not_190_out,
       not_191_out, not_192_out, not_193_out, not_194_out, not_195_out, not_196_out, not_197_out,
       not_198_out, not_199_out, not_200_out, not_201_out, not_202_out, not_203_out, not_204_out,
       not_205_out, not_206_out, not_207_out, not_208_out, not_209_out, not_210_out, not_211_out,
       not_212_out, not_213_out, not_214_out, not_215_out, not_216_out, not_217_out, not_218_out,
       not_219_out, not_220_out, not_221_out, not_222_out, not_223_out, not_224_out, not_225_out,
       not_226_out, not_227_out, not_228_out, not_229_out, not_230_out, not_231_out, not_232_out,
       not_233_out, not_234_out, not_235_out, not_236_out, not_237_out, not_238_out, not_239_out,
       not_240_out, not_241_out, not_242_out, not_243_out, not_244_out, not_245_out, not_246_out,
       not_247_out, not_248_out, not_249_out, not_250_out, not_251_out, not_252_out, not_253_out,
       not_254_out, not_255_out, not_256_out, not_257_out, not_258_out, not_259_out, not_260_out,
       not_261_out, not_262_out, not_263_out, not_264_out, not_265_out, not_266_out, not_267_out,
       not_268_out, not_269_out;

  not not_1 (not_1_out, OP5);
  not not_2 (not_2_out, OP4);
  not not_3 (not_3_out, OP3);
  not not_4 (not_4_out, OP2);
  not not_5 (not_5_out, OP1);
  not not_6 (not_6_out, OP0);
  not not_7 (not_7_out, F5);
  not not_8 (not_8_out, F4);
  not not_9 (not_9_out, F3);
  not not_10 (not_10_out, F2);
  not not_11 (not_11_out, OP5);
  not not_12 (not_12_out, OP4);
  not not_13 (not_13_out, OP3);
  not not_14 (not_14_out, OP2);
  not not_15 (not_15_out, OP1);
  not not_16 (not_16_out, OP0);
  not not_17 (not_17_out, F4);
  not not_18 (not_18_out, F3);
  not not_19 (not_19_out, F2);
  not not_20 (not_20_out, F1);
  not not_21 (not_21_out, F0);
  not not_22 (not_22_out, OP5);
  not not_23 (not_23_out, OP4);
  not not_24 (not_24_out, OP3);
  not not_25 (not_25_out, OP2);
  not not_26 (not_26_out, OP1);
  not not_27 (not_27_out, OP0);
  not not_28 (not_28_out, F4);
  not not_29 (not_29_out, F3);
  not not_30 (not_30_out, F2);
  not not_31 (not_31_out, F1);
  not not_32 (not_32_out, OP5);
  not not_33 (not_33_out, OP4);
  not not_34 (not_34_out, OP3);
  not not_35 (not_35_out, OP2);
  not not_36 (not_36_out, OP1);
  not not_37 (not_37_out, OP0);
  not not_38 (not_38_out, F4);
  not not_39 (not_39_out, F3);
  not not_40 (not_40_out, F1);
  not not_41 (not_41_out, F0);
  not not_42 (not_42_out, OP5);
  not not_43 (not_43_out, OP4);
  not not_44 (not_44_out, OP3);
  not not_45 (not_45_out, OP2);
  not not_46 (not_46_out, OP1);
  not not_47 (not_47_out, OP0);
  not not_48 (not_48_out, F4);
  not not_49 (not_49_out, F2);
  not not_50 (not_50_out, F0);
  not not_51 (not_51_out, OP5);
  not not_52 (not_52_out, OP4);
  not not_53 (not_53_out, OP2);
  not not_54 (not_54_out, OP1);
  not not_55 (not_55_out, OP0);
  not not_56 (not_56_out, OP5);
  not not_57 (not_57_out, OP4);
  not not_58 (not_58_out, OP1);
  not not_59 (not_59_out, OP0);
  not not_60 (not_60_out, OP5);
  not not_61 (not_61_out, OP4);
  not not_62 (not_62_out, OP2);
  not not_63 (not_63_out, OP1);
  not not_64 (not_64_out, OP5);
  not not_65 (not_65_out, OP4);
  not not_66 (not_66_out, OP2);
  not not_67 (not_67_out, OP0);
  not not_68 (not_68_out, OP4);
  not not_69 (not_69_out, OP3);
  not not_70 (not_70_out, OP2);
  not not_71 (not_71_out, OP4);
  not not_72 (not_72_out, OP2);
  not not_73 (not_73_out, OP4);
  not not_74 (not_74_out, OP3);
  not not_75 (not_75_out, OP1);
  not not_76 (not_76_out, OP0);
  not not_77 (not_77_out, OP5);
  not not_78 (not_78_out, OP4);
  not not_79 (not_79_out, OP3);
  not not_80 (not_80_out, OP2);
  not not_81 (not_81_out, OP1);
  not not_82 (not_82_out, OP5);
  not not_83 (not_83_out, OP4);
  not not_84 (not_84_out, OP3);
  not not_85 (not_85_out, OP2);
  not not_86 (not_86_out, OP1);
  not not_87 (not_87_out, OP0);
  not not_88 (not_88_out, F5);
  not not_89 (not_89_out, F4);
  not not_90 (not_90_out, F3);
  not not_91 (not_91_out, F2);
  not not_92 (not_92_out, F0);
  not not_93 (not_93_out, OP5);
  not not_94 (not_94_out, OP4);
  not not_95 (not_95_out, OP3);
  not not_96 (not_96_out, OP2);
  not not_97 (not_97_out, OP1);
  not not_98 (not_98_out, OP0);
  not not_99 (not_99_out, F4);
  not not_100 (not_100_out, F3);
  not not_101 (not_101_out, F2);
  not not_102 (not_102_out, F0);
  not not_103 (not_103_out, OP5);
  not not_104 (not_104_out, OP4);
  not not_105 (not_105_out, OP3);
  not not_106 (not_106_out, OP2);
  not not_107 (not_107_out, OP1);
  not not_108 (not_108_out, OP0);
  not not_109 (not_109_out, F4);
  not not_110 (not_110_out, F3);
  not not_111 (not_111_out, F1);
  not not_112 (not_112_out, F0);
  not not_113 (not_113_out, OP5);
  not not_114 (not_114_out, OP4);
  not not_115 (not_115_out, OP3);
  not not_116 (not_116_out, OP2);
  not not_117 (not_117_out, OP1);
  not not_118 (not_118_out, OP0);
  not not_119 (not_119_out, F4);
  not not_120 (not_120_out, F3);
  not not_121 (not_121_out, OP5);
  not not_122 (not_122_out, OP4);
  not not_123 (not_123_out, OP3);
  not not_124 (not_124_out, OP2);
  not not_125 (not_125_out, OP1);
  not not_126 (not_126_out, OP0);
  not not_127 (not_127_out, F4);
  not not_128 (not_128_out, F2);
  not not_129 (not_129_out, F0);
  not not_130 (not_130_out, OP5);
  not not_131 (not_131_out, OP4);
  not not_132 (not_132_out, OP1);
  not not_133 (not_133_out, OP0);
  not not_134 (not_134_out, OP5);
  not not_135 (not_135_out, OP4);
  not not_136 (not_136_out, OP2);
  not not_137 (not_137_out, OP0);
  not not_138 (not_138_out, OP5);
  not not_139 (not_139_out, OP4);
  not not_140 (not_140_out, OP3);
  not not_141 (not_141_out, OP2);
  not not_142 (not_142_out, OP1);
  not not_143 (not_143_out, OP0);
  not not_144 (not_144_out, F5);
  not not_145 (not_145_out, F4);
  not not_146 (not_146_out, F3);
  not not_147 (not_147_out, F0);
  not not_148 (not_148_out, OP5);
  not not_149 (not_149_out, OP4);
  not not_150 (not_150_out, OP3);
  not not_151 (not_151_out, OP2);
  not not_152 (not_152_out, OP1);
  not not_153 (not_153_out, OP5);
  not not_154 (not_154_out, OP4);
  not not_155 (not_155_out, OP3);
  not not_156 (not_156_out, OP2);
  not not_157 (not_157_out, OP1);
  not not_158 (not_158_out, OP0);
  not not_159 (not_159_out, F4);
  not not_160 (not_160_out, F3);
  not not_161 (not_161_out, F2);
  not not_162 (not_162_out, F1);
  not not_163 (not_163_out, F0);
  not not_164 (not_164_out, OP5);
  not not_165 (not_165_out, OP4);
  not not_166 (not_166_out, OP3);
  not not_167 (not_167_out, OP2);
  not not_168 (not_168_out, OP1);
  not not_169 (not_169_out, OP0);
  not not_170 (not_170_out, F4);
  not not_171 (not_171_out, F3);
  not not_172 (not_172_out, F2);
  not not_173 (not_173_out, F1);
  not not_174 (not_174_out, OP5);
  not not_175 (not_175_out, OP4);
  not not_176 (not_176_out, OP3);
  not not_177 (not_177_out, OP2);
  not not_178 (not_178_out, OP1);
  not not_179 (not_179_out, OP0);
  not not_180 (not_180_out, F4);
  not not_181 (not_181_out, F3);
  not not_182 (not_182_out, F2);
  not not_183 (not_183_out, F0);
  not not_184 (not_184_out, OP5);
  not not_185 (not_185_out, OP4);
  not not_186 (not_186_out, OP3);
  not not_187 (not_187_out, OP2);
  not not_188 (not_188_out, OP1);
  not not_189 (not_189_out, OP0);
  not not_190 (not_190_out, F4);
  not not_191 (not_191_out, F3);
  not not_192 (not_192_out, F1);
  not not_193 (not_193_out, F0);
  not not_194 (not_194_out, OP5);
  not not_195 (not_195_out, OP4);
  not not_196 (not_196_out, OP3);
  not not_197 (not_197_out, OP2);
  not not_198 (not_198_out, OP1);
  not not_199 (not_199_out, OP0);
  not not_200 (not_200_out, F4);
  not not_201 (not_201_out, F2);
  not not_202 (not_202_out, OP5);
  not not_203 (not_203_out, OP4);
  not not_204 (not_204_out, OP2);
  not not_205 (not_205_out, OP1);
  not not_206 (not_206_out, OP0);
  not not_207 (not_207_out, OP5);
  not not_208 (not_208_out, OP4);
  not not_209 (not_209_out, OP1);
  not not_210 (not_210_out, OP0);
  not not_211 (not_211_out, OP5);
  not not_212 (not_212_out, OP4);
  not not_213 (not_213_out, OP2);
  not not_214 (not_214_out, OP1);
  not not_215 (not_215_out, OP4);
  not not_216 (not_216_out, OP3);
  not not_217 (not_217_out, OP2);
  not not_218 (not_218_out, OP4);
  not not_219 (not_219_out, OP2);
  not not_220 (not_220_out, OP4);
  not not_221 (not_221_out, OP3);
  not not_222 (not_222_out, OP1);
  not not_223 (not_223_out, OP0);
  not not_224 (not_224_out, OP5);
  not not_225 (not_225_out, OP4);
  not not_226 (not_226_out, OP3);
  not not_227 (not_227_out, OP2);
  not not_228 (not_228_out, OP1);
  not not_229 (not_229_out, OP0);
  not not_230 (not_230_out, F4);
  not not_231 (not_231_out, F3);
  not not_232 (not_232_out, F1);
  not not_233 (not_233_out, OP5);
  not not_234 (not_234_out, OP4);
  not not_235 (not_235_out, OP3);
  not not_236 (not_236_out, OP2);
  not not_237 (not_237_out, OP1);
  not not_238 (not_238_out, OP0);
  not not_239 (not_239_out, F4);
  not not_240 (not_240_out, F3);
  not not_241 (not_241_out, OP5);
  not not_242 (not_242_out, OP4);
  not not_243 (not_243_out, OP3);
  not not_244 (not_244_out, OP2);
  not not_245 (not_245_out, OP1);
  not not_246 (not_246_out, OP0);
  not not_247 (not_247_out, F4);
  not not_248 (not_248_out, F2);
  not not_249 (not_249_out, F0);
  not not_250 (not_250_out, OP5);
  not not_251 (not_251_out, OP4);
  not not_252 (not_252_out, OP3);
  not not_253 (not_253_out, OP2);
  not not_254 (not_254_out, OP1);
  not not_255 (not_255_out, OP0);
  not not_256 (not_256_out, F4);
  not not_257 (not_257_out, F2);
  not not_258 (not_258_out, OP5);
  not not_259 (not_259_out, OP4);
  not not_260 (not_260_out, OP2);
  not not_261 (not_261_out, OP0);
  not not_262 (not_262_out, OP5);
  not not_263 (not_263_out, OP4);
  not not_264 (not_264_out, OP1);
  not not_265 (not_265_out, OP5);
  not not_266 (not_266_out, OP4);
  not not_267 (not_267_out, OP3);
  not not_268 (not_268_out, OP2);
  not not_269 (not_269_out, OP1);
  and and_1 (and_1_out, not_1_out, not_2_out, not_3_out, not_4_out, not_5_out, not_6_out, not_7_out, not_8_out, not_9_out, not_10_out, F1, F0);
  and and_2 (and_2_out, not_11_out, not_12_out, not_13_out, not_14_out, not_15_out, not_16_out, F5, not_17_out, not_18_out, not_19_out, not_20_out, not_21_out);
  and and_3 (and_3_out, not_22_out, not_23_out, not_24_out, not_25_out, not_26_out, not_27_out, F5, not_28_out, not_29_out, not_30_out, not_31_out, F0);
  and and_4 (and_4_out, not_32_out, not_33_out, not_34_out, not_35_out, not_36_out, not_37_out, F5, not_38_out, not_39_out, F2, not_40_out, not_41_out);
  and and_5 (and_5_out, not_42_out, not_43_out, not_44_out, not_45_out, not_46_out, not_47_out, F5, not_48_out, F3, not_49_out, F1, not_50_out);
  and and_6 (and_6_out, not_51_out, not_52_out, OP3, not_53_out, not_54_out, not_55_out);
  and and_7 (and_7_out, not_56_out, not_57_out, OP3, OP2, not_58_out, not_59_out);
  and and_8 (and_8_out, not_60_out, not_61_out, OP3, not_62_out, not_63_out, OP0);
  and and_9 (and_9_out, not_64_out, not_65_out, OP3, not_66_out, OP1, not_67_out);
  and and_10 (and_10_out, OP5, not_68_out, not_69_out, not_70_out, OP1, OP0);
  and and_11 (and_11_out, OP5, not_71_out, OP3, not_72_out, OP1, OP0);
  and and_12 (and_12_out, OP5, not_73_out, not_74_out, OP2, not_75_out, not_76_out);
  and and_13 (and_13_out, not_77_out, not_78_out, not_79_out, not_80_out, not_81_out, OP0);
  and and_14 (and_14_out, not_82_out, not_83_out, not_84_out, not_85_out, not_86_out, not_87_out, not_88_out, not_89_out, not_90_out, not_91_out, F1, not_92_out);
  and and_15 (and_15_out, not_93_out, not_94_out, not_95_out, not_96_out, not_97_out, not_98_out, F5, not_99_out, not_100_out, not_101_out, F1, not_102_out);
  and and_16 (and_16_out, not_103_out, not_104_out, not_105_out, not_106_out, not_107_out, not_108_out, F5, not_109_out, not_110_out, F2, not_111_out, not_112_out);
  and and_17 (and_17_out, not_113_out, not_114_out, not_115_out, not_116_out, not_117_out, not_118_out, F5, not_119_out, not_120_out, F2, F1, F0);
  and and_18 (and_18_out, not_121_out, not_122_out, not_123_out, not_124_out, not_125_out, not_126_out, F5, not_127_out, F3, not_128_out, F1, not_129_out);
  and and_19 (and_19_out, not_130_out, not_131_out, OP3, OP2, not_132_out, not_133_out);
  and and_20 (and_20_out, not_134_out, not_135_out, OP3, not_136_out, OP1, not_137_out);
  and and_21 (and_21_out, not_138_out, not_139_out, not_140_out, not_141_out, not_142_out, not_143_out, not_144_out, not_145_out, not_146_out, F2, F1, not_147_out);
  and and_22 (and_22_out, not_148_out, not_149_out, not_150_out, not_151_out, not_152_out, OP0);
  and and_23 (and_23_out, not_153_out, not_154_out, not_155_out, not_156_out, not_157_out, not_158_out, F5, not_159_out, not_160_out, not_161_out, not_162_out, not_163_out);
  and and_24 (and_24_out, not_164_out, not_165_out, not_166_out, not_167_out, not_168_out, not_169_out, F5, not_170_out, not_171_out, not_172_out, not_173_out, F0);
  and and_25 (and_25_out, not_174_out, not_175_out, not_176_out, not_177_out, not_178_out, not_179_out, F5, not_180_out, not_181_out, not_182_out, F1, not_183_out);
  and and_26 (and_26_out, not_184_out, not_185_out, not_186_out, not_187_out, not_188_out, not_189_out, F5, not_190_out, not_191_out, F2, not_192_out, not_193_out);
  and and_27 (and_27_out, not_194_out, not_195_out, not_196_out, not_197_out, not_198_out, not_199_out, F5, not_200_out, F3, not_201_out, F1, F0);
  and and_28 (and_28_out, not_202_out, not_203_out, OP3, not_204_out, not_205_out, not_206_out);
  and and_29 (and_29_out, not_207_out, not_208_out, OP3, OP2, not_209_out, not_210_out);
  and and_30 (and_30_out, not_211_out, not_212_out, OP3, not_213_out, not_214_out, OP0);
  and and_31 (and_31_out, OP5, not_215_out, not_216_out, not_217_out, OP1, OP0);
  and and_32 (and_32_out, OP5, not_218_out, OP3, not_219_out, OP1, OP0);
  and and_33 (and_33_out, OP5, not_220_out, not_221_out, OP2, not_222_out, not_223_out);
  and and_34 (and_34_out, not_224_out, not_225_out, not_226_out, not_227_out, not_228_out, not_229_out, F5, not_230_out, not_231_out, F2, not_232_out, F0);
  and and_35 (and_35_out, not_233_out, not_234_out, not_235_out, not_236_out, not_237_out, not_238_out, F5, not_239_out, not_240_out, F2, F1, F0);
  and and_36 (and_36_out, not_241_out, not_242_out, not_243_out, not_244_out, not_245_out, not_246_out, F5, not_247_out, F3, not_248_out, F1, not_249_out);
  and and_37 (and_37_out, not_250_out, not_251_out, not_252_out, not_253_out, not_254_out, not_255_out, F5, not_256_out, F3, not_257_out, F1, F0);
  and and_38 (and_38_out, not_258_out, not_259_out, OP3, not_260_out, OP1, not_261_out);
  and and_39 (and_39_out, not_262_out, not_263_out, OP3, OP2, not_264_out, OP0);
  and and_40 (and_40_out, not_265_out, not_266_out, not_267_out, not_268_out, not_269_out, OP0);
  or or_1 (S1, and_14_out, and_15_out, and_16_out, and_17_out, and_18_out, and_19_out, and_20_out, and_21_out, and_22_out);
  or or_2 (S2, and_23_out, and_24_out, and_25_out, and_26_out, and_27_out, and_28_out, and_29_out, and_30_out, and_31_out, and_32_out, and_33_out);
  or or_3 (S3, and_34_out, and_35_out, and_36_out, and_37_out, and_38_out, and_39_out, and_40_out);
  or or_4 (S0, and_1_out, and_2_out, and_3_out, and_4_out, and_5_out, and_6_out, and_7_out, and_8_out, and_9_out, and_10_out, and_11_out, and_12_out, and_13_out);
endmodule

// 控制信号生成
module \控制信号自动生成  (
  input  OP0,
  input  OP1,
  input  OP2,
  input  OP3,
  input  OP4,
  input  OP5,
  input  F0,
  input  F1,
  input  F2,
  input  F3,
  input  F4,
  input  F5,
  output MemToReg,
  output MemWrite,
  output ALU_SRC,
  output RegWrite,
  output SysCALL,
  output SignedExt,
  output RegDst,
  output BEQ,
  output BNE,
  output JR,
  output JUMP,
  output JAL,
  output ERET,
  output SV,
  output LBU,
  output BGEZ
);

  wire and_1_out, and_2_out, and_4_out, and_5_out, and_6_out, and_7_out, and_8_out, and_9_out, and_10_out,
       and_11_out, and_12_out, and_13_out, and_14_out, and_15_out, and_16_out, and_18_out, and_19_out,
       and_20_out, and_21_out, and_22_out, and_23_out, and_24_out, and_25_out, and_26_out, and_27_out,
       and_28_out, and_29_out, and_30_out, and_31_out, and_32_out, and_33_out, and_37_out, and_38_out,
       and_41_out, and_42_out, not_1_out, not_2_out, not_3_out, not_4_out, not_5_out, not_6_out, not_7_out,
       not_8_out, not_9_out, not_10_out, not_11_out, not_12_out, not_13_out, not_14_out, not_15_out,
       not_16_out, not_17_out, not_18_out, not_19_out, not_20_out, not_21_out, not_22_out, not_23_out,
       not_24_out, not_25_out, not_26_out, not_27_out, not_28_out, not_29_out, not_30_out, not_31_out,
       not_32_out, not_33_out, not_34_out, not_35_out, not_36_out, not_37_out, not_38_out, not_39_out,
       not_40_out, not_41_out, not_42_out, not_43_out, not_44_out, not_45_out, not_46_out, not_47_out,
       not_48_out, not_49_out, not_50_out, not_51_out, not_52_out, not_53_out, not_54_out, not_55_out,
       not_56_out, not_57_out, not_58_out, not_59_out, not_60_out, not_61_out, not_62_out, not_63_out,
       not_64_out, not_65_out, not_66_out, not_67_out, not_68_out, not_69_out, not_70_out, not_71_out,
       not_72_out, not_73_out, not_74_out, not_75_out, not_76_out, not_77_out, not_78_out, not_79_out,
       not_80_out, not_81_out, not_82_out, not_83_out, not_84_out, not_85_out, not_86_out, not_87_out,
       not_88_out, not_89_out, not_90_out, not_91_out, not_92_out, not_93_out, not_94_out, not_95_out,
       not_96_out, not_97_out, not_98_out, not_99_out, not_100_out, not_101_out, not_102_out, not_103_out,
       not_104_out, not_105_out, not_106_out, not_107_out, not_108_out, not_109_out, not_110_out,
       not_111_out, not_112_out, not_113_out, not_114_out, not_115_out, not_116_out, not_117_out,
       not_118_out, not_119_out, not_120_out, not_121_out, not_122_out, not_123_out, not_124_out,
       not_125_out, not_126_out, not_127_out, not_128_out, not_129_out, not_130_out, not_131_out,
       not_132_out, not_133_out, not_134_out, not_135_out, not_136_out, not_137_out, not_138_out,
       not_139_out, not_140_out, not_141_out, not_142_out, not_143_out, not_144_out, not_145_out,
       not_146_out, not_147_out, not_148_out, not_149_out, not_150_out, not_151_out, not_152_out,
       not_153_out, not_154_out, not_155_out, not_156_out, not_157_out, not_158_out, not_159_out,
       not_160_out, not_161_out, not_162_out, not_163_out, not_164_out, not_165_out, not_166_out,
       not_167_out, not_168_out, not_169_out, not_170_out, not_171_out, not_172_out, not_173_out,
       not_174_out, not_175_out, not_176_out, not_177_out, not_178_out, not_179_out, not_180_out,
       not_181_out, not_182_out, not_183_out, not_184_out, not_185_out, not_186_out, not_187_out,
       not_188_out, not_189_out, not_190_out, not_191_out, not_192_out, not_193_out, not_194_out,
       not_195_out, not_196_out, not_197_out, not_198_out, not_199_out, not_200_out, not_201_out,
       not_202_out, not_203_out, not_204_out, not_205_out, not_206_out, not_207_out, not_208_out,
       not_209_out, not_210_out, not_211_out, not_212_out, not_213_out, not_214_out, not_215_out,
       not_216_out, not_217_out, not_218_out, not_219_out, not_220_out, not_221_out, not_222_out,
       not_223_out, not_224_out, not_225_out, not_226_out, not_227_out, not_228_out, not_229_out,
       not_230_out, not_231_out, not_232_out, not_233_out, not_234_out, not_235_out, not_236_out,
       not_237_out, not_238_out, not_239_out, not_240_out, not_241_out, not_242_out, not_243_out,
       not_244_out, not_245_out, not_246_out, not_247_out, not_248_out, not_249_out, not_250_out,
       not_251_out, not_252_out, not_253_out, not_254_out, not_255_out, not_256_out, not_257_out,
       not_258_out, not_259_out, not_260_out, not_261_out, not_262_out, not_263_out, not_264_out,
       not_265_out, not_266_out, not_267_out, not_268_out;

  not not_1 (not_1_out, OP0);
  not not_2 (not_2_out, OP1);
  not not_3 (not_3_out, OP3);
  not not_4 (not_4_out, OP4);
  not not_5 (not_5_out, OP2);
  not not_6 (not_6_out, OP3);
  not not_7 (not_7_out, OP4);
  not not_8 (not_8_out, OP2);
  not not_9 (not_9_out, OP4);
  not not_10 (not_10_out, OP0);
  not not_11 (not_11_out, OP2);
  not not_12 (not_12_out, OP4);
  not not_13 (not_13_out, OP5);
  not not_14 (not_14_out, OP1);
  not not_15 (not_15_out, OP4);
  not not_16 (not_16_out, OP5);
  not not_17 (not_17_out, OP2);
  not not_18 (not_18_out, OP4);
  not not_19 (not_19_out, OP0);
  not not_20 (not_20_out, OP1);
  not not_21 (not_21_out, OP2);
  not not_22 (not_22_out, OP4);
  not not_23 (not_23_out, OP5);
  not not_24 (not_24_out, F0);
  not not_25 (not_25_out, F2);
  not not_26 (not_26_out, F3);
  not not_27 (not_27_out, F4);
  not not_28 (not_28_out, OP0);
  not not_29 (not_29_out, OP1);
  not not_30 (not_30_out, OP2);
  not not_31 (not_31_out, OP4);
  not not_32 (not_32_out, OP5);
  not not_33 (not_33_out, F1);
  not not_34 (not_34_out, F3);
  not not_35 (not_35_out, F4);
  not not_36 (not_36_out, OP0);
  not not_37 (not_37_out, OP1);
  not not_38 (not_38_out, OP2);
  not not_39 (not_39_out, OP4);
  not not_40 (not_40_out, OP5);
  not not_41 (not_41_out, F0);
  not not_42 (not_42_out, F3);
  not not_43 (not_43_out, F4);
  not not_44 (not_44_out, F5);
  not not_45 (not_45_out, OP0);
  not not_46 (not_46_out, OP1);
  not not_47 (not_47_out, OP2);
  not not_48 (not_48_out, OP4);
  not not_49 (not_49_out, OP5);
  not not_50 (not_50_out, F2);
  not not_51 (not_51_out, F3);
  not not_52 (not_52_out, F4);
  not not_53 (not_53_out, F5);
  not not_54 (not_54_out, OP0);
  not not_55 (not_55_out, OP1);
  not not_56 (not_56_out, OP2);
  not not_57 (not_57_out, OP4);
  not not_58 (not_58_out, OP5);
  not not_59 (not_59_out, F2);
  not not_60 (not_60_out, F4);
  not not_61 (not_61_out, OP0);
  not not_62 (not_62_out, OP1);
  not not_63 (not_63_out, OP2);
  not not_64 (not_64_out, OP4);
  not not_65 (not_65_out, OP5);
  not not_66 (not_66_out, F3);
  not not_67 (not_67_out, F4);
  not not_68 (not_68_out, OP0);
  not not_69 (not_69_out, OP2);
  not not_70 (not_70_out, OP4);
  not not_71 (not_71_out, OP5);
  not not_72 (not_72_out, OP1);
  not not_73 (not_73_out, OP4);
  not not_74 (not_74_out, OP5);
  not not_75 (not_75_out, OP0);
  not not_76 (not_76_out, OP1);
  not not_77 (not_77_out, OP3);
  not not_78 (not_78_out, OP4);
  not not_79 (not_79_out, OP2);
  not not_80 (not_80_out, OP3);
  not not_81 (not_81_out, OP4);
  not not_82 (not_82_out, OP0);
  not not_83 (not_83_out, OP1);
  not not_84 (not_84_out, OP2);
  not not_85 (not_85_out, OP3);
  not not_86 (not_86_out, OP4);
  not not_87 (not_87_out, OP5);
  not not_88 (not_88_out, F0);
  not not_89 (not_89_out, F1);
  not not_90 (not_90_out, F4);
  not not_91 (not_91_out, F5);
  not not_92 (not_92_out, OP5);
  not not_93 (not_93_out, OP4);
  not not_94 (not_94_out, OP3);
  not not_95 (not_95_out, OP1);
  not not_96 (not_96_out, OP0);
  not not_97 (not_97_out, OP5);
  not not_98 (not_98_out, OP4);
  not not_99 (not_99_out, OP3);
  not not_100 (not_100_out, OP1);
  not not_101 (not_101_out, OP5);
  not not_102 (not_102_out, OP4);
  not not_103 (not_103_out, OP2);
  not not_104 (not_104_out, OP1);
  not not_105 (not_105_out, OP0);
  not not_106 (not_106_out, OP5);
  not not_107 (not_107_out, OP4);
  not not_108 (not_108_out, OP2);
  not not_109 (not_109_out, OP1);
  not not_110 (not_110_out, OP5);
  not not_111 (not_111_out, OP4);
  not not_112 (not_112_out, OP2);
  not not_113 (not_113_out, OP0);
  not not_114 (not_114_out, OP4);
  not not_115 (not_115_out, OP3);
  not not_116 (not_116_out, OP2);
  not not_117 (not_117_out, OP4);
  not not_118 (not_118_out, OP2);
  not not_119 (not_119_out, OP4);
  not not_120 (not_120_out, OP3);
  not not_121 (not_121_out, OP1);
  not not_122 (not_122_out, OP0);
  not not_123 (not_123_out, OP5);
  not not_124 (not_124_out, OP4);
  not not_125 (not_125_out, OP3);
  not not_126 (not_126_out, OP2);
  not not_127 (not_127_out, OP1);
  not not_128 (not_128_out, OP0);
  not not_129 (not_129_out, OP1);
  not not_130 (not_130_out, OP2);
  not not_131 (not_131_out, OP3);
  not not_132 (not_132_out, OP4);
  not not_133 (not_133_out, OP5);
  not not_134 (not_134_out, F0);
  not not_135 (not_135_out, F1);
  not not_136 (not_136_out, F2);
  not not_137 (not_137_out, F4);
  not not_138 (not_138_out, F5);
  not not_139 (not_139_out, OP0);
  not not_140 (not_140_out, OP1);
  not not_141 (not_141_out, OP2);
  not not_142 (not_142_out, OP3);
  not not_143 (not_143_out, OP4);
  not not_144 (not_144_out, OP5);
  not not_145 (not_145_out, F0);
  not not_146 (not_146_out, F2);
  not not_147 (not_147_out, F3);
  not not_148 (not_148_out, F4);
  not not_149 (not_149_out, OP0);
  not not_150 (not_150_out, OP1);
  not not_151 (not_151_out, OP2);
  not not_152 (not_152_out, OP3);
  not not_153 (not_153_out, OP4);
  not not_154 (not_154_out, OP5);
  not not_155 (not_155_out, F1);
  not not_156 (not_156_out, F3);
  not not_157 (not_157_out, F4);
  not not_158 (not_158_out, OP0);
  not not_159 (not_159_out, OP1);
  not not_160 (not_160_out, OP2);
  not not_161 (not_161_out, OP3);
  not not_162 (not_162_out, OP4);
  not not_163 (not_163_out, OP5);
  not not_164 (not_164_out, F0);
  not not_165 (not_165_out, F3);
  not not_166 (not_166_out, F4);
  not not_167 (not_167_out, F5);
  not not_168 (not_168_out, OP0);
  not not_169 (not_169_out, OP1);
  not not_170 (not_170_out, OP2);
  not not_171 (not_171_out, OP3);
  not not_172 (not_172_out, OP4);
  not not_173 (not_173_out, OP5);
  not not_174 (not_174_out, F2);
  not not_175 (not_175_out, F3);
  not not_176 (not_176_out, F4);
  not not_177 (not_177_out, F5);
  not not_178 (not_178_out, OP0);
  not not_179 (not_179_out, OP1);
  not not_180 (not_180_out, OP2);
  not not_181 (not_181_out, OP3);
  not not_182 (not_182_out, OP4);
  not not_183 (not_183_out, OP5);
  not not_184 (not_184_out, F2);
  not not_185 (not_185_out, F4);
  not not_186 (not_186_out, OP0);
  not not_187 (not_187_out, OP1);
  not not_188 (not_188_out, OP2);
  not not_189 (not_189_out, OP3);
  not not_190 (not_190_out, OP4);
  not not_191 (not_191_out, OP5);
  not not_192 (not_192_out, F3);
  not not_193 (not_193_out, F4);
  not not_194 (not_194_out, OP0);
  not not_195 (not_195_out, OP1);
  not not_196 (not_196_out, OP3);
  not not_197 (not_197_out, OP4);
  not not_198 (not_198_out, OP5);
  not not_199 (not_199_out, OP1);
  not not_200 (not_200_out, OP3);
  not not_201 (not_201_out, OP4);
  not not_202 (not_202_out, OP5);
  not not_203 (not_203_out, OP0);
  not not_204 (not_204_out, OP1);
  not not_205 (not_205_out, OP2);
  not not_206 (not_206_out, OP3);
  not not_207 (not_207_out, OP4);
  not not_208 (not_208_out, OP5);
  not not_209 (not_209_out, F0);
  not not_210 (not_210_out, F1);
  not not_211 (not_211_out, F2);
  not not_212 (not_212_out, F4);
  not not_213 (not_213_out, F5);
  not not_214 (not_214_out, OP0);
  not not_215 (not_215_out, OP2);
  not not_216 (not_216_out, OP3);
  not not_217 (not_217_out, OP4);
  not not_218 (not_218_out, OP5);
  not not_219 (not_219_out, F0);
  not not_220 (not_220_out, F1);
  not not_221 (not_221_out, F2);
  not not_222 (not_222_out, F4);
  not not_223 (not_223_out, F5);
  not not_224 (not_224_out, OP2);
  not not_225 (not_225_out, OP3);
  not not_226 (not_226_out, OP4);
  not not_227 (not_227_out, OP5);
  not not_228 (not_228_out, OP2);
  not not_229 (not_229_out, OP3);
  not not_230 (not_230_out, OP4);
  not not_231 (not_231_out, OP5);
  not not_232 (not_232_out, OP0);
  not not_233 (not_233_out, OP1);
  not not_234 (not_234_out, OP2);
  not not_235 (not_235_out, OP3);
  not not_236 (not_236_out, OP5);
  not not_237 (not_237_out, F0);
  not not_238 (not_238_out, F1);
  not not_239 (not_239_out, F2);
  not not_240 (not_240_out, F5);
  not not_241 (not_241_out, OP0);
  not not_242 (not_242_out, OP1);
  not not_243 (not_243_out, OP2);
  not not_244 (not_244_out, OP3);
  not not_245 (not_245_out, OP4);
  not not_246 (not_246_out, OP5);
  not not_247 (not_247_out, F0);
  not not_248 (not_248_out, F2);
  not not_249 (not_249_out, F4);
  not not_250 (not_250_out, OP0);
  not not_251 (not_251_out, OP1);
  not not_252 (not_252_out, OP2);
  not not_253 (not_253_out, OP3);
  not not_254 (not_254_out, OP4);
  not not_255 (not_255_out, OP5);
  not not_256 (not_256_out, F0);
  not not_257 (not_257_out, F3);
  not not_258 (not_258_out, F4);
  not not_259 (not_259_out, F5);
  not not_260 (not_260_out, OP0);
  not not_261 (not_261_out, OP1);
  not not_262 (not_262_out, OP3);
  not not_263 (not_263_out, OP4);
  not not_264 (not_264_out, OP1);
  not not_265 (not_265_out, OP2);
  not not_266 (not_266_out, OP3);
  not not_267 (not_267_out, OP4);
  not not_268 (not_268_out, OP5);
  and and_1 (and_1_out, not_1_out, not_2_out, OP2, not_3_out, not_4_out, OP5);
  and and_2 (and_2_out, OP0, OP1, not_5_out, not_6_out, not_7_out, OP5);
  and and_3 (MemWrite, OP0, OP1, not_8_out, OP3, not_9_out, OP5);
  and and_4 (and_4_out, not_10_out, not_11_out, OP3, not_12_out, not_13_out);
  and and_5 (and_5_out, not_14_out, OP3, not_15_out, not_16_out);
  or or_1 (ALU_SRC, and_4_out, and_5_out, and_6_out);
  and and_6 (and_6_out, OP0, OP1, not_17_out, not_18_out, OP5);
  and and_7 (and_7_out, not_19_out, not_20_out, not_21_out, not_22_out, not_23_out, not_24_out, not_25_out, not_26_out, not_27_out);
  and and_8 (and_8_out, not_28_out, not_29_out, not_30_out, not_31_out, not_32_out, not_33_out, not_34_out, not_35_out, F5);
  and and_9 (and_9_out, not_36_out, not_37_out, not_38_out, not_39_out, not_40_out, not_41_out, F1, not_42_out, not_43_out, not_44_out);
  and and_10 (and_10_out, not_45_out, not_46_out, not_47_out, not_48_out, not_49_out, F1, not_50_out, not_51_out, not_52_out, not_53_out);
  and and_11 (and_11_out, not_54_out, not_55_out, not_56_out, not_57_out, not_58_out, F1, not_59_out, F3, not_60_out, F5);
  and and_12 (and_12_out, not_61_out, not_62_out, not_63_out, not_64_out, not_65_out, F0, F2, not_66_out, not_67_out, F5);
  and and_13 (and_13_out, not_68_out, not_69_out, OP3, not_70_out, not_71_out);
  and and_14 (and_14_out, not_72_out, OP3, not_73_out, not_74_out);
  and and_15 (and_15_out, not_75_out, not_76_out, OP2, not_77_out, not_78_out, OP5);
  and and_16 (and_16_out, OP0, OP1, not_79_out, not_80_out, not_81_out);
  and and_17 (SysCALL, not_82_out, not_83_out, not_84_out, not_85_out, not_86_out, not_87_out, not_88_out, not_89_out, F2, F3, not_90_out, not_91_out);
  and and_18 (and_18_out, not_92_out, not_93_out, not_94_out, OP2, not_95_out, not_96_out);
  and and_19 (and_19_out, not_97_out, not_98_out, not_99_out, OP2, not_100_out, OP0);
  and and_20 (and_20_out, not_101_out, not_102_out, OP3, not_103_out, not_104_out, not_105_out);
  and and_21 (and_21_out, not_106_out, not_107_out, OP3, not_108_out, not_109_out, OP0);
  and and_22 (and_22_out, not_110_out, not_111_out, OP3, not_112_out, OP1, not_113_out);
  and and_23 (and_23_out, OP5, not_114_out, not_115_out, not_116_out, OP1, OP0);
  and and_24 (and_24_out, OP5, not_117_out, OP3, not_118_out, OP1, OP0);
  and and_25 (and_25_out, OP5, not_119_out, not_120_out, OP2, not_121_out, not_122_out);
  and and_26 (and_26_out, not_123_out, not_124_out, not_125_out, not_126_out, not_127_out, OP0);
  and and_27 (and_27_out, not_128_out, not_129_out, not_130_out, not_131_out, not_132_out, not_133_out, not_134_out, not_135_out, not_136_out, not_137_out, not_138_out);
  and and_28 (and_28_out, not_139_out, not_140_out, not_141_out, not_142_out, not_143_out, not_144_out, not_145_out, not_146_out, not_147_out, not_148_out);
  and and_29 (and_29_out, not_149_out, not_150_out, not_151_out, not_152_out, not_153_out, not_154_out, not_155_out, not_156_out, not_157_out, F5);
  and and_30 (and_30_out, not_158_out, not_159_out, not_160_out, not_161_out, not_162_out, not_163_out, not_164_out, F1, not_165_out, not_166_out, not_167_out);
  and and_31 (and_31_out, not_168_out, not_169_out, not_170_out, not_171_out, not_172_out, not_173_out, F1, not_174_out, not_175_out, not_176_out, not_177_out);
  and and_32 (and_32_out, not_178_out, not_179_out, not_180_out, not_181_out, not_182_out, not_183_out, F1, not_184_out, F3, not_185_out, F5);
  and and_33 (and_33_out, not_186_out, not_187_out, not_188_out, not_189_out, not_190_out, not_191_out, F0, F2, not_192_out, not_193_out, F5);
  and and_34 (BEQ, not_194_out, not_195_out, OP2, not_196_out, not_197_out, not_198_out);
  and and_35 (BNE, OP0, not_199_out, OP2, not_200_out, not_201_out, not_202_out);
  and and_36 (JR, not_203_out, not_204_out, not_205_out, not_206_out, not_207_out, not_208_out, not_209_out, not_210_out, not_211_out, F3, not_212_out, not_213_out);
  and and_37 (and_37_out, not_214_out, not_215_out, not_216_out, not_217_out, not_218_out, not_219_out, not_220_out, not_221_out, F3, not_222_out, not_223_out);
  and and_38 (and_38_out, OP1, not_224_out, not_225_out, not_226_out, not_227_out);
  and and_39 (JAL, OP0, OP1, not_228_out, not_229_out, not_230_out, not_231_out);
  and and_40 (ERET, not_232_out, not_233_out, not_234_out, not_235_out, OP4, not_236_out, not_237_out, not_238_out, not_239_out, F3, F4, not_240_out);
  and and_41 (and_41_out, not_241_out, not_242_out, not_243_out, not_244_out, not_245_out, not_246_out, not_247_out, F1, not_248_out, F3, not_249_out, F5);
  and and_42 (and_42_out, not_250_out, not_251_out, not_252_out, not_253_out, not_254_out, not_255_out, not_256_out, F1, F2, not_257_out, not_258_out, not_259_out);
  and and_43 (LBU, not_260_out, not_261_out, OP2, not_262_out, not_263_out, OP5);
  and and_44 (BGEZ, OP0, not_264_out, not_265_out, not_266_out, not_267_out, not_268_out);
  or or_2 (MemToReg, and_1_out, and_2_out);
  or or_3 (RegWrite, and_7_out, and_8_out, and_9_out, and_10_out, and_11_out, and_12_out, and_13_out, and_14_out, and_15_out, and_16_out);
  or or_4 (SignedExt, and_18_out, and_19_out, and_20_out, and_21_out, and_22_out, and_23_out, and_24_out, and_25_out, and_26_out);
  or or_5 (RegDst, and_27_out, and_28_out, and_29_out, and_30_out, and_31_out, and_32_out, and_33_out);
  or or_6 (JUMP, and_37_out, and_38_out);
  or or_7 (SV, and_41_out, and_42_out);
endmodule

// ALU
module MIPS_ALU (
  input  [4:0] shamt,
  input  [31:0] X,
  input  [31:0] Y,
  input  [3:0] AluOP,
  output Equal,
  output [31:0] Result,
  output [31:0] Result_2
);

  wire [0:0] comparator_1_lt, comparator_2_lt;
  wire [31:0] adder_1_out, AND_out, divider_1_out, divider_1_rem, multiplier_1_cout, multiplier_1_out,
       NOR_out, OR_out, shifter_1_out, shifter_2_out, shifter_3_out, subtractor_1_out, XOR_out;

  assign AND_out = X & Y;  // AND_Gate AND, 32 bits wide
  assign OR_out = X | Y;  // OR_Gate OR, 32 bits wide
  Shifter #(.width(32), .shift("ll")) shifter_1 (.in(Y), .\dist (shamt), .out(shifter_1_out));
  Shifter #(.width(32), .shift("ar")) shifter_2 (.in(Y), .\dist (shamt), .out(shifter_2_out));
  Shifter #(.width(32), .shift("lr")) shifter_3 (.in(Y), .\dist (shamt), .out(shifter_3_out));
  Multiplier #(.width(32)) multiplier_1 (.a(X), .b(Y), .out(multiplier_1_out), .cout(multiplier_1_cout));  // open: cin
  Divider #(.width(32)) divider_1 (.a(X), .b(Y), .out(divider_1_out), .rem(divider_1_rem));  // open: upper
  Adder #(.width(32)) adder_1 (.a(X), .b(Y), .out(adder_1_out));  // open: cin, cout
  Subtractor #(.width(32)) subtractor_1 (.a(X), .b(Y), .out(subtractor_1_out));  // open: bin, bout
  assign XOR_out = X ^ Y;  // XOR_Gate XOR, 32 bits wide
  assign NOR_out = ~(X | Y);  // NOR_Gate NOR, 32 bits wide
  Comparator #(.width(32), .mode("twosComplement")) comparator_1 (
    .a(X), .b(Y), .eq(Equal), .lt(comparator_1_lt[0]));  // open: gt
  Comparator #(.width(32), .mode("unsigned")) comparator_2 (.a(X), .b(Y), .lt(comparator_2_lt[0]));  // open: gt, eq
  Multiplexer #(.select(4), .width(32), .disabled("Z"), .enable("false")) multiplexer_1 (
    .in0(shifter_1_out), .in1(shifter_2_out), .in2(shifter_3_out), .in3(multiplier_1_out),
    .in4(divider_1_out), .in5(adder_1_out), .in6(subtractor_1_out), .in7(AND_out), .in8(OR_out),
    .in9(XOR_out), .in10(NOR_out), .in11({{31{1'b0}}, comparator_1_lt[0]}),
    .in12({{31{1'b0}}, comparator_2_lt[0]}), .in13({32{1'b0}}), .in14({32{1'b0}}), .in15({32{1'b0}}),
    .out(Result), .sel(AluOP));
  Multiplexer #(.select(4), .width(32), .disabled("Z"), .enable("false")) multiplexer_2 (
    .in0({32{1'b0}}), .in1({32{1'b0}}), .in2({32{1'b0}}), .in3(multiplier_1_cout), .in4(divider_1_rem),
    .in5({32{1'b0}}), .in6({32{1'b0}}), .in7({32{1'b0}}), .in8({32{1'b0}}), .in9({32{1'b0}}),
    .in10({32{1'b0}}), .in11({32{1'b0}}), .in12({32{1'b0}}), .in13({32{1'b0}}), .in14({32{1'b0}}),
    .in15({32{1'b0}}), .out(Result_2), .sel(AluOP));

  // Other names for the same wires on the sheet: Result2[31:0] = Result_2; S[3:0] = AluOP

  // Notes on the sheet:
  //   不要改变此引脚区域内容，也不要改变ALU封装形式
  //   输入引脚
  //   输出引脚
endmodule

module MIPS_Regifile (
  input  [31:0] Din,
  input  Clk,
  input  WE,
  input  [4:0] R1_num,
  input  [4:0] W_num,
  input  [4:0] R2_num,
  output [31:0] R1,
  output [31:0] R2
);

  // RegisterFile registerfile_1: pin names not known; wires that end beside it: Din, Clk, WE, W_num, R1_num, R2_num, R1, R2
endmodule

// imm_EX
module \理想流水线  (
  output RegWrite,
  output MemWrite,
  output [31:0] IF_PC,
  output [31:0] ID_PC,
  output [31:0] EX_PC,
  output [31:0] M_PC,
  output [31:0] WB_PC,
  output [31:0] RDin,
  output [31:0] MDin,
  output [31:0] LedData
);

  wire AluSrcB_EX, AluSrcB_ID, Beq, BGEZ, Bne, CLK, clock_1_out, clock_2_out, comparator_1_eq,
       comparator_1_lt, comparator_2_eq, d_ff_1_q, ERET, Go, Halt, IR1, IR2, IR3, JAL, JMP, JR, LBU, LED_EN,
       MemToReg_EX, MemToReg_ID, MemToReg_MEM, MemWrite_EX, MemWrite_ID, nand_1_out, not_1_out, RegDst_EX,
       RegDst_ID, RegDst_MEM, RegDst_WB, RegWrite_EX, RegWrite_ID, RegWrite_MEM, RST, SignedExt_EX,
       SignedExt_ID, SV, Syscall_EX, Syscall_ID, W1, W2, W3;
  wire [3:0] AluOP_EX, AluOP_ID;
  wire [4:0] multiplexer_1_out, multiplexer_2_out, multiplexer_3_out, multiplexer_4_out, rd_WB, rt_WB;
  wire [5:0] Func;
  wire [12:0] CNT_num;
  wire [15:0] \LoadUse次数 , \总周期数 , \插入气泡数 , \无条件分支数 , \条件分支成功数 ;
  wire [31:0] a0, adder_1_out, AluRes_EX, AluRes_MEM, bit_extender_1_out, bit_extender_2_out, EX_IR, IF_IR,
       imm_EX, imm_ID, MDin_EX, MEM_IR, multiplexer_6_out, PC_4, R1_EX, R1_ID, R2_ID, ram_1_data, RDin_MEM,
       WB_IR;
  wire [31:6] ID_IR;

  Button \u_总复位  (.out(RST));
  Button _1 (.out(IR1));
  Button _2 (.out(IR2));
  Button _3 (.out(IR3));
  // Probe on \总周期数 
  // Probe on \总周期数 
  Button \u_继续运行  (.out(Go));
  LED #(.active("true")) led_1 (.in(W1));
  LED #(.active("true")) led_2 (.in(W2));
  LED #(.active("true")) led_3 (.in(W3));
  Adder #(.width(32)) adder_1 (.a(IF_PC), .b(32'h4), .out(adder_1_out));  // open: cin, cout
  Hex_Digit_Display hex_digit_display_1 (.value(LedData[31:28]));  // open: dp
  // Probe on IF_PC[19:0]
  // Mips_Probe mips_probe_1: pin names not known; wires that end beside it: IF_IR
  Hex_Digit_Display hex_digit_display_2 (.value(LedData[23:20]));  // open: dp
  Hex_Digit_Display hex_digit_display_3 (.value(LedData[27:24]));  // open: dp
  // Probe on ID_PC[19:0]
  // Mips_Probe mips_probe_2: pin names not known; wires that end beside it: {ID_IR, Func}
  Register #(.width(32), .trigger("rising"), .Select("low")) PC (
    .D(adder_1_out), .Q(IF_PC), .clk(CLK));  // open: en, clr
  // Probe on IF_PC
  Hex_Digit_Display hex_digit_display_4 (.value(LedData[19:16]));  // open: dp
  Hex_Digit_Display hex_digit_display_5 (.value(LedData[15:12]));  // open: dp
  // Mips_Probe mips_probe_3: pin names not known; wires that end beside it: IF_IR
  // Probe on IF_IR
  Hex_Digit_Display hex_digit_display_6 (.value(LedData[11:8]));  // open: dp
  Hex_Digit_Display hex_digit_display_7 (.value(LedData[7:4]));  // open: dp
  Clock #(.highDuration(1), .lowDuration(1)) clock_1 (.out(clock_1_out));
  // Probe on EX_PC[19:0]
  // Mips_Probe mips_probe_4: pin names not known; wires that end beside it: clock_1_out, EX_IR, CLK
  ROM #(.addrWidth(10), .dataWidth(32), .Select("high")) rom_1 (.addr(IF_PC[11:2]), .data(IF_IR));
  Hex_Digit_Display hex_digit_display_8 (.value(LedData[3:0]));  // open: dp
  // Probe on \总周期数 
  // Probe on M_PC[19:0]
  // Mips_Probe mips_probe_5: pin names not known; wires that end beside it: MEM_IR
  \理想流水线IF_ID  \u_理想流水线if_id_1  (.IR_IN(IF_IR), .IR_OUT({ID_IR, Func}), .PC_IN(IF_PC), .PC_OUT(ID_PC), .CLK(CLK));
  // Probe on \总周期数 
  // Probe on \无条件分支数 
  // Probe on \条件分支成功数 
  // Probe on \插入气泡数 
  // Probe on \LoadUse次数 
  // Probe on IF_PC[11:0]
  // Probe on WB_PC[19:0]
  // Mips_Probe mips_probe_6: pin names not known; wires that end beside it: {WB_IR[31:21], rt_WB, rd_WB, WB_IR[10:0]}
  // Probe on ID_PC[11:0]
  // Probe on EX_PC[11:0]
  // Probe on M_PC[11:0]
  D_Flip_Flop #(.trigger("high"), .Pre_Clr_Positions("LEGACY"), .NegatePresetClear("false"), .enable("true"), .NewFFLayout("false")) d_ff_1 (.Q(d_ff_1_q));  // open: clk, D, Qn, preset, en, reset
  // Probe on 13'hc
  \单周期硬布线控制器  \u_单周期硬布线控制器_1  (
    .Func(Func), .OP(ID_IR[31:26]), .ALU_OP(AluOP_ID), .MemToReg(MemToReg_ID), .MemWrite(MemWrite_ID),
    .ALU_SRC(AluSrcB_ID), .RegWrite(RegWrite_ID), .SysCALL(Syscall_ID), .SignedExt(SignedExt_ID),
    .RegDst(RegDst_ID), .JR(JR), .JMP(JMP), .Beq(Beq), .JAL(JAL), .Bne(Bne), .ERET(ERET), .SV(SV), .LBU(LBU),
    .BGEZ(BGEZ));
  // Probe on WB_PC[11:0]
  Comparator #(.width(13), .mode("twosComplement")) comparator_1 (
    .a(CNT_num), .b(13'hc), .eq(comparator_1_eq), .lt(comparator_1_lt));  // open: gt
  Clock #(.highDuration(1), .lowDuration(1)) clock_2 (.out(clock_2_out));
  nand nand_1 (nand_1_out, d_ff_1_q, comparator_1_eq);
  Counter #(.width(13), .max('h1fff), .ongoal("stay"), .trigger("rising"), .behavior("old")) counter_1 (
    .count(comparator_1_lt), .Q(CNT_num), .clk(clock_2_out));  // open: load, D, carry, clr, preset
  assign CLK = nand_1_out ? clock_2_out : 1'bz;  // Controlled_Buffer controlled_buffer_1
  Multiplexer #(.select(1), .width(5), .disabled("Z"), .enable("false")) multiplexer_1 (
    .in0(rt_WB), .in1(rd_WB), .out(multiplexer_1_out), .sel(RegDst_WB));
  Pull_Resistor #(.pull(1)) pull_resistor_1 (.node(CLK));
  Multiplexer #(.select(1), .width(5), .disabled("Z"), .enable("false")) multiplexer_2 (
    .in0(ID_IR[25:21]), .in1(5'b00010), .out(multiplexer_2_out), .sel(Syscall_ID));
  Multiplexer #(.select(1), .width(5), .disabled("Z"), .enable("false")) multiplexer_3 (
    .in0(ID_IR[20:16]), .in1(5'b00100), .out(multiplexer_3_out), .sel(Syscall_ID));
  Multiplexer #(.select(1), .width(5), .disabled("Z"), .enable("false")) multiplexer_4 (
    .in0(multiplexer_1_out), .in1({5{1'b1}}), .out(multiplexer_4_out), .sel(JAL));
  // Probe on multiplexer_2_out
  // Probe on multiplexer_3_out
  // Probe on multiplexer_4_out
  not not_1 (not_1_out, Halt);
  Counter #(.width(16), .max('hffff), .ongoal("wrap"), .trigger("rising"), .behavior("new")) counter_2 (
    .count(not_1_out), .Q(\总周期数 ), .clk(CLK));  // open: load, D, carry, clr, preset, down
  MIPS_Regifile mips_regifile_1 (
    .Din(RDin), .Clk(CLK), .R1(R1_ID), .R2(R2_ID), .WE(RegWrite), .W_num(multiplexer_4_out),
    .R1_num(multiplexer_2_out), .R2_num(multiplexer_3_out));
  assign bit_extender_1_out = {{16{1'b0}}, {ID_IR[15:6], Func}};  // Bit_Extender bit_extender_1
  Multiplexer #(.select(1), .width(32), .disabled("Z"), .enable("false")) multiplexer_5 (
    .in0(bit_extender_1_out), .in1(bit_extender_2_out), .out(imm_ID), .sel(SignedExt_ID));
  assign bit_extender_2_out = {{16{ID_IR[15]}}, {ID_IR[15:6], Func}};  // Bit_Extender bit_extender_2
  Register #(.width(32), .trigger("rising"), .Select("low")) register_1 (
    .D(a0), .en(LED_EN), .Q(LedData), .clk(CLK));  // open: clr
  \理想流水线ID_EX  \u_理想流水线id_ex_1  (
    .IR_IN({ID_IR, Func}), .PC_IN(ID_PC), .SignedExt_IN(SignedExt_ID), .MemToReg_IN(MemToReg_ID),
    .MemWrite_IN(MemWrite_ID), .Aluop_IN(AluOP_ID), .AluSrcB_IN(AluSrcB_ID), .RegWrite_IN(RegWrite_ID),
    .RegDst_IN(RegDst_ID), .Syscall_IN(Syscall_ID), .R1_IN(R1_ID), .R2_IN(R2_ID), .imm_IN(imm_ID), .CLK(CLK),
    .IR_OUT(EX_IR), .PC_OUT(EX_PC), .SignedExt_OUT(SignedExt_EX), .MemToReg_OUT(MemToReg_EX),
    .MemWrite_OUT(MemWrite_EX), .Aluop_OUT(AluOP_EX), .AluSrcB_OUT(AluSrcB_EX), .RegWrite_OUT(RegWrite_EX),
    .RegDst_OUT(RegDst_EX), .Syscall_OUT(Syscall_EX), .R1_OUT(R1_EX), .R2_OUT(MDin_EX), .imm_OUT(imm_EX));
  Comparator #(.width(32), .mode("twosComplement")) comparator_2 (
    .a(32'ha), .b(R1_EX), .eq(comparator_2_eq));  // open: gt, lt
  Multiplexer #(.select(1), .width(32), .disabled("Z"), .enable("false")) multiplexer_6 (
    .in0(MDin_EX), .in1(imm_EX), .out(multiplexer_6_out), .sel(AluSrcB_EX));
  and and_1 (Halt, Syscall_EX, comparator_2_eq);
  MIPS_ALU mips_alu_1 (
    .X(R1_EX), .Y(multiplexer_6_out), .AluOP(AluOP_EX), .Result(AluRes_EX), .shamt(EX_PC[10:6]));  // open: Equal, Result_2
  \理想流水线EX_MEM  \u_理想流水线ex_mem_1  (
    .IR_IN(EX_IR), .PC_IN(EX_PC), .MemToReg_IN(MemToReg_EX), .MemWrite_IN(MemWrite_EX),
    .RegWrite_IN(RegWrite_EX), .RegDst_IN(RegDst_EX), .AluRes_IN(AluRes_EX), .MDin_IN(MDin_EX), .CLK(CLK),
    .IR_OUT(MEM_IR), .PC_OUT(M_PC), .MemToReg_OUT(MemToReg_MEM), .MemWrite_OUT(MemWrite),
    .RegWrite_OUT(RegWrite_MEM), .RegDst_OUT(RegDst_MEM), .AluRes_OUT(AluRes_MEM), .MDin_OUT(MDin));
  Adder #(.width(32)) adder_2 (.a(M_PC), .b(32'h4), .out(PC_4));  // open: cin, cout
  RAM #(.addrWidth(10), .dataWidth(32), .bus("separate"), .Select("high")) ram_1 (
    .addr(AluRes_MEM[11:2]), .din(MDin), .data(ram_1_data), .str(MemWrite), .clk(CLK));  // open: sel, ld, clr
  Multiplexer #(.select(2), .width(32), .disabled("Z"), .enable("false")) multiplexer_7 (
    .in0(AluRes_MEM), .in1(ram_1_data), .in2(PC_4), .in3(PC_4), .out(RDin_MEM), .sel({1'b0, MemToReg_MEM}));
  \理想流水线MEM_WB  \u_理想流水线mem_wb_1  (
    .IR_IN(MEM_IR), .PC_IN(M_PC), .RegWrite_IN(RegWrite_MEM), .RegDst_IN(RegDst_MEM), .Reg_IN(RDin_MEM),
    .CLK(CLK), .IR_OUT({WB_IR[31:21], rt_WB, rd_WB, WB_IR[10:0]}), .PC_OUT(WB_PC), .RegWrite_OUT(RegWrite),
    .RegDst_OUT(RegDst_WB), .Reg_OUT(RDin));

  // Other names for the same wires on the sheet: shamt[4:0] = EX_PC[10:6]; ID_IR[5:0] = Func;
  //   imm[15:0] = {ID_IR[15:6], Func}; rt[4:0] = ID_IR[20:16]; rs[4:0] = ID_IR[25:21]; OP[5:0] = ID_IR[31:26];
  //   MDin_MEM[31:0] = MDin; MEM_PC[31:0] = M_PC; MemWrite_MEM = MemWrite; R2_EX[31:0] = MDin_EX;
  //   WB_IR[20:11] = {rt_WB, rd_WB}

  // Notes on the sheet:
  //   中断源
  //   时空图监测，可删除
  //   中断等待指示
  //   数码管输出
  //   指令存储器
  //   contents of rom_1 (hex, n*v repeats v):
  //   20100000 20110000 20120000 20130000 36100000 36310001 36520002 36730003 ae100000 ae110004 ae120008
  //   ae13000c 2002000a 20110000 20120000 20130000 c
  //   OP
  //   Func
  //   rs
  //   rt
  //   控制位
  //   JMP
  //   JR
  //   SV
  //   LBU
  //   BGEZ
  //   OP
  //   Func
  //   流水调试日志用
  //   暂停节拍，不能为0
  //   用这个时钟源需要去掉电路中的其他时钟源
  //   因为理想流水线无分支跳转指令，所以j型指令无信号产生
  //   Beq
  //   Bne
  //   MemToReg
  //   MemWrite
  //   AluOP
  //   AluSrcB
  //   RegWrite
  //   JAL
  //   RegDst
  //   Syscall
  //   戳工具置1进入计数暂停模式，ctrl+k时钟自动运行到对应节拍暂停
  //   ctrl+k关闭时钟连续运行，将控制位置零，进入单步调试模式调试
  //   可计数暂停的时钟源
  //   为方便自动评测，需要输出流水线各段保存的PC值，注意是PC不是PC+4，另外ID段寄存器写入信息，Mem段内存写入信息也要输出
endmodule

module \理想流水线IF_ID  (
  input  [31:0] IR_IN,
  input  [31:0] PC_IN,
  input  CLK,
  output [31:0] IR_OUT,
  output [31:0] PC_OUT
);

  Register #(.width(32), .trigger("rising"), .Select("low")) register_1 (
    .D(IR_IN), .Q(IR_OUT), .clk(CLK));  // open: en, clr
  Register #(.width(32), .trigger("rising"), .Select("low")) register_2 (
    .D(PC_IN), .Q(PC_OUT), .clk(CLK));  // open: en, clr
endmodule

// 理想流水线ID/Ex
module \理想流水线ID_EX  (
  input  [31:0] IR_IN,
  input  [31:0] PC_IN,
  input  SignedExt_IN,
  input  MemToReg_IN,
  input  MemWrite_IN,
  input  [3:0] Aluop_IN,
  input  AluSrcB_IN,
  input  RegWrite_IN,
  input  RegDst_IN,
  input  Syscall_IN,
  input  [31:0] R1_IN,
  input  [31:0] R2_IN,
  input  [31:0] imm_IN,
  input  CLK,
  output [31:0] IR_OUT,
  output [31:0] PC_OUT,
  output SignedExt_OUT,
  output MemToReg_OUT,
  output MemWrite_OUT,
  output [3:0] Aluop_OUT,
  output AluSrcB_OUT,
  output RegWrite_OUT,
  output RegDst_OUT,
  output Syscall_OUT,
  output [31:0] R1_OUT,
  output [31:0] R2_OUT,
  output [31:0] imm_OUT
);

  Register #(.width(32), .trigger("rising"), .Select("low")) register_1 (
    .D(IR_IN), .Q(IR_OUT), .clk(CLK));  // open: en, clr
  Register #(.width(32), .trigger("rising"), .Select("low")) register_2 (
    .D(PC_IN), .Q(PC_OUT), .clk(CLK));  // open: en, clr
  Register #(.width(1), .trigger("rising"), .Select("low")) register_3 (
    .D(SignedExt_IN), .Q(SignedExt_OUT), .clk(CLK));  // open: en, clr
  Register #(.width(1), .trigger("rising"), .Select("low")) register_4 (
    .D(MemToReg_IN), .Q(MemToReg_OUT), .clk(CLK));  // open: en, clr
  Register #(.width(1), .trigger("rising"), .Select("low")) register_5 (
    .D(MemWrite_IN), .Q(MemWrite_OUT), .clk(CLK));  // open: en, clr
  Register #(.width(4), .trigger("rising"), .Select("low")) register_6 (
    .D(Aluop_IN), .Q(Aluop_OUT), .clk(CLK));  // open: en, clr
  Register #(.width(1), .trigger("rising"), .Select("low")) register_7 (
    .D(AluSrcB_IN), .Q(AluSrcB_OUT), .clk(CLK));  // open: en, clr
  Register #(.width(1), .trigger("rising"), .Select("low")) register_8 (
    .D(RegWrite_IN), .Q(RegWrite_OUT), .clk(CLK));  // open: en, clr
  Register #(.width(1), .trigger("rising"), .Select("low")) register_9 (
    .D(RegDst_IN), .Q(RegDst_OUT), .clk(CLK));  // open: en, clr
  Register #(.width(1), .trigger("rising"), .Select("low")) register_10 (
    .D(Syscall_IN), .Q(Syscall_OUT), .clk(CLK));  // open: en, clr
  Register #(.width(32), .trigger("rising"), .Select("low")) register_11 (
    .D(R1_IN), .Q(R1_OUT), .clk(CLK));  // open: en, clr
  Register #(.width(32), .trigger("rising"), .Select("low")) register_12 (
    .D(R2_IN), .Q(R2_OUT), .clk(CLK));  // open: en, clr
  Register #(.width(32), .trigger("rising"), .Select("low")) register_13 (
    .D(imm_IN), .Q(imm_OUT), .clk(CLK));  // open: en, clr
endmodule

module \理想流水线EX_MEM  (
  input  [31:0] IR_IN,
  input  [31:0] PC_IN,
  input  MemToReg_IN,
  input  MemWrite_IN,
  input  RegWrite_IN,
  input  RegDst_IN,
  input  [31:0] AluRes_IN,
  input  [31:0] MDin_IN,
  input  CLK,
  output [31:0] IR_OUT,
  output [31:0] PC_OUT,
  output MemToReg_OUT,
  output MemWrite_OUT,
  output RegWrite_OUT,
  output RegDst_OUT,
  output [31:0] AluRes_OUT,
  output [31:0] MDin_OUT
);

  Register #(.width(32), .trigger("rising"), .Select("low")) register_1 (
    .D(IR_IN), .Q(IR_OUT), .clk(CLK));  // open: en, clr
  Register #(.width(32), .trigger("rising"), .Select("low")) register_2 (
    .D(PC_IN), .Q(PC_OUT), .clk(CLK));  // open: en, clr
  Register #(.width(1), .trigger("rising"), .Select("low")) register_3 (
    .D(MemToReg_IN), .Q(MemToReg_OUT), .clk(CLK));  // open: en, clr
  Register #(.width(1), .trigger("rising"), .Select("low")) register_4 (
    .D(MemWrite_IN), .Q(MemWrite_OUT), .clk(CLK));  // open: en, clr
  Register #(.width(1), .trigger("rising"), .Select("low")) register_5 (
    .D(RegWrite_IN), .Q(RegWrite_OUT), .clk(CLK));  // open: en, clr
  Register #(.width(1), .trigger("rising"), .Select("low")) register_6 (
    .D(RegDst_IN), .Q(RegDst_OUT), .clk(CLK));  // open: en, clr
  Register #(.width(32), .trigger("rising"), .Select("low")) register_7 (
    .D(AluRes_IN), .Q(AluRes_OUT), .clk(CLK));  // open: en, clr
  Register #(.width(32), .trigger("rising"), .Select("low")) register_8 (
    .D(MDin_IN), .Q(MDin_OUT), .clk(CLK));  // open: en, clr
endmodule

module \理想流水线MEM_WB  (
  input  [31:0] IR_IN,
  input  [31:0] PC_IN,
  input  RegWrite_IN,
  input  RegDst_IN,
  input  [31:0] Reg_IN,
  input  CLK,
  output [31:0] IR_OUT,
  output [31:0] PC_OUT,
  output RegWrite_OUT,
  output RegDst_OUT,
  output [31:0] Reg_OUT
);

  Register #(.width(32), .trigger("rising"), .Select("low")) register_1 (
    .D(IR_IN), .Q(IR_OUT), .clk(CLK));  // open: en, clr
  Register #(.width(32), .trigger("rising"), .Select("low")) register_2 (
    .D(PC_IN), .Q(PC_OUT), .clk(CLK));  // open: en, clr
  Register #(.width(1), .trigger("rising"), .Select("low")) register_3 (
    .D(RegWrite_IN), .Q(RegWrite_OUT), .clk(CLK));  // open: en, clr
  Register #(.width(1), .trigger("rising"), .Select("low")) register_4 (
    .D(RegDst_IN), .Q(RegDst_OUT), .clk(CLK));  // open: en, clr
  Register #(.width(32), .trigger("rising"), .Select("low")) register_5 (
    .D(Reg_IN), .Q(Reg_OUT), .clk(CLK));  // open: en, clr
endmodule

module \气泡流水线  (
  output RegWrite,
  output MemWrite,
  output [31:0] IF_PC,
  output [31:0] ID_PC,
  output [31:0] EX_PC,
  output [31:0] M_PC,
  output [31:0] WB_PC,
  output [31:0] RDin,
  output [31:0] MDin,
  output [31:0] LedData
);

  wire AluSrcB_EX, AluSrcB_ID, and_1_out, and_2_out, and_3_out, and_6_out, B_EX, BEQ_EX, BEQ_ID, BGEZ_EX,
       BGEZ_ID, BNE_EX, BNE_ID, CLK, clock_1_out, clock_2_out, comparator_1_eq, comparator_1_lt,
       comparator_2_eq, comparator_3_eq, comparator_4_eq, comparator_5_eq, d_ff_1_q, Equal, ERET_ID, Exit,
       Go, IF_STALL, IR1, IR2, IR3, JAL_EX, JAL_ID, JAL_MEM, JAL_WB, JMP_EX, JMP_ID, JR_EX, JR_ID, LBU_EX,
       LBU_ID, LBU_MEM, LBU_WB, MEM_STALL, MemToReg_EX, MemToReg_ID, MemToReg_MEM, MemToReg_WB, MemWrite_EX,
       MemWrite_ID, nand_1_out, not_1_out, not_2_out, or_1_out, or_2_out, Pause, RegDst_EX, RegDst_ID,
       RegDst_MEM, RegWrite_EX, RegWrite_ID, RegWrite_MEM, RST, SignedExt_EX, SignedExt_ID, SV_EX, SV_ID,
       Syscall_EX, Syscall_ID, W1, W2, W3, \寄存器使用情况_1_r1_used , \寄存器使用情况_1_r2_used ;
  wire [1:0] xor_1_out;
  wire [3:0] AluOP_EX, AluOP_ID;
  wire [4:0] multiplexer_2_out, R1__ID, R2__ID, RegWrite__EX, RegWrite__ID, RegWrite__MEM, RegWrite__WB,
       shamt;
  wire [5:0] Func;
  wire [7:0] multiplexer_11_out;
  wire [12:0] CNT_num;
  wire [15:0] \LoadUse次数 , \总周期数 , \插入气泡数 , \无条件分支数 , \条件分支成功数 ;
  wire [27:0] adder_2_out;
  wire [31:0] adder_3_out, adder_5_out, AluRes_EX, AluRes_MEM, AluRes_WB, bit_extender_1_out,
       bit_extender_2_out, bit_extender_3_out, EX_IR, EX_PC_imm, EX_PC_JR, IF_IR, imm_EX, imm_ID, MDin_EX,
       MEM_IR, multiplexer_1_out, multiplexer_7_out, multiplexer_8_out, multiplexer_10_out,
       multiplexer_12_out, PC_4, R1_ID, R2_ID, RDin_MEM, RDin_WB, shifter_1_out, WB_IR;
  wire [31:6] ID_IR;
  wire [31:28] EX_PC_J_JAL;

  Button \u_总复位  (.out(RST));
  Button _1 (.out(IR1));
  Button _2 (.out(IR2));
  Button _3 (.out(IR3));
  // Probe on \总周期数 
  // Probe on \总周期数 
  Button \u_继续运行  (.out(Go));
  LED #(.active("true")) led_1 (.in(W1));
  LED #(.active("true")) led_2 (.in(W2));
  LED #(.active("true")) led_3 (.in(W3));
  Hex_Digit_Display hex_digit_display_1 (.value(LedData[31:28]));  // open: dp
  // Probe on IF_PC[19:0]
  // Mips_Probe mips_probe_1: pin names not known; wires that end beside it: IF_IR
  Hex_Digit_Display hex_digit_display_2 (.value(LedData[23:20]));  // open: dp
  Hex_Digit_Display hex_digit_display_3 (.value(LedData[27:24]));  // open: dp
  // Probe on ID_PC[19:0]
  // Mips_Probe mips_probe_2: pin names not known; wires that end beside it: {ID_IR, Func}
  Hex_Digit_Display hex_digit_display_4 (.value(LedData[15:12]));  // open: dp
  Hex_Digit_Display hex_digit_display_5 (.value(LedData[19:16]));  // open: dp
  not not_1 (not_1_out, IF_STALL);
  Multiplexer #(.select(3), .width(32), .disabled("Z"), .enable("false")) multiplexer_1 (
    .in0(PC_4), .in1(EX_PC_imm), .in2({EX_PC_J_JAL, EX_IR[25:0], 2'b00}), .in6(EX_PC_JR),
    .out(multiplexer_1_out), .sel({JR_EX, JMP_EX, B_EX}));  // open: in3, in4, in5, in7
  Hex_Digit_Display hex_digit_display_6 (.value(LedData[11:8]));  // open: dp
  Hex_Digit_Display hex_digit_display_7 (.value(LedData[7:4]));  // open: dp
  Clock #(.highDuration(1), .lowDuration(1)) clock_1 (.out(clock_1_out));
  // Probe on EX_PC[19:0]
  // Mips_Probe mips_probe_3: pin names not known; wires that end beside it: clock_1_out, EX_IR, CLK
  Register #(.width(32), .trigger("rising"), .Select("low")) register_1 (
    .D(multiplexer_1_out), .en(not_1_out), .Q(IF_PC), .clk(CLK));  // open: clr
  // Probe on IF_PC
  Hex_Digit_Display hex_digit_display_8 (.value(LedData[3:0]));  // open: dp
  Counter #(.width(16), .max('hffff), .ongoal("wrap"), .trigger("rising"), .behavior("new")) counter_1 (
    .Q(\总周期数 ), .clk(CLK));  // open: load, D, count, carry, clr, preset, down
  // Probe on IF_IR
  Adder #(.width(32)) adder_1 (.a(IF_PC), .b(32'h4), .out(PC_4));  // open: cin, cout
  // Probe on \总周期数 
  // Probe on M_PC[19:0]
  // Mips_Probe mips_probe_4: pin names not known; wires that end beside it: MEM_IR
  ROM #(.addrWidth(10), .dataWidth(32), .Select("high")) rom_1 (.addr(IF_PC[11:2]), .data(IF_IR));
  // Probe on \总周期数 
  // Probe on \无条件分支数 
  // Probe on \条件分支成功数 
  // Probe on \插入气泡数 
  // Probe on \LoadUse次数 
  // Mips_Probe mips_probe_5: pin names not known; wires that end beside it: IF_IR
  or or_1 (or_1_out, JMP_EX, B_EX);
  // Probe on IF_PC[11:0]
  // Probe on WB_PC[19:0]
  // Mips_Probe mips_probe_6: pin names not known; wires that end beside it: WB_IR
  \气泡流水线接口IF_ID  \u_气泡流水线接口if_id_1  (
    .IR_IN(IF_IR), .PC_IN(IF_PC), .CLK(CLK), .IR_OUT({ID_IR, Func}), .PC_OUT(ID_PC),
    .\同步清零_气泡_高电平有效 (or_1_out), .\使能端_低电平有效_stall_高电平有效 (IF_STALL));  // open: 传输状态In_表明当前传输数据有效, 传输状态Out_表明当前传输数据有效
  // Probe on ID_PC[11:0]
  // Probe on EX_PC[11:0]
  // Mips_Probe mips_probe_7: pin names not known; wires that end beside it: {ID_IR, Func}
  // Probe on M_PC[11:0]
  D_Flip_Flop #(.trigger("high"), .Pre_Clr_Positions("LEGACY"), .NegatePresetClear("false"), .enable("true"), .NewFFLayout("false")) d_ff_1 (.Q(d_ff_1_q));  // open: clk, D, Qn, preset, en, reset
  // Probe on 13'h610
  // Probe on WB_PC[11:0]
  Comparator #(.width(13), .mode("twosComplement")) comparator_1 (
    .a(CNT_num), .b(13'h610), .eq(comparator_1_eq), .lt(comparator_1_lt));  // open: gt
  Clock #(.highDuration(1), .lowDuration(1)) clock_2 (.out(clock_2_out));
  Multiplexer #(.select(1), .width(5), .disabled("Z"), .enable("false")) multiplexer_2 (
    .in0(ID_IR[20:16]), .in1(ID_IR[15:11]), .out(multiplexer_2_out), .sel(RegDst_ID));
  nand nand_1 (nand_1_out, d_ff_1_q, comparator_1_eq);
  Counter #(.width(13), .max('h1fff), .ongoal("stay"), .trigger("rising"), .behavior("old")) counter_2 (
    .count(comparator_1_lt), .Q(CNT_num), .clk(clock_2_out));  // open: load, D, carry, clr, preset
  \单周期硬布线控制器  \u_单周期硬布线控制器_1  (
    .Func(Func), .OP(ID_IR[31:26]), .ALU_OP(AluOP_ID), .MemToReg(MemToReg_ID), .MemWrite(MemWrite_ID),
    .ALU_SRC(AluSrcB_ID), .RegWrite(RegWrite_ID), .SysCALL(Syscall_ID), .SignedExt(SignedExt_ID),
    .RegDst(RegDst_ID), .JR(JR_ID), .JMP(JMP_ID), .Beq(BEQ_ID), .JAL(JAL_ID), .Bne(BNE_ID), .ERET(ERET_ID),
    .SV(SV_ID), .LBU(LBU_ID), .BGEZ(BGEZ_ID));
  Multiplexer #(.select(1), .width(5), .disabled("Z"), .enable("false")) multiplexer_3 (
    .in0(multiplexer_2_out), .in1({5{1'b1}}), .out(RegWrite__ID), .sel(JAL_ID));
  assign CLK = nand_1_out ? clock_2_out : 1'bz;  // Controlled_Buffer controlled_buffer_1
  \寄存器使用情况  \u_寄存器使用情况_1  (
    .OP0(ID_IR[26]), .OP1(ID_IR[27]), .OP2(ID_IR[28]), .OP3(ID_IR[29]), .OP4(ID_IR[30]), .OP5(ID_IR[31]),
    .F0(Func[0]), .F1(Func[1]), .F2(Func[2]), .F3(Func[3]), .F4(Func[4]), .F5(Func[5]),
    .R1_Used(\寄存器使用情况_1_r1_used ), .R2_Used(\寄存器使用情况_1_r2_used ));
  Pull_Resistor #(.pull(1)) pull_resistor_1 (.node(CLK));
  \数据相关检测  \u_数据相关检测_1  (
    .RegWrite__MEM(RegWrite__MEM), .RegWrite_MEM(RegWrite_MEM), .RegWrite__EX(RegWrite__EX),
    .RegWrite_EX(RegWrite_EX), .R1_Used(\寄存器使用情况_1_r1_used ), .\数据相关 (IF_STALL),
    .R2_Used(\寄存器使用情况_1_r2_used ), .R1_num(R1__ID), .R2_num(R2__ID));
  Multiplexer #(.select(1), .width(5), .disabled("Z"), .enable("false")) multiplexer_4 (
    .in0(ID_IR[25:21]), .in1(5'b00010), .out(R1__ID), .sel(Syscall_ID));
  Multiplexer #(.select(1), .width(5), .disabled("Z"), .enable("false")) multiplexer_5 (
    .in0(ID_IR[20:16]), .in1(5'b00100), .out(R2__ID), .sel(Syscall_ID));
  Counter #(.width(16), .max('hffff), .ongoal("wrap"), .trigger("rising"), .behavior("new")) counter_3 (
    .count(IF_STALL), .Q(\插入气泡数 ), .clk(CLK), .clr(RST));  // open: load, D, carry, preset, down
  // Probe on R1__ID
  // Probe on R2__ID
  // Probe on RegWrite__WB
  assign bit_extender_1_out = {{16{1'b0}}, {ID_IR[15:6], Func}};  // Bit_Extender bit_extender_1
  assign bit_extender_2_out = {{16{ID_IR[15]}}, {ID_IR[15:6], Func}};  // Bit_Extender bit_extender_2
  \气泡regfile  \u_气泡regfile_1  (
    .Din(RDin), .Clk(CLK), .R1(R1_ID), .R2(R2_ID), .WE(RegWrite), .W_num(RegWrite__WB), .R1_num(R1__ID),
    .R2_num(R2__ID));
  Multiplexer #(.select(1), .width(32), .disabled("Z"), .enable("false")) multiplexer_6 (
    .in0(bit_extender_1_out), .in1(bit_extender_2_out), .out(imm_ID), .sel(SignedExt_ID));
  or or_2 (or_2_out, JMP_EX, B_EX, IF_STALL);
  // Mips_Probe mips_probe_8: pin names not known; wires that end beside it: EX_IR
  \气泡流水线接口ID_EX  \u_气泡流水线接口id_ex_1  (
    .IR_IN({ID_IR, Func}), .PC_IN(ID_PC), .JMP_IN(JMP_ID), .Beq_IN(BEQ_ID), .JR_IN(JR_ID), .Bne_IN(BNE_ID),
    .SignedExt_IN(SignedExt_ID), .MemToReg_IN(MemToReg_ID), .MemWrite_IN(MemWrite_ID), .LBU_IN(LBU_ID),
    .AluOp_IN(AluOP_ID), .BGEZ_IN(BGEZ_ID), .AluSrcB_IN(AluSrcB_ID), .RegWrite_IN(RegWrite_ID),
    .JAL_IN(JAL_ID), .RegDst_IN(RegDst_ID), .Syscall_IN(Syscall_ID), .RegWrite__IN(RegWrite__ID),
    .R1_IN(R1_ID), .R2_IN(R2_ID), .Imm__IN(imm_ID), .CLK(CLK), .IR_OUT_2(EX_IR), .PC_OUT(EX_PC),
    .JMP_OUT(JMP_EX), .Beq_OUT(BEQ_EX), .JR_OUT(JR_EX), .Bne_OUT(BNE_EX), .SignedExt_OUT(SignedExt_EX),
    .MemToReg_OUT(MemToReg_EX), .MemWrite_OUT(MemWrite_EX), .LBU_OUT(LBU_EX), .AluOp_OUT(AluOP_EX),
    .BGEZ_OUT(BGEZ_EX), .AluSrcB_OUT(AluSrcB_EX), .RegWrite_OUT(RegWrite_EX), .JAL_OUT(JAL_EX),
    .RegDst_OUT(RegDst_EX), .Syscall_OUT(Syscall_EX), .RegWrite__OUT(RegWrite__EX), .R1_OUT(EX_PC_JR),
    .R2_OUT(MDin_EX), .Imm_OUT(imm_EX), .\同步清零_气泡_高电平有效 (or_2_out), .\使能端_低电平有效_stall_高电平有效 (1'b0),
    .SV_IN(SV_ID), .IR_OUT(SV_EX));  // open: ERET_IN, R1Forward_IN, R2Forward_IN, MFC0_IN, MTC0_IN, 传输状态In_表明当前传输数据有效, ERET_OUT, R1Forward_OUT, R2Forward_OUT, MFC0_OUT, MTC0_OUT, 传输状态Out_表明当前传输数据有效
  Counter #(.width(16), .max('hffff), .ongoal("wrap"), .trigger("rising"), .behavior("new")) counter_4 (
    .count(JMP_EX), .Q(\无条件分支数 ), .clk(CLK), .clr(RST));  // open: load, D, carry, preset, down
  Counter #(.width(16), .max('hffff), .ongoal("wrap"), .trigger("rising"), .behavior("new")) counter_5 (
    .count(B_EX), .Q(\条件分支成功数 ), .clk(CLK), .clr(RST));  // open: load, D, carry, preset, down
  Multiplexer #(.select(1), .width(32), .disabled("Z"), .enable("false")) multiplexer_7 (
    .in0(MDin_EX), .in1(imm_EX), .out(multiplexer_7_out), .sel(AluSrcB_EX));
  Comparator #(.width(32), .mode("twosComplement")) comparator_2 (
    .a(32'ha), .b(EX_PC_JR), .eq(comparator_2_eq));  // open: gt, lt
  Comparator #(.width(32), .mode("twosComplement")) comparator_3 (
    .a(32'h32), .b(EX_PC_JR), .eq(comparator_3_eq));  // open: gt, lt
  Comparator #(.width(32), .mode("twosComplement")) comparator_4 (
    .a(32'h22), .b(EX_PC_JR), .eq(comparator_4_eq));  // open: gt, lt
  and and_1 (and_1_out, BGEZ_EX, comparator_5_eq);
  Comparator #(.width(32), .mode("twosComplement")) comparator_5 (
    .a(AluRes_EX), .b({32{1'b0}}), .eq(comparator_5_eq));  // open: gt, lt
  and and_2 (and_2_out, BEQ_EX, Equal);
  and and_3 (and_3_out, BNE_EX, not_2_out);
  not not_2 (not_2_out, Equal);
  Multiplexer #(.select(1), .width(32), .disabled("Z"), .enable("false")) multiplexer_8 (
    .in0(multiplexer_7_out), .in1({32{1'b0}}), .out(multiplexer_8_out), .sel(BGEZ_EX));
  and and_4 (Exit, Syscall_EX, comparator_2_eq);
  and and_5 (Pause, Syscall_EX, comparator_3_eq);
  and and_6 (and_6_out, Syscall_EX, comparator_4_eq);
  or or_3 (B_EX, and_1_out, and_2_out, and_3_out);
  MIPS_ALU mips_alu_1 (
    .X(EX_PC_JR), .Y(multiplexer_8_out), .AluOP(AluOP_EX), .Equal(Equal), .Result(AluRes_EX), .shamt(shamt));  // open: Result_2
  Multiplexer #(.select(1), .width(5), .disabled("Z"), .enable("false")) multiplexer_9 (
    .in0(EX_IR[10:6]), .in1(EX_PC_JR[4:0]), .out(shamt), .sel(SV_EX));
  Register #(.width(32), .trigger("rising"), .Select("low")) register_2 (
    .D(MDin_EX), .en(and_6_out), .Q(LedData), .clk(CLK));  // open: clr
  Adder #(.width(32)) adder_2 (.a(EX_PC), .b(32'h4), .out({EX_PC_J_JAL, adder_2_out}));  // open: cin, cout
  Shifter #(.width(32), .shift("ll")) shifter_1 (.in(imm_EX), .\dist (5'b00010), .out(shifter_1_out));
  Adder #(.width(32)) adder_3 (.a(32'h4), .b(EX_PC), .out(adder_3_out));  // open: cin, cout
  Adder #(.width(32)) adder_4 (.a(shifter_1_out), .b(adder_3_out), .out(EX_PC_imm));  // open: cin, cout
  // Mips_Probe mips_probe_9: pin names not known; wires that end beside it: MEM_IR
  \气泡流水线接口EX_MEM  \u_气泡流水线接口ex_mem_1  (
    .IR_IN(EX_IR), .PC_IN(EX_PC), .MemToReg_IN(MemToReg_EX), .MemWrite_IN(MemWrite_EX), .LBU_IN(LBU_EX),
    .RegWrite_IN(RegWrite_EX), .JAL_IN(JAL_EX), .RegDst_IN(RegDst_EX), .RegWrite__IN(RegWrite__EX),
    .AluRst_IN(AluRes_EX), .Mem_IN(MDin_EX), .CLK(CLK), .IR_OUT(MEM_IR), .PC_OUT(M_PC),
    .MemToReg_OUT(MemToReg_MEM), .MemWrite_OUT(MemWrite), .LBU_OUT(LBU_MEM), .RegWrite_OUT(RegWrite_MEM),
    .JAL_OUT(JAL_MEM), .RegDst_OUT(RegDst_MEM), .RegWrite__OUT(RegWrite__MEM), .AluRst_OUT(AluRes_MEM),
    .Mem_OUT(MDin), .\使能端_低电平有效_stall_高电平有效 (MEM_STALL));  // open: ERET_IN, 传输状态In_表明当前传输数据有效, ERET_OUT, 传输状态Out_表明当前传输数据有效, 同步清零_气泡_高电平有效
  RAM #(.addrWidth(10), .dataWidth(32), .bus("separate"), .Select("high")) ram_1 (
    .addr(AluRes_MEM[11:2]), .din(MDin), .data(RDin_MEM), .str(MemWrite), .clk(CLK));  // open: sel, ld, clr
  // Mips_Probe mips_probe_10: pin names not known; wires that end beside it: WB_IR
  \气泡流水线MEM_WB  \u_气泡流水线mem_wb_1  (
    .IR_IN(MEM_IR), .PC_IN(M_PC), .MemToReg_IN(MemToReg_MEM), .LBU_IN(LBU_MEM), .RegWrite_IN(RegWrite_MEM),
    .JAL_IN(JAL_MEM), .RegDst_IN(RegDst_MEM), .RegWrite__IN(RegWrite__MEM), .Mem_IN(RDin_MEM),
    .AluRst_IN(AluRes_MEM), .CLK(CLK), .IR_OUT(WB_IR), .PC_OUT(WB_PC), .MemToReg_OUT(MemToReg_WB),
    .LBU_OUT(LBU_WB), .RegWrite_OUT(RegWrite), .JAL_OUT(JAL_WB), .RegWrite__OUT(RegWrite__WB),
    .Mem_OUT(RDin_WB), .AluRst_OUT(AluRes_WB), .\使能端_低电平有效_stall_高电平有效 (1'b0));  // open: ERET_IN, 传输状态In_表明当前传输数据有效, ERET_OUT, RegDst_OUT, 传输状态Out_表明当前传输数据有效, 同步清零_气泡_高电平有效
  Multiplexer #(.select(1), .width(32), .disabled("Z"), .enable("false")) multiplexer_10 (
    .in0(AluRes_WB), .in1(RDin_WB), .out(multiplexer_10_out), .sel(MemToReg_WB));
  assign xor_1_out = AluRes_WB[1:0] ^ 2'b11;  // XOR_Gate xor_1, 2 bits wide
  Multiplexer #(.select(2), .width(8), .disabled("Z"), .enable("false")) multiplexer_11 (
    .in0(multiplexer_10_out[7:0]), .in1(multiplexer_10_out[15:8]), .in2(multiplexer_10_out[23:16]),
    .in3(multiplexer_10_out[31:24]), .out(multiplexer_11_out), .sel(xor_1_out));
  Multiplexer #(.select(1), .width(32), .disabled("Z"), .enable("false")) multiplexer_12 (
    .in0(multiplexer_10_out), .in1(bit_extender_3_out), .out(multiplexer_12_out), .sel(LBU_WB));
  assign bit_extender_3_out = {{24{1'b0}}, multiplexer_11_out};  // Bit_Extender bit_extender_3
  Adder #(.width(32)) adder_5 (.a(WB_PC), .b(32'h4), .out(adder_5_out));  // open: cin, cout
  Multiplexer #(.select(1), .width(32), .disabled("Z"), .enable("false")) multiplexer_13 (
    .in0(multiplexer_12_out), .in1(adder_5_out), .out(RDin), .sel(JAL_WB));

  // Other names for the same wires on the sheet: BGEZ_RES[31:0] = AluRes_EX; EX_PC_J_JAL[27:2] = EX_IR[25:0];
  //   ID_IR[5:0] = Func; imm[15:0] = {ID_IR[15:6], Func}; rd[4:0] = ID_IR[15:11]; rt[4:0] = ID_IR[20:16];
  //   rs[4:0] = ID_IR[25:21]; OP[5:0] = ID_IR[31:26]; MDin_MEM[31:0] = MDin; MEM_PC[31:0] = M_PC;
  //   MemWrite_MEM = MemWrite; R1_EX[31:0] = EX_PC_JR; R2_EX[31:0] = MDin_EX; Vaddr_WB[31:0] = AluRes_WB;
  //   WB_RegWrite = RegWrite

  // Notes on the sheet:
  //   中断源
  //   时空图监测，可删除
  //   中断等待指示
  //   数码管输出
  //   指令存储器
  //   contents of rom_1 (hex, n*v repeats v):
  //   20110001 8000c05 20110001 20120002 20130003 8000c09 20110001 20120002 20130003 8000c0d 20110001
  //   20120002 20130003 8000c11 20110001 20120002 20130003 c000cb8 20100001 20110001 118fc0 112020
  //   20020022 c 118882 12200001 8000c15 112020 20020022 c 20110001 118880 112020 20020022 c 12200001
  //   8000c1f 20110001 118fc0 112020 20020022 c 1188c3 112020 20020022 c 118903 112020 20020022 c 118903
  //   112020 20020022 c 118903 112020 20020022 c 118903 112020 20020022 c 118903 112020 20020022 c 118903
  //   112020 20020022 c 118903 112020 20020022 c 20100001 109fc0 139fc3 8021 2012000c 24160003 26100001
  //   3210000f 20080008 20090001 139900 2709825 132020 20020022 c 1094022 1500fff9 22100001 2018000f
  //   2188024 108700 20080008 20090001 139902 2709825 132021 20020022 c 1094022 1500fff9 108702 2c9b022
  //   12c00001 8000c50 4020 1084027 84400 3508ffff 82021 20020022 c 2010ffff 20110000 ae300000 22100001
  //   22310004 ae300000 22100001 22310004 ae300000 22100001 22310004 ae300000 22100001 22310004 ae300000
  //   22100001 22310004 ae300000 22100001 22310004 ae300000 22100001 22310004 ae300000 22100001 22310004
  //   ae300000 22100001 22310004 ae300000 22100001 22310004 ae300000 22100001 22310004 ae300000 22100001
  //   22310004 ae300000 22100001 22310004 ae300000 22100001 22310004 ae300000 22100001 22310004 ae300000
  //   22100001 22310004 22100001 8020 2011003c 8e130000 8e340000 274402a 11000002 ae330000 ae140000
  //   2231fffc 1611fff8 102020 20020022 c 22100004 2011003c 1611fff2 20020032 c 20100000 22100001 102020
  //   20020022 c 22100002 102020 20020022 c 22100003 102020 20020022 c 22100004 102020 20020022 c 22100005
  //   102020 20020022 c 22100006 102020 20020022 c 22100007 102020 20020022 c 22100008 102020 20020022
  //   20020022 c 3e00008
  //   控制位
  //   OP
  //   Func
  //   rs
  //   rt
  //   流水调试日志用
  //   暂停节拍，不能为0
  //   戳工具置1进入计数暂停模式，ctrl+k时钟自动运行到对应节拍暂停
  //   ctrl+k关闭时钟连续运行，将控制位置零，进入单步调试模式调试
  //   JMP
  //   JR
  //   SV
  //   LBU
  //   BGEZ
  //   OP
  //   Func
  //   Beq
  //   Bne
  //   MemToReg
  //   MemWrite
  //   AluOP
  //   AluSrcB
  //   RegWrite
  //   JAL
  //   RegDst
  //   Syscall
  //   可计数暂停的时钟源
  //   为方便自动评测，需要输出流水线各段保存的PC值，注意是PC不是PC+4，另外ID段寄存器写入信息，Mem段内存写入信息也要输出
endmodule

module \气泡流水线接口IF_ID  (
  input  [31:0] IR_IN,
  input  [31:0] PC_IN,
  input  \传输状态In_表明当前传输数据有效 ,
  input  CLK,
  input  \同步清零_气泡_高电平有效 ,
  input  \使能端_低电平有效_stall_高电平有效 ,
  output [31:0] IR_OUT,
  output [31:0] PC_OUT,
  output \传输状态Out_表明当前传输数据有效 
);

  wire multiplexer_3_out, pull_resistor_2_node;
  wire [31:0] multiplexer_1_out, multiplexer_2_out;

  Multiplexer #(.select(1), .width(32), .disabled("Z"), .enable("false")) multiplexer_1 (
    .in0(IR_IN), .in1({32{1'b0}}), .out(multiplexer_1_out), .sel(\同步清零_气泡_高电平有效 ));
  Multiplexer #(.select(1), .width(32), .disabled("Z"), .enable("false")) multiplexer_2 (
    .in0(PC_IN), .in1({32{1'b0}}), .out(multiplexer_2_out), .sel(\同步清零_气泡_高电平有效 ));
  Multiplexer #(.select(1), .width(1), .disabled("Z"), .enable("false")) multiplexer_3 (
    .in0(\传输状态In_表明当前传输数据有效 ), .in1(1'b0), .out(multiplexer_3_out), .sel(\同步清零_气泡_高电平有效 ));
  Pull_Resistor #(.pull(0)) pull_resistor_1 (.node(\同步清零_气泡_高电平有效 ));
  Register #(.width(32), .trigger("rising"), .Select("low")) register_1 (
    .D(multiplexer_1_out), .en(pull_resistor_2_node), .Q(IR_OUT), .clk(CLK));  // open: clr
  Register #(.width(32), .trigger("rising"), .Select("low")) register_2 (
    .D(multiplexer_2_out), .en(pull_resistor_2_node), .Q(PC_OUT), .clk(CLK));  // open: clr
  Register #(.width(1), .trigger("rising"), .Select("low")) register_3 (
    .D(multiplexer_3_out), .en(pull_resistor_2_node), .Q(\传输状态Out_表明当前传输数据有效 ), .clk(CLK));  // open: clr
  Pull_Resistor #(.pull(0)) pull_resistor_2 (.node(pull_resistor_2_node));
  not not_1 (pull_resistor_2_node, \使能端_低电平有效_stall_高电平有效 );
endmodule
module \气泡流水线接口ID_EX  (
  input  SV_IN,
  input  [31:0] IR_IN,
  input  [31:0] PC_IN,
  input  JMP_IN,
  input  Beq_IN,
  input  JR_IN,
  input  Bne_IN,
  input  SignedExt_IN,
  input  MemToReg_IN,
  input  ERET_IN,
  input  MemWrite_IN,
  input  LBU_IN,
  input  [3:0] AluOp_IN,
  input  BGEZ_IN,
  input  AluSrcB_IN,
  input  RegWrite_IN,
  input  JAL_IN,
  input  RegDst_IN,
  input  Syscall_IN,
  input  [4:0] RegWrite__IN,
  input  [1:0] R1Forward_IN,
  input  [1:0] R2Forward_IN,
  input  [31:0] R1_IN,
  input  [31:0] R2_IN,
  input  [31:0] Imm__IN,
  input  MFC0_IN,
  input  MTC0_IN,
  input  \传输状态In_表明当前传输数据有效 ,
  input  CLK,
  input  \同步清零_气泡_高电平有效 ,
  input  \使能端_低电平有效_stall_高电平有效 ,
  output IR_OUT,
  output [31:0] IR_OUT_2,
  output [31:0] PC_OUT,
  output JMP_OUT,
  output Beq_OUT,
  output JR_OUT,
  output Bne_OUT,
  output SignedExt_OUT,
  output MemToReg_OUT,
  output ERET_OUT,
  output MemWrite_OUT,
  output LBU_OUT,
  output [3:0] AluOp_OUT,
  output BGEZ_OUT,
  output AluSrcB_OUT,
  output RegWrite_OUT,
  output JAL_OUT,
  output RegDst_OUT,
  output Syscall_OUT,
  output [4:0] RegWrite__OUT,
  output [1:0] R1Forward_OUT,
  output [1:0] R2Forward_OUT,
  output [31:0] R1_OUT,
  output [31:0] R2_OUT,
  output [31:0] Imm_OUT,
  output MFC0_OUT,
  output MTC0_OUT,
  output \传输状态Out_表明当前传输数据有效 
);

  wire multiplexer_1_out, multiplexer_4_out, multiplexer_5_out, multiplexer_6_out, multiplexer_7_out,
       multiplexer_8_out, multiplexer_9_out, multiplexer_10_out, multiplexer_11_out, multiplexer_12_out,
       multiplexer_14_out, multiplexer_15_out, multiplexer_16_out, multiplexer_17_out, multiplexer_18_out,
       multiplexer_19_out, multiplexer_26_out, multiplexer_27_out, multiplexer_28_out, pull_resistor_2_node;
  wire [1:0] multiplexer_21_out, multiplexer_22_out;
  wire [3:0] multiplexer_13_out;
  wire [4:0] multiplexer_20_out;
  wire [31:0] multiplexer_2_out, multiplexer_3_out, multiplexer_23_out, multiplexer_24_out,
       multiplexer_25_out;

  Multiplexer #(.select(1), .width(1), .disabled("Z"), .enable("false")) multiplexer_1 (
    .in0(SV_IN), .in1(1'b0), .out(multiplexer_1_out), .sel(\同步清零_气泡_高电平有效 ));
  Multiplexer #(.select(1), .width(32), .disabled("Z"), .enable("false")) multiplexer_2 (
    .in0(IR_IN), .in1({32{1'b0}}), .out(multiplexer_2_out), .sel(\同步清零_气泡_高电平有效 ));
  Multiplexer #(.select(1), .width(32), .disabled("Z"), .enable("false")) multiplexer_3 (
    .in0(PC_IN), .in1({32{1'b0}}), .out(multiplexer_3_out), .sel(\同步清零_气泡_高电平有效 ));
  Multiplexer #(.select(1), .width(1), .disabled("Z"), .enable("false")) multiplexer_4 (
    .in0(JMP_IN), .in1(1'b0), .out(multiplexer_4_out), .sel(\同步清零_气泡_高电平有效 ));
  Multiplexer #(.select(1), .width(1), .disabled("Z"), .enable("false")) multiplexer_5 (
    .in0(Beq_IN), .in1(1'b0), .out(multiplexer_5_out), .sel(\同步清零_气泡_高电平有效 ));
  Multiplexer #(.select(1), .width(1), .disabled("Z"), .enable("false")) multiplexer_6 (
    .in0(JR_IN), .in1(1'b0), .out(multiplexer_6_out), .sel(\同步清零_气泡_高电平有效 ));
  Multiplexer #(.select(1), .width(1), .disabled("Z"), .enable("false")) multiplexer_7 (
    .in0(Bne_IN), .in1(1'b0), .out(multiplexer_7_out), .sel(\同步清零_气泡_高电平有效 ));
  Multiplexer #(.select(1), .width(1), .disabled("Z"), .enable("false")) multiplexer_8 (
    .in0(SignedExt_IN), .in1(1'b0), .out(multiplexer_8_out), .sel(\同步清零_气泡_高电平有效 ));
  Multiplexer #(.select(1), .width(1), .disabled("Z"), .enable("false")) multiplexer_9 (
    .in0(MemToReg_IN), .in1(1'b0), .out(multiplexer_9_out), .sel(\同步清零_气泡_高电平有效 ));
  Multiplexer #(.select(1), .width(1), .disabled("Z"), .enable("false")) multiplexer_10 (
    .in0(ERET_IN), .in1(1'b0), .out(multiplexer_10_out), .sel(\同步清零_气泡_高电平有效 ));
  Multiplexer #(.select(1), .width(1), .disabled("Z"), .enable("false")) multiplexer_11 (
    .in0(MemWrite_IN), .in1(1'b0), .out(multiplexer_11_out), .sel(\同步清零_气泡_高电平有效 ));
  Multiplexer #(.select(1), .width(1), .disabled("Z"), .enable("false")) multiplexer_12 (
    .in0(LBU_IN), .in1(1'b0), .out(multiplexer_12_out), .sel(\同步清零_气泡_高电平有效 ));
  Multiplexer #(.select(1), .width(4), .disabled("Z"), .enable("false")) multiplexer_13 (
    .in0(AluOp_IN), .in1(4'b0000), .out(multiplexer_13_out), .sel(\同步清零_气泡_高电平有效 ));
  Multiplexer #(.select(1), .width(1), .disabled("Z"), .enable("false")) multiplexer_14 (
    .in0(BGEZ_IN), .in1(1'b0), .out(multiplexer_14_out), .sel(\同步清零_气泡_高电平有效 ));
  Multiplexer #(.select(1), .width(1), .disabled("Z"), .enable("false")) multiplexer_15 (
    .in0(AluSrcB_IN), .in1(1'b0), .out(multiplexer_15_out), .sel(\同步清零_气泡_高电平有效 ));
  Multiplexer #(.select(1), .width(1), .disabled("Z"), .enable("false")) multiplexer_16 (
    .in0(RegWrite_IN), .in1(1'b0), .out(multiplexer_16_out), .sel(\同步清零_气泡_高电平有效 ));
  Multiplexer #(.select(1), .width(1), .disabled("Z"), .enable("false")) multiplexer_17 (
    .in0(JAL_IN), .in1(1'b0), .out(multiplexer_17_out), .sel(\同步清零_气泡_高电平有效 ));
  Multiplexer #(.select(1), .width(1), .disabled("Z"), .enable("false")) multiplexer_18 (
    .in0(RegDst_IN), .in1(1'b0), .out(multiplexer_18_out), .sel(\同步清零_气泡_高电平有效 ));
  Multiplexer #(.select(1), .width(1), .disabled("Z"), .enable("false")) multiplexer_19 (
    .in0(Syscall_IN), .in1(1'b0), .out(multiplexer_19_out), .sel(\同步清零_气泡_高电平有效 ));
  Multiplexer #(.select(1), .width(5), .disabled("Z"), .enable("false")) multiplexer_20 (
    .in0(RegWrite__IN), .in1({5{1'b0}}), .out(multiplexer_20_out), .sel(\同步清零_气泡_高电平有效 ));
  Multiplexer #(.select(1), .width(2), .disabled("Z"), .enable("false")) multiplexer_21 (
    .in0(R1Forward_IN), .in1(2'b00), .out(multiplexer_21_out), .sel(\同步清零_气泡_高电平有效 ));
  Multiplexer #(.select(1), .width(2), .disabled("Z"), .enable("false")) multiplexer_22 (
    .in0(R2Forward_IN), .in1(2'b00), .out(multiplexer_22_out), .sel(\同步清零_气泡_高电平有效 ));
  Multiplexer #(.select(1), .width(32), .disabled("Z"), .enable("false")) multiplexer_23 (
    .in0(R1_IN), .in1({32{1'b0}}), .out(multiplexer_23_out), .sel(\同步清零_气泡_高电平有效 ));
  Multiplexer #(.select(1), .width(32), .disabled("Z"), .enable("false")) multiplexer_24 (
    .in0(R2_IN), .in1({32{1'b0}}), .out(multiplexer_24_out), .sel(\同步清零_气泡_高电平有效 ));
  Multiplexer #(.select(1), .width(32), .disabled("Z"), .enable("false")) multiplexer_25 (
    .in0(Imm__IN), .in1({32{1'b0}}), .out(multiplexer_25_out), .sel(\同步清零_气泡_高电平有效 ));
  Multiplexer #(.select(1), .width(1), .disabled("Z"), .enable("false")) multiplexer_26 (
    .in0(MFC0_IN), .in1(1'b0), .out(multiplexer_26_out), .sel(\同步清零_气泡_高电平有效 ));
  Multiplexer #(.select(1), .width(1), .disabled("Z"), .enable("false")) multiplexer_27 (
    .in0(MTC0_IN), .in1(1'b0), .out(multiplexer_27_out), .sel(\同步清零_气泡_高电平有效 ));
  Multiplexer #(.select(1), .width(1), .disabled("Z"), .enable("false")) multiplexer_28 (
    .in0(\传输状态In_表明当前传输数据有效 ), .in1(1'b0), .out(multiplexer_28_out), .sel(\同步清零_气泡_高电平有效 ));
  Pull_Resistor #(.pull(0)) pull_resistor_1 (.node(\同步清零_气泡_高电平有效 ));
  Register #(.width(1), .trigger("rising"), .Select("low")) register_1 (
    .D(multiplexer_1_out), .en(pull_resistor_2_node), .Q(IR_OUT), .clk(CLK));  // open: clr
  Register #(.width(32), .trigger("rising"), .Select("low")) register_2 (
    .D(multiplexer_2_out), .en(pull_resistor_2_node), .Q(IR_OUT_2), .clk(CLK));  // open: clr
  Register #(.width(32), .trigger("rising"), .Select("low")) register_3 (
    .D(multiplexer_3_out), .en(pull_resistor_2_node), .Q(PC_OUT), .clk(CLK));  // open: clr
  Register #(.width(1), .trigger("rising"), .Select("low")) register_4 (
    .D(multiplexer_4_out), .en(pull_resistor_2_node), .Q(JMP_OUT), .clk(CLK));  // open: clr
  Register #(.width(1), .trigger("rising"), .Select("low")) register_5 (
    .D(multiplexer_5_out), .en(pull_resistor_2_node), .Q(Beq_OUT), .clk(CLK));  // open: clr
  Register #(.width(1), .trigger("rising"), .Select("low")) register_6 (
    .D(multiplexer_6_out), .en(pull_resistor_2_node), .Q(JR_OUT), .clk(CLK));  // open: clr
  Register #(.width(1), .trigger("rising"), .Select("low")) register_7 (
    .D(multiplexer_7_out), .en(pull_resistor_2_node), .Q(Bne_OUT), .clk(CLK));  // open: clr
  Register #(.width(1), .trigger("rising"), .Select("low")) register_8 (
    .D(multiplexer_8_out), .en(pull_resistor_2_node), .Q(SignedExt_OUT), .clk(CLK));  // open: clr
  Register #(.width(1), .trigger("rising"), .Select("low")) register_9 (
    .D(multiplexer_9_out), .en(pull_resistor_2_node), .Q(MemToReg_OUT), .clk(CLK));  // open: clr
  Register #(.width(1), .trigger("rising"), .Select("low")) register_10 (
    .D(multiplexer_10_out), .en(pull_resistor_2_node), .Q(ERET_OUT), .clk(CLK));  // open: clr
  Register #(.width(1), .trigger("rising"), .Select("low")) register_11 (
    .D(multiplexer_11_out), .en(pull_resistor_2_node), .Q(MemWrite_OUT), .clk(CLK));  // open: clr
  Register #(.width(1), .trigger("rising"), .Select("low")) register_12 (
    .D(multiplexer_12_out), .en(pull_resistor_2_node), .Q(LBU_OUT), .clk(CLK));  // open: clr
  Register #(.width(4), .trigger("rising"), .Select("low")) register_13 (
    .D(multiplexer_13_out), .en(pull_resistor_2_node), .Q(AluOp_OUT), .clk(CLK));  // open: clr
  Register #(.width(1), .trigger("rising"), .Select("low")) register_14 (
    .D(multiplexer_14_out), .en(pull_resistor_2_node), .Q(BGEZ_OUT), .clk(CLK));  // open: clr
  Register #(.width(1), .trigger("rising"), .Select("low")) register_15 (
    .D(multiplexer_15_out), .en(pull_resistor_2_node), .Q(AluSrcB_OUT), .clk(CLK));  // open: clr
  Register #(.width(1), .trigger("rising"), .Select("low")) register_16 (
    .D(multiplexer_16_out), .en(pull_resistor_2_node), .Q(RegWrite_OUT), .clk(CLK));  // open: clr
  Register #(.width(1), .trigger("rising"), .Select("low")) register_17 (
    .D(multiplexer_17_out), .en(pull_resistor_2_node), .Q(JAL_OUT), .clk(CLK));  // open: clr
  Register #(.width(1), .trigger("rising"), .Select("low")) register_18 (
    .D(multiplexer_18_out), .en(pull_resistor_2_node), .Q(RegDst_OUT), .clk(CLK));  // open: clr
  Register #(.width(1), .trigger("rising"), .Select("low")) register_19 (
    .D(multiplexer_19_out), .en(pull_resistor_2_node), .Q(Syscall_OUT), .clk(CLK));  // open: clr
  Register #(.width(5), .trigger("rising"), .Select("low")) register_20 (
    .D(multiplexer_20_out), .en(pull_resistor_2_node), .Q(RegWrite__OUT), .clk(CLK));  // open: clr
  Register #(.width(2), .trigger("rising"), .Select("low")) register_21 (
    .D(multiplexer_21_out), .en(pull_resistor_2_node), .Q(R1Forward_OUT), .clk(CLK));  // open: clr
  Register #(.width(2), .trigger("rising"), .Select("low")) register_22 (
    .D(multiplexer_22_out), .en(pull_resistor_2_node), .Q(R2Forward_OUT), .clk(CLK));  // open: clr
  Register #(.width(32), .trigger("rising"), .Select("low")) register_23 (
    .D(multiplexer_23_out), .en(pull_resistor_2_node), .Q(R1_OUT), .clk(CLK));  // open: clr
  Register #(.width(32), .trigger("rising"), .Select("low")) register_24 (
    .D(multiplexer_24_out), .en(pull_resistor_2_node), .Q(R2_OUT), .clk(CLK));  // open: clr
  Register #(.width(32), .trigger("rising"), .Select("low")) register_25 (
    .D(multiplexer_25_out), .en(pull_resistor_2_node), .Q(Imm_OUT), .clk(CLK));  // open: clr
  Register #(.width(1), .trigger("rising"), .Select("low")) register_26 (
    .D(multiplexer_26_out), .en(pull_resistor_2_node), .Q(MFC0_OUT), .clk(CLK));  // open: clr
  Register #(.width(1), .trigger("rising"), .Select("low")) register_27 (
    .D(multiplexer_27_out), .en(pull_resistor_2_node), .Q(MTC0_OUT), .clk(CLK));  // open: clr
  Register #(.width(1), .trigger("rising"), .Select("low")) register_28 (
    .D(multiplexer_28_out), .en(pull_resistor_2_node), .Q(\传输状态Out_表明当前传输数据有效 ), .clk(CLK));  // open: clr
  Pull_Resistor #(.pull(0)) pull_resistor_2 (.node(pull_resistor_2_node));
  not not_1 (pull_resistor_2_node, \使能端_低电平有效_stall_高电平有效 );
endmodule

module \气泡流水线接口EX_MEM  (
  input  [31:0] IR_IN,
  input  [31:0] PC_IN,
  input  MemToReg_IN,
  input  ERET_IN,
  input  MemWrite_IN,
  input  LBU_IN,
  input  RegWrite_IN,
  input  JAL_IN,
  input  RegDst_IN,
  input  [4:0] RegWrite__IN,
  input  [31:0] AluRst_IN,
  input  [31:0] Mem_IN,
  input  \传输状态In_表明当前传输数据有效 ,
  input  CLK,
  input  \同步清零_气泡_高电平有效 ,
  input  \使能端_低电平有效_stall_高电平有效 ,
  output [31:0] IR_OUT,
  output [31:0] PC_OUT,
  output MemToReg_OUT,
  output ERET_OUT,
  output MemWrite_OUT,
  output LBU_OUT,
  output RegWrite_OUT,
  output JAL_OUT,
  output RegDst_OUT,
  output [4:0] RegWrite__OUT,
  output [31:0] AluRst_OUT,
  output [31:0] Mem_OUT,
  output \传输状态Out_表明当前传输数据有效 
);

  wire multiplexer_3_out, multiplexer_4_out, multiplexer_5_out, multiplexer_6_out, multiplexer_7_out,
       multiplexer_8_out, multiplexer_9_out, multiplexer_13_out, pull_resistor_2_node;
  wire [4:0] multiplexer_10_out;
  wire [31:0] multiplexer_1_out, multiplexer_2_out, multiplexer_11_out, multiplexer_12_out;

  Multiplexer #(.select(1), .width(32), .disabled("Z"), .enable("false")) multiplexer_1 (
    .in0(IR_IN), .in1({32{1'b0}}), .out(multiplexer_1_out), .sel(\同步清零_气泡_高电平有效 ));
  Multiplexer #(.select(1), .width(32), .disabled("Z"), .enable("false")) multiplexer_2 (
    .in0(PC_IN), .in1({32{1'b0}}), .out(multiplexer_2_out), .sel(\同步清零_气泡_高电平有效 ));
  Multiplexer #(.select(1), .width(1), .disabled("Z"), .enable("false")) multiplexer_3 (
    .in0(MemToReg_IN), .in1(1'b0), .out(multiplexer_3_out), .sel(\同步清零_气泡_高电平有效 ));
  Multiplexer #(.select(1), .width(1), .disabled("Z"), .enable("false")) multiplexer_4 (
    .in0(ERET_IN), .in1(1'b0), .out(multiplexer_4_out), .sel(\同步清零_气泡_高电平有效 ));
  Multiplexer #(.select(1), .width(1), .disabled("Z"), .enable("false")) multiplexer_5 (
    .in0(MemWrite_IN), .in1(1'b0), .out(multiplexer_5_out), .sel(\同步清零_气泡_高电平有效 ));
  Multiplexer #(.select(1), .width(1), .disabled("Z"), .enable("false")) multiplexer_6 (
    .in0(LBU_IN), .in1(1'b0), .out(multiplexer_6_out), .sel(\同步清零_气泡_高电平有效 ));
  Multiplexer #(.select(1), .width(1), .disabled("Z"), .enable("false")) multiplexer_7 (
    .in0(RegWrite_IN), .in1(1'b0), .out(multiplexer_7_out), .sel(\同步清零_气泡_高电平有效 ));
  Multiplexer #(.select(1), .width(1), .disabled("Z"), .enable("false")) multiplexer_8 (
    .in0(JAL_IN), .in1(1'b0), .out(multiplexer_8_out), .sel(\同步清零_气泡_高电平有效 ));
  Multiplexer #(.select(1), .width(1), .disabled("Z"), .enable("false")) multiplexer_9 (
    .in0(RegDst_IN), .in1(1'b0), .out(multiplexer_9_out), .sel(\同步清零_气泡_高电平有效 ));
  Multiplexer #(.select(1), .width(5), .disabled("Z"), .enable("false")) multiplexer_10 (
    .in0(RegWrite__IN), .in1({5{1'b0}}), .out(multiplexer_10_out), .sel(\同步清零_气泡_高电平有效 ));
  Multiplexer #(.select(1), .width(32), .disabled("Z"), .enable("false")) multiplexer_11 (
    .in0(AluRst_IN), .in1({32{1'b0}}), .out(multiplexer_11_out), .sel(\同步清零_气泡_高电平有效 ));
  Multiplexer #(.select(1), .width(32), .disabled("Z"), .enable("false")) multiplexer_12 (
    .in0(Mem_IN), .in1({32{1'b0}}), .out(multiplexer_12_out), .sel(\同步清零_气泡_高电平有效 ));
  Multiplexer #(.select(1), .width(1), .disabled("Z"), .enable("false")) multiplexer_13 (
    .in0(\传输状态In_表明当前传输数据有效 ), .in1(1'b0), .out(multiplexer_13_out), .sel(\同步清零_气泡_高电平有效 ));
  Pull_Resistor #(.pull(0)) pull_resistor_1 (.node(\同步清零_气泡_高电平有效 ));
  Register #(.width(32), .trigger("rising"), .Select("low")) register_1 (
    .D(multiplexer_1_out), .en(pull_resistor_2_node), .Q(IR_OUT), .clk(CLK));  // open: clr
  Register #(.width(32), .trigger("rising"), .Select("low")) register_2 (
    .D(multiplexer_2_out), .en(pull_resistor_2_node), .Q(PC_OUT), .clk(CLK));  // open: clr
  Register #(.width(1), .trigger("rising"), .Select("low")) register_3 (
    .D(multiplexer_3_out), .en(pull_resistor_2_node), .Q(MemToReg_OUT), .clk(CLK));  // open: clr
  Register #(.width(1), .trigger("rising"), .Select("low")) register_4 (
    .D(multiplexer_4_out), .en(pull_resistor_2_node), .Q(ERET_OUT), .clk(CLK));  // open: clr
  Register #(.width(1), .trigger("rising"), .Select("low")) register_5 (
    .D(multiplexer_5_out), .en(pull_resistor_2_node), .Q(MemWrite_OUT), .clk(CLK));  // open: clr
  Register #(.width(1), .trigger("rising"), .Select("low")) register_6 (
    .D(multiplexer_6_out), .en(pull_resistor_2_node), .Q(LBU_OUT), .clk(CLK));  // open: clr
  Register #(.width(1), .trigger("rising"), .Select("low")) register_7 (
    .D(multiplexer_7_out), .en(pull_resistor_2_node), .Q(RegWrite_OUT), .clk(CLK));  // open: clr
  Register #(.width(1), .trigger("rising"), .Select("low")) register_8 (
    .D(multiplexer_8_out), .en(pull_resistor_2_node), .Q(JAL_OUT), .clk(CLK));  // open: clr
  Register #(.width(1), .trigger("rising"), .Select("low")) register_9 (
    .D(multiplexer_9_out), .en(pull_resistor_2_node), .Q(RegDst_OUT), .clk(CLK));  // open: clr
  Register #(.width(5), .trigger("rising"), .Select("low")) register_10 (
    .D(multiplexer_10_out), .en(pull_resistor_2_node), .Q(RegWrite__OUT), .clk(CLK));  // open: clr
  Register #(.width(32), .trigger("rising"), .Select("low")) register_11 (
    .D(multiplexer_11_out), .en(pull_resistor_2_node), .Q(AluRst_OUT), .clk(CLK));  // open: clr
  Register #(.width(32), .trigger("rising"), .Select("low")) register_12 (
    .D(multiplexer_12_out), .en(pull_resistor_2_node), .Q(Mem_OUT), .clk(CLK));  // open: clr
  Register #(.width(1), .trigger("rising"), .Select("low")) register_13 (
    .D(multiplexer_13_out), .en(pull_resistor_2_node), .Q(\传输状态Out_表明当前传输数据有效 ), .clk(CLK));  // open: clr
  Pull_Resistor #(.pull(0)) pull_resistor_2 (.node(pull_resistor_2_node));
  not not_1 (pull_resistor_2_node, \使能端_低电平有效_stall_高电平有效 );
endmodule

module \气泡流水线MEM_WB  (
  input  [31:0] IR_IN,
  input  [31:0] PC_IN,
  input  MemToReg_IN,
  input  ERET_IN,
  input  LBU_IN,
  input  RegWrite_IN,
  input  JAL_IN,
  input  RegDst_IN,
  input  [4:0] RegWrite__IN,
  input  [31:0] Mem_IN,
  input  [31:0] AluRst_IN,
  input  \传输状态In_表明当前传输数据有效 ,
  input  CLK,
  input  \同步清零_气泡_高电平有效 ,
  input  \使能端_低电平有效_stall_高电平有效 ,
  output [31:0] IR_OUT,
  output [31:0] PC_OUT,
  output MemToReg_OUT,
  output ERET_OUT,
  output LBU_OUT,
  output RegWrite_OUT,
  output JAL_OUT,
  output RegDst_OUT,
  output [4:0] RegWrite__OUT,
  output [31:0] Mem_OUT,
  output [31:0] AluRst_OUT,
  output \传输状态Out_表明当前传输数据有效 
);

  wire multiplexer_3_out, multiplexer_4_out, multiplexer_5_out, multiplexer_6_out, multiplexer_7_out,
       multiplexer_8_out, multiplexer_12_out, pull_resistor_2_node;
  wire [4:0] multiplexer_9_out;
  wire [31:0] multiplexer_1_out, multiplexer_2_out, multiplexer_10_out, multiplexer_11_out;

  Multiplexer #(.select(1), .width(32), .disabled("Z"), .enable("false")) multiplexer_1 (
    .in0(IR_IN), .in1({32{1'b0}}), .out(multiplexer_1_out), .sel(\同步清零_气泡_高电平有效 ));
  Multiplexer #(.select(1), .width(32), .disabled("Z"), .enable("false")) multiplexer_2 (
    .in0(PC_IN), .in1({32{1'b0}}), .out(multiplexer_2_out), .sel(\同步清零_气泡_高电平有效 ));
  Multiplexer #(.select(1), .width(1), .disabled("Z"), .enable("false")) multiplexer_3 (
    .in0(MemToReg_IN), .in1(1'b0), .out(multiplexer_3_out), .sel(\同步清零_气泡_高电平有效 ));
  Multiplexer #(.select(1), .width(1), .disabled("Z"), .enable("false")) multiplexer_4 (
    .in0(ERET_IN), .in1(1'b0), .out(multiplexer_4_out), .sel(\同步清零_气泡_高电平有效 ));
  Multiplexer #(.select(1), .width(1), .disabled("Z"), .enable("false")) multiplexer_5 (
    .in0(LBU_IN), .in1(1'b0), .out(multiplexer_5_out), .sel(\同步清零_气泡_高电平有效 ));
  Multiplexer #(.select(1), .width(1), .disabled("Z"), .enable("false")) multiplexer_6 (
    .in0(RegWrite_IN), .in1(1'b0), .out(multiplexer_6_out), .sel(\同步清零_气泡_高电平有效 ));
  Multiplexer #(.select(1), .width(1), .disabled("Z"), .enable("false")) multiplexer_7 (
    .in0(JAL_IN), .in1(1'b0), .out(multiplexer_7_out), .sel(\同步清零_气泡_高电平有效 ));
  Multiplexer #(.select(1), .width(1), .disabled("Z"), .enable("false")) multiplexer_8 (
    .in0(RegDst_IN), .in1(1'b0), .out(multiplexer_8_out), .sel(\同步清零_气泡_高电平有效 ));
  Multiplexer #(.select(1), .width(5), .disabled("Z"), .enable("false")) multiplexer_9 (
    .in0(RegWrite__IN), .in1({5{1'b0}}), .out(multiplexer_9_out), .sel(\同步清零_气泡_高电平有效 ));
  Multiplexer #(.select(1), .width(32), .disabled("Z"), .enable("false")) multiplexer_10 (
    .in0(Mem_IN), .in1({32{1'b0}}), .out(multiplexer_10_out), .sel(\同步清零_气泡_高电平有效 ));
  Multiplexer #(.select(1), .width(32), .disabled("Z"), .enable("false")) multiplexer_11 (
    .in0(AluRst_IN), .in1({32{1'b0}}), .out(multiplexer_11_out), .sel(\同步清零_气泡_高电平有效 ));
  Multiplexer #(.select(1), .width(1), .disabled("Z"), .enable("false")) multiplexer_12 (
    .in0(\传输状态In_表明当前传输数据有效 ), .in1(1'b0), .out(multiplexer_12_out), .sel(\同步清零_气泡_高电平有效 ));
  Pull_Resistor #(.pull(0)) pull_resistor_1 (.node(\同步清零_气泡_高电平有效 ));
  Register #(.width(32), .trigger("rising"), .Select("low")) register_1 (
    .D(multiplexer_1_out), .en(pull_resistor_2_node), .Q(IR_OUT), .clk(CLK));  // open: clr
  Register #(.width(32), .trigger("rising"), .Select("low")) register_2 (
    .D(multiplexer_2_out), .en(pull_resistor_2_node), .Q(PC_OUT), .clk(CLK));  // open: clr
  Register #(.width(1), .trigger("rising"), .Select("low")) register_3 (
    .D(multiplexer_3_out), .en(pull_resistor_2_node), .Q(MemToReg_OUT), .clk(CLK));  // open: clr
  Register #(.width(1), .trigger("rising"), .Select("low")) register_4 (
    .D(multiplexer_4_out), .en(pull_resistor_2_node), .Q(ERET_OUT), .clk(CLK));  // open: clr
  Register #(.width(1), .trigger("rising"), .Select("low")) register_5 (
    .D(multiplexer_5_out), .en(pull_resistor_2_node), .Q(LBU_OUT), .clk(CLK));  // open: clr
  Register #(.width(1), .trigger("rising"), .Select("low")) register_6 (
    .D(multiplexer_6_out), .en(pull_resistor_2_node), .Q(RegWrite_OUT), .clk(CLK));  // open: clr
  Register #(.width(1), .trigger("rising"), .Select("low")) register_7 (
    .D(multiplexer_7_out), .en(pull_resistor_2_node), .Q(JAL_OUT), .clk(CLK));  // open: clr
  Register #(.width(1), .trigger("rising"), .Select("low")) register_8 (
    .D(multiplexer_8_out), .en(pull_resistor_2_node), .Q(RegDst_OUT), .clk(CLK));  // open: clr
  Register #(.width(5), .trigger("rising"), .Select("low")) register_9 (
    .D(multiplexer_9_out), .en(pull_resistor_2_node), .Q(RegWrite__OUT), .clk(CLK));  // open: clr
  Register #(.width(32), .trigger("rising"), .Select("low")) register_10 (
    .D(multiplexer_10_out), .en(pull_resistor_2_node), .Q(Mem_OUT), .clk(CLK));  // open: clr
  Register #(.width(32), .trigger("rising"), .Select("low")) register_11 (
    .D(multiplexer_11_out), .en(pull_resistor_2_node), .Q(AluRst_OUT), .clk(CLK));  // open: clr
  Register #(.width(1), .trigger("rising"), .Select("low")) register_12 (
    .D(multiplexer_12_out), .en(pull_resistor_2_node), .Q(\传输状态Out_表明当前传输数据有效 ), .clk(CLK));  // open: clr
  Pull_Resistor #(.pull(0)) pull_resistor_2 (.node(pull_resistor_2_node));
  not not_1 (pull_resistor_2_node, \使能端_低电平有效_stall_高电平有效 );
endmodule

module \气泡regfile  (
  input  [31:0] Din,
  input  Clk,
  input  WE,
  input  [4:0] R1_num,
  input  [4:0] W_num,
  input  [4:0] R2_num,
  output [31:0] R1,
  output [31:0] R2
);

  // RegisterFile registerfile_1: pin names not known; wires that end beside it: Din, Clk, WE, W_num, R1_num, R2_num, R1, R2
endmodule

module \寄存器使用情况  (
  input  OP0,
  input  OP1,
  input  OP2,
  input  OP3,
  input  OP4,
  input  OP5,
  input  F0,
  input  F1,
  input  F2,
  input  F3,
  input  F4,
  input  F5,
  output R1_Used,
  output R2_Used
);

  wire and_1_out, and_2_out, and_3_out, and_4_out, and_5_out, and_6_out, and_7_out, and_8_out, and_9_out,
       and_10_out, and_11_out, and_12_out, and_13_out, and_14_out, and_15_out, and_16_out, and_17_out,
       and_18_out, and_19_out, and_20_out, not_1_out, not_2_out, not_3_out, not_4_out, not_5_out, not_6_out,
       not_7_out, not_8_out, not_9_out, not_10_out, not_11_out, not_12_out, not_13_out, not_14_out,
       not_15_out, not_16_out, not_17_out, not_18_out, not_19_out, not_20_out, not_21_out, not_22_out,
       not_23_out, not_24_out, not_25_out, not_26_out, not_27_out, not_28_out, not_29_out, not_30_out,
       not_31_out, not_32_out, not_33_out, not_34_out, not_35_out, not_36_out, not_37_out, not_38_out,
       not_39_out, not_40_out, not_41_out, not_42_out, not_43_out, not_44_out, not_45_out, not_46_out,
       not_47_out, not_48_out, not_49_out, not_50_out, not_51_out, not_52_out, not_53_out, not_54_out,
       not_55_out, not_56_out, not_57_out, not_58_out, not_59_out, not_60_out, not_61_out, not_62_out,
       not_63_out, not_64_out, not_65_out, not_66_out, not_67_out, not_68_out, not_69_out, not_70_out,
       not_71_out, not_72_out, not_73_out, not_74_out, not_75_out, not_76_out, not_77_out, not_78_out,
       not_79_out, not_80_out, not_81_out, not_82_out, not_83_out, not_84_out, not_85_out, not_86_out,
       not_87_out, not_88_out, not_89_out, not_90_out, not_91_out, not_92_out, not_93_out, not_94_out,
       not_95_out, not_96_out, not_97_out, not_98_out, not_99_out, not_100_out, not_101_out, not_102_out,
       not_103_out, not_104_out, not_105_out, not_106_out, not_107_out, not_108_out, not_109_out,
       not_110_out, not_111_out, not_112_out, not_113_out, not_114_out, not_115_out, not_116_out, not_117_out;

  not not_1 (not_1_out, OP1);
  not not_2 (not_2_out, OP4);
  not not_3 (not_3_out, OP5);
  not not_4 (not_4_out, F1);
  not not_5 (not_5_out, F3);
  not not_6 (not_6_out, F4);
  not not_7 (not_7_out, OP1);
  not not_8 (not_8_out, OP4);
  not not_9 (not_9_out, OP5);
  not not_10 (not_10_out, F2);
  not not_11 (not_11_out, F3);
  not not_12 (not_12_out, F4);
  not not_13 (not_13_out, F0);
  not not_14 (not_14_out, OP1);
  not not_15 (not_15_out, OP4);
  not not_16 (not_16_out, OP5);
  not not_17 (not_17_out, F1);
  not not_18 (not_18_out, F4);
  not not_19 (not_19_out, F5);
  not not_20 (not_20_out, F0);
  not not_21 (not_21_out, OP1);
  not not_22 (not_22_out, OP4);
  not not_23 (not_23_out, OP5);
  not not_24 (not_24_out, F3);
  not not_25 (not_25_out, F4);
  not not_26 (not_26_out, OP1);
  not not_27 (not_27_out, OP4);
  not not_28 (not_28_out, OP5);
  not not_29 (not_29_out, F2);
  not not_30 (not_30_out, F4);
  not not_31 (not_31_out, OP1);
  not not_32 (not_32_out, OP4);
  not not_33 (not_33_out, OP5);
  not not_34 (not_34_out, F3);
  not not_35 (not_35_out, F4);
  not not_36 (not_36_out, F5);
  not not_37 (not_37_out, F0);
  not not_38 (not_38_out, OP0);
  not not_39 (not_39_out, OP2);
  not not_40 (not_40_out, OP4);
  not not_41 (not_41_out, OP5);
  not not_42 (not_42_out, OP0);
  not not_43 (not_43_out, OP1);
  not not_44 (not_44_out, OP3);
  not not_45 (not_45_out, OP4);
  not not_46 (not_46_out, OP1);
  not not_47 (not_47_out, OP4);
  not not_48 (not_48_out, OP5);
  not not_49 (not_49_out, OP1);
  not not_50 (not_50_out, OP4);
  not not_51 (not_51_out, OP5);
  not not_52 (not_52_out, OP2);
  not not_53 (not_53_out, OP4);
  not not_54 (not_54_out, OP0);
  not not_55 (not_55_out, OP1);
  not not_56 (not_56_out, OP3);
  not not_57 (not_57_out, OP4);
  not not_58 (not_58_out, OP5);
  not not_59 (not_59_out, F0);
  not not_60 (not_60_out, F2);
  not not_61 (not_61_out, F3);
  not not_62 (not_62_out, F4);
  not not_63 (not_63_out, OP0);
  not not_64 (not_64_out, OP1);
  not not_65 (not_65_out, OP3);
  not not_66 (not_66_out, OP4);
  not not_67 (not_67_out, OP5);
  not not_68 (not_68_out, F1);
  not not_69 (not_69_out, F3);
  not not_70 (not_70_out, F4);
  not not_71 (not_71_out, OP0);
  not not_72 (not_72_out, OP1);
  not not_73 (not_73_out, OP3);
  not not_74 (not_74_out, OP4);
  not not_75 (not_75_out, OP5);
  not not_76 (not_76_out, F0);
  not not_77 (not_77_out, F1);
  not not_78 (not_78_out, F4);
  not not_79 (not_79_out, F5);
  not not_80 (not_80_out, OP0);
  not not_81 (not_81_out, OP1);
  not not_82 (not_82_out, OP3);
  not not_83 (not_83_out, OP4);
  not not_84 (not_84_out, OP5);
  not not_85 (not_85_out, F0);
  not not_86 (not_86_out, F3);
  not not_87 (not_87_out, F4);
  not not_88 (not_88_out, F5);
  not not_89 (not_89_out, OP0);
  not not_90 (not_90_out, OP1);
  not not_91 (not_91_out, OP3);
  not not_92 (not_92_out, OP4);
  not not_93 (not_93_out, OP5);
  not not_94 (not_94_out, F2);
  not not_95 (not_95_out, F3);
  not not_96 (not_96_out, F4);
  not not_97 (not_97_out, F5);
  not not_98 (not_98_out, OP0);
  not not_99 (not_99_out, OP1);
  not not_100 (not_100_out, OP3);
  not not_101 (not_101_out, OP4);
  not not_102 (not_102_out, OP5);
  not not_103 (not_103_out, F2);
  not not_104 (not_104_out, F4);
  not not_105 (not_105_out, OP0);
  not not_106 (not_106_out, OP1);
  not not_107 (not_107_out, OP3);
  not not_108 (not_108_out, OP4);
  not not_109 (not_109_out, OP5);
  not not_110 (not_110_out, F3);
  not not_111 (not_111_out, F4);
  not not_112 (not_112_out, OP1);
  not not_113 (not_113_out, OP3);
  not not_114 (not_114_out, OP4);
  not not_115 (not_115_out, OP5);
  not not_116 (not_116_out, OP2);
  not not_117 (not_117_out, OP4);
  and and_1 (and_1_out, not_1_out, not_2_out, not_3_out, not_4_out, not_5_out, not_6_out, F5);
  and and_2 (and_2_out, not_7_out, not_8_out, not_9_out, not_10_out, not_11_out, not_12_out, F5, not_13_out);
  and and_3 (and_3_out, not_14_out, not_15_out, not_16_out, not_17_out, F3, not_18_out, not_19_out, not_20_out);
  and and_4 (and_4_out, not_21_out, not_22_out, not_23_out, F2, not_24_out, not_25_out, F5, F0);
  and and_5 (and_5_out, not_26_out, not_27_out, not_28_out, F1, not_29_out, F3, not_30_out, F5);
  and and_6 (and_6_out, not_31_out, not_32_out, not_33_out, F1, F2, not_34_out, not_35_out, not_36_out, not_37_out);
  and and_7 (and_7_out, not_38_out, not_39_out, OP3, not_40_out, not_41_out);
  and and_8 (and_8_out, not_42_out, not_43_out, OP2, not_44_out, not_45_out);
  and and_9 (and_9_out, not_46_out, OP2, not_47_out, not_48_out);
  and and_10 (and_10_out, OP0, not_49_out, not_50_out, not_51_out);
  and and_11 (and_11_out, OP0, OP1, not_52_out, not_53_out, OP5);
  and and_12 (and_12_out, not_54_out, not_55_out, not_56_out, not_57_out, not_58_out, not_59_out, not_60_out, not_61_out, not_62_out);
  and and_13 (and_13_out, not_63_out, not_64_out, not_65_out, not_66_out, not_67_out, not_68_out, not_69_out, not_70_out, F5);
  and and_14 (and_14_out, not_71_out, not_72_out, not_73_out, not_74_out, not_75_out, not_76_out, not_77_out, F2, F3, not_78_out, not_79_out);
  and and_15 (and_15_out, not_80_out, not_81_out, not_82_out, not_83_out, not_84_out, not_85_out, F1, not_86_out, not_87_out, not_88_out);
  and and_16 (and_16_out, not_89_out, not_90_out, not_91_out, not_92_out, not_93_out, F1, not_94_out, not_95_out, not_96_out, not_97_out);
  and and_17 (and_17_out, not_98_out, not_99_out, not_100_out, not_101_out, not_102_out, F1, not_103_out, F3, not_104_out, F5);
  and and_18 (and_18_out, not_105_out, not_106_out, not_107_out, not_108_out, not_109_out, F0, F2, not_110_out, not_111_out, F5);
  and and_19 (and_19_out, not_112_out, OP2, not_113_out, not_114_out, not_115_out);
  and and_20 (and_20_out, OP0, OP1, not_116_out, OP3, not_117_out, OP5);
  or or_1 (R1_Used, and_1_out, and_2_out, and_3_out, and_4_out, and_5_out, and_6_out, and_7_out, and_8_out, and_9_out, and_10_out, and_11_out);
  or or_2 (R2_Used, and_12_out, and_13_out, and_14_out, and_15_out, and_16_out, and_17_out, and_18_out, and_19_out, and_20_out);
endmodule

module \数据相关检测  (
  input  [4:0] R1_num,
  input  R1_Used,
  input  [4:0] RegWrite__MEM,
  input  RegWrite_MEM,
  input  [4:0] RegWrite__EX,
  input  RegWrite_EX,
  input  [4:0] R2_num,
  input  R2_Used,
  output \数据相关 
);

  wire and_1_out, and_2_out, and_3_out, and_4_out, and_5_out, and_6_out, comparator_1_eq, comparator_2_eq,
       pull_resistor_1_node, pull_resistor_2_node, pull_resistor_3_node, pull_resistor_4_node;
  wire [4:0] controlled_buffer_1_out, controlled_buffer_2_out;

  Comparator #(.width(5), .mode("twosComplement")) comparator_1 (
    .a({5{1'b0}}), .b(R1_num), .eq(comparator_1_eq));  // open: gt, lt
  and and_1 (and_1_out, ~comparator_1_eq, R1_Used);  // AND_Gate
  assign controlled_buffer_1_out = and_1_out ? R1_num : 5'bz;  // Controlled_Buffer controlled_buffer_1
  Comparator #(.width(5), .mode("twosComplement")) comparator_2 (
    .a({5{1'b0}}), .b(R2_num), .eq(comparator_2_eq));  // open: gt, lt
  and and_2 (and_2_out, ~comparator_2_eq, R2_Used);  // AND_Gate
  assign controlled_buffer_2_out = and_2_out ? R2_num : 5'bz;  // Controlled_Buffer controlled_buffer_2
  Pull_Resistor #(.pull(0)) pull_resistor_1 (.node(pull_resistor_1_node));
  Comparator #(.width(5), .mode("twosComplement")) comparator_3 (
    .a(controlled_buffer_1_out), .b(RegWrite__MEM), .eq(pull_resistor_1_node));  // open: gt, lt
  Pull_Resistor #(.pull(0)) pull_resistor_2 (.node(pull_resistor_2_node));
  Comparator #(.width(5), .mode("twosComplement")) comparator_4 (
    .a(controlled_buffer_1_out), .b(RegWrite__EX), .eq(pull_resistor_2_node));  // open: gt, lt
  Pull_Resistor #(.pull(0)) pull_resistor_3 (.node(pull_resistor_3_node));
  Comparator #(.width(5), .mode("twosComplement")) comparator_5 (
    .a(RegWrite__MEM), .b(controlled_buffer_2_out), .eq(pull_resistor_3_node));  // open: gt, lt
  Pull_Resistor #(.pull(0)) pull_resistor_4 (.node(pull_resistor_4_node));
  Comparator #(.width(5), .mode("twosComplement")) comparator_6 (
    .a(RegWrite__EX), .b(controlled_buffer_2_out), .eq(pull_resistor_4_node));  // open: gt, lt
  and and_3 (and_3_out, pull_resistor_1_node, RegWrite_MEM);
  and and_4 (and_4_out, pull_resistor_2_node, RegWrite_EX);
  and and_5 (and_5_out, pull_resistor_3_node, RegWrite_MEM);
  and and_6 (and_6_out, pull_resistor_4_node, RegWrite_EX);
  or or_1 (\数据相关 , and_3_out, and_4_out, and_5_out, and_6_out);
endmodule

module \重定向流水线中断  (
  output RegWrite,
  output MemWrite,
  output [31:0] IF_PC,
  output [31:0] ID_PC,
  output [31:0] EX_PC,
  output [31:0] M_PC,
  output [31:0] WB_PC,
  output [31:0] RDin,
  output [31:0] MDin,
  output [31:0] LedData
);

  wire AluSrcB_EX, AluSrcB_ID, and_1_out, and_2_out, and_3_out, and_6_out, and_7_out, B_EX, BEQ_EX, BEQ_ID,
       BGEZ_EX, BGEZ_ID, BNE_EX, BNE_ID, CLK, clock_1_out, clock_2_out, comparator_1_eq, comparator_1_lt,
       comparator_4_eq, comparator_5_eq, comparator_6_eq, comparator_7_eq, d_ff_1_q, d_ff_2_qn, Equal, ERET,
       ERET_EX, ERET_ID, ERET_MEM, ERET_WB, EX_MFC0, EX_MTC0, Exit, Go, ID_MFC0, ID_MTC0, IF_STALL, intChan,
       IntR, IR1, IR2, IR3, JAL_EX, JAL_ID, JAL_MEM, JAL_WB, JMP_EX, JMP_ID, JR_EX, JR_ID, LBU_EX, LBU_ID,
       LBU_MEM, LBU_WB, MEM_STALL, MemToReg_EX, MemToReg_ID, MemToReg_MEM, MemToReg_WB, MemWrite_EX,
       MemWrite_ID, nand_1_out, not_1_out, not_2_out, or_1_out, or_2_out, or_3_out, or_4_out, or_5_out,
       or_7_out, Pause, RegDst_EX, RegDst_ID, RegDst_MEM, RegWrite_EX, RegWrite_ID, RegWrite_MEM, RST,
       SignedExt_EX, SignedExt_ID, SV_EX, SV_ID, Syscall_EX, Syscall_ID, W1, W2, W3, \中断请求 ,
       \寄存器使用情况_1_r1_used , \寄存器使用情况_1_r2_used ;
  wire [1:0] forwadr2_ID, forward1_EX, forward1_ID, forward2_EX, xor_1_out, \单周期mips_单级中断中断控制器_1_intnum ,
       \硬件堆栈_1_1_输出 ;
  wire [3:0] AluOP_EX, AluOP_ID;
  wire [4:0] multiplexer_2_out, R1__ID, R2__ID, RegWrite__EX, RegWrite__ID, RegWrite__MEM, RegWrite__WB,
       shamt;
  wire [5:0] Func;
  wire [7:0] multiplexer_14_out;
  wire [12:0] CNT_num;
  wire [15:0] \LoadUse次数 , \总周期数 , \插入气泡数 , \无条件分支数 , \条件分支成功数 ;
  wire [27:0] adder_2_out;
  wire [31:0] adder_3_out, adder_5_out, AluRes_EX, AluRes_MEM, AluRes_WB, bit_extender_1_out,
       bit_extender_2_out, bit_extender_3_out, EpcIn, EpcOut, EX_IR, EX_PC_imm, EX_PC_JR, IF_IR, imm_EX,
       imm_ID, MDin_EX, MEM_IR, multiplexer_1_out, multiplexer_9_out, multiplexer_11_out, multiplexer_13_out,
       multiplexer_15_out, PC_4, PC_IRQ, R1_EX_1, R1_ID, R2_EX, R2_EX_1, R2_ID, RDin_MEM, RDin_WB,
       shifter_1_out, WB_IR;
  wire [31:6] ID_IR;
  wire [31:28] EX_PC_J_JAL;

  Button \u_总复位  (.out(RST));
  Button _1 (.out(IR1));
  Button _2 (.out(IR2));
  Button _3 (.out(IR3));
  // Probe on \总周期数 
  // Probe on \总周期数 
  Button \u_继续运行  (.out(Go));
  LED #(.active("true")) led_1 (.in(W1));
  LED #(.active("true")) led_2 (.in(W2));
  LED #(.active("true")) led_3 (.in(W3));
  Hex_Digit_Display hex_digit_display_1 (.value(LedData[31:28]));  // open: dp
  // Probe on IF_PC[19:0]
  // Mips_Probe mips_probe_1: pin names not known; wires that end beside it: IF_IR
  Hex_Digit_Display hex_digit_display_2 (.value(LedData[23:20]));  // open: dp
  Hex_Digit_Display hex_digit_display_3 (.value(LedData[27:24]));  // open: dp
  // Probe on ID_PC[19:0]
  // Mips_Probe mips_probe_2: pin names not known; wires that end beside it: {ID_IR, Func}
  Hex_Digit_Display hex_digit_display_4 (.value(LedData[15:12]));  // open: dp
  Hex_Digit_Display hex_digit_display_5 (.value(LedData[19:16]));  // open: dp
  not not_1 (not_1_out, IF_STALL);
  Multiplexer #(.select(3), .width(32), .disabled("Z"), .enable("false")) multiplexer_1 (
    .in0(PC_4), .in1(EX_PC_imm), .in2({EX_PC_J_JAL, EX_IR[25:0], 2'b00}), .in6(EX_PC_JR),
    .out(multiplexer_1_out), .sel({JR_EX, JMP_EX, B_EX}));  // open: in3, in4, in5, in7
  Hex_Digit_Display hex_digit_display_6 (.value(LedData[11:8]));  // open: dp
  Hex_Digit_Display hex_digit_display_7 (.value(LedData[7:4]));  // open: dp
  Clock #(.highDuration(1), .lowDuration(1)) clock_1 (.out(clock_1_out));
  // Probe on EX_PC[19:0]
  // Mips_Probe mips_probe_3: pin names not known; wires that end beside it: clock_1_out, EX_IR, CLK
  Register #(.width(32), .trigger("rising"), .Select("low")) register_1 (
    .D(multiplexer_1_out), .en(not_1_out), .Q(IF_PC), .clk(CLK));  // open: clr
  // Probe on IF_PC
  Hex_Digit_Display hex_digit_display_8 (.value(LedData[3:0]));  // open: dp
  // Probe on IF_IR
  Adder #(.width(32)) adder_1 (.a(IF_PC), .b(32'h4), .out(PC_4));  // open: cin, cout
  // Probe on \总周期数 
  // Probe on M_PC[19:0]
  // Mips_Probe mips_probe_4: pin names not known; wires that end beside it: MEM_IR
  ROM #(.addrWidth(10), .dataWidth(32), .Select("high")) rom_1 (.addr(IF_PC[11:2]), .data(IF_IR));
  // Probe on \总周期数 
  // Probe on \无条件分支数 
  // Probe on \条件分支成功数 
  // Probe on \插入气泡数 
  // Probe on \LoadUse次数 
  // Mips_Probe mips_probe_5: pin names not known; wires that end beside it: IF_IR
  or or_1 (or_1_out, JMP_EX, B_EX);
  // Probe on IF_PC[11:0]
  // Probe on WB_PC[19:0]
  // Mips_Probe mips_probe_6: pin names not known; wires that end beside it: WB_IR
  \气泡流水线接口IF_ID  \u_气泡流水线接口if_id_1  (
    .IR_IN(IF_IR), .PC_IN(IF_PC), .CLK(CLK), .IR_OUT({ID_IR, Func}), .PC_OUT(ID_PC),
    .\同步清零_气泡_高电平有效 (or_1_out), .\使能端_低电平有效_stall_高电平有效 (IF_STALL));  // open: 传输状态In_表明当前传输数据有效, 传输状态Out_表明当前传输数据有效
  // Probe on ID_PC[11:0]
  // Probe on EX_PC[11:0]
  // Mips_Probe mips_probe_7: pin names not known; wires that end beside it: {ID_IR, Func}
  // Probe on M_PC[11:0]
  D_Flip_Flop #(.trigger("high"), .Pre_Clr_Positions("LEGACY"), .NegatePresetClear("false"), .enable("true"), .NewFFLayout("false")) d_ff_1 (.Q(d_ff_1_q));  // open: clk, D, Qn, preset, en, reset
  // Probe on 13'h343
  // Probe on WB_PC[11:0]
  Comparator #(.width(13), .mode("twosComplement")) comparator_1 (
    .a(CNT_num), .b(13'h343), .eq(comparator_1_eq), .lt(comparator_1_lt));  // open: gt
  Clock #(.highDuration(1), .lowDuration(1)) clock_2 (.out(clock_2_out));
  Multiplexer #(.select(1), .width(5), .disabled("Z"), .enable("false")) multiplexer_2 (
    .in0(ID_IR[20:16]), .in1(ID_IR[15:11]), .out(multiplexer_2_out), .sel(RegDst_ID));
  nand nand_1 (nand_1_out, d_ff_1_q, comparator_1_eq);
  Counter #(.width(13), .max('h1fff), .ongoal("stay"), .trigger("rising"), .behavior("old")) counter_1 (
    .count(comparator_1_lt), .Q(CNT_num), .clk(clock_2_out));  // open: load, D, carry, clr, preset
  \单周期硬布线控制器  \u_单周期硬布线控制器_1  (
    .Func(Func), .OP(ID_IR[31:26]), .ALU_OP(AluOP_ID), .MemToReg(MemToReg_ID), .MemWrite(MemWrite_ID),
    .ALU_SRC(AluSrcB_ID), .RegWrite(RegWrite_ID), .SysCALL(Syscall_ID), .SignedExt(SignedExt_ID),
    .RegDst(RegDst_ID), .JR(JR_ID), .JMP(JMP_ID), .Beq(BEQ_ID), .JAL(JAL_ID), .Bne(BNE_ID), .ERET(ERET_ID),
    .SV(SV_ID), .LBU(LBU_ID), .BGEZ(BGEZ_ID));
  Multiplexer #(.select(1), .width(5), .disabled("Z"), .enable("false")) multiplexer_3 (
    .in0(multiplexer_2_out), .in1({5{1'b1}}), .out(RegWrite__ID), .sel(JAL_ID));
  Comparator #(.width(32), .mode("twosComplement")) comparator_2 (
    .a({ID_IR, Func}), .b(32'h40800000), .eq(ID_MTC0));  // open: gt, lt
  Comparator #(.width(32), .mode("twosComplement")) comparator_3 (
    .a({ID_IR, Func}), .b(32'h40000000), .eq(ID_MFC0));  // open: gt, lt
  assign CLK = nand_1_out ? clock_2_out : 1'bz;  // Controlled_Buffer controlled_buffer_1
  \寄存器使用情况  \u_寄存器使用情况_1  (
    .OP0(ID_IR[26]), .OP1(ID_IR[27]), .OP2(ID_IR[28]), .OP3(ID_IR[29]), .OP4(ID_IR[30]), .OP5(ID_IR[31]),
    .F0(Func[0]), .F1(Func[1]), .F2(Func[2]), .F3(Func[3]), .F4(Func[4]), .F5(Func[5]),
    .R1_Used(\寄存器使用情况_1_r1_used ), .R2_Used(\寄存器使用情况_1_r2_used ));
  Pull_Resistor #(.pull(1)) pull_resistor_1 (.node(CLK));
  Forward forward_1 (
    .RegWrite__MEM(RegWrite__MEM), .RegWrite_MEM(RegWrite_MEM), .RegWrite__EX(RegWrite__EX),
    .RegWrite_EX(RegWrite_EX), .R1_Used(\寄存器使用情况_1_r1_used ), .R1_forward(forward1_ID),
    .R2_Used(\寄存器使用情况_1_r2_used ), .R2_forward(forwadr2_ID), .R1_num(R1__ID), .R2_num(R2__ID));
  \Load_Use相关  \load_use相关_1  (
    .RegWrite__EX(RegWrite__EX), .MemToReg_EX(MemToReg_EX), .R1_Used(\寄存器使用情况_1_r1_used ),
    .\Load_Usex相关 (IF_STALL), .R2_Used(\寄存器使用情况_1_r2_used ), .R1_num(R1__ID), .R2_num(R2__ID));
  Multiplexer #(.select(1), .width(5), .disabled("Z"), .enable("false")) multiplexer_4 (
    .in0(ID_IR[25:21]), .in1(5'b00010), .out(R1__ID), .sel(Syscall_ID));
  Multiplexer #(.select(1), .width(5), .disabled("Z"), .enable("false")) multiplexer_5 (
    .in0(ID_IR[20:16]), .in1(5'b00100), .out(R2__ID), .sel(Syscall_ID));
  Counter #(.width(16), .max('hffff), .ongoal("wrap"), .trigger("rising"), .behavior("new")) counter_2 (
    .count(IF_STALL), .Q(\LoadUse次数 ), .clk(CLK), .clr(RST));  // open: load, D, carry, preset, down
  // Probe on R1__ID
  // Probe on R2__ID
  // Probe on RegWrite__WB
  assign bit_extender_1_out = {{16{1'b0}}, {ID_IR[15:6], Func}};  // Bit_Extender bit_extender_1
  assign bit_extender_2_out = {{16{ID_IR[15]}}, {ID_IR[15:6], Func}};  // Bit_Extender bit_extender_2
  \气泡regfile  \u_气泡regfile_1  (
    .Din(RDin), .Clk(CLK), .R1(R1_ID), .R2(R2_ID), .WE(RegWrite), .W_num(RegWrite__WB), .R1_num(R1__ID),
    .R2_num(R2__ID));
  Multiplexer #(.select(1), .width(32), .disabled("Z"), .enable("false")) multiplexer_6 (
    .in0(bit_extender_1_out), .in1(bit_extender_2_out), .out(imm_ID), .sel(SignedExt_ID));
  or or_2 (or_2_out, JMP_EX, B_EX, IF_STALL);
  // Mips_Probe mips_probe_8: pin names not known; wires that end beside it: EX_IR
  \气泡流水线接口ID_EX  \u_气泡流水线接口id_ex_1  (
    .IR_IN({ID_IR, Func}), .PC_IN(ID_PC), .JMP_IN(JMP_ID), .Beq_IN(BEQ_ID), .JR_IN(JR_ID), .Bne_IN(BNE_ID),
    .SignedExt_IN(SignedExt_ID), .MemToReg_IN(MemToReg_ID), .ERET_IN(ERET_ID), .MemWrite_IN(MemWrite_ID),
    .LBU_IN(LBU_ID), .AluOp_IN(AluOP_ID), .BGEZ_IN(BGEZ_ID), .AluSrcB_IN(AluSrcB_ID),
    .RegWrite_IN(RegWrite_ID), .JAL_IN(JAL_ID), .RegDst_IN(RegDst_ID), .Syscall_IN(Syscall_ID),
    .RegWrite__IN(RegWrite__ID), .R1Forward_IN(forward1_ID), .R2Forward_IN(forwadr2_ID), .R1_IN(R1_ID),
    .R2_IN(R2_ID), .Imm__IN(imm_ID), .MFC0_IN(ID_MTC0), .MTC0_IN(ID_MFC0), .CLK(CLK), .IR_OUT_2(EX_IR),
    .PC_OUT(EX_PC), .JMP_OUT(JMP_EX), .Beq_OUT(BEQ_EX), .JR_OUT(JR_EX), .Bne_OUT(BNE_EX),
    .SignedExt_OUT(SignedExt_EX), .MemToReg_OUT(MemToReg_EX), .ERET_OUT(ERET_EX), .MemWrite_OUT(MemWrite_EX),
    .LBU_OUT(LBU_EX), .AluOp_OUT(AluOP_EX), .BGEZ_OUT(BGEZ_EX), .AluSrcB_OUT(AluSrcB_EX),
    .RegWrite_OUT(RegWrite_EX), .JAL_OUT(JAL_EX), .RegDst_OUT(RegDst_EX), .Syscall_OUT(Syscall_EX),
    .RegWrite__OUT(RegWrite__EX), .R1Forward_OUT(forward1_EX), .R2Forward_OUT(forward2_EX), .R1_OUT(R1_EX_1),
    .R2_OUT(R2_EX_1), .Imm_OUT(imm_EX), .MFC0_OUT(EX_MTC0), .MTC0_OUT(EX_MFC0), .\同步清零_气泡_高电平有效 (or_2_out),
    .\使能端_低电平有效_stall_高电平有效 (1'b0), .SV_IN(SV_ID), .IR_OUT(SV_EX));  // open: 传输状态In_表明当前传输数据有效, 传输状态Out_表明当前传输数据有效
  Multiplexer #(.select(2), .width(32), .disabled("Z"), .enable("false")) multiplexer_7 (
    .in1(32'h30ac), .in2(32'h3158), .in3(32'h3204), .out(PC_IRQ), .sel(\单周期mips_单级中断中断控制器_1_intnum ));  // open: in0
  Counter #(.width(16), .max('hffff), .ongoal("wrap"), .trigger("rising"), .behavior("new")) counter_3 (
    .count(JMP_EX), .Q(\无条件分支数 ), .clk(CLK), .clr(RST));  // open: load, D, carry, preset, down
  Counter #(.width(16), .max('hffff), .ongoal("wrap"), .trigger("rising"), .behavior("new")) counter_4 (
    .count(B_EX), .Q(\条件分支成功数 ), .clk(CLK), .clr(RST));  // open: load, D, carry, preset, down
  Comparator #(.width(32), .mode("twosComplement")) comparator_4 (
    .a(32'ha), .b(EX_PC_JR), .eq(comparator_4_eq));  // open: gt, lt
  Comparator #(.width(32), .mode("twosComplement")) comparator_5 (
    .a(32'h32), .b(EX_PC_JR), .eq(comparator_5_eq));  // open: gt, lt
  Comparator #(.width(32), .mode("twosComplement")) comparator_6 (
    .a(32'h22), .b(EX_PC_JR), .eq(comparator_6_eq));  // open: gt, lt
  or or_3 (or_3_out, ERET_EX, \中断请求 );
  \单周期MIPS_单级中断中断控制器  \u_单周期mips_单级中断中断控制器_1  (
    .CLK(CLK), .IR1(IR1), .IR2(IR2), .IR3(IR3), .Clr(ERET_EX), .TEST(\硬件堆栈_1_1_输出 ), .IR1W(W1), .IR2W(W2),
    .IR3W(W3), .IntNum(\单周期mips_单级中断中断控制器_1_intnum ), .IntR(IntR));
  or or_4 (or_4_out, ERET_EX, EX_MFC0);
  or or_5 (or_5_out, IntR, EX_MTC0);
  and and_1 (and_1_out, BGEZ_EX, comparator_7_eq);
  Comparator #(.width(32), .mode("twosComplement")) comparator_7 (
    .a(AluRes_EX), .b({32{1'b0}}), .eq(comparator_7_eq));  // open: gt, lt
  and and_2 (and_2_out, BEQ_EX, Equal);
  and and_3 (and_3_out, BNE_EX, not_2_out);
  not not_2 (not_2_out, Equal);
  Multiplexer #(.select(2), .width(32), .disabled("Z"), .enable("false")) multiplexer_8 (
    .in0(R2_EX_1), .in1(RDin), .in2(AluRes_MEM), .out(R2_EX), .sel(forward2_EX));  // open: in3
  and and_4 (Exit, Syscall_EX, comparator_4_eq);
  and and_5 (Pause, Syscall_EX, comparator_5_eq);
  and and_6 (and_6_out, Syscall_EX, comparator_6_eq);
  \硬件堆栈_1  \u_硬件堆栈_1_1  (
    .CLK(CLK), .read(ERET_EX), .change(or_3_out), .\输入 (\单周期mips_单级中断中断控制器_1_intnum ), .\输出 (\硬件堆栈_1_1_输出 ));
  and and_7 (and_7_out, ~or_4_out, or_5_out);  // AND_Gate
  or or_6 (B_EX, and_1_out, and_2_out, and_3_out);
  Multiplexer #(.select(1), .width(32), .disabled("Z"), .enable("false")) multiplexer_9 (
    .in0(R2_EX), .in1(imm_EX), .out(multiplexer_9_out), .sel(AluSrcB_EX));
  Register #(.width(32), .trigger("rising"), .Select("low")) register_2 (
    .D(MDin_EX), .en(and_6_out), .Q(LedData), .clk(CLK));  // open: clr
  Comparator #(.width(2), .mode("unsigned")) comparator_8 (
    .a(\单周期mips_单级中断中断控制器_1_intnum ), .b(\硬件堆栈_1_1_输出 ), .gt(intChan));  // open: eq, lt
  D_Flip_Flop #(.trigger("rising"), .Pre_Clr_Positions("LEGACY"), .NegatePresetClear("false"), .enable("true"), .NewFFLayout("false")) d_ff_2 (
    .clk(CLK), .D(and_7_out), .Qn(d_ff_2_qn));  // open: Q, preset, en, reset
  Counter #(.width(16), .max('hffff), .ongoal("wrap"), .trigger("rising"), .behavior("new")) counter_5 (
    .Q(\总周期数 ), .clk(CLK));  // open: load, D, count, carry, clr, preset, down
  Multiplexer #(.select(2), .width(32), .disabled("Z"), .enable("false")) multiplexer_10 (
    .in0(R1_EX_1), .in1(RDin), .in2(AluRes_MEM), .out(EX_PC_JR), .sel(forward1_EX));  // open: in3
  Multiplexer #(.select(1), .width(32), .disabled("Z"), .enable("false")) multiplexer_11 (
    .in0(multiplexer_9_out), .in1({32{1'b0}}), .out(multiplexer_11_out), .sel(BGEZ_EX));
  and and_8 (\中断请求 , d_ff_2_qn, intChan, IntR);
  Adder #(.width(32)) adder_2 (.a(EX_PC), .b(32'h4), .out({EX_PC_J_JAL, adder_2_out}));  // open: cin, cout
  Shifter #(.width(32), .shift("ll")) shifter_1 (.in(imm_EX), .\dist (5'b00010), .out(shifter_1_out));
  Adder #(.width(32)) adder_3 (.a(32'h4), .b(EX_PC), .out(adder_3_out));  // open: cin, cout
  Adder #(.width(32)) adder_4 (.a(shifter_1_out), .b(adder_3_out), .out(EX_PC_imm));  // open: cin, cout
  MIPS_ALU mips_alu_1 (
    .X(EX_PC_JR), .Y(multiplexer_11_out), .AluOP(AluOP_EX), .Equal(Equal), .Result(AluRes_EX), .shamt(shamt));  // open: Result_2
  Multiplexer #(.select(1), .width(5), .disabled("Z"), .enable("false")) multiplexer_12 (
    .in0(EX_IR[10:6]), .in1(EX_PC_JR[4:0]), .out(shamt), .sel(SV_EX));
  \硬件堆栈  \u_硬件堆栈_1  (.CLK(CLK), .read(ERET), .change(or_7_out), .\输入 (EpcIn), .\输出 (EpcOut));
  or or_7 (or_7_out, ERET, \中断请求 );
  // Mips_Probe mips_probe_9: pin names not known; wires that end beside it: MEM_IR
  \气泡流水线接口EX_MEM  \u_气泡流水线接口ex_mem_1  (
    .IR_IN(EX_IR), .PC_IN(EX_PC), .MemToReg_IN(MemToReg_EX), .ERET_IN(ERET_EX), .MemWrite_IN(MemWrite_EX),
    .LBU_IN(LBU_EX), .RegWrite_IN(RegWrite_EX), .JAL_IN(JAL_EX), .RegDst_IN(RegDst_EX),
    .RegWrite__IN(RegWrite__EX), .AluRst_IN(AluRes_EX), .Mem_IN(R2_EX), .CLK(CLK), .IR_OUT(MEM_IR),
    .PC_OUT(M_PC), .MemToReg_OUT(MemToReg_MEM), .ERET_OUT(ERET_MEM), .MemWrite_OUT(MemWrite),
    .LBU_OUT(LBU_MEM), .RegWrite_OUT(RegWrite_MEM), .JAL_OUT(JAL_MEM), .RegDst_OUT(RegDst_MEM),
    .RegWrite__OUT(RegWrite__MEM), .AluRst_OUT(AluRes_MEM), .Mem_OUT(MDin),
    .\使能端_低电平有效_stall_高电平有效 (MEM_STALL));  // open: 传输状态In_表明当前传输数据有效, 传输状态Out_表明当前传输数据有效, 同步清零_气泡_高电平有效
  RAM #(.addrWidth(10), .dataWidth(32), .bus("separate"), .Select("high")) ram_1 (
    .addr(AluRes_MEM[11:2]), .din(MDin), .data(RDin_MEM), .str(MemWrite), .clk(CLK));  // open: sel, ld, clr
  // Mips_Probe mips_probe_10: pin names not known; wires that end beside it: WB_IR
  \气泡流水线MEM_WB  \u_气泡流水线mem_wb_1  (
    .IR_IN(MEM_IR), .PC_IN(M_PC), .MemToReg_IN(MemToReg_MEM), .ERET_IN(ERET_MEM), .LBU_IN(LBU_MEM),
    .RegWrite_IN(RegWrite_MEM), .JAL_IN(JAL_MEM), .RegDst_IN(RegDst_MEM), .RegWrite__IN(RegWrite__MEM),
    .Mem_IN(RDin_MEM), .AluRst_IN(AluRes_MEM), .CLK(CLK), .IR_OUT(WB_IR), .PC_OUT(WB_PC),
    .MemToReg_OUT(MemToReg_WB), .ERET_OUT(ERET_WB), .LBU_OUT(LBU_WB), .RegWrite_OUT(RegWrite),
    .JAL_OUT(JAL_WB), .RegWrite__OUT(RegWrite__WB), .Mem_OUT(RDin_WB), .AluRst_OUT(AluRes_WB),
    .\使能端_低电平有效_stall_高电平有效 (1'b0));  // open: 传输状态In_表明当前传输数据有效, RegDst_OUT, 传输状态Out_表明当前传输数据有效, 同步清零_气泡_高电平有效
  Multiplexer #(.select(1), .width(32), .disabled("Z"), .enable("false")) multiplexer_13 (
    .in0(AluRes_WB), .in1(RDin_WB), .out(multiplexer_13_out), .sel(MemToReg_WB));
  assign xor_1_out = AluRes_WB[1:0] ^ 2'b11;  // XOR_Gate xor_1, 2 bits wide
  Multiplexer #(.select(2), .width(8), .disabled("Z"), .enable("false")) multiplexer_14 (
    .in0(multiplexer_13_out[7:0]), .in1(multiplexer_13_out[15:8]), .in2(multiplexer_13_out[23:16]),
    .in3(multiplexer_13_out[31:24]), .out(multiplexer_14_out), .sel(xor_1_out));
  Multiplexer #(.select(1), .width(32), .disabled("Z"), .enable("false")) multiplexer_15 (
    .in0(multiplexer_13_out), .in1(bit_extender_3_out), .out(multiplexer_15_out), .sel(LBU_WB));
  assign bit_extender_3_out = {{24{1'b0}}, multiplexer_14_out};  // Bit_Extender bit_extender_3
  Adder #(.width(32)) adder_5 (.a(WB_PC), .b(32'h4), .out(adder_5_out));  // open: cin, cout
  Multiplexer #(.select(1), .width(32), .disabled("Z"), .enable("false")) multiplexer_16 (
    .in0(multiplexer_15_out), .in1(adder_5_out), .out(RDin), .sel(JAL_WB));

  // Other names for the same wires on the sheet: BGEZ_RES[31:0] = AluRes_EX; EX_PC_J_JAL[27:2] = EX_IR[25:0];
  //   ID_IR[5:0] = Func; imm[15:0] = {ID_IR[15:6], Func}; rd[4:0] = ID_IR[15:11]; rt[4:0] = ID_IR[20:16];
  //   rs[4:0] = ID_IR[25:21]; OP[5:0] = ID_IR[31:26]; MDin_MEM[31:0] = MDin; MEM_PC[31:0] = M_PC;
  //   MemWrite_MEM = MemWrite; R1_EX[31:0] = EX_PC_JR; Vaddr_WB[31:0] = AluRes_WB; WB_RegWrite = RegWrite

  // Notes on the sheet:
  //   中断源
  //   时空图监测，可删除
  //   中断等待指示
  //   数码管输出
  //   指令存储器
  //   contents of rom_1 (hex, n*v repeats v):
  //   20110001 8000c05 20110001 20120002 20130003 8000c09 20110001 20120002 20130003 8000c0d 20110001
  //   20120002 20130003 8000c11 20110001 20120002 20130003 c000cb8 20100001 20110001 118fc0 112020
  //   20020022 c 118882 12200001 8000c15 112020 20020022 c 20110001 118880 112020 20020022 c 12200001
  //   8000c1f 20110001 118fc0 112020 20020022 c 1188c3 112020 20020022 c 118903 112020 20020022 c 118903
  //   112020 20020022 c 118903 112020 20020022 c 118903 112020 20020022 c 118903 112020 20020022 c 118903
  //   112020 20020022 c 118903 112020 20020022 c 20100001 109fc0 139fc3 8021 2012000c 24160003 26100001
  //   3210000f 20080008 20090001 139900 2709825 132020 20020022 c 1094022 1500fff9 22100001 2018000f
  //   2188024 108700 20080008 20090001 139902 2709825 132021 20020022 c 1094022 1500fff9 108702 2c9b022
  //   12c00001 8000c50 4020 1084027 84400 3508ffff 82021 20020022 c 2010ffff 20110000 ae300000 22100001
  //   22310004 ae300000 22100001 22310004 ae300000 22100001 22310004 ae300000 22100001 22310004 ae300000
  //   22100001 22310004 ae300000 22100001 22310004 ae300000 22100001 22310004 ae300000 22100001 22310004
  //   ae300000 22100001 22310004 ae300000 22100001 22310004 ae300000 22100001 22310004 ae300000 22100001
  //   22310004 ae300000 22100001 22310004 ae300000 22100001 22310004 ae300000 22100001 22310004 ae300000
  //   22100001 22310004 22100001 8020 2011003c 8e130000 8e340000 274402a 11000002 ae330000 ae140000
  //   2231fffc 1611fff8 102020 20020022 c 22100004 2011003c 1611fff2 20020032 c 20100000 22100001 102020
  //   20020022 c 22100002 102020 20020022 c 22100003 102020 20020022 c 22100004 102020 20020022 c 22100005
  //   102020 20020022 c 22100006 102020 20020022 c 22100007 102020 20020022 c 22100008 102020 20020022
  //   20020022 c 3e00008
  //   控制位
  //   OP
  //   Func
  //   rs
  //   rt
  //   流水调试日志用
  //   暂停节拍，不能为0
  //   戳工具置1进入计数暂停模式，ctrl+k时钟自动运行到对应节拍暂停
  //   ctrl+k关闭时钟连续运行，将控制位置零，进入单步调试模式调试
  //   JMP
  //   JR
  //   SV
  //   LBU
  //   BGEZ
  //   OP
  //   Func
  //   Beq
  //   Bne
  //   MemToReg
  //   MemWrite
  //   AluOP
  //   AluSrcB
  //   RegWrite
  //   JAL
  //   RegDst
  //   Syscall
  //   可计数暂停的时钟源
  //   为方便自动评测，需要输出流水线各段保存的PC值，注意是PC不是PC+4，另外ID段寄存器写入信息，Mem段内存写入信息也要输出
endmodule

module \重定向流水线  (
  output RegWrite,
  output MemWrite,
  output [31:0] IF_PC,
  output [31:0] ID_PC,
  output [31:0] EX_PC,
  output [31:0] M_PC,
  output [31:0] WB_PC,
  output [31:0] RDin,
  output [31:0] MDin,
  output [31:0] LedData
);

  wire AluSrcB_EX, AluSrcB_ID, and_1_out, and_2_out, and_3_out, and_6_out, B_EX, BEQ_EX, BEQ_ID, BGEZ_EX,
       BGEZ_ID, BNE_EX, BNE_ID, CLK, clock_1_out, clock_2_out, comparator_1_eq, comparator_1_lt,
       comparator_2_eq, comparator_3_eq, comparator_4_eq, comparator_5_eq, d_ff_1_q, Equal, ERET_ID, Exit,
       Go, IF_STALL, IR1, IR2, IR3, JAL_EX, JAL_ID, JAL_MEM, JAL_WB, JMP_EX, JMP_ID, JR_EX, JR_ID, LBU_EX,
       LBU_ID, LBU_MEM, LBU_WB, MEM_STALL, MemToReg_EX, MemToReg_ID, MemToReg_MEM, MemToReg_WB, MemWrite_EX,
       MemWrite_ID, nand_1_out, not_1_out, not_2_out, or_1_out, or_2_out, Pause, RegDst_EX, RegDst_ID,
       RegDst_MEM, RegWrite_EX, RegWrite_ID, RegWrite_MEM, RST, SignedExt_EX, SignedExt_ID, SV_EX, SV_ID,
       Syscall_EX, Syscall_ID, W1, W2, W3, \寄存器使用情况_1_r1_used , \寄存器使用情况_1_r2_used ;
  wire [1:0] forwadr2_ID, forward1_EX, forward1_ID, forward2_EX, xor_1_out;
  wire [3:0] AluOP_EX, AluOP_ID;
  wire [4:0] multiplexer_2_out, R1__ID, R2__ID, RegWrite__EX, RegWrite__ID, RegWrite__MEM, RegWrite__WB,
       shamt;
  wire [5:0] Func;
  wire [7:0] multiplexer_13_out;
  wire [12:0] CNT_num;
  wire [15:0] \LoadUse次数 , \总周期数 , \插入气泡数 , \无条件分支数 , \条件分支成功数 ;
  wire [27:0] adder_2_out;
  wire [31:0] adder_3_out, adder_5_out, AluRes_EX, AluRes_MEM, AluRes_WB, bit_extender_1_out,
       bit_extender_2_out, bit_extender_3_out, EX_IR, EX_PC_imm, EX_PC_JR, IF_IR, imm_EX, imm_ID, MDin_EX,
       MEM_IR, multiplexer_1_out, multiplexer_8_out, multiplexer_10_out, multiplexer_12_out,
       multiplexer_14_out, PC_4, R1_EX_1, R1_ID, R2_EX, R2_EX_1, R2_ID, RDin_MEM, RDin_WB, shifter_1_out,
       WB_IR;
  wire [31:6] ID_IR;
  wire [31:28] EX_PC_J_JAL;

  Button \u_总复位  (.out(RST));
  Button _1 (.out(IR1));
  Button _2 (.out(IR2));
  Button _3 (.out(IR3));
  // Probe on \总周期数 
  // Probe on \总周期数 
  Button \u_继续运行  (.out(Go));
  LED #(.active("true")) led_1 (.in(W1));
  LED #(.active("true")) led_2 (.in(W2));
  LED #(.active("true")) led_3 (.in(W3));
  Hex_Digit_Display hex_digit_display_1 (.value(LedData[31:28]));  // open: dp
  // Probe on IF_PC[19:0]
  // Mips_Probe mips_probe_1: pin names not known; wires that end beside it: IF_IR
  Hex_Digit_Display hex_digit_display_2 (.value(LedData[27:24]));  // open: dp
  Hex_Digit_Display hex_digit_display_3 (.value(LedData[23:20]));  // open: dp
  // Probe on ID_PC[19:0]
  // Mips_Probe mips_probe_2: pin names not known; wires that end beside it: {ID_IR, Func}
  Hex_Digit_Display hex_digit_display_4 (.value(LedData[19:16]));  // open: dp
  Hex_Digit_Display hex_digit_display_5 (.value(LedData[15:12]));  // open: dp
  not not_1 (not_1_out, IF_STALL);
  Multiplexer #(.select(3), .width(32), .disabled("Z"), .enable("false")) multiplexer_1 (
    .in0(PC_4), .in1(EX_PC_imm), .in2({EX_PC_J_JAL, EX_IR[25:0], 2'b00}), .in6(EX_PC_JR),
    .out(multiplexer_1_out), .sel({JR_EX, JMP_EX, B_EX}));  // open: in3, in4, in5, in7
  Hex_Digit_Display hex_digit_display_6 (.value(LedData[11:8]));  // open: dp
  Hex_Digit_Display hex_digit_display_7 (.value(LedData[7:4]));  // open: dp
  Clock #(.highDuration(1), .lowDuration(1)) clock_1 (.out(clock_1_out));
  // Probe on EX_PC[19:0]
  // Mips_Probe mips_probe_3: pin names not known; wires that end beside it: clock_1_out, EX_IR, CLK
  Register #(.width(32), .trigger("rising"), .Select("low")) register_1 (
    .D(multiplexer_1_out), .en(not_1_out), .Q(IF_PC), .clk(CLK));  // open: clr
  // Probe on IF_PC
  Hex_Digit_Display hex_digit_display_8 (.value(LedData[3:0]));  // open: dp
  // Probe on IF_IR
  Adder #(.width(32)) adder_1 (.a(IF_PC), .b(32'h4), .out(PC_4));  // open: cin, cout
  // Probe on \总周期数 
  // Probe on M_PC[19:0]
  // Mips_Probe mips_probe_4: pin names not known; wires that end beside it: MEM_IR
  ROM #(.addrWidth(10), .dataWidth(32), .Select("high")) rom_1 (.addr(IF_PC[11:2]), .data(IF_IR));
  // Probe on \总周期数 
  // Probe on \无条件分支数 
  // Probe on \条件分支成功数 
  // Probe on \插入气泡数 
  // Probe on \LoadUse次数 
  // Mips_Probe mips_probe_5: pin names not known; wires that end beside it: IF_IR
  or or_1 (or_1_out, JMP_EX, B_EX);
  // Probe on IF_PC[11:0]
  // Probe on WB_PC[19:0]
  // Mips_Probe mips_probe_6: pin names not known; wires that end beside it: WB_IR
  \气泡流水线接口IF_ID  \u_气泡流水线接口if_id_1  (
    .IR_IN(IF_IR), .PC_IN(IF_PC), .CLK(CLK), .IR_OUT({ID_IR, Func}), .PC_OUT(ID_PC),
    .\同步清零_气泡_高电平有效 (or_1_out), .\使能端_低电平有效_stall_高电平有效 (IF_STALL));  // open: 传输状态In_表明当前传输数据有效, 传输状态Out_表明当前传输数据有效
  // Probe on ID_PC[11:0]
  // Probe on EX_PC[11:0]
  // Mips_Probe mips_probe_7: pin names not known; wires that end beside it: {ID_IR, Func}
  // Probe on M_PC[11:0]
  D_Flip_Flop #(.trigger("high"), .Pre_Clr_Positions("LEGACY"), .NegatePresetClear("false"), .enable("true"), .NewFFLayout("false")) d_ff_1 (.Q(d_ff_1_q));  // open: clk, D, Qn, preset, en, reset
  // Probe on 13'h343
  // Probe on WB_PC[11:0]
  Comparator #(.width(13), .mode("twosComplement")) comparator_1 (
    .a(CNT_num), .b(13'h343), .eq(comparator_1_eq), .lt(comparator_1_lt));  // open: gt
  Clock #(.highDuration(1), .lowDuration(1)) clock_2 (.out(clock_2_out));
  nand nand_1 (nand_1_out, d_ff_1_q, comparator_1_eq);
  Counter #(.width(13), .max('h1fff), .ongoal("stay"), .trigger("rising"), .behavior("old")) counter_1 (
    .count(comparator_1_lt), .Q(CNT_num), .clk(clock_2_out));  // open: load, D, carry, clr, preset
  \单周期硬布线控制器  \u_单周期硬布线控制器_1  (
    .Func(Func), .OP(ID_IR[31:26]), .ALU_OP(AluOP_ID), .MemToReg(MemToReg_ID), .MemWrite(MemWrite_ID),
    .ALU_SRC(AluSrcB_ID), .RegWrite(RegWrite_ID), .SysCALL(Syscall_ID), .SignedExt(SignedExt_ID),
    .RegDst(RegDst_ID), .JR(JR_ID), .JMP(JMP_ID), .Beq(BEQ_ID), .JAL(JAL_ID), .Bne(BNE_ID), .ERET(ERET_ID),
    .SV(SV_ID), .LBU(LBU_ID), .BGEZ(BGEZ_ID));
  Multiplexer #(.select(1), .width(5), .disabled("Z"), .enable("false")) multiplexer_2 (
    .in0(ID_IR[20:16]), .in1(ID_IR[15:11]), .out(multiplexer_2_out), .sel(RegDst_ID));
  Multiplexer #(.select(1), .width(5), .disabled("Z"), .enable("false")) multiplexer_3 (
    .in0(multiplexer_2_out), .in1({5{1'b1}}), .out(RegWrite__ID), .sel(JAL_ID));
  assign CLK = nand_1_out ? clock_2_out : 1'bz;  // Controlled_Buffer controlled_buffer_1
  \寄存器使用情况  \u_寄存器使用情况_1  (
    .OP0(ID_IR[26]), .OP1(ID_IR[27]), .OP2(ID_IR[28]), .OP3(ID_IR[29]), .OP4(ID_IR[30]), .OP5(ID_IR[31]),
    .F0(Func[0]), .F1(Func[1]), .F2(Func[2]), .F3(Func[3]), .F4(Func[4]), .F5(Func[5]),
    .R1_Used(\寄存器使用情况_1_r1_used ), .R2_Used(\寄存器使用情况_1_r2_used ));
  Pull_Resistor #(.pull(1)) pull_resistor_1 (.node(CLK));
  Forward forward_1 (
    .RegWrite__MEM(RegWrite__MEM), .RegWrite_MEM(RegWrite_MEM), .RegWrite__EX(RegWrite__EX),
    .RegWrite_EX(RegWrite_EX), .R1_Used(\寄存器使用情况_1_r1_used ), .R1_forward(forward1_ID),
    .R2_Used(\寄存器使用情况_1_r2_used ), .R2_forward(forwadr2_ID), .R1_num(R1__ID), .R2_num(R2__ID));
  \Load_Use相关  \load_use相关_1  (
    .RegWrite__EX(RegWrite__EX), .MemToReg_EX(MemToReg_EX), .R1_Used(\寄存器使用情况_1_r1_used ),
    .\Load_Usex相关 (IF_STALL), .R2_Used(\寄存器使用情况_1_r2_used ), .R1_num(R1__ID), .R2_num(R2__ID));
  Multiplexer #(.select(1), .width(5), .disabled("Z"), .enable("false")) multiplexer_4 (
    .in0(ID_IR[25:21]), .in1(5'b00010), .out(R1__ID), .sel(Syscall_ID));
  Multiplexer #(.select(1), .width(5), .disabled("Z"), .enable("false")) multiplexer_5 (
    .in0(ID_IR[20:16]), .in1(5'b00100), .out(R2__ID), .sel(Syscall_ID));
  Counter #(.width(16), .max('hffff), .ongoal("wrap"), .trigger("rising"), .behavior("new")) counter_2 (
    .count(IF_STALL), .Q(\LoadUse次数 ), .clk(CLK), .clr(RST));  // open: load, D, carry, preset, down
  // Probe on R1__ID
  // Probe on R2__ID
  // Probe on RegWrite__WB
  assign bit_extender_1_out = {{16{1'b0}}, {ID_IR[15:6], Func}};  // Bit_Extender bit_extender_1
  assign bit_extender_2_out = {{16{ID_IR[15]}}, {ID_IR[15:6], Func}};  // Bit_Extender bit_extender_2
  Multiplexer #(.select(1), .width(32), .disabled("Z"), .enable("false")) multiplexer_6 (
    .in0(bit_extender_1_out), .in1(bit_extender_2_out), .out(imm_ID), .sel(SignedExt_ID));
  \气泡regfile  \u_气泡regfile_1  (
    .Din(RDin), .Clk(CLK), .R1(R1_ID), .R2(R2_ID), .WE(RegWrite), .W_num(RegWrite__WB), .R1_num(R1__ID),
    .R2_num(R2__ID));
  or or_2 (or_2_out, JMP_EX, B_EX, IF_STALL);
  // Mips_Probe mips_probe_8: pin names not known; wires that end beside it: EX_IR
  \气泡流水线接口ID_EX  \u_气泡流水线接口id_ex_1  (
    .IR_IN({ID_IR, Func}), .PC_IN(ID_PC), .JMP_IN(JMP_ID), .Beq_IN(BEQ_ID), .JR_IN(JR_ID), .Bne_IN(BNE_ID),
    .SignedExt_IN(SignedExt_ID), .MemToReg_IN(MemToReg_ID), .MemWrite_IN(MemWrite_ID), .LBU_IN(LBU_ID),
    .AluOp_IN(AluOP_ID), .BGEZ_IN(BGEZ_ID), .AluSrcB_IN(AluSrcB_ID), .RegWrite_IN(RegWrite_ID),
    .JAL_IN(JAL_ID), .RegDst_IN(RegDst_ID), .Syscall_IN(Syscall_ID), .RegWrite__IN(RegWrite__ID),
    .R1Forward_IN(forward1_ID), .R2Forward_IN(forwadr2_ID), .R1_IN(R1_ID), .R2_IN(R2_ID), .Imm__IN(imm_ID),
    .CLK(CLK), .IR_OUT_2(EX_IR), .PC_OUT(EX_PC), .JMP_OUT(JMP_EX), .Beq_OUT(BEQ_EX), .JR_OUT(JR_EX),
    .Bne_OUT(BNE_EX), .SignedExt_OUT(SignedExt_EX), .MemToReg_OUT(MemToReg_EX), .MemWrite_OUT(MemWrite_EX),
    .LBU_OUT(LBU_EX), .AluOp_OUT(AluOP_EX), .BGEZ_OUT(BGEZ_EX), .AluSrcB_OUT(AluSrcB_EX),
    .RegWrite_OUT(RegWrite_EX), .JAL_OUT(JAL_EX), .RegDst_OUT(RegDst_EX), .Syscall_OUT(Syscall_EX),
    .RegWrite__OUT(RegWrite__EX), .R1Forward_OUT(forward1_EX), .R2Forward_OUT(forward2_EX), .R1_OUT(R1_EX_1),
    .R2_OUT(R2_EX_1), .Imm_OUT(imm_EX), .\同步清零_气泡_高电平有效 (or_2_out), .\使能端_低电平有效_stall_高电平有效 (1'b0),
    .SV_IN(SV_ID), .IR_OUT(SV_EX));  // open: ERET_IN, MFC0_IN, MTC0_IN, 传输状态In_表明当前传输数据有效, ERET_OUT, MFC0_OUT, MTC0_OUT, 传输状态Out_表明当前传输数据有效
  Counter #(.width(16), .max('hffff), .ongoal("wrap"), .trigger("rising"), .behavior("new")) counter_3 (
    .count(JMP_EX), .Q(\无条件分支数 ), .clk(CLK), .clr(RST));  // open: load, D, carry, preset, down
  Counter #(.width(16), .max('hffff), .ongoal("wrap"), .trigger("rising"), .behavior("new")) counter_4 (
    .count(B_EX), .Q(\条件分支成功数 ), .clk(CLK), .clr(RST));  // open: load, D, carry, preset, down
  Comparator #(.width(32), .mode("twosComplement")) comparator_2 (
    .a(32'ha), .b(EX_PC_JR), .eq(comparator_2_eq));  // open: gt, lt
  Comparator #(.width(32), .mode("twosComplement")) comparator_3 (
    .a(32'h32), .b(EX_PC_JR), .eq(comparator_3_eq));  // open: gt, lt
  Comparator #(.width(32), .mode("twosComplement")) comparator_4 (
    .a(32'h22), .b(EX_PC_JR), .eq(comparator_4_eq));  // open: gt, lt
  and and_1 (and_1_out, BGEZ_EX, comparator_5_eq);
  Comparator #(.width(32), .mode("twosComplement")) comparator_5 (
    .a(AluRes_EX), .b({32{1'b0}}), .eq(comparator_5_eq));  // open: gt, lt
  and and_2 (and_2_out, BEQ_EX, Equal);
  and and_3 (and_3_out, BNE_EX, not_2_out);
  not not_2 (not_2_out, Equal);
  Multiplexer #(.select(2), .width(32), .disabled("Z"), .enable("false")) multiplexer_7 (
    .in0(R2_EX_1), .in1(RDin), .in2(AluRes_MEM), .out(R2_EX), .sel(forward2_EX));  // open: in3
  and and_4 (Exit, Syscall_EX, comparator_2_eq);
  and and_5 (Pause, Syscall_EX, comparator_3_eq);
  and and_6 (and_6_out, Syscall_EX, comparator_4_eq);
  or or_3 (B_EX, and_1_out, and_2_out, and_3_out);
  Multiplexer #(.select(1), .width(32), .disabled("Z"), .enable("false")) multiplexer_8 (
    .in0(R2_EX), .in1(imm_EX), .out(multiplexer_8_out), .sel(AluSrcB_EX));
  Register #(.width(32), .trigger("rising"), .Select("low")) register_2 (
    .D(MDin_EX), .en(and_6_out), .Q(LedData), .clk(CLK));  // open: clr
  Counter #(.width(16), .max('hffff), .ongoal("wrap"), .trigger("rising"), .behavior("new")) counter_5 (
    .Q(\总周期数 ), .clk(CLK));  // open: load, D, count, carry, clr, preset, down
  Multiplexer #(.select(2), .width(32), .disabled("Z"), .enable("false")) multiplexer_9 (
    .in0(R1_EX_1), .in1(RDin), .in2(AluRes_MEM), .out(EX_PC_JR), .sel(forward1_EX));  // open: in3
  Multiplexer #(.select(1), .width(32), .disabled("Z"), .enable("false")) multiplexer_10 (
    .in0(multiplexer_8_out), .in1({32{1'b0}}), .out(multiplexer_10_out), .sel(BGEZ_EX));
  Adder #(.width(32)) adder_2 (.a(EX_PC), .b(32'h4), .out({EX_PC_J_JAL, adder_2_out}));  // open: cin, cout
  Shifter #(.width(32), .shift("ll")) shifter_1 (.in(imm_EX), .\dist (5'b00010), .out(shifter_1_out));
  Adder #(.width(32)) adder_3 (.a(32'h4), .b(EX_PC), .out(adder_3_out));  // open: cin, cout
  Adder #(.width(32)) adder_4 (.a(shifter_1_out), .b(adder_3_out), .out(EX_PC_imm));  // open: cin, cout
  MIPS_ALU mips_alu_1 (
    .X(EX_PC_JR), .Y(multiplexer_10_out), .AluOP(AluOP_EX), .Equal(Equal), .Result(AluRes_EX), .shamt(shamt));  // open: Result_2
  Multiplexer #(.select(1), .width(5), .disabled("Z"), .enable("false")) multiplexer_11 (
    .in0(EX_IR[10:6]), .in1(EX_PC_JR[4:0]), .out(shamt), .sel(SV_EX));
  // Mips_Probe mips_probe_9: pin names not known; wires that end beside it: MEM_IR
  \气泡流水线接口EX_MEM  \u_气泡流水线接口ex_mem_1  (
    .IR_IN(EX_IR), .PC_IN(EX_PC), .MemToReg_IN(MemToReg_EX), .MemWrite_IN(MemWrite_EX), .LBU_IN(LBU_EX),
    .RegWrite_IN(RegWrite_EX), .JAL_IN(JAL_EX), .RegDst_IN(RegDst_EX), .RegWrite__IN(RegWrite__EX),
    .AluRst_IN(AluRes_EX), .Mem_IN(R2_EX), .CLK(CLK), .IR_OUT(MEM_IR), .PC_OUT(M_PC),
    .MemToReg_OUT(MemToReg_MEM), .MemWrite_OUT(MemWrite), .LBU_OUT(LBU_MEM), .RegWrite_OUT(RegWrite_MEM),
    .JAL_OUT(JAL_MEM), .RegDst_OUT(RegDst_MEM), .RegWrite__OUT(RegWrite__MEM), .AluRst_OUT(AluRes_MEM),
    .Mem_OUT(MDin), .\使能端_低电平有效_stall_高电平有效 (MEM_STALL));  // open: ERET_IN, 传输状态In_表明当前传输数据有效, ERET_OUT, 传输状态Out_表明当前传输数据有效, 同步清零_气泡_高电平有效
  RAM #(.addrWidth(10), .dataWidth(32), .bus("separate"), .Select("high")) ram_1 (
    .addr(AluRes_MEM[11:2]), .din(MDin), .data(RDin_MEM), .str(MemWrite), .clk(CLK));  // open: sel, ld, clr
  // Mips_Probe mips_probe_10: pin names not known; wires that end beside it: WB_IR
  \气泡流水线MEM_WB  \u_气泡流水线mem_wb_1  (
    .IR_IN(MEM_IR), .PC_IN(M_PC), .MemToReg_IN(MemToReg_MEM), .LBU_IN(LBU_MEM), .RegWrite_IN(RegWrite_MEM),
    .JAL_IN(JAL_MEM), .RegDst_IN(RegDst_MEM), .RegWrite__IN(RegWrite__MEM), .Mem_IN(RDin_MEM),
    .AluRst_IN(AluRes_MEM), .CLK(CLK), .IR_OUT(WB_IR), .PC_OUT(WB_PC), .MemToReg_OUT(MemToReg_WB),
    .LBU_OUT(LBU_WB), .RegWrite_OUT(RegWrite), .JAL_OUT(JAL_WB), .RegWrite__OUT(RegWrite__WB),
    .Mem_OUT(RDin_WB), .AluRst_OUT(AluRes_WB), .\使能端_低电平有效_stall_高电平有效 (1'b0));  // open: ERET_IN, 传输状态In_表明当前传输数据有效, ERET_OUT, RegDst_OUT, 传输状态Out_表明当前传输数据有效, 同步清零_气泡_高电平有效
  Multiplexer #(.select(1), .width(32), .disabled("Z"), .enable("false")) multiplexer_12 (
    .in0(AluRes_WB), .in1(RDin_WB), .out(multiplexer_12_out), .sel(MemToReg_WB));
  assign xor_1_out = AluRes_WB[1:0] ^ 2'b11;  // XOR_Gate xor_1, 2 bits wide
  Multiplexer #(.select(2), .width(8), .disabled("Z"), .enable("false")) multiplexer_13 (
    .in0(multiplexer_12_out[7:0]), .in1(multiplexer_12_out[15:8]), .in2(multiplexer_12_out[23:16]),
    .in3(multiplexer_12_out[31:24]), .out(multiplexer_13_out), .sel(xor_1_out));
  Multiplexer #(.select(1), .width(32), .disabled("Z"), .enable("false")) multiplexer_14 (
    .in0(multiplexer_12_out), .in1(bit_extender_3_out), .out(multiplexer_14_out), .sel(LBU_WB));
  assign bit_extender_3_out = {{24{1'b0}}, multiplexer_13_out};  // Bit_Extender bit_extender_3
  Adder #(.width(32)) adder_5 (.a(WB_PC), .b(32'h4), .out(adder_5_out));  // open: cin, cout
  Multiplexer #(.select(1), .width(32), .disabled("Z"), .enable("false")) multiplexer_15 (
    .in0(multiplexer_14_out), .in1(adder_5_out), .out(RDin), .sel(JAL_WB));

  // Other names for the same wires on the sheet: BGEZ_RES[31:0] = AluRes_EX; EX_PC_J_JAL[27:2] = EX_IR[25:0];
  //   ID_IR[5:0] = Func; imm[15:0] = {ID_IR[15:6], Func}; rd[4:0] = ID_IR[15:11]; rt[4:0] = ID_IR[20:16];
  //   rs[4:0] = ID_IR[25:21]; OP[5:0] = ID_IR[31:26]; MDin_MEM[31:0] = MDin; MEM_PC[31:0] = M_PC;
  //   MemWrite_MEM = MemWrite; R1_EX[31:0] = EX_PC_JR; Vaddr_WB[31:0] = AluRes_WB; WB_RegWrite = RegWrite

  // Notes on the sheet:
  //   中断源
  //   时空图监测，可删除
  //   中断等待指示
  //   数码管输出
  //   指令存储器
  //   contents of rom_1 (hex, n*v repeats v):
  //   20110001 8000c05 20110001 20120002 20130003 8000c09 20110001 20120002 20130003 8000c0d 20110001
  //   20120002 20130003 8000c11 20110001 20120002 20130003 c000cb8 20100001 20110001 118fc0 112020
  //   20020022 c 118882 12200001 8000c15 112020 20020022 c 20110001 118880 112020 20020022 c 12200001
  //   8000c1f 20110001 118fc0 112020 20020022 c 1188c3 112020 20020022 c 118903 112020 20020022 c 118903
  //   112020 20020022 c 118903 112020 20020022 c 118903 112020 20020022 c 118903 112020 20020022 c 118903
  //   112020 20020022 c 118903 112020 20020022 c 20100001 109fc0 139fc3 8021 2012000c 24160003 26100001
  //   3210000f 20080008 20090001 139900 2709825 132020 20020022 c 1094022 1500fff9 22100001 2018000f
  //   2188024 108700 20080008 20090001 139902 2709825 132021 20020022 c 1094022 1500fff9 108702 2c9b022
  //   12c00001 8000c50 4020 1084027 84400 3508ffff 82021 20020022 c 2010ffff 20110000 ae300000 22100001
  //   22310004 ae300000 22100001 22310004 ae300000 22100001 22310004 ae300000 22100001 22310004 ae300000
  //   22100001 22310004 ae300000 22100001 22310004 ae300000 22100001 22310004 ae300000 22100001 22310004
  //   ae300000 22100001 22310004 ae300000 22100001 22310004 ae300000 22100001 22310004 ae300000 22100001
  //   22310004 ae300000 22100001 22310004 ae300000 22100001 22310004 ae300000 22100001 22310004 ae300000
  //   22100001 22310004 22100001 8020 2011003c 8e130000 8e340000 274402a 11000002 ae330000 ae140000
  //   2231fffc 1611fff8 102020 20020022 c 22100004 2011003c 1611fff2 20020032 c 20100000 22100001 102020
  //   20020022 c 22100002 102020 20020022 c 22100003 102020 20020022 c 22100004 102020 20020022 c 22100005
  //   102020 20020022 c 22100006 102020 20020022 c 22100007 102020 20020022 c 22100008 102020 20020022
  //   20020022 c 3e00008
  //   控制位
  //   OP
  //   Func
  //   rs
  //   rt
  //   流水调试日志用
  //   暂停节拍，不能为0
  //   戳工具置1进入计数暂停模式，ctrl+k时钟自动运行到对应节拍暂停
  //   ctrl+k关闭时钟连续运行，将控制位置零，进入单步调试模式调试
  //   SV
  //   LBU
  //   BGEZ
  //   Beq
  //   JMP
  //   Bne
  //   JR
  //   JAL
  //   OP
  //   Func
  //   Syscall
  //   可计数暂停的时钟源
  //   MemToReg
  //   MemWrite
  //   AluOP
  //   AluSrcB
  //   RegWrite
  //   RegDst
  //   为方便自动评测，需要输出流水线各段保存的PC值，注意是PC不是PC+4，另外ID段寄存器写入信息，Mem段内存写入信息也要输出
endmodule

module \Load_Use相关  (
  input  [4:0] R1_num,
  input  R1_Used,
  input  [4:0] RegWrite__EX,
  input  MemToReg_EX,
  input  [4:0] R2_num,
  input  R2_Used,
  output \Load_Usex相关 
);

  wire and_1_out, and_2_out, comparator_1_eq, comparator_2_eq, or_1_out, pull_resistor_1_node,
       pull_resistor_2_node;
  wire [4:0] controlled_buffer_1_out, controlled_buffer_2_out;

  Comparator #(.width(5), .mode("twosComplement")) comparator_1 (
    .a({5{1'b0}}), .b(R1_num), .eq(comparator_1_eq));  // open: gt, lt
  and and_1 (and_1_out, ~comparator_1_eq, R1_Used);  // AND_Gate
  assign controlled_buffer_1_out = and_1_out ? R1_num : 5'bz;  // Controlled_Buffer controlled_buffer_1
  Comparator #(.width(5), .mode("twosComplement")) comparator_2 (
    .a({5{1'b0}}), .b(R2_num), .eq(comparator_2_eq));  // open: gt, lt
  and and_2 (and_2_out, ~comparator_2_eq, R2_Used);  // AND_Gate
  assign controlled_buffer_2_out = and_2_out ? R2_num : 5'bz;  // Controlled_Buffer controlled_buffer_2
  Pull_Resistor #(.pull(0)) pull_resistor_1 (.node(pull_resistor_1_node));
  Comparator #(.width(5), .mode("twosComplement")) comparator_3 (
    .a(controlled_buffer_1_out), .b(RegWrite__EX), .eq(pull_resistor_1_node));  // open: gt, lt
  Pull_Resistor #(.pull(0)) pull_resistor_2 (.node(pull_resistor_2_node));
  Comparator #(.width(5), .mode("twosComplement")) comparator_4 (
    .a(RegWrite__EX), .b(controlled_buffer_2_out), .eq(pull_resistor_2_node));  // open: gt, lt
  or or_1 (or_1_out, pull_resistor_1_node, pull_resistor_2_node);
  and and_3 (\Load_Usex相关 , MemToReg_EX, or_1_out);
endmodule

module Forward (
  input  [4:0] R1_num,
  input  R1_Used,
  input  [4:0] RegWrite__MEM,
  input  RegWrite_MEM,
  input  [4:0] RegWrite__EX,
  input  RegWrite_EX,
  input  [4:0] R2_num,
  input  R2_Used,
  output [1:0] R1_forward,
  output [1:0] R2_forward
);

  wire and_1_out, and_2_out, and_3_out, and_4_out, and_5_out, and_6_out, comparator_1_eq, comparator_2_eq,
       pull_resistor_1_node, pull_resistor_2_node, pull_resistor_3_node, pull_resistor_4_node;
  wire [4:0] controlled_buffer_1_out, controlled_buffer_2_out;

  Comparator #(.width(5), .mode("twosComplement")) comparator_1 (
    .a({5{1'b0}}), .b(R1_num), .eq(comparator_1_eq));  // open: gt, lt
  and and_1 (and_1_out, ~comparator_1_eq, R1_Used);  // AND_Gate
  assign controlled_buffer_1_out = and_1_out ? R1_num : 5'bz;  // Controlled_Buffer controlled_buffer_1
  Comparator #(.width(5), .mode("twosComplement")) comparator_2 (
    .a({5{1'b0}}), .b(R2_num), .eq(comparator_2_eq));  // open: gt, lt
  and and_2 (and_2_out, ~comparator_2_eq, R2_Used);  // AND_Gate
  assign controlled_buffer_2_out = and_2_out ? R2_num : 5'bz;  // Controlled_Buffer controlled_buffer_2
  Pull_Resistor #(.pull(0)) pull_resistor_1 (.node(pull_resistor_1_node));
  Comparator #(.width(5), .mode("twosComplement")) comparator_3 (
    .a(controlled_buffer_1_out), .b(RegWrite__MEM), .eq(pull_resistor_1_node));  // open: gt, lt
  Pull_Resistor #(.pull(0)) pull_resistor_2 (.node(pull_resistor_2_node));
  Comparator #(.width(5), .mode("twosComplement")) comparator_4 (
    .a(controlled_buffer_1_out), .b(RegWrite__EX), .eq(pull_resistor_2_node));  // open: gt, lt
  Pull_Resistor #(.pull(0)) pull_resistor_3 (.node(pull_resistor_3_node));
  Comparator #(.width(5), .mode("twosComplement")) comparator_5 (
    .a(RegWrite__MEM), .b(controlled_buffer_2_out), .eq(pull_resistor_3_node));  // open: gt, lt
  Pull_Resistor #(.pull(0)) pull_resistor_4 (.node(pull_resistor_4_node));
  Comparator #(.width(5), .mode("twosComplement")) comparator_6 (
    .a(RegWrite__EX), .b(controlled_buffer_2_out), .eq(pull_resistor_4_node));  // open: gt, lt
  and and_3 (and_3_out, pull_resistor_1_node, RegWrite_MEM);
  and and_4 (and_4_out, pull_resistor_2_node, RegWrite_EX);
  and and_5 (and_5_out, pull_resistor_3_node, RegWrite_MEM);
  and and_6 (and_6_out, pull_resistor_4_node, RegWrite_EX);
  Priority_Encoder #(.select(2), .disabled("Z")) priority_encoder_1 (
    .in0(1'b1), .in1(and_3_out), .in2(and_4_out), .out(R1_forward));  // open: in3, gs, en_out, en_in
  Priority_Encoder #(.select(2), .disabled("Z")) priority_encoder_2 (
    .in0(1'b1), .in1(and_5_out), .in2(and_6_out), .out(R2_forward));  // open: in3, gs, en_out, en_in
endmodule

module \中断按键参考电路  (
  input  \同步清零信号 ,
  output \与中断屏蔽位与 
);

  wire \_1号中断_out , and_1_out, clock_1_out, d_ff_1_q, or_1_out, or_2_out;

  Clock #(.highDuration(1), .lowDuration(1)) clock_1 (.out(clock_1_out));
  Button \_1号中断  (.out(\_1号中断_out ));
  or or_1 (or_1_out, \与中断屏蔽位与 , d_ff_1_q);
  LED #(.active("true")) \_1号中断等待指示灯  (.in(or_1_out));
  D_Flip_Flop #(.trigger("rising"), .Pre_Clr_Positions("LEGACY"), .NegatePresetClear("false"), .enable("true"), .NewFFLayout("false")) d_ff_1 (
    .clk(\_1号中断_out ), .D(1'b1), .Q(d_ff_1_q), .reset(\与中断屏蔽位与 ));  // open: Qn, preset, en
  or or_2 (or_2_out, d_ff_1_q, \与中断屏蔽位与 );
  and and_1 (and_1_out, or_2_out, ~\同步清零信号 );  // AND_Gate
  D_Flip_Flop #(.trigger("rising"), .Pre_Clr_Positions("LEGACY"), .NegatePresetClear("false"), .enable("true"), .NewFFLayout("false")) IR1 (
    .clk(clock_1_out), .D(and_1_out), .Q(\与中断屏蔽位与 ));  // open: Qn, preset, en, reset

  // Notes on the sheet:
  //   中断信号采样参考电路
  //   Reset 
endmodule

module \单周期MIPS_单级中断  (
  input  IR1,
  input  IR2,
  input  IR3,
  output RegWrite,
  output MemWrite,
  output [31:0] PC,
  output [31:0] IR,
  output [31:0] RDin,
  output [31:0] MDin,
  output [31:0] LedData
);

  wire AluSrcB, and_1_out, and_2_out, and_3_out, Beq, Beq_Bne, Bne, CLK, clock_2_out, comparator_1_eq,
       comparator_2_eq, comparator_3_eq, comparator_4_eq, comparator_5_eq, comparator_6_eq, comparator_6_lt,
       d_ff_1_q, d_ff_2_qn, Equal, ERET, Go, Halt, IR1_t, IR2_t, IR3_t, IRA, IRB, IRC, JAL, JMP, JR, LED_EN,
       MemToReg, nand_1_out, not_1_out, not_2_out, not_3_out, not_4_out, not_5_out, or_1_out, or_2_out,
       RegDst, SignedExt, Syscall, W1, W2, W3, \中断请求 , \单周期mips_单级中断中断控制器_1_intr ;
  wire [1:0] register_2_q, \单周期mips_单级中断中断控制器_1_intnum ;
  wire [3:0] AluOP;
  wire [4:0] multiplexer_4_out, multiplexer_5_out, multiplexer_6_out, multiplexer_7_out;
  wire [12:0] CNT_num;
  wire [15:0] \总周期数 ;
  wire [31:0] bit_extender_1_out, bit_extender_2_out, EpcIn, EpcOut, mips_alu_1_result, multiplexer_1_out,
       multiplexer_3_out, multiplexer_10_out, multiplexer_11_out, PC_4, PC_imm, PC_IRQ, PC_JR, ram_1_data,
       shifter_1_out;

  Clock #(.highDuration(1), .lowDuration(1)) clock_1 ();  // open: out
  Button _1 ();  // open: out
  Button _2 ();  // open: out
  Button _3 ();  // open: out
  Button \u_继续运行  (.out(Go));
  LED #(.active("true")) led_1 (.in(W1));
  LED #(.active("true")) led_2 (.in(W2));
  LED #(.active("true")) led_3 (.in(W3));
  Hex_Digit_Display hex_digit_display_1 (.value(LedData[31:28]));  // open: dp
  Comparator #(.width(16), .mode("twosComplement")) comparator_1 (
    .a(16'h23b), .b(\总周期数 ), .eq(comparator_1_eq));  // open: gt, lt
  Comparator #(.width(16), .mode("twosComplement")) comparator_2 (
    .a(\总周期数 ), .b(16'h1), .eq(comparator_2_eq));  // open: gt, lt
  Comparator #(.width(16), .mode("twosComplement")) comparator_3 (
    .a(\总周期数 ), .b(16'h4), .eq(comparator_3_eq));  // open: gt, lt
  Comparator #(.width(16), .mode("twosComplement")) comparator_4 (
    .a(\总周期数 ), .b(16'h7), .eq(comparator_4_eq));  // open: gt, lt
  Hex_Digit_Display hex_digit_display_2 (.value(LedData[23:20]));  // open: dp
  Hex_Digit_Display hex_digit_display_3 (.value(LedData[27:24]));  // open: dp
  or or_1 (or_1_out, comparator_1_eq, comparator_2_eq);
  assign IRA = or_1_out ? ~CLK : 1'bz;  // Controlled_Inverter controlled_inverter_1
  assign IRB = comparator_3_eq ? ~CLK : 1'bz;  // Controlled_Inverter controlled_inverter_2
  assign IRC = comparator_4_eq ? ~CLK : 1'bz;  // Controlled_Inverter controlled_inverter_3
  \单周期MIPS_单级中断硬布线控制器  \u_单周期mips_单级中断硬布线控制器_1  (
    .OP(IR[31:26]), .Func(IR[5:0]), .ALU_OP(AluOP), .MemToReg(MemToReg), .MemWrite(MemWrite),
    .ALU_SRC(AluSrcB), .RegWrite(RegWrite), .SysCALL(Syscall), .SignedExt(SignedExt), .RegDst(RegDst),
    .Beq(Beq), .Bne(Bne), .JR(JR), .JMP(JMP), .JAL(JAL), .ERET(ERET));
  Multiplexer #(.select(3), .width(32), .disabled("Z"), .enable("false")) multiplexer_1 (
    .in0(PC_4), .in1(PC_imm), .in2({PC_4[31:28], IR[25:0], 2'b00}), .in6(PC_JR), .out(multiplexer_1_out),
    .sel({JR, JMP, Beq_Bne}));  // open: in3, in4, in5, in7
  Multiplexer #(.select(1), .width(32), .disabled("Z"), .enable("false")) multiplexer_2 (
    .in0(multiplexer_1_out), .in1(EpcOut), .out(EpcIn), .sel(ERET));
  Hex_Digit_Display hex_digit_display_4 (.value(LedData[15:12]));  // open: dp
  Hex_Digit_Display hex_digit_display_5 (.value(LedData[19:16]));  // open: dp
  Pull_Resistor #(.pull(0)) pull_resistor_1 (.node(IRA));
  Pull_Resistor #(.pull(0)) pull_resistor_2 (.node(IRB));
  Pull_Resistor #(.pull(0)) pull_resistor_3 (.node(IRC));
  Multiplexer #(.select(1), .width(32), .disabled("Z"), .enable("false")) multiplexer_3 (
    .in0(EpcIn), .in1(PC_IRQ), .out(multiplexer_3_out), .sel(\中断请求 ));
  or or_2 (or_2_out, not_1_out, Go);
  not not_1 (not_1_out, Halt);
  Hex_Digit_Display hex_digit_display_6 (.value(LedData[11:8]));  // open: dp
  Hex_Digit_Display hex_digit_display_7 (.value(LedData[7:4]));  // open: dp
  // Probe on \总周期数 
  Register #(.width(32), .trigger("rising"), .Select("low")) u_PC (
    .D(multiplexer_3_out), .en(or_2_out), .Q(PC), .clk(CLK));  // open: clr
  // Probe on PC
  Hex_Digit_Display hex_digit_display_8 (.value(LedData[3:0]));  // open: dp
  // Probe on IR
  or or_3 (IR1_t, IR1, IRA);
  Register #(.width(32), .trigger("rising"), .Select("low")) register_1 (
    .D(MDin), .en(LED_EN), .Q(LedData), .clk(CLK));  // open: clr
  Adder #(.width(32)) adder_1 (.a(PC), .b(32'h4), .out(PC_4));  // open: cin, cout
  // Probe on PC_imm
  // Mips_Probe mips_probe_1: pin names not known; wires that end beside it: IR
  ROM #(.addrWidth(10), .dataWidth(32), .Select("high")) rom_1 (.addr(PC[11:2]), .data(IR));
  or or_4 (IR2_t, IR2, IRB);
  not not_2 (not_2_out, Halt);
  Counter #(.width(16), .max('hffff), .ongoal("wrap"), .trigger("rising"), .behavior("new")) counter_1 (
    .count(not_2_out), .Q(\总周期数 ), .clk(CLK));  // open: load, D, carry, clr, preset, down
  // Probe on PC_JR
  or or_5 (IR3_t, IR3, IRC);
  Multiplexer #(.select(1), .width(5), .disabled("Z"), .enable("false")) multiplexer_4 (
    .in0(IR[25:21]), .in1(5'b00010), .out(multiplexer_4_out), .sel(Syscall));
  Multiplexer #(.select(1), .width(5), .disabled("Z"), .enable("false")) multiplexer_5 (
    .in0(IR[20:16]), .in1(5'b00100), .out(multiplexer_5_out), .sel(Syscall));
  Multiplexer #(.select(1), .width(5), .disabled("Z"), .enable("false")) multiplexer_6 (
    .in0(IR[20:16]), .in1(IR[15:11]), .out(multiplexer_6_out), .sel(RegDst));
  Multiplexer #(.select(1), .width(5), .disabled("Z"), .enable("false")) multiplexer_7 (
    .in0(multiplexer_6_out), .in1({5{1'b1}}), .out(multiplexer_7_out), .sel(JAL));
  not not_3 (not_3_out, Equal);
  // Probe on multiplexer_4_out
  // Probe on multiplexer_5_out
  // Probe on multiplexer_7_out
  Multiplexer #(.select(1), .width(32), .disabled("Z"), .enable("false")) multiplexer_8 (
    .in0(multiplexer_11_out), .in1(PC_4), .out(RDin), .sel(JAL));
  and and_1 (and_1_out, Beq, Equal);
  and and_2 (and_2_out, Bne, not_3_out);
  MIPS_Regifile mips_regifile_1 (
    .Din(RDin), .Clk(CLK), .R1(PC_JR), .R2(MDin), .WE(RegWrite), .W_num(multiplexer_7_out),
    .R1_num(multiplexer_4_out), .R2_num(multiplexer_5_out));
  or or_6 (Beq_Bne, and_1_out, and_2_out);
  assign bit_extender_1_out = {{16{1'b0}}, IR[15:0]};  // Bit_Extender bit_extender_1
  assign bit_extender_2_out = {{16{IR[15]}}, IR[15:0]};  // Bit_Extender bit_extender_2
  Multiplexer #(.select(2), .width(32), .disabled("Z"), .enable("false")) multiplexer_9 (
    .in1(32'h30ac), .in2(32'h3150), .in3(32'h31f4), .out(PC_IRQ), .sel(\单周期mips_单级中断中断控制器_1_intnum ));  // open: in0
  Register #(.width(2), .trigger("rising"), .Select("low")) register_2 (
    .D(\单周期mips_单级中断中断控制器_1_intnum ), .en(\中断请求 ), .Q(register_2_q), .clk(CLK));  // open: clr
  Multiplexer #(.select(2), .width(32), .disabled("Z"), .enable("false")) multiplexer_10 (
    .in0(MDin), .in1(MDin), .in2(bit_extender_1_out), .in3(bit_extender_2_out), .out(multiplexer_10_out),
    .sel({AluSrcB, SignedExt}));
  Shifter #(.width(32), .shift("ll")) shifter_1 (.in(bit_extender_2_out), .\dist (5'b00010), .out(shifter_1_out));
  Comparator #(.width(32), .mode("twosComplement")) comparator_5 (
    .a(PC_JR), .b(32'h22), .eq(comparator_5_eq));  // open: gt, lt
  \单周期MIPS_单级中断中断控制器  \u_单周期mips_单级中断中断控制器_1  (
    .CLK(CLK), .IR1(IR1_t), .IR2(IR2_t), .IR3(IR3_t), .Clr(ERET), .TEST(register_2_q), .IR1W(W1), .IR2W(W2),
    .IR3W(W3), .IntNum(\单周期mips_单级中断中断控制器_1_intnum ), .IntR(\单周期mips_单级中断中断控制器_1_intr ));
  not not_4 (not_4_out, ERET);
  Adder #(.width(32)) adder_2 (.a(shifter_1_out), .b(PC_4), .out(PC_imm));  // open: cin, cout
  D_Flip_Flop #(.trigger("high"), .Pre_Clr_Positions("LEGACY"), .NegatePresetClear("false"), .enable("true"), .NewFFLayout("false")) d_ff_1 (.Q(d_ff_1_q));  // open: clk, D, Qn, preset, en, reset
  // Probe on 13'hbb
  not not_5 (not_5_out, comparator_5_eq);
  D_Flip_Flop #(.trigger("rising"), .Pre_Clr_Positions("LEGACY"), .NegatePresetClear("false"), .enable("true"), .NewFFLayout("false")) d_ff_2 (
    .clk(CLK), .D(and_3_out), .Qn(d_ff_2_qn));  // open: Q, preset, en, reset
  and and_3 (and_3_out, \单周期mips_单级中断中断控制器_1_intr , not_4_out);
  MIPS_ALU mips_alu_1 (
    .X(PC_JR), .Y(multiplexer_10_out), .AluOP(AluOP), .Equal(Equal), .Result(mips_alu_1_result),
    .shamt(IR[10:6]));  // open: Result_2
  Clock #(.highDuration(1), .lowDuration(1)) clock_2 (.out(clock_2_out));
  and and_4 (LED_EN, Syscall, comparator_5_eq);
  and and_5 (Halt, Syscall, not_5_out);
  Register #(.width(32), .trigger("rising"), .Select("low")) EPC (
    .D(EpcIn), .en(\中断请求 ), .Q(EpcOut), .clk(CLK));  // open: clr
  and and_6 (\中断请求 , d_ff_2_qn, \单周期mips_单级中断中断控制器_1_intr );
  Comparator #(.width(13), .mode("twosComplement")) comparator_6 (
    .a(CNT_num), .b(13'hbb), .eq(comparator_6_eq), .lt(comparator_6_lt));  // open: gt
  RAM #(.addrWidth(10), .dataWidth(32), .bus("separate"), .Select("high")) ram_1 (
    .addr(mips_alu_1_result[11:2]), .din(MDin), .data(ram_1_data), .str(MemWrite), .clk(CLK));  // open: sel, ld, clr
  nand nand_1 (nand_1_out, d_ff_1_q, comparator_6_eq);
  Counter #(.width(13), .max('h1fff), .ongoal("stay"), .trigger("rising"), .behavior("old")) counter_2 (
    .count(comparator_6_lt), .Q(CNT_num), .clk(clock_2_out));  // open: load, D, carry, clr, preset
  Multiplexer #(.select(1), .width(32), .disabled("Z"), .enable("false")) multiplexer_11 (
    .in0(mips_alu_1_result), .in1(ram_1_data), .out(multiplexer_11_out), .sel(MemToReg));
  assign CLK = nand_1_out ? clock_2_out : 1'bz;  // Controlled_Buffer controlled_buffer_1
  Pull_Resistor #(.pull(1)) pull_resistor_4 (.node(CLK));

  // Other names for the same wires on the sheet: a0[31:0] = MDin; OP[5:0] = IR[31:26];
  //   PC_J_JAL[31:2] = {PC_4[31:28], IR[25:0]}; addr[25:0] = IR[25:0]; Func[5:0] = IR[5:0]; imm[15:0] = IR[15:0];
  //   shamt[4:0] = IR[10:6]; rd[4:0] = IR[15:11]; rt[4:0] = IR[20:16]; rs[4:0] = IR[25:21]; v0[31:0] = PC_JR

  // Notes on the sheet:
  //   中断源
  //   中断等待指示
  //   总复位信号应将除ROM以外所有存储组件全部清零
  //   单级中断测试信号模拟器
  //   JMP
  //   JR
  //   OP
  //   Func
  //   Syscall
  //   数码管输出
  //   数码管输出应该用寄存器锁存，否则显示数据只能一闪而过
  //   无跳转时PC的值
  //   Beq或Bne时PC的值
  //   指令存储器
  //   OP
  //   rs
  //   指令字
  //   contents of rom_1 (hex, n*v repeats v):
  //   201d07d0 20100001 109fc0 139fc3 8021 2012000c 24160008 26100001 3210000f 20080008 20090001 139900
  //   2709825 132020 20020022 c 1094022 1500fff9 22100001 2018000f 2188024 108700 20080008 20090001 139902
  //   2709825 132021 20020022 c 1094022 1500fff9 108702 2c9b022 12c00001 8000c07 4020 1084027 84400
  //   3508ffff 82021 20020022 c 8000c01 afa20000 23bd0004 afa40000 23bd0004 afb00000 23bd0004 afb30000
  //   23bd0004 afb40000 23bd0004 afb50000 23bd0004 afb60000 23bd0004 20160001 20140003 20150001 168020
  //   108100 2149825 132020 20020022 c 1600fffa 295a022 1680fff7 23bdfffc 8fb60000 23bdfffc 8fb50000
  //   23bdfffc 8fb40000 23bdfffc 8fb30000 23bdfffc 8fb00000 23bdfffc 8fa40000 23bdfffc 8fa20000 42000018
  //   afa20000 23bd0004 afa40000 23bd0004 afb00000 23bd0004 afb30000 23bd0004 afb40000 23bd0004 afb50000
  //   23bd0004 afb60000 23bd0004 20160002 20140003 20150001 168020 108100 2149825 132020 20020022 c
  //   1600fffa 295a022 1680fff7 23bdfffc 8fb60000 23bdfffc 8fb50000 23bdfffc 8fb40000 23bdfffc 8fb30000
  //   23bdfffc 8fb00000 23bdfffc 8fa40000 23bdfffc 8fa20000 42000018 afa20000 23bd0004 afa40000 23bd0004
  //   afb00000 23bd0004 afb30000 23bd0004 afb40000 23bd0004 afb50000 23bd0004 afb60000 23bd0004 20160003
  //   20140003 20150001 168020 108100 2149825 132020 20020022 c 1600fffa 295a022 1680fff7 23bdfffc
  //   8fb60000 23bdfffc 8fb50000 23bdfffc 8fb40000 23bdfffc 8fb30000 23bdfffc 8fb00000 23bdfffc 8fa40000
  //   23bdfffc 8fa20000 42000018
  //   rt
  //   rd
  //   Func
  //   J或JAL指令时PC的值
  //   jr指令时PC的值
  //   为方便自动评测，需要输出PC，IR，寄存器堆写如数据RDin
  //   RAM写使能MemWrite、RAM写入数据MDin等信号
  //   控制位
  //   暂停节拍，不能为0
  //   戳工具置1进入计数暂停模式，ctrl+k时钟自动运行到对应节拍暂停
  //   ctrl+k关闭时钟连续运行，将控制位置零，进入单步调试模式调试
  //   用这个时钟源需要去掉电路中的其他时钟源
  //   可计数暂停的时钟源
endmodule

// 中断控制器
module \单周期MIPS_单级中断中断控制器  (
  input  CLK,
  input  IR1,
  input  IR2,
  input  IR3,
  input  Clr,
  input  [1:0] TEST,
  output IR1W,
  output IR2W,
  output IR3W,
  output [1:0] IntNum,
  output IntR
);

  wire and_1_out, and_2_out, and_3_out, Clr0, Clr1, Clr2, Clr3, d_ff_1_q, d_ff_2_q, d_ff_3_q, INT1, INT2,
       INT3, not_1_out, not_2_out, not_3_out, or_1_out, or_2_out, or_3_out;

  D_Flip_Flop #(.trigger("rising"), .Pre_Clr_Positions("LEGACY"), .NegatePresetClear("false"), .enable("true"), .NewFFLayout("false")) d_ff_1 (
    .clk(IR1), .D(1'b1), .Q(d_ff_1_q), .reset(INT1));  // open: Qn, preset, en
  D_Flip_Flop #(.trigger("rising"), .Pre_Clr_Positions("LEGACY"), .NegatePresetClear("false"), .enable("true"), .NewFFLayout("false")) d_ff_2 (
    .clk(IR2), .D(1'b1), .Q(d_ff_2_q), .reset(INT2));  // open: Qn, preset, en
  D_Flip_Flop #(.trigger("rising"), .Pre_Clr_Positions("LEGACY"), .NegatePresetClear("false"), .enable("true"), .NewFFLayout("false")) d_ff_3 (
    .clk(IR3), .D(1'b1), .Q(d_ff_3_q), .reset(INT3));  // open: Qn, preset, en
  or or_1 (or_1_out, d_ff_1_q, INT1);
  or or_2 (or_2_out, d_ff_2_q, INT2);
  or or_3 (or_3_out, d_ff_3_q, INT3);
  and and_1 (and_1_out, or_1_out, not_1_out);
  not not_1 (not_1_out, Clr1);
  and and_2 (and_2_out, or_2_out, not_2_out);
  not not_2 (not_2_out, Clr2);
  and and_3 (and_3_out, or_3_out, not_3_out);
  not not_3 (not_3_out, Clr3);
  D_Flip_Flop #(.trigger("rising"), .Pre_Clr_Positions("LEGACY"), .NegatePresetClear("false"), .enable("true"), .NewFFLayout("false")) d_ff_4 (
    .clk(CLK), .D(and_1_out), .Q(INT1));  // open: Qn, preset, en, reset
  D_Flip_Flop #(.trigger("rising"), .Pre_Clr_Positions("LEGACY"), .NegatePresetClear("false"), .enable("true"), .NewFFLayout("false")) d_ff_5 (
    .clk(CLK), .D(and_2_out), .Q(INT2));  // open: Qn, preset, en, reset
  D_Flip_Flop #(.trigger("rising"), .Pre_Clr_Positions("LEGACY"), .NegatePresetClear("false"), .enable("true"), .NewFFLayout("false")) d_ff_6 (
    .clk(CLK), .D(and_3_out), .Q(INT3));  // open: Qn, preset, en, reset
  or or_4 (IR1W, INT1, d_ff_1_q);
  or or_5 (IR2W, INT2, d_ff_2_q);
  or or_6 (IR3W, INT3, d_ff_3_q);
  Decoder #(.select(2), .tristate("false"), .disabled(0), .enable("true")) decoder_1 (
    .out0(Clr0), .out1(Clr1), .out2(Clr2), .out3(Clr3), .sel(TEST), .en(Clr));
  Priority_Encoder #(.select(2), .disabled("Z")) priority_encoder_1 (
    .in1(INT1), .in2(INT2), .in3(INT3), .out(IntNum), .gs(IntR));  // open: in0, en_out, en_in

  // Other names for the same wires on the sheet: ClrIntNum[1:0] = TEST
endmodule

// 单周期硬布线控制器
module \单周期MIPS_单级中断硬布线控制器  (
  input  [5:0] OP,
  input  [5:0] Func,
  output [3:0] ALU_OP,
  output MemToReg,
  output MemWrite,
  output ALU_SRC,
  output RegWrite,
  output SysCALL,
  output SignedExt,
  output RegDst,
  output Beq,
  output Bne,
  output JR,
  output JMP,
  output JAL,
  output ERET
);

  \单周期MIPS_单级中断运算器自动生成  \u_单周期mips_单级中断运算器自动生成_1  (
    .OP0(OP[0]), .OP1(OP[1]), .OP2(OP[2]), .OP3(OP[3]), .OP4(OP[4]), .OP5(OP[5]), .F0(Func[0]), .F1(Func[1]),
    .F2(Func[2]), .F3(Func[3]), .F4(Func[4]), .F5(Func[5]), .S0(ALU_OP[0]), .S1(ALU_OP[1]), .S2(ALU_OP[2]),
    .S3(ALU_OP[3]));
  \单周期MIPS_单级中断控制信号自动生成  \u_单周期mips_单级中断控制信号自动生成_1  (
    .OP0(OP[0]), .OP1(OP[1]), .OP2(OP[2]), .OP3(OP[3]), .OP4(OP[4]), .OP5(OP[5]), .F0(Func[0]), .F1(Func[1]),
    .F2(Func[2]), .F3(Func[3]), .F4(Func[4]), .F5(Func[5]), .MemToReg(MemToReg), .MemWrite(MemWrite),
    .ALU_SRC(ALU_SRC), .RegWrite(RegWrite), .SysCALL(SysCALL), .SignedExt(SignedExt), .RegDst(RegDst),
    .BEQ(Beq), .BNE(Bne), .JR(JR), .JUMP(JMP), .JAL(JAL), .ERET(ERET));

  // Other names for the same wires on the sheet: OP_CODE[5:0] = OP

  // Notes on the sheet:
  //   运算器控制器，根据指令生成运算器功能选择信号
  //   控制信号生成，产生数据通路需要的其他控制信号
endmodule
// 运算器自动生成
module \单周期MIPS_单级中断运算器自动生成  (
  input  OP0,
  input  OP1,
  input  OP2,
  input  OP3,
  input  OP4,
  input  OP5,
  input  F0,
  input  F1,
  input  F2,
  input  F3,
  input  F4,
  input  F5,
  output S0,
  output S1,
  output S2,
  output S3
);

  wire and_1_out, and_2_out, and_3_out, and_4_out, and_5_out, and_6_out, and_7_out, and_8_out, and_9_out,
       and_10_out, and_11_out, and_12_out, and_13_out, and_14_out, and_15_out, and_16_out, and_17_out,
       and_18_out, and_19_out, and_20_out, and_21_out, and_22_out, and_23_out, and_24_out, and_25_out,
       and_26_out, and_27_out, and_28_out, and_29_out, and_30_out, and_31_out, and_32_out, and_33_out,
       and_34_out, not_1_out, not_2_out, not_3_out, not_4_out, not_5_out, not_6_out, not_7_out, not_8_out,
       not_9_out, not_10_out, not_11_out, not_12_out, not_13_out, not_14_out, not_15_out, not_16_out,
       not_17_out, not_18_out, not_19_out, not_20_out, not_21_out, not_22_out, not_23_out, not_24_out,
       not_25_out, not_26_out, not_27_out, not_28_out, not_29_out, not_30_out, not_31_out, not_32_out,
       not_33_out, not_34_out, not_35_out, not_36_out, not_37_out, not_38_out, not_39_out, not_40_out,
       not_41_out, not_42_out, not_43_out, not_44_out, not_45_out, not_46_out, not_47_out, not_48_out,
       not_49_out, not_50_out, not_51_out, not_52_out, not_53_out, not_54_out, not_55_out, not_56_out,
       not_57_out, not_58_out, not_59_out, not_60_out, not_61_out, not_62_out, not_63_out, not_64_out,
       not_65_out, not_66_out, not_67_out, not_68_out, not_69_out, not_70_out, not_71_out, not_72_out,
       not_73_out, not_74_out, not_75_out, not_76_out, not_77_out, not_78_out, not_79_out, not_80_out,
       not_81_out, not_82_out, not_83_out, not_84_out, not_85_out, not_86_out, not_87_out, not_88_out,
       not_89_out, not_90_out, not_91_out, not_92_out, not_93_out, not_94_out, not_95_out, not_96_out,
       not_97_out, not_98_out, not_99_out, not_100_out, not_101_out, not_102_out, not_103_out, not_104_out,
       not_105_out, not_106_out, not_107_out, not_108_out, not_109_out, not_110_out, not_111_out,
       not_112_out, not_113_out, not_114_out, not_115_out, not_116_out, not_117_out, not_118_out,
       not_119_out, not_120_out, not_121_out, not_122_out, not_123_out, not_124_out, not_125_out,
       not_126_out, not_127_out, not_128_out, not_129_out, not_130_out, not_131_out, not_132_out,
       not_133_out, not_134_out, not_135_out, not_136_out, not_137_out, not_138_out, not_139_out,
       not_140_out, not_141_out, not_142_out, not_143_out, not_144_out, not_145_out, not_146_out,
       not_147_out, not_148_out, not_149_out, not_150_out, not_151_out, not_152_out, not_153_out,
       not_154_out, not_155_out, not_156_out, not_157_out, not_158_out, not_159_out, not_160_out,
       not_161_out, not_162_out, not_163_out, not_164_out, not_165_out, not_166_out, not_167_out,
       not_168_out, not_169_out, not_170_out, not_171_out, not_172_out, not_173_out, not_174_out,
       not_175_out, not_176_out, not_177_out, not_178_out, not_179_out, not_180_out, not_181_out,
       not_182_out, not_183_out, not_184_out, not_185_out, not_186_out, not_187_out, not_188_out,
       not_189_out, not_190_out, not_191_out, not_192_out, not_193_out, not_194_out, not_195_out,
       not_196_out, not_197_out, not_198_out, not_199_out, not_200_out, not_201_out, not_202_out,
       not_203_out, not_204_out, not_205_out, not_206_out, not_207_out, not_208_out, not_209_out,
       not_210_out, not_211_out, not_212_out, not_213_out, not_214_out, not_215_out, not_216_out,
       not_217_out, not_218_out, not_219_out, not_220_out, not_221_out, not_222_out, not_223_out,
       not_224_out, not_225_out, not_226_out, not_227_out, not_228_out, not_229_out, not_230_out,
       not_231_out, not_232_out, not_233_out, not_234_out, not_235_out, not_236_out;

  not not_1 (not_1_out, OP5);
  not not_2 (not_2_out, OP4);
  not not_3 (not_3_out, OP3);
  not not_4 (not_4_out, OP2);
  not not_5 (not_5_out, OP1);
  not not_6 (not_6_out, OP0);
  not not_7 (not_7_out, F5);
  not not_8 (not_8_out, F4);
  not not_9 (not_9_out, F3);
  not not_10 (not_10_out, F2);
  not not_11 (not_11_out, OP5);
  not not_12 (not_12_out, OP4);
  not not_13 (not_13_out, OP3);
  not not_14 (not_14_out, OP2);
  not not_15 (not_15_out, OP1);
  not not_16 (not_16_out, OP0);
  not not_17 (not_17_out, F4);
  not not_18 (not_18_out, F3);
  not not_19 (not_19_out, F2);
  not not_20 (not_20_out, F1);
  not not_21 (not_21_out, F0);
  not not_22 (not_22_out, OP5);
  not not_23 (not_23_out, OP4);
  not not_24 (not_24_out, OP3);
  not not_25 (not_25_out, OP2);
  not not_26 (not_26_out, OP1);
  not not_27 (not_27_out, OP0);
  not not_28 (not_28_out, F4);
  not not_29 (not_29_out, F3);
  not not_30 (not_30_out, F2);
  not not_31 (not_31_out, F1);
  not not_32 (not_32_out, OP5);
  not not_33 (not_33_out, OP4);
  not not_34 (not_34_out, OP3);
  not not_35 (not_35_out, OP2);
  not not_36 (not_36_out, OP1);
  not not_37 (not_37_out, OP0);
  not not_38 (not_38_out, F4);
  not not_39 (not_39_out, F3);
  not not_40 (not_40_out, F1);
  not not_41 (not_41_out, F0);
  not not_42 (not_42_out, OP5);
  not not_43 (not_43_out, OP4);
  not not_44 (not_44_out, OP3);
  not not_45 (not_45_out, OP2);
  not not_46 (not_46_out, OP1);
  not not_47 (not_47_out, OP0);
  not not_48 (not_48_out, F4);
  not not_49 (not_49_out, F2);
  not not_50 (not_50_out, F0);
  not not_51 (not_51_out, OP5);
  not not_52 (not_52_out, OP4);
  not not_53 (not_53_out, OP2);
  not not_54 (not_54_out, OP1);
  not not_55 (not_55_out, OP0);
  not not_56 (not_56_out, OP5);
  not not_57 (not_57_out, OP4);
  not not_58 (not_58_out, OP1);
  not not_59 (not_59_out, OP0);
  not not_60 (not_60_out, OP5);
  not not_61 (not_61_out, OP4);
  not not_62 (not_62_out, OP2);
  not not_63 (not_63_out, OP1);
  not not_64 (not_64_out, OP5);
  not not_65 (not_65_out, OP4);
  not not_66 (not_66_out, OP2);
  not not_67 (not_67_out, OP0);
  not not_68 (not_68_out, OP4);
  not not_69 (not_69_out, OP3);
  not not_70 (not_70_out, OP2);
  not not_71 (not_71_out, OP4);
  not not_72 (not_72_out, OP2);
  not not_73 (not_73_out, OP5);
  not not_74 (not_74_out, OP4);
  not not_75 (not_75_out, OP3);
  not not_76 (not_76_out, OP2);
  not not_77 (not_77_out, OP1);
  not not_78 (not_78_out, OP0);
  not not_79 (not_79_out, F5);
  not not_80 (not_80_out, F4);
  not not_81 (not_81_out, F3);
  not not_82 (not_82_out, F2);
  not not_83 (not_83_out, F0);
  not not_84 (not_84_out, OP5);
  not not_85 (not_85_out, OP4);
  not not_86 (not_86_out, OP3);
  not not_87 (not_87_out, OP2);
  not not_88 (not_88_out, OP1);
  not not_89 (not_89_out, OP0);
  not not_90 (not_90_out, F4);
  not not_91 (not_91_out, F3);
  not not_92 (not_92_out, F2);
  not not_93 (not_93_out, F0);
  not not_94 (not_94_out, OP5);
  not not_95 (not_95_out, OP4);
  not not_96 (not_96_out, OP3);
  not not_97 (not_97_out, OP2);
  not not_98 (not_98_out, OP1);
  not not_99 (not_99_out, OP0);
  not not_100 (not_100_out, F4);
  not not_101 (not_101_out, F3);
  not not_102 (not_102_out, F1);
  not not_103 (not_103_out, F0);
  not not_104 (not_104_out, OP5);
  not not_105 (not_105_out, OP4);
  not not_106 (not_106_out, OP3);
  not not_107 (not_107_out, OP2);
  not not_108 (not_108_out, OP1);
  not not_109 (not_109_out, OP0);
  not not_110 (not_110_out, F4);
  not not_111 (not_111_out, F3);
  not not_112 (not_112_out, OP5);
  not not_113 (not_113_out, OP4);
  not not_114 (not_114_out, OP3);
  not not_115 (not_115_out, OP2);
  not not_116 (not_116_out, OP1);
  not not_117 (not_117_out, OP0);
  not not_118 (not_118_out, F4);
  not not_119 (not_119_out, F2);
  not not_120 (not_120_out, F0);
  not not_121 (not_121_out, OP5);
  not not_122 (not_122_out, OP4);
  not not_123 (not_123_out, OP1);
  not not_124 (not_124_out, OP0);
  not not_125 (not_125_out, OP5);
  not not_126 (not_126_out, OP4);
  not not_127 (not_127_out, OP2);
  not not_128 (not_128_out, OP0);
  not not_129 (not_129_out, OP5);
  not not_130 (not_130_out, OP4);
  not not_131 (not_131_out, OP3);
  not not_132 (not_132_out, OP2);
  not not_133 (not_133_out, OP1);
  not not_134 (not_134_out, OP0);
  not not_135 (not_135_out, F4);
  not not_136 (not_136_out, F3);
  not not_137 (not_137_out, F2);
  not not_138 (not_138_out, F1);
  not not_139 (not_139_out, F0);
  not not_140 (not_140_out, OP5);
  not not_141 (not_141_out, OP4);
  not not_142 (not_142_out, OP3);
  not not_143 (not_143_out, OP2);
  not not_144 (not_144_out, OP1);
  not not_145 (not_145_out, OP0);
  not not_146 (not_146_out, F4);
  not not_147 (not_147_out, F3);
  not not_148 (not_148_out, F2);
  not not_149 (not_149_out, F1);
  not not_150 (not_150_out, OP5);
  not not_151 (not_151_out, OP4);
  not not_152 (not_152_out, OP3);
  not not_153 (not_153_out, OP2);
  not not_154 (not_154_out, OP1);
  not not_155 (not_155_out, OP0);
  not not_156 (not_156_out, F4);
  not not_157 (not_157_out, F3);
  not not_158 (not_158_out, F2);
  not not_159 (not_159_out, F0);
  not not_160 (not_160_out, OP5);
  not not_161 (not_161_out, OP4);
  not not_162 (not_162_out, OP3);
  not not_163 (not_163_out, OP2);
  not not_164 (not_164_out, OP1);
  not not_165 (not_165_out, OP0);
  not not_166 (not_166_out, F4);
  not not_167 (not_167_out, F3);
  not not_168 (not_168_out, F1);
  not not_169 (not_169_out, F0);
  not not_170 (not_170_out, OP5);
  not not_171 (not_171_out, OP4);
  not not_172 (not_172_out, OP3);
  not not_173 (not_173_out, OP2);
  not not_174 (not_174_out, OP1);
  not not_175 (not_175_out, OP0);
  not not_176 (not_176_out, F4);
  not not_177 (not_177_out, F2);
  not not_178 (not_178_out, OP5);
  not not_179 (not_179_out, OP4);
  not not_180 (not_180_out, OP2);
  not not_181 (not_181_out, OP1);
  not not_182 (not_182_out, OP0);
  not not_183 (not_183_out, OP5);
  not not_184 (not_184_out, OP4);
  not not_185 (not_185_out, OP1);
  not not_186 (not_186_out, OP0);
  not not_187 (not_187_out, OP5);
  not not_188 (not_188_out, OP4);
  not not_189 (not_189_out, OP2);
  not not_190 (not_190_out, OP1);
  not not_191 (not_191_out, OP4);
  not not_192 (not_192_out, OP3);
  not not_193 (not_193_out, OP2);
  not not_194 (not_194_out, OP4);
  not not_195 (not_195_out, OP2);
  not not_196 (not_196_out, OP5);
  not not_197 (not_197_out, OP4);
  not not_198 (not_198_out, OP3);
  not not_199 (not_199_out, OP2);
  not not_200 (not_200_out, OP1);
  not not_201 (not_201_out, OP0);
  not not_202 (not_202_out, F4);
  not not_203 (not_203_out, F3);
  not not_204 (not_204_out, F1);
  not not_205 (not_205_out, OP5);
  not not_206 (not_206_out, OP4);
  not not_207 (not_207_out, OP3);
  not not_208 (not_208_out, OP2);
  not not_209 (not_209_out, OP1);
  not not_210 (not_210_out, OP0);
  not not_211 (not_211_out, F4);
  not not_212 (not_212_out, F3);
  not not_213 (not_213_out, OP5);
  not not_214 (not_214_out, OP4);
  not not_215 (not_215_out, OP3);
  not not_216 (not_216_out, OP2);
  not not_217 (not_217_out, OP1);
  not not_218 (not_218_out, OP0);
  not not_219 (not_219_out, F4);
  not not_220 (not_220_out, F2);
  not not_221 (not_221_out, F0);
  not not_222 (not_222_out, OP5);
  not not_223 (not_223_out, OP4);
  not not_224 (not_224_out, OP3);
  not not_225 (not_225_out, OP2);
  not not_226 (not_226_out, OP1);
  not not_227 (not_227_out, OP0);
  not not_228 (not_228_out, F4);
  not not_229 (not_229_out, F2);
  not not_230 (not_230_out, OP5);
  not not_231 (not_231_out, OP4);
  not not_232 (not_232_out, OP2);
  not not_233 (not_233_out, OP0);
  not not_234 (not_234_out, OP5);
  not not_235 (not_235_out, OP4);
  not not_236 (not_236_out, OP1);
  and and_1 (and_1_out, not_1_out, not_2_out, not_3_out, not_4_out, not_5_out, not_6_out, not_7_out, not_8_out, not_9_out, not_10_out, F1, F0);
  and and_2 (and_2_out, not_11_out, not_12_out, not_13_out, not_14_out, not_15_out, not_16_out, F5, not_17_out, not_18_out, not_19_out, not_20_out, not_21_out);
  and and_3 (and_3_out, not_22_out, not_23_out, not_24_out, not_25_out, not_26_out, not_27_out, F5, not_28_out, not_29_out, not_30_out, not_31_out, F0);
  and and_4 (and_4_out, not_32_out, not_33_out, not_34_out, not_35_out, not_36_out, not_37_out, F5, not_38_out, not_39_out, F2, not_40_out, not_41_out);
  and and_5 (and_5_out, not_42_out, not_43_out, not_44_out, not_45_out, not_46_out, not_47_out, F5, not_48_out, F3, not_49_out, F1, not_50_out);
  and and_6 (and_6_out, not_51_out, not_52_out, OP3, not_53_out, not_54_out, not_55_out);
  and and_7 (and_7_out, not_56_out, not_57_out, OP3, OP2, not_58_out, not_59_out);
  and and_8 (and_8_out, not_60_out, not_61_out, OP3, not_62_out, not_63_out, OP0);
  and and_9 (and_9_out, not_64_out, not_65_out, OP3, not_66_out, OP1, not_67_out);
  and and_10 (and_10_out, OP5, not_68_out, not_69_out, not_70_out, OP1, OP0);
  and and_11 (and_11_out, OP5, not_71_out, OP3, not_72_out, OP1, OP0);
  and and_12 (and_12_out, not_73_out, not_74_out, not_75_out, not_76_out, not_77_out, not_78_out, not_79_out, not_80_out, not_81_out, not_82_out, F1, not_83_out);
  and and_13 (and_13_out, not_84_out, not_85_out, not_86_out, not_87_out, not_88_out, not_89_out, F5, not_90_out, not_91_out, not_92_out, F1, not_93_out);
  and and_14 (and_14_out, not_94_out, not_95_out, not_96_out, not_97_out, not_98_out, not_99_out, F5, not_100_out, not_101_out, F2, not_102_out, not_103_out);
  and and_15 (and_15_out, not_104_out, not_105_out, not_106_out, not_107_out, not_108_out, not_109_out, F5, not_110_out, not_111_out, F2, F1, F0);
  and and_16 (and_16_out, not_112_out, not_113_out, not_114_out, not_115_out, not_116_out, not_117_out, F5, not_118_out, F3, not_119_out, F1, not_120_out);
  and and_17 (and_17_out, not_121_out, not_122_out, OP3, OP2, not_123_out, not_124_out);
  and and_18 (and_18_out, not_125_out, not_126_out, OP3, not_127_out, OP1, not_128_out);
  and and_19 (and_19_out, not_129_out, not_130_out, not_131_out, not_132_out, not_133_out, not_134_out, F5, not_135_out, not_136_out, not_137_out, not_138_out, not_139_out);
  and and_20 (and_20_out, not_140_out, not_141_out, not_142_out, not_143_out, not_144_out, not_145_out, F5, not_146_out, not_147_out, not_148_out, not_149_out, F0);
  and and_21 (and_21_out, not_150_out, not_151_out, not_152_out, not_153_out, not_154_out, not_155_out, F5, not_156_out, not_157_out, not_158_out, F1, not_159_out);
  and and_22 (and_22_out, not_160_out, not_161_out, not_162_out, not_163_out, not_164_out, not_165_out, F5, not_166_out, not_167_out, F2, not_168_out, not_169_out);
  and and_23 (and_23_out, not_170_out, not_171_out, not_172_out, not_173_out, not_174_out, not_175_out, F5, not_176_out, F3, not_177_out, F1, F0);
  and and_24 (and_24_out, not_178_out, not_179_out, OP3, not_180_out, not_181_out, not_182_out);
  and and_25 (and_25_out, not_183_out, not_184_out, OP3, OP2, not_185_out, not_186_out);
  and and_26 (and_26_out, not_187_out, not_188_out, OP3, not_189_out, not_190_out, OP0);
  and and_27 (and_27_out, OP5, not_191_out, not_192_out, not_193_out, OP1, OP0);
  and and_28 (and_28_out, OP5, not_194_out, OP3, not_195_out, OP1, OP0);
  and and_29 (and_29_out, not_196_out, not_197_out, not_198_out, not_199_out, not_200_out, not_201_out, F5, not_202_out, not_203_out, F2, not_204_out, F0);
  and and_30 (and_30_out, not_205_out, not_206_out, not_207_out, not_208_out, not_209_out, not_210_out, F5, not_211_out, not_212_out, F2, F1, F0);
  and and_31 (and_31_out, not_213_out, not_214_out, not_215_out, not_216_out, not_217_out, not_218_out, F5, not_219_out, F3, not_220_out, F1, not_221_out);
  and and_32 (and_32_out, not_222_out, not_223_out, not_224_out, not_225_out, not_226_out, not_227_out, F5, not_228_out, F3, not_229_out, F1, F0);
  and and_33 (and_33_out, not_230_out, not_231_out, OP3, not_232_out, OP1, not_233_out);
  and and_34 (and_34_out, not_234_out, not_235_out, OP3, OP2, not_236_out, OP0);
  or or_1 (S0, and_1_out, and_2_out, and_3_out, and_4_out, and_5_out, and_6_out, and_7_out, and_8_out, and_9_out, and_10_out, and_11_out);
  or or_2 (S1, and_12_out, and_13_out, and_14_out, and_15_out, and_16_out, and_17_out, and_18_out);
  or or_3 (S2, and_19_out, and_20_out, and_21_out, and_22_out, and_23_out, and_24_out, and_25_out, and_26_out, and_27_out, and_28_out);
  or or_4 (S3, and_29_out, and_30_out, and_31_out, and_32_out, and_33_out, and_34_out);
endmodule

// 控制信号自动生成
module \单周期MIPS_单级中断控制信号自动生成  (
  input  OP0,
  input  OP1,
  input  OP2,
  input  OP3,
  input  OP4,
  input  OP5,
  input  F0,
  input  F1,
  input  F2,
  input  F3,
  input  F4,
  input  F5,
  output MemToReg,
  output MemWrite,
  output ALU_SRC,
  output RegWrite,
  output SysCALL,
  output SignedExt,
  output RegDst,
  output BEQ,
  output BNE,
  output JR,
  output JUMP,
  output JAL,
  output ERET
);

  wire and_3_out, and_4_out, and_5_out, and_6_out, and_7_out, and_8_out, and_9_out, and_10_out, and_11_out,
       and_12_out, and_13_out, and_15_out, and_16_out, and_17_out, and_18_out, and_19_out, and_20_out,
       and_21_out, and_22_out, and_23_out, and_27_out, and_28_out, not_1_out, not_2_out, not_3_out,
       not_4_out, not_5_out, not_6_out, not_7_out, not_8_out, not_9_out, not_10_out, not_11_out, not_12_out,
       not_13_out, not_14_out, not_15_out, not_16_out, not_17_out, not_18_out, not_19_out, not_20_out,
       not_21_out, not_22_out, not_23_out, not_24_out, not_25_out, not_26_out, not_27_out, not_28_out,
       not_29_out, not_30_out, not_31_out, not_32_out, not_33_out, not_34_out, not_35_out, not_36_out,
       not_37_out, not_38_out, not_39_out, not_40_out, not_41_out, not_42_out, not_43_out, not_44_out,
       not_45_out, not_46_out, not_47_out, not_48_out, not_49_out, not_50_out, not_51_out, not_52_out,
       not_53_out, not_54_out, not_55_out, not_56_out, not_57_out, not_58_out, not_59_out, not_60_out,
       not_61_out, not_62_out, not_63_out, not_64_out, not_65_out, not_66_out, not_67_out, not_68_out,
       not_69_out, not_70_out, not_71_out, not_72_out, not_73_out, not_74_out, not_75_out, not_76_out,
       not_77_out, not_78_out, not_79_out, not_80_out, not_81_out, not_82_out, not_83_out, not_84_out,
       not_85_out, not_86_out, not_87_out, not_88_out, not_89_out, not_90_out, not_91_out, not_92_out,
       not_93_out, not_94_out, not_95_out, not_96_out, not_97_out, not_98_out, not_99_out, not_100_out,
       not_101_out, not_102_out, not_103_out, not_104_out, not_105_out, not_106_out, not_107_out,
       not_108_out, not_109_out, not_110_out, not_111_out, not_112_out, not_113_out, not_114_out,
       not_115_out, not_116_out, not_117_out, not_118_out, not_119_out, not_120_out, not_121_out,
       not_122_out, not_123_out, not_124_out, not_125_out, not_126_out, not_127_out, not_128_out,
       not_129_out, not_130_out, not_131_out, not_132_out, not_133_out, not_134_out, not_135_out,
       not_136_out, not_137_out, not_138_out, not_139_out, not_140_out, not_141_out, not_142_out,
       not_143_out, not_144_out, not_145_out, not_146_out, not_147_out, not_148_out, not_149_out,
       not_150_out, not_151_out, not_152_out, not_153_out, not_154_out, not_155_out, not_156_out,
       not_157_out, not_158_out, not_159_out, not_160_out, not_161_out, not_162_out, not_163_out,
       not_164_out, not_165_out, not_166_out, not_167_out, not_168_out, not_169_out, not_170_out,
       not_171_out, not_172_out, not_173_out, not_174_out, not_175_out, not_176_out, not_177_out,
       not_178_out, not_179_out, not_180_out, not_181_out, not_182_out, not_183_out, not_184_out,
       not_185_out, not_186_out, not_187_out;

  not not_1 (not_1_out, OP2);
  not not_2 (not_2_out, OP3);
  not not_3 (not_3_out, OP4);
  not not_4 (not_4_out, OP2);
  not not_5 (not_5_out, OP4);
  not not_6 (not_6_out, OP0);
  not not_7 (not_7_out, OP2);
  not not_8 (not_8_out, OP4);
  not not_9 (not_9_out, OP5);
  not not_10 (not_10_out, OP1);
  not not_11 (not_11_out, OP4);
  not not_12 (not_12_out, OP5);
  not not_13 (not_13_out, OP2);
  not not_14 (not_14_out, OP4);
  not not_15 (not_15_out, OP0);
  not not_16 (not_16_out, OP1);
  not not_17 (not_17_out, OP2);
  not not_18 (not_18_out, OP4);
  not not_19 (not_19_out, OP5);
  not not_20 (not_20_out, F0);
  not not_21 (not_21_out, F2);
  not not_22 (not_22_out, F3);
  not not_23 (not_23_out, F4);
  not not_24 (not_24_out, OP0);
  not not_25 (not_25_out, OP1);
  not not_26 (not_26_out, OP2);
  not not_27 (not_27_out, OP4);
  not not_28 (not_28_out, OP5);
  not not_29 (not_29_out, F1);
  not not_30 (not_30_out, F3);
  not not_31 (not_31_out, F4);
  not not_32 (not_32_out, OP0);
  not not_33 (not_33_out, OP1);
  not not_34 (not_34_out, OP2);
  not not_35 (not_35_out, OP4);
  not not_36 (not_36_out, OP5);
  not not_37 (not_37_out, F2);
  not not_38 (not_38_out, F3);
  not not_39 (not_39_out, F4);
  not not_40 (not_40_out, F5);
  not not_41 (not_41_out, OP0);
  not not_42 (not_42_out, OP1);
  not not_43 (not_43_out, OP2);
  not not_44 (not_44_out, OP4);
  not not_45 (not_45_out, OP5);
  not not_46 (not_46_out, F2);
  not not_47 (not_47_out, F4);
  not not_48 (not_48_out, OP0);
  not not_49 (not_49_out, OP1);
  not not_50 (not_50_out, OP2);
  not not_51 (not_51_out, OP4);
  not not_52 (not_52_out, OP5);
  not not_53 (not_53_out, F3);
  not not_54 (not_54_out, F4);
  not not_55 (not_55_out, OP0);
  not not_56 (not_56_out, OP2);
  not not_57 (not_57_out, OP4);
  not not_58 (not_58_out, OP5);
  not not_59 (not_59_out, OP1);
  not not_60 (not_60_out, OP4);
  not not_61 (not_61_out, OP5);
  not not_62 (not_62_out, OP2);
  not not_63 (not_63_out, OP3);
  not not_64 (not_64_out, OP4);
  not not_65 (not_65_out, OP0);
  not not_66 (not_66_out, OP1);
  not not_67 (not_67_out, OP2);
  not not_68 (not_68_out, OP3);
  not not_69 (not_69_out, OP4);
  not not_70 (not_70_out, OP5);
  not not_71 (not_71_out, F0);
  not not_72 (not_72_out, F1);
  not not_73 (not_73_out, F4);
  not not_74 (not_74_out, F5);
  not not_75 (not_75_out, OP0);
  not not_76 (not_76_out, OP2);
  not not_77 (not_77_out, OP4);
  not not_78 (not_78_out, OP5);
  not not_79 (not_79_out, OP1);
  not not_80 (not_80_out, OP2);
  not not_81 (not_81_out, OP4);
  not not_82 (not_82_out, OP5);
  not not_83 (not_83_out, OP2);
  not not_84 (not_84_out, OP4);
  not not_85 (not_85_out, OP0);
  not not_86 (not_86_out, OP1);
  not not_87 (not_87_out, OP2);
  not not_88 (not_88_out, OP3);
  not not_89 (not_89_out, OP4);
  not not_90 (not_90_out, OP5);
  not not_91 (not_91_out, F0);
  not not_92 (not_92_out, F1);
  not not_93 (not_93_out, F2);
  not not_94 (not_94_out, F4);
  not not_95 (not_95_out, F5);
  not not_96 (not_96_out, OP0);
  not not_97 (not_97_out, OP1);
  not not_98 (not_98_out, OP2);
  not not_99 (not_99_out, OP3);
  not not_100 (not_100_out, OP4);
  not not_101 (not_101_out, OP5);
  not not_102 (not_102_out, F0);
  not not_103 (not_103_out, F2);
  not not_104 (not_104_out, F3);
  not not_105 (not_105_out, F4);
  not not_106 (not_106_out, OP0);
  not not_107 (not_107_out, OP1);
  not not_108 (not_108_out, OP2);
  not not_109 (not_109_out, OP3);
  not not_110 (not_110_out, OP4);
  not not_111 (not_111_out, OP5);
  not not_112 (not_112_out, F1);
  not not_113 (not_113_out, F3);
  not not_114 (not_114_out, F4);
  not not_115 (not_115_out, OP0);
  not not_116 (not_116_out, OP1);
  not not_117 (not_117_out, OP2);
  not not_118 (not_118_out, OP3);
  not not_119 (not_119_out, OP4);
  not not_120 (not_120_out, OP5);
  not not_121 (not_121_out, F2);
  not not_122 (not_122_out, F3);
  not not_123 (not_123_out, F4);
  not not_124 (not_124_out, F5);
  not not_125 (not_125_out, OP0);
  not not_126 (not_126_out, OP1);
  not not_127 (not_127_out, OP2);
  not not_128 (not_128_out, OP3);
  not not_129 (not_129_out, OP4);
  not not_130 (not_130_out, OP5);
  not not_131 (not_131_out, F2);
  not not_132 (not_132_out, F4);
  not not_133 (not_133_out, OP0);
  not not_134 (not_134_out, OP1);
  not not_135 (not_135_out, OP2);
  not not_136 (not_136_out, OP3);
  not not_137 (not_137_out, OP4);
  not not_138 (not_138_out, OP5);
  not not_139 (not_139_out, F3);
  not not_140 (not_140_out, F4);
  not not_141 (not_141_out, OP0);
  not not_142 (not_142_out, OP1);
  not not_143 (not_143_out, OP3);
  not not_144 (not_144_out, OP4);
  not not_145 (not_145_out, OP5);
  not not_146 (not_146_out, OP1);
  not not_147 (not_147_out, OP3);
  not not_148 (not_148_out, OP4);
  not not_149 (not_149_out, OP5);
  not not_150 (not_150_out, OP0);
  not not_151 (not_151_out, OP1);
  not not_152 (not_152_out, OP2);
  not not_153 (not_153_out, OP3);
  not not_154 (not_154_out, OP4);
  not not_155 (not_155_out, OP5);
  not not_156 (not_156_out, F0);
  not not_157 (not_157_out, F1);
  not not_158 (not_158_out, F2);
  not not_159 (not_159_out, F4);
  not not_160 (not_160_out, F5);
  not not_161 (not_161_out, OP0);
  not not_162 (not_162_out, OP2);
  not not_163 (not_163_out, OP3);
  not not_164 (not_164_out, OP4);
  not not_165 (not_165_out, OP5);
  not not_166 (not_166_out, F0);
  not not_167 (not_167_out, F1);
  not not_168 (not_168_out, F2);
  not not_169 (not_169_out, F4);
  not not_170 (not_170_out, F5);
  not not_171 (not_171_out, OP2);
  not not_172 (not_172_out, OP3);
  not not_173 (not_173_out, OP4);
  not not_174 (not_174_out, OP5);
  not not_175 (not_175_out, OP2);
  not not_176 (not_176_out, OP3);
  not not_177 (not_177_out, OP4);
  not not_178 (not_178_out, OP5);
  not not_179 (not_179_out, OP5);
  not not_180 (not_180_out, OP3);
  not not_181 (not_181_out, OP2);
  not not_182 (not_182_out, OP1);
  not not_183 (not_183_out, OP0);
  not not_184 (not_184_out, F5);
  not not_185 (not_185_out, F2);
  not not_186 (not_186_out, F1);
  not not_187 (not_187_out, F0);
  and and_1 (MemToReg, OP0, OP1, not_1_out, not_2_out, not_3_out, OP5);
  and and_2 (MemWrite, OP0, OP1, not_4_out, OP3, not_5_out, OP5);
  and and_3 (and_3_out, not_6_out, not_7_out, OP3, not_8_out, not_9_out);
  or or_1 (ALU_SRC, and_3_out, and_4_out, and_5_out);
  and and_4 (and_4_out, not_10_out, OP3, not_11_out, not_12_out);
  and and_5 (and_5_out, OP0, OP1, not_13_out, not_14_out, OP5);
  and and_6 (and_6_out, not_15_out, not_16_out, not_17_out, not_18_out, not_19_out, not_20_out, not_21_out, not_22_out, not_23_out);
  and and_7 (and_7_out, not_24_out, not_25_out, not_26_out, not_27_out, not_28_out, not_29_out, not_30_out, not_31_out, F5);
  and and_8 (and_8_out, not_32_out, not_33_out, not_34_out, not_35_out, not_36_out, F1, not_37_out, not_38_out, not_39_out, not_40_out);
  and and_9 (and_9_out, not_41_out, not_42_out, not_43_out, not_44_out, not_45_out, F1, not_46_out, F3, not_47_out, F5);
  and and_10 (and_10_out, not_48_out, not_49_out, not_50_out, not_51_out, not_52_out, F0, F2, not_53_out, not_54_out, F5);
  and and_11 (and_11_out, not_55_out, not_56_out, OP3, not_57_out, not_58_out);
  and and_12 (and_12_out, not_59_out, OP3, not_60_out, not_61_out);
  and and_13 (and_13_out, OP0, OP1, not_62_out, not_63_out, not_64_out);
  and and_14 (SysCALL, not_65_out, not_66_out, not_67_out, not_68_out, not_69_out, not_70_out, not_71_out, not_72_out, F2, F3, not_73_out, not_74_out);
  and and_15 (and_15_out, not_75_out, not_76_out, OP3, not_77_out, not_78_out);
  and and_16 (and_16_out, not_79_out, not_80_out, OP3, not_81_out, not_82_out);
  or or_2 (SignedExt, and_15_out, and_16_out, and_17_out);
  and and_17 (and_17_out, OP0, OP1, not_83_out, not_84_out, OP5);
  and and_18 (and_18_out, not_85_out, not_86_out, not_87_out, not_88_out, not_89_out, not_90_out, not_91_out, not_92_out, not_93_out, not_94_out, not_95_out);
  and and_19 (and_19_out, not_96_out, not_97_out, not_98_out, not_99_out, not_100_out, not_101_out, not_102_out, not_103_out, not_104_out, not_105_out);
  and and_20 (and_20_out, not_106_out, not_107_out, not_108_out, not_109_out, not_110_out, not_111_out, not_112_out, not_113_out, not_114_out, F5);
  and and_21 (and_21_out, not_115_out, not_116_out, not_117_out, not_118_out, not_119_out, not_120_out, F1, not_121_out, not_122_out, not_123_out, not_124_out);
  and and_22 (and_22_out, not_125_out, not_126_out, not_127_out, not_128_out, not_129_out, not_130_out, F1, not_131_out, F3, not_132_out, F5);
  and and_23 (and_23_out, not_133_out, not_134_out, not_135_out, not_136_out, not_137_out, not_138_out, F0, F2, not_139_out, not_140_out, F5);
  and and_24 (BEQ, not_141_out, not_142_out, OP2, not_143_out, not_144_out, not_145_out);
  and and_25 (BNE, OP0, not_146_out, OP2, not_147_out, not_148_out, not_149_out);
  and and_26 (JR, not_150_out, not_151_out, not_152_out, not_153_out, not_154_out, not_155_out, not_156_out, not_157_out, not_158_out, F3, not_159_out, not_160_out);
  and and_27 (and_27_out, not_161_out, not_162_out, not_163_out, not_164_out, not_165_out, not_166_out, not_167_out, not_168_out, F3, not_169_out, not_170_out);
  and and_28 (and_28_out, OP1, not_171_out, not_172_out, not_173_out, not_174_out);
  and and_29 (JAL, OP0, OP1, not_175_out, not_176_out, not_177_out, not_178_out);
  and and_30 (ERET, not_179_out, OP4, not_180_out, not_181_out, not_182_out, not_183_out, not_184_out, F4, F3, not_185_out, not_186_out, not_187_out);
  or or_3 (RegWrite, and_6_out, and_7_out, and_8_out, and_9_out, and_10_out, and_11_out, and_12_out, and_13_out);
  or or_4 (RegDst, and_18_out, and_19_out, and_20_out, and_21_out, and_22_out, and_23_out);
  or or_5 (JUMP, and_27_out, and_28_out);
endmodule

module \单周期MIPS_多级中断  (
  input  IR1,
  input  IR2,
  input  IR3,
  output RegWrite,
  output MemWrite,
  output [31:0] PC,
  output [31:0] IR,
  output [31:0] RDin,
  output [31:0] MDin,
  output [31:0] LedData
);

  wire AluSrcB, and_1_out, and_2_out, and_3_out, Beq, Beq_Bne, Bne, CLK, clock_2_out, comparator_1_eq,
       comparator_2_eq, comparator_5_eq, comparator_6_eq, comparator_7_eq, comparator_8_eq, comparator_10_eq,
       comparator_10_lt, d_ff_1_q, d_ff_2_qn, Equal, ERET, Go, Halt, intChan, IntR, IR1_t, IR2_t, IR3_t, IRA,
       IRB, IRC, JAL, JMP, JR, LED_EN, MemToReg, MFC0, MTC0, nand_1_out, not_1_out, not_2_out, not_3_out,
       not_4_out, or_1_out, or_2_out, or_3_out, or_8_out, or_9_out, or_10_out, or_11_out, RegDst, SignedExt,
       Syscall, W1, W2, W3, \中断请求 ;
  wire [1:0] \单周期mips_单级中断中断控制器_1_intnum , \硬件堆栈_1_1_输出 ;
  wire [3:0] AluOP;
  wire [4:0] multiplexer_4_out, multiplexer_5_out, multiplexer_6_out, multiplexer_7_out;
  wire [12:0] CNT_num;
  wire [15:0] \总周期数 ;
  wire [31:0] bit_extender_1_out, bit_extender_2_out, EpcIn, EpcOut, mips_alu_1_result, multiplexer_1_out,
       multiplexer_3_out, multiplexer_10_out, multiplexer_11_out, PC_4, PC_imm, PC_IRQ, PC_JR, ram_1_data,
       shifter_1_out;

  Clock #(.highDuration(1), .lowDuration(1)) clock_1 ();  // open: out
  Button _1 ();  // open: out
  Button _2 ();  // open: out
  Button _3 ();  // open: out
  Button \u_继续运行  (.out(Go));
  LED #(.active("true")) led_1 (.in(W1));
  LED #(.active("true")) led_2 (.in(W2));
  LED #(.active("true")) led_3 (.in(W3));
  Hex_Digit_Display hex_digit_display_1 (.value(LedData[31:28]));  // open: dp
  Comparator #(.width(16), .mode("twosComplement")) comparator_1 (
    .a(\总周期数 ), .b(16'h7), .eq(comparator_1_eq));  // open: gt, lt
  Comparator #(.width(16), .mode("twosComplement")) comparator_2 (
    .a(\总周期数 ), .b(16'h241), .eq(comparator_2_eq));  // open: gt, lt
  Multiplexer #(.select(3), .width(32), .disabled("Z"), .enable("false")) multiplexer_1 (
    .in0(PC_4), .in1(PC_imm), .in2({PC_4[31:28], IR[25:0], 2'b00}), .in6(PC_JR), .out(multiplexer_1_out),
    .sel({JR, JMP, Beq_Bne}));  // open: in3, in4, in5, in7
  Comparator #(.width(32), .mode("twosComplement")) comparator_3 (.a(IR), .b(32'h40800000), .eq(MTC0));  // open: gt, lt
  Comparator #(.width(32), .mode("twosComplement")) comparator_4 (.a(IR), .b(32'h40000000), .eq(MFC0));  // open: gt, lt
  Hex_Digit_Display hex_digit_display_2 (.value(LedData[23:20]));  // open: dp
  Hex_Digit_Display hex_digit_display_3 (.value(LedData[27:24]));  // open: dp
  Comparator #(.width(16), .mode("twosComplement")) comparator_5 (
    .a(16'h258), .b(\总周期数 ), .eq(comparator_5_eq));  // open: gt, lt
  or or_1 (or_1_out, comparator_5_eq, comparator_6_eq);
  Comparator #(.width(16), .mode("twosComplement")) comparator_6 (
    .a(\总周期数 ), .b(16'h1), .eq(comparator_6_eq));  // open: gt, lt
  Comparator #(.width(16), .mode("twosComplement")) comparator_7 (
    .a(\总周期数 ), .b(16'h4), .eq(comparator_7_eq));  // open: gt, lt
  or or_2 (or_2_out, comparator_1_eq, comparator_2_eq);
  \单周期MIPS_单级中断硬布线控制器  \u_单周期mips_单级中断硬布线控制器_1  (
    .OP(IR[31:26]), .Func(IR[5:0]), .ALU_OP(AluOP), .MemToReg(MemToReg), .MemWrite(MemWrite),
    .ALU_SRC(AluSrcB), .RegWrite(RegWrite), .SysCALL(Syscall), .SignedExt(SignedExt), .RegDst(RegDst),
    .Beq(Beq), .Bne(Bne), .JR(JR), .JMP(JMP), .JAL(JAL), .ERET(ERET));
  Multiplexer #(.select(1), .width(32), .disabled("Z"), .enable("false")) multiplexer_2 (
    .in0(multiplexer_1_out), .in1(EpcOut), .out(EpcIn), .sel(ERET));
  Hex_Digit_Display hex_digit_display_4 (.value(LedData[19:16]));  // open: dp
  Hex_Digit_Display hex_digit_display_5 (.value(LedData[15:12]));  // open: dp
  Pull_Resistor #(.pull(0)) pull_resistor_1 (.node(IRA));
  assign IRA = or_1_out ? ~CLK : 1'bz;  // Controlled_Inverter controlled_inverter_1
  Pull_Resistor #(.pull(0)) pull_resistor_2 (.node(IRB));
  assign IRB = comparator_7_eq ? ~CLK : 1'bz;  // Controlled_Inverter controlled_inverter_2
  Pull_Resistor #(.pull(0)) pull_resistor_3 (.node(IRC));
  assign IRC = or_2_out ? ~CLK : 1'bz;  // Controlled_Inverter controlled_inverter_3
  Multiplexer #(.select(1), .width(32), .disabled("Z"), .enable("false")) multiplexer_3 (
    .in0(EpcIn), .in1(PC_IRQ), .out(multiplexer_3_out), .sel(\中断请求 ));
  or or_3 (or_3_out, not_1_out, Go);
  not not_1 (not_1_out, Halt);
  Hex_Digit_Display hex_digit_display_6 (.value(LedData[7:4]));  // open: dp
  Hex_Digit_Display hex_digit_display_7 (.value(LedData[11:8]));  // open: dp
  // Probe on \总周期数 
  Register #(.width(32), .trigger("rising"), .Select("low")) u_PC (
    .D(multiplexer_3_out), .en(or_3_out), .Q(PC), .clk(CLK));  // open: clr
  // Probe on PC
  Hex_Digit_Display hex_digit_display_8 (.value(LedData[3:0]));  // open: dp
  // Probe on IR
  or or_4 (IR1_t, IR1, IRA);
  Register #(.width(32), .trigger("rising"), .Select("low")) register_1 (
    .D(MDin), .en(LED_EN), .Q(LedData), .clk(CLK));  // open: clr
  Adder #(.width(32)) adder_1 (.a(PC), .b(32'h4), .out(PC_4));  // open: cin, cout
  // Probe on PC_imm
  // Mips_Probe mips_probe_1: pin names not known; wires that end beside it: IR
  ROM #(.addrWidth(10), .dataWidth(32), .Select("high")) rom_1 (.addr(PC[11:2]), .data(IR));
  or or_5 (IR2_t, IR2, IRB);
  not not_2 (not_2_out, Halt);
  Counter #(.width(16), .max('hffff), .ongoal("wrap"), .trigger("rising"), .behavior("new")) counter_1 (
    .count(not_2_out), .Q(\总周期数 ), .clk(CLK));  // open: load, D, carry, clr, preset, down
  // Probe on PC_JR
  or or_6 (IR3_t, IR3, IRC);
  Multiplexer #(.select(1), .width(5), .disabled("Z"), .enable("false")) multiplexer_4 (
    .in0(IR[25:21]), .in1(5'b00010), .out(multiplexer_4_out), .sel(Syscall));
  Multiplexer #(.select(1), .width(5), .disabled("Z"), .enable("false")) multiplexer_5 (
    .in0(IR[20:16]), .in1(5'b00100), .out(multiplexer_5_out), .sel(Syscall));
  Multiplexer #(.select(1), .width(5), .disabled("Z"), .enable("false")) multiplexer_6 (
    .in0(IR[20:16]), .in1(IR[15:11]), .out(multiplexer_6_out), .sel(RegDst));
  Multiplexer #(.select(1), .width(5), .disabled("Z"), .enable("false")) multiplexer_7 (
    .in0(multiplexer_6_out), .in1({5{1'b1}}), .out(multiplexer_7_out), .sel(JAL));
  not not_3 (not_3_out, Equal);
  // Probe on multiplexer_4_out
  // Probe on multiplexer_5_out
  // Probe on multiplexer_7_out
  Multiplexer #(.select(1), .width(32), .disabled("Z"), .enable("false")) multiplexer_8 (
    .in0(multiplexer_11_out), .in1(PC_4), .out(RDin), .sel(JAL));
  and and_1 (and_1_out, Beq, Equal);
  or or_7 (Beq_Bne, and_1_out, and_2_out);
  and and_2 (and_2_out, Bne, not_3_out);
  MIPS_Regifile mips_regifile_1 (
    .Din(RDin), .Clk(CLK), .R1(PC_JR), .R2(MDin), .WE(RegWrite), .W_num(multiplexer_7_out),
    .R1_num(multiplexer_4_out), .R2_num(multiplexer_5_out));
  Multiplexer #(.select(2), .width(32), .disabled("Z"), .enable("false")) multiplexer_9 (
    .in1(32'h30ac), .in2(32'h3158), .in3(32'h3204), .out(PC_IRQ), .sel(\单周期mips_单级中断中断控制器_1_intnum ));  // open: in0
  assign bit_extender_1_out = {{16{1'b0}}, IR[15:0]};  // Bit_Extender bit_extender_1
  assign bit_extender_2_out = {{16{IR[15]}}, IR[15:0]};  // Bit_Extender bit_extender_2
  or or_8 (or_8_out, ERET, \中断请求 );
  \单周期MIPS_单级中断中断控制器  \u_单周期mips_单级中断中断控制器_1  (
    .CLK(CLK), .IR1(IR1_t), .IR2(IR2_t), .IR3(IR3_t), .Clr(ERET), .TEST(\硬件堆栈_1_1_输出 ), .IR1W(W1), .IR2W(W2),
    .IR3W(W3), .IntNum(\单周期mips_单级中断中断控制器_1_intnum ), .IntR(IntR));
  or or_9 (or_9_out, ERET, MFC0);
  or or_10 (or_10_out, IntR, MTC0);
  Multiplexer #(.select(2), .width(32), .disabled("Z"), .enable("false")) multiplexer_10 (
    .in0(MDin), .in1(MDin), .in2(bit_extender_1_out), .in3(bit_extender_2_out), .out(multiplexer_10_out),
    .sel({AluSrcB, SignedExt}));
  Shifter #(.width(32), .shift("ll")) shifter_1 (.in(bit_extender_2_out), .\dist (5'b00010), .out(shifter_1_out));
  Comparator #(.width(32), .mode("twosComplement")) comparator_8 (
    .a(PC_JR), .b(32'h22), .eq(comparator_8_eq));  // open: gt, lt
  \硬件堆栈_1  \u_硬件堆栈_1_1  (
    .CLK(CLK), .read(ERET), .change(or_8_out), .\输入 (\单周期mips_单级中断中断控制器_1_intnum ), .\输出 (\硬件堆栈_1_1_输出 ));
  and and_3 (and_3_out, ~or_9_out, or_10_out);  // AND_Gate
  Adder #(.width(32)) adder_2 (.a(shifter_1_out), .b(PC_4), .out(PC_imm));  // open: cin, cout
  D_Flip_Flop #(.trigger("high"), .Pre_Clr_Positions("LEGACY"), .NegatePresetClear("false"), .enable("true"), .NewFFLayout("false")) d_ff_1 (.Q(d_ff_1_q));  // open: clk, D, Qn, preset, en, reset
  // Probe on 13'h10
  not not_4 (not_4_out, comparator_8_eq);
  Comparator #(.width(2), .mode("unsigned")) comparator_9 (
    .a(\单周期mips_单级中断中断控制器_1_intnum ), .b(\硬件堆栈_1_1_输出 ), .gt(intChan));  // open: eq, lt
  D_Flip_Flop #(.trigger("rising"), .Pre_Clr_Positions("LEGACY"), .NegatePresetClear("false"), .enable("true"), .NewFFLayout("false")) d_ff_2 (
    .clk(CLK), .D(and_3_out), .Qn(d_ff_2_qn));  // open: Q, preset, en, reset
  MIPS_ALU mips_alu_1 (
    .X(PC_JR), .Y(multiplexer_10_out), .AluOP(AluOP), .Equal(Equal), .Result(mips_alu_1_result),
    .shamt(IR[10:6]));  // open: Result_2
  Clock #(.highDuration(1), .lowDuration(1)) clock_2 (.out(clock_2_out));
  and and_4 (LED_EN, Syscall, comparator_8_eq);
  and and_5 (Halt, Syscall, not_4_out);
  and and_6 (\中断请求 , d_ff_2_qn, intChan, IntR);
  Comparator #(.width(13), .mode("twosComplement")) comparator_10 (
    .a(CNT_num), .b(13'h10), .eq(comparator_10_eq), .lt(comparator_10_lt));  // open: gt
  \硬件堆栈  \u_硬件堆栈_1  (.CLK(CLK), .read(ERET), .change(or_11_out), .\输入 (EpcIn), .\输出 (EpcOut));
  or or_11 (or_11_out, ERET, \中断请求 );
  RAM #(.addrWidth(10), .dataWidth(32), .bus("separate"), .Select("high")) ram_1 (
    .addr(mips_alu_1_result[11:2]), .din(MDin), .data(ram_1_data), .str(MemWrite), .clk(CLK));  // open: sel, ld, clr
  nand nand_1 (nand_1_out, d_ff_1_q, comparator_10_eq);
  Counter #(.width(13), .max('h1fff), .ongoal("stay"), .trigger("rising"), .behavior("old")) counter_2 (
    .count(comparator_10_lt), .Q(CNT_num), .clk(clock_2_out));  // open: load, D, carry, clr, preset
  Multiplexer #(.select(1), .width(32), .disabled("Z"), .enable("false")) multiplexer_11 (
    .in0(mips_alu_1_result), .in1(ram_1_data), .out(multiplexer_11_out), .sel(MemToReg));
  assign CLK = nand_1_out ? clock_2_out : 1'bz;  // Controlled_Buffer controlled_buffer_1
  Pull_Resistor #(.pull(1)) pull_resistor_4 (.node(CLK));

  // Other names for the same wires on the sheet: a0[31:0] = MDin; OP[5:0] = IR[31:26];
  //   PC_J_JAL[31:2] = {PC_4[31:28], IR[25:0]}; addr[25:0] = IR[25:0]; Func[5:0] = IR[5:0]; imm[15:0] = IR[15:0];
  //   shamt[4:0] = IR[10:6]; rd[4:0] = IR[15:11]; rt[4:0] = IR[20:16]; rs[4:0] = IR[25:21]; v0[31:0] = PC_JR

  // Notes on the sheet:
  //   中断源
  //   中断等待指示
  //   总复位信号应将除ROM以外所有存储组件全部清零
  //   多级中断测试信号模拟器
  //   JMP
  //   JR
  //   OP
  //   Func
  //   Syscall
  //   数码管输出
  //   数码管输出应该用寄存器锁存，否则显示数据只能一闪而过
  //   无跳转时PC的值
  //   Beq或Bne时PC的值
  //   指令存储器
  //   OP
  //   rs
  //   指令字
  //   contents of rom_1 (hex, n*v repeats v):
  //   201d07d0 20100001 109fc0 139fc3 8021 2012000c 24160008 26100001 3210000f 20080008 20090001 139900
  //   2709825 132020 20020022 c 1094022 1500fff9 22100001 2018000f 2188024 108700 20080008 20090001 139902
  //   2709825 132021 20020022 c 1094022 1500fff9 108702 2c9b022 12c00001 8000c07 4020 1084027 84400
  //   3508ffff 82021 20020022 c 8000c01 afa20000 23bd0004 afa40000 23bd0004 afb00000 23bd0004 afb30000
  //   23bd0004 afb40000 23bd0004 afb50000 23bd0004 afb60000 23bd0004 40000000 20160001 20140003 20150001
  //   168020 108100 2149825 132020 20020022 c 1600fffa 295a022 1680fff7 40800000 23bdfffc 8fb60000
  //   23bdfffc 8fb50000 23bdfffc 8fb40000 23bdfffc 8fb30000 23bdfffc 8fb00000 23bdfffc 8fa40000 23bdfffc
  //   8fa20000 42000018 afa20000 23bd0004 afa40000 23bd0004 afb00000 23bd0004 afb30000 23bd0004 afb40000
  //   23bd0004 afb50000 23bd0004 afb60000 23bd0004 40000000 20160002 20140003 20150001 168020 108100
  //   2149825 132020 20020022 c 1600fffa 295a022 1680fff7 40800000 23bdfffc 8fb60000 23bdfffc 8fb50000
  //   23bdfffc 8fb40000 23bdfffc 8fb30000 23bdfffc 8fb00000 23bdfffc 8fa40000 23bdfffc 8fa20000 42000018
  //   afa20000 23bd0004 afa40000 23bd0004 afb00000 23bd0004 afb30000 23bd0004 afb40000 23bd0004 afb50000
  //   23bd0004 afb60000 23bd0004 40000000 20160003 20140003 20150001 168020 108100 2149825 132020 20020022
  //   c 1600fffa 295a022 1680fff7 40800000 23bdfffc 8fb60000 23bdfffc 8fb50000 23bdfffc 8fb40000 23bdfffc
  //   8fb30000 23bdfffc 8fb00000 23bdfffc 8fa40000 23bdfffc 8fa20000 42000018
  //   rt
  //   rd
  //   Func
  //   J或JAL指令时PC的值
  //   jr指令时PC的值
  //   为方便自动评测，需要输出PC，IR，寄存器堆写如数据RDin
  //   RAM写使能MemWrite、RAM写入数据MDin等信号
  //   控制位
  //   暂停节拍，不能为0
  //   戳工具置1进入计数暂停模式，ctrl+k时钟自动运行到对应节拍暂停
  //   ctrl+k关闭时钟连续运行，将控制位置零，进入单步调试模式调试
  //   用这个时钟源需要去掉电路中的其他时钟源
  //   可计数暂停的时钟源
endmodule

module \硬件堆栈  (
  input  CLK,
  input  read,
  input  change,
  input  [31:0] \输入 ,
  output [31:0] \输出 
);

  wire and_1_out, and_2_out, buffer_1_out_2, demultiplexer_1_out0, demultiplexer_1_out1,
       demultiplexer_1_out2, demultiplexer_1_out3;
  wire [1:0] SP;
  wire [31:0] multiplexer_1_out, register_1_q, register_2_q, register_3_q, register_4_q;

  and and_1 (and_1_out, change, ~read);  // AND_Gate
  Demultiplexer #(.select(2), .width(1), .tristate("false"), .disabled("Z"), .enable("false")) demultiplexer_1 (
    .out0(demultiplexer_1_out0), .out1(demultiplexer_1_out1), .out2(demultiplexer_1_out2),
    .out3(demultiplexer_1_out3), .in(and_1_out), .sel(SP));
  and and_2 (and_2_out, buffer_1_out_2, change);
  buffer buffer_1 (.in_1(CLK), .out_2(buffer_1_out_2));
  Register #(.width(32), .trigger("falling"), .Select("low")) register_1 (
    .D(\输入 ), .en(demultiplexer_1_out0), .Q(register_1_q), .clk(CLK));  // open: clr
  Counter #(.width(2), .max('h3), .ongoal("wrap"), .trigger("rising"), .behavior("new")) counter_1 (
    .Q(SP), .clk(and_2_out), .down(read));  // open: load, D, count, carry, clr, preset
  Register #(.width(32), .trigger("falling"), .Select("low")) register_2 (
    .D(\输入 ), .en(demultiplexer_1_out2), .Q(register_2_q), .clk(CLK));  // open: clr
  Register #(.width(32), .trigger("falling"), .Select("low")) register_3 (
    .D(\输入 ), .en(demultiplexer_1_out1), .Q(register_3_q), .clk(CLK));  // open: clr
  Register #(.width(32), .trigger("falling"), .Select("low")) register_4 (
    .D(\输入 ), .en(demultiplexer_1_out3), .Q(register_4_q), .clk(CLK));  // open: clr
  Register #(.width(32), .trigger("rising"), .Select("low")) register_5 (
    .D(multiplexer_1_out), .Q(\输出 ), .clk(CLK));  // open: en, clr
  Multiplexer #(.select(2), .width(32), .disabled("Z"), .enable("false")) multiplexer_1 (
    .in0(register_1_q), .in1(register_3_q), .in2(register_2_q), .in3(register_4_q), .out(multiplexer_1_out),
    .sel(SP));

  // Other names for the same wires on the sheet: input[31:0] = \输入 ; output[31:0] = \输出 
endmodule

module \硬件堆栈_1  (
  input  CLK,
  input  read,
  input  change,
  input  [1:0] \输入 ,
  output [1:0] \输出 
);

  wire and_1_out, and_2_out, buffer_1_out_2, demultiplexer_1_out0, demultiplexer_1_out1,
       demultiplexer_1_out2, demultiplexer_1_out3;
  wire [1:0] multiplexer_1_out, register_1_q, register_2_q, register_3_q, register_4_q, SP;

  Demultiplexer #(.select(2), .width(1), .tristate("false"), .disabled("Z"), .enable("false")) demultiplexer_1 (
    .out0(demultiplexer_1_out0), .out1(demultiplexer_1_out1), .out2(demultiplexer_1_out2),
    .out3(demultiplexer_1_out3), .in(and_1_out), .sel(SP));
  and and_1 (and_1_out, change, ~read);  // AND_Gate
  and and_2 (and_2_out, buffer_1_out_2, change);
  buffer buffer_1 (.in_1(CLK), .out_2(buffer_1_out_2));
  Register #(.width(2), .trigger("falling"), .Select("low")) register_1 (
    .D(\输入 ), .en(demultiplexer_1_out0), .Q(register_1_q), .clk(CLK));  // open: clr
  Counter #(.width(2), .max('h3), .ongoal("wrap"), .trigger("rising"), .behavior("new")) counter_1 (
    .Q(SP), .clk(and_2_out), .down(read));  // open: load, D, count, carry, clr, preset
  Register #(.width(2), .trigger("falling"), .Select("low")) register_2 (
    .D(\输入 ), .en(demultiplexer_1_out2), .Q(register_2_q), .clk(CLK));  // open: clr
  Register #(.width(2), .trigger("falling"), .Select("low")) register_3 (
    .D(\输入 ), .en(demultiplexer_1_out1), .Q(register_3_q), .clk(CLK));  // open: clr
  Register #(.width(2), .trigger("falling"), .Select("low")) register_4 (
    .D(\输入 ), .en(demultiplexer_1_out3), .Q(register_4_q), .clk(CLK));  // open: clr
  Register #(.width(2), .trigger("rising"), .Select("low")) register_5 (
    .D(multiplexer_1_out), .Q(\输出 ), .clk(CLK));  // open: en, clr
  Multiplexer #(.select(2), .width(2), .disabled("Z"), .enable("false")) multiplexer_1 (
    .in0(register_1_q), .in1(register_3_q), .in2(register_2_q), .in3(register_4_q), .out(multiplexer_1_out),
    .sel(SP));

  // Other names for the same wires on the sheet: input[1:0] = \输入 ; output[1:0] = \输出 
endmodule

module buffer (
  input  in_1,
  output out_2
);

  wire buffer_1_out, buffer_2_out, buffer_3_out, buffer_4_out, buffer_5_out, buffer_6_out, buffer_7_out,
       buffer_8_out, buffer_9_out, buffer_10_out, buffer_11_out, buffer_12_out, buffer_13_out, buffer_14_out,
       buffer_15_out, buffer_16_out, buffer_17_out, buffer_18_out, buffer_19_out, buffer_20_out,
       buffer_21_out, buffer_22_out, buffer_23_out, buffer_24_out, buffer_25_out, buffer_26_out,
       buffer_27_out, buffer_28_out, buffer_30_out;

  buf buffer_1 (buffer_1_out, in_1);
  buf buffer_2 (buffer_2_out, buffer_3_out);
  buf buffer_3 (buffer_3_out, buffer_1_out);
  buf buffer_4 (buffer_4_out, buffer_2_out);
  buf buffer_5 (buffer_5_out, buffer_7_out);
  buf buffer_6 (buffer_6_out, buffer_5_out);
  buf buffer_7 (buffer_7_out, buffer_4_out);
  buf buffer_8 (buffer_8_out, buffer_10_out);
  buf buffer_9 (buffer_9_out, buffer_11_out);
  buf buffer_10 (buffer_10_out, buffer_6_out);
  buf buffer_11 (buffer_11_out, buffer_8_out);
  buf buffer_12 (buffer_12_out, buffer_15_out);
  buf buffer_13 (buffer_13_out, buffer_12_out);
  buf buffer_14 (buffer_14_out, buffer_9_out);
  buf buffer_15 (buffer_15_out, buffer_14_out);
  buf buffer_16 (buffer_16_out, buffer_13_out);
  buf buffer_17 (buffer_17_out, buffer_19_out);
  buf buffer_18 (buffer_18_out, buffer_16_out);
  buf buffer_19 (buffer_19_out, buffer_18_out);
  buf buffer_20 (buffer_20_out, buffer_22_out);
  buf buffer_21 (buffer_21_out, buffer_17_out);
  buf buffer_22 (buffer_22_out, buffer_21_out);
  buf buffer_23 (buffer_23_out, buffer_20_out);
  buf buffer_24 (buffer_24_out, buffer_23_out);
  buf buffer_25 (buffer_25_out, buffer_26_out);
  buf buffer_26 (buffer_26_out, buffer_24_out);
  buf buffer_27 (buffer_27_out, buffer_25_out);
  buf buffer_28 (buffer_28_out, buffer_27_out);
  buf buffer_29 (out_2, buffer_30_out);
  buf buffer_30 (buffer_30_out, buffer_28_out);
endmodule

module \封装正确性测试  (
);

  wire IR1, IR2, IR3, MemW, RegW;
  wire [31:0] EX_PC, ID_PC, IF_PC, IR, LED, MDin, MDinr, MEM_PC, PC, RDin, RDinr, WB_PC;

  \单周期MIPS  \u_单周期mips_1  (
    .RegWrite(RegW), .MemWrite(MemW), .PC(PC), .IR(IR), .RDin(RDin), .MDin(MDin), .LedData(LED));  // open: IR1, IR2, IR3
  \气泡流水线  \u_气泡流水线_1  (
    .RegWrite(RegW), .MemWrite(MemW), .IF_PC(IF_PC), .ID_PC(ID_PC), .EX_PC(EX_PC), .M_PC(MEM_PC),
    .WB_PC(WB_PC), .RDin(RDinr), .MDin(MDinr), .LedData(LED));
  \单周期MIPS_单级中断  \u_单周期mips_单级中断_1  (
    .IR1(IR1), .IR2(IR2), .IR3(IR3), .RegWrite(RegW), .MemWrite(MemW), .PC(PC), .IR(IR), .RDin(RDin),
    .MDin(MDin), .LedData(LED));
  \理想流水线  \u_理想流水线_1  (
    .RegWrite(RegW), .MemWrite(MemW), .IF_PC(IF_PC), .ID_PC(ID_PC), .EX_PC(EX_PC), .M_PC(MEM_PC),
    .WB_PC(WB_PC), .RDin(RDinr), .MDin(MDinr), .LedData(LED));
  \重定向流水线  \u_重定向流水线_1  (
    .RegWrite(RegW), .MemWrite(MemW), .IF_PC(IF_PC), .ID_PC(ID_PC), .EX_PC(EX_PC), .M_PC(MEM_PC),
    .WB_PC(WB_PC), .RDin(RDinr), .MDin(MDinr), .LedData(LED));
  \单周期MIPS_多级中断  \u_单周期mips_多级中断_1  (
    .IR1(IR1), .IR2(IR2), .IR3(IR3), .RegWrite(RegW), .MemWrite(MemW), .PC(PC), .IR(IR), .RDin(RDin),
    .MDin(MDin), .LedData(LED));

  // Notes on the sheet:
  //   单周期封装测试
  //   气泡流水封装测试
  //   单周期+单级中断封装测试
  //   请检查上面封装有无位宽不匹配，引脚标签是否和连接的标签相对应，否则无法在educoder平台上正确测试
  //   理想流水封装测试
  //   重定向流水封装测试
  //   单周期+多级中断封装测试
endmodule
